// Logisim project SYSLOG.circ as structural Verilog: 29 circuits, main circuit main
module main (
  output gnd,
  output sign
);

  wire Alarm_1_buzzer, and_1_out, and_2_out, boutonA_out, BoutonB_out, clock_1_out, cndt_1_buzzready,
       cndt_1_zero, demultiplexer_1_out0, demultiplexer_1_out1, demultiplexer_1_out3, demultiplexer_1_out4,
       demultiplexer_2_out0, demultiplexer_2_out1, demultiplexer_2_out4, demultiplexer_3_out0,
       demultiplexer_3_out1, demultiplexer_3_out2, demultiplexer_3_out3, demultiplexer_3_out4,
       demultiplexer_4_out0, demultiplexer_4_out1, demultiplexer_4_out2, demultiplexer_4_out3,
       demultiplexer_4_out4, or_1_out, smartbutton_1_fall, smartbutton_1_long, smartbutton_1_tlong,
       smartbutton_2_fall, smartbutton_2_long, smartbutton_2_tlong;
  wire [2:0] primary_1_choice;
  wire [3:0] decodeur_SEPT_segm_1_a, decodeur_SEPT_segm_1_p, decodeur_SEPT_segm_2_a, decodeur_SEPT_segm_2_p,
       decodeur_SEPT_segm_3_a, decodeur_SEPT_segm_3_p, decodeur_SEPT_segm_4_a, decodeur_SEPT_segm_4_p,
       decodeur_SEPT_segm_5_a, decodeur_SEPT_segm_5_p, decodeur_SEPT_segm_6_a, decodeur_SEPT_segm_6_p;
  wire [4:0] decalhorraire_1_hour_shift;
  wire [5:0] Alarm_1_hour0, Alarm_1_hour1, Alarm_1_min0, Alarm_1_min1, Alarm_1_s0, Alarm_1_s1, chrono_1_h0,
       chrono_1_h1, chrono_1_m0, chrono_1_m1, chrono_1_s0, chrono_1_s1, cndt_1_h0, cndt_1_h1, cndt_1_m0,
       cndt_1_m1, cndt_1_s0, cndt_1_s1, decalhorraire_1_hour0, decalhorraire_1_hour1, decalhorraire_1_min0,
       decalhorraire_1_min1, decalhorraire_1_sec0, decalhorraire_1_sec1, ModHorloge_1_h0, ModHorloge_1_h1,
       ModHorloge_1_hours, ModHorloge_1_m0, ModHorloge_1_m1, ModHorloge_1_minutes, ModHorloge_1_s0,
       ModHorloge_1_s1, multiplexer_1_out, multiplexer_2_out, multiplexer_3_out, multiplexer_4_out,
       multiplexer_5_out, multiplexer_6_out, nav_1_hour0, nav_1_hour1, nav_1_min0, nav_1_min1, nav_1_sec0,
       nav_1_sec1;

  Clock clock_1 (.out(clock_1_out));
  Button boutonA (.out(boutonA_out));
  Button BoutonB (.out(BoutonB_out));
  and and_1 (and_1_out, smartbutton_1_long, smartbutton_2_long);
  smartbutton smartbutton_1 (
    .button(boutonA_out), .clk(clock_1_out), .fall(smartbutton_1_fall), .Tlong(smartbutton_1_tlong),
    .long(smartbutton_1_long));
  smartbutton smartbutton_2 (
    .button(BoutonB_out), .clk(clock_1_out), .fall(smartbutton_2_fall), .Tlong(smartbutton_2_tlong),
    .long(smartbutton_2_long));
  Demultiplexer #(.select(3), .enable("false")) demultiplexer_1 (
    .out0(demultiplexer_1_out0), .out1(demultiplexer_1_out1), .out3(demultiplexer_1_out3),
    .out4(demultiplexer_1_out4), .in(smartbutton_1_fall), .sel(primary_1_choice));  // open: out2, out5, out6, out7
  Demultiplexer #(.select(3), .enable("false")) demultiplexer_2 (
    .out0(demultiplexer_2_out0), .out1(demultiplexer_2_out1), .out4(demultiplexer_2_out4),
    .in(smartbutton_1_tlong), .sel(primary_1_choice));  // open: out2, out3, out5, out6, out7
  Demultiplexer #(.select(3), .enable("false")) demultiplexer_3 (
    .out0(demultiplexer_3_out0), .out1(demultiplexer_3_out1), .out2(demultiplexer_3_out2),
    .out3(demultiplexer_3_out3), .out4(demultiplexer_3_out4), .in(smartbutton_2_fall), .sel(primary_1_choice));  // open: out5, out6, out7
  primary primary_1 (.TlongB(smartbutton_2_tlong), .clk(clock_1_out), .rst(and_1_out), .choice(primary_1_choice));
  ModHorloge ModHorloge_1 (
    .mrst(and_1_out), .clk(clock_1_out), .LongA(demultiplexer_2_out0), .ButtA(demultiplexer_1_out0),
    .ButtB(demultiplexer_3_out0), .shift(decalhorraire_1_hour_shift), .s0(ModHorloge_1_s0),
    .s1(ModHorloge_1_s1), .m0(ModHorloge_1_m0), .m1(ModHorloge_1_m1), .h0(ModHorloge_1_h0),
    .h1(ModHorloge_1_h1), .Hours(ModHorloge_1_hours), .minutes(ModHorloge_1_minutes));
  Alarm Alarm_1 (
    .LongA(demultiplexer_2_out1), .rst(and_1_out), .clk(clock_1_out), .A(demultiplexer_1_out1),
    .B(demultiplexer_3_out1), .hour(ModHorloge_1_hours), .min(ModHorloge_1_minutes), .s0(Alarm_1_s0),
    .s1(Alarm_1_s1), .min0(Alarm_1_min0), .min1(Alarm_1_min1), .hour0(Alarm_1_hour0), .hour1(Alarm_1_hour1),
    .buzzer(Alarm_1_buzzer));
  decalhorraire decalhorraire_1 (
    .rst(and_1_out), .button(demultiplexer_3_out2), .clk(clock_1_out), .hour1(decalhorraire_1_hour1),
    .hour0(decalhorraire_1_hour0), .min1(decalhorraire_1_min1), .min0(decalhorraire_1_min0),
    .sec1(decalhorraire_1_sec1), .sec0(decalhorraire_1_sec0), .hour_shift(decalhorraire_1_hour_shift));
  chrono chrono_1 (
    .rst(and_1_out), .clk(clock_1_out), .FallA(demultiplexer_1_out3), .fallB(demultiplexer_3_out3),
    .h0(chrono_1_h0), .h1(chrono_1_h1), .m0(chrono_1_m0), .m1(chrono_1_m1), .s0(chrono_1_s0), .s1(chrono_1_s1));
  cndt cndt_1 (
    .rst(and_1_out), .clk(clock_1_out), .change(demultiplexer_2_out4), .choice(demultiplexer_1_out4),
    .inc(demultiplexer_3_out4), .s0(cndt_1_s0), .s1(cndt_1_s1), .m0(cndt_1_m0), .m1(cndt_1_m1),
    .h0(cndt_1_h0), .h1(cndt_1_h1), .zero(cndt_1_zero), .buzzReady(cndt_1_buzzready));
  and and_2 (and_2_out, cndt_1_zero, cndt_1_buzzready);
  Multiplexer #(.select(3), .width(6), .enable("false")) multiplexer_1 (
    .in0(ModHorloge_1_s0), .in1(Alarm_1_s0), .in2(decalhorraire_1_sec0), .in3(chrono_1_s0), .in4(cndt_1_s0),
    .in5(6'b001010), .in6(6'b001010), .in7(6'b001010), .out(multiplexer_1_out), .sel(primary_1_choice));
  Multiplexer #(.select(3), .width(6), .enable("false")) multiplexer_2 (
    .in0(ModHorloge_1_s1), .in1(Alarm_1_s1), .in2(decalhorraire_1_sec1), .in3(chrono_1_s1), .in4(cndt_1_s1),
    .in5(6'b001010), .in6(6'b001010), .in7(6'b001010), .out(multiplexer_2_out), .sel(primary_1_choice));
  Multiplexer #(.select(3), .width(6), .enable("false")) multiplexer_3 (
    .in0(ModHorloge_1_m0), .in1(Alarm_1_min0), .in2(decalhorraire_1_min0), .in3(chrono_1_m0),
    .in4(cndt_1_m0), .in5(6'b001010), .in6(6'b001010), .in7(6'b001010), .out(multiplexer_3_out),
    .sel(primary_1_choice));
  Multiplexer #(.select(3), .width(6), .enable("false")) multiplexer_4 (
    .in0(ModHorloge_1_m1), .in1(Alarm_1_min1), .in2(decalhorraire_1_min1), .in3(chrono_1_m1),
    .in4(cndt_1_m1), .in5(6'b001010), .in6(6'b001010), .in7(6'b001010), .out(multiplexer_4_out),
    .sel(primary_1_choice));
  Multiplexer #(.select(3), .width(6), .enable("false")) multiplexer_5 (
    .in0(ModHorloge_1_h0), .in1(Alarm_1_hour0), .in2(decalhorraire_1_hour0), .in3(chrono_1_h0),
    .in4(cndt_1_h0), .in5(6'b001010), .in6(6'b001010), .in7(6'b001010), .out(multiplexer_5_out),
    .sel(primary_1_choice));
  Multiplexer #(.select(3), .width(6), .enable("false")) multiplexer_6 (
    .in0(ModHorloge_1_h1), .in1(Alarm_1_hour1), .in2(decalhorraire_1_hour1), .in3(chrono_1_h1),
    .in4(cndt_1_h1), .in5(6'b001010), .in6(6'b001010), .in7(6'b001010), .out(multiplexer_6_out),
    .sel(primary_1_choice));
  or or_1 (or_1_out, Alarm_1_buzzer, and_2_out);
  nav nav_1 (
    .pos(primary_1_choice), .longB(smartbutton_2_long), .h1(multiplexer_6_out), .h0(multiplexer_5_out),
    .m1(multiplexer_4_out), .m0(multiplexer_3_out), .s1(multiplexer_2_out), .s0(multiplexer_1_out),
    .hour1(nav_1_hour1), .hour0(nav_1_hour0), .min1(nav_1_min1), .min0(nav_1_min0), .sec1(nav_1_sec1),
    .sec0(nav_1_sec0));
  partition partition_1 (.en(or_1_out), .clk(clock_1_out), .rst(and_1_out), .gnd(gnd), .sgn(sign));
  decodeur_SEPT_segm decodeur_SEPT_segm_1 (
    .i0(nav_1_sec0[5]), .i1(nav_1_sec0[4]), .i2(nav_1_sec0[3]), .i3(nav_1_sec0[2]), .i4(nav_1_sec0[1]),
    .i5(nav_1_sec0[0]), .a(decodeur_SEPT_segm_1_a[0]), .b(decodeur_SEPT_segm_1_a[1]),
    .c(decodeur_SEPT_segm_1_p[1]), .d(decodeur_SEPT_segm_1_p[2]), .e(decodeur_SEPT_segm_1_p[3]),
    .f(decodeur_SEPT_segm_1_a[2]), .g(decodeur_SEPT_segm_1_a[3]), .p(decodeur_SEPT_segm_1_p[0]));
  decodeur_SEPT_segm decodeur_SEPT_segm_3 (
    .i0(nav_1_min0[5]), .i1(nav_1_min0[4]), .i2(nav_1_min0[3]), .i3(nav_1_min0[2]), .i4(nav_1_min0[1]),
    .i5(nav_1_min0[0]), .a(decodeur_SEPT_segm_3_a[0]), .b(decodeur_SEPT_segm_3_a[1]),
    .c(decodeur_SEPT_segm_3_p[1]), .d(decodeur_SEPT_segm_3_p[2]), .e(decodeur_SEPT_segm_3_p[3]),
    .f(decodeur_SEPT_segm_3_a[2]), .g(decodeur_SEPT_segm_3_a[3]), .p(decodeur_SEPT_segm_3_p[0]));
  decodeur_SEPT_segm decodeur_SEPT_segm_5 (
    .i0(nav_1_hour0[5]), .i1(nav_1_hour0[4]), .i2(nav_1_hour0[3]), .i3(nav_1_hour0[2]), .i4(nav_1_hour0[1]),
    .i5(nav_1_hour0[0]), .a(decodeur_SEPT_segm_5_a[0]), .b(decodeur_SEPT_segm_5_a[1]),
    .c(decodeur_SEPT_segm_5_p[1]), .d(decodeur_SEPT_segm_5_p[2]), .e(decodeur_SEPT_segm_5_p[3]),
    .f(decodeur_SEPT_segm_5_a[2]), .g(decodeur_SEPT_segm_5_a[3]), .p(decodeur_SEPT_segm_5_p[0]));
  LED LED_1 (.in(demultiplexer_4_out0));
  LED LED_2 (.in(demultiplexer_4_out1));
  LED LED_4 (.in(demultiplexer_4_out3));
  LED LED_3 (.in(demultiplexer_4_out2));
  LED LED_5 (.in(demultiplexer_4_out4));
  Demultiplexer #(.select(3), .enable("false")) demultiplexer_4 (
    .out0(demultiplexer_4_out0), .out1(demultiplexer_4_out1), .out2(demultiplexer_4_out2),
    .out3(demultiplexer_4_out3), .out4(demultiplexer_4_out4), .in(1'b1), .sel(primary_1_choice));  // open: out5, out6, out7
  decodeur_SEPT_segm decodeur_SEPT_segm_2 (
    .i0(nav_1_sec1[5]), .i1(nav_1_sec1[4]), .i2(nav_1_sec1[3]), .i3(nav_1_sec1[2]), .i4(nav_1_sec1[1]),
    .i5(nav_1_sec1[0]), .a(decodeur_SEPT_segm_2_a[0]), .b(decodeur_SEPT_segm_2_a[1]),
    .c(decodeur_SEPT_segm_2_p[1]), .d(decodeur_SEPT_segm_2_p[2]), .e(decodeur_SEPT_segm_2_p[3]),
    .f(decodeur_SEPT_segm_2_a[2]), .g(decodeur_SEPT_segm_2_a[3]), .p(decodeur_SEPT_segm_2_p[0]));
  decodeur_SEPT_segm decodeur_SEPT_segm_4 (
    .i0(nav_1_min1[5]), .i1(nav_1_min1[4]), .i2(nav_1_min1[3]), .i3(nav_1_min1[2]), .i4(nav_1_min1[1]),
    .i5(nav_1_min1[0]), .a(decodeur_SEPT_segm_4_a[0]), .b(decodeur_SEPT_segm_4_a[1]),
    .c(decodeur_SEPT_segm_4_p[1]), .d(decodeur_SEPT_segm_4_p[2]), .e(decodeur_SEPT_segm_4_p[3]),
    .f(decodeur_SEPT_segm_4_a[2]), .g(decodeur_SEPT_segm_4_a[3]), .p(decodeur_SEPT_segm_4_p[0]));
  decodeur_SEPT_segm decodeur_SEPT_segm_6 (
    .i0(nav_1_hour1[5]), .i1(nav_1_hour1[4]), .i2(nav_1_hour1[3]), .i3(nav_1_hour1[2]), .i4(nav_1_hour1[1]),
    .i5(nav_1_hour1[0]), .a(decodeur_SEPT_segm_6_a[0]), .b(decodeur_SEPT_segm_6_a[1]),
    .c(decodeur_SEPT_segm_6_p[1]), .d(decodeur_SEPT_segm_6_p[2]), .e(decodeur_SEPT_segm_6_p[3]),
    .f(decodeur_SEPT_segm_6_a[2]), .g(decodeur_SEPT_segm_6_a[3]), .p(decodeur_SEPT_segm_6_p[0]));
  LED mrst (.in(and_1_out));
  _7_Segment_Display L_7_Segment_Display_1 (
    .g(decodeur_SEPT_segm_6_a[3]), .f(decodeur_SEPT_segm_6_a[2]), .a(decodeur_SEPT_segm_6_a[0]),
    .b(decodeur_SEPT_segm_6_a[1]), .e(decodeur_SEPT_segm_6_p[3]), .d(decodeur_SEPT_segm_6_p[2]),
    .c(decodeur_SEPT_segm_6_p[1]), .dp(decodeur_SEPT_segm_6_p[0]));
  _7_Segment_Display L_7_Segment_Display_3 (
    .g(decodeur_SEPT_segm_4_a[3]), .f(decodeur_SEPT_segm_4_a[2]), .a(decodeur_SEPT_segm_4_a[0]),
    .b(decodeur_SEPT_segm_4_a[1]), .e(decodeur_SEPT_segm_4_p[3]), .d(decodeur_SEPT_segm_4_p[2]),
    .c(decodeur_SEPT_segm_4_p[1]), .dp(decodeur_SEPT_segm_4_p[0]));
  _7_Segment_Display L_7_Segment_Display_2 (
    .g(decodeur_SEPT_segm_5_a[3]), .f(decodeur_SEPT_segm_5_a[2]), .a(decodeur_SEPT_segm_5_a[0]),
    .b(decodeur_SEPT_segm_5_a[1]), .e(decodeur_SEPT_segm_5_p[3]), .d(decodeur_SEPT_segm_5_p[2]),
    .c(decodeur_SEPT_segm_5_p[1]), .dp(decodeur_SEPT_segm_5_p[0]));
  _7_Segment_Display L_7_Segment_Display_4 (
    .g(decodeur_SEPT_segm_3_a[3]), .f(decodeur_SEPT_segm_3_a[2]), .a(decodeur_SEPT_segm_3_a[0]),
    .b(decodeur_SEPT_segm_3_a[1]), .e(decodeur_SEPT_segm_3_p[3]), .d(decodeur_SEPT_segm_3_p[2]),
    .c(decodeur_SEPT_segm_3_p[1]), .dp(decodeur_SEPT_segm_3_p[0]));
  _7_Segment_Display L_7_Segment_Display_5 (
    .g(decodeur_SEPT_segm_2_a[3]), .f(decodeur_SEPT_segm_2_a[2]), .a(decodeur_SEPT_segm_2_a[0]),
    .b(decodeur_SEPT_segm_2_a[1]), .e(decodeur_SEPT_segm_2_p[3]), .d(decodeur_SEPT_segm_2_p[2]),
    .c(decodeur_SEPT_segm_2_p[1]), .dp(decodeur_SEPT_segm_2_p[0]));
  _7_Segment_Display L_7_Segment_Display_6 (
    .g(decodeur_SEPT_segm_1_a[3]), .f(decodeur_SEPT_segm_1_a[2]), .a(decodeur_SEPT_segm_1_a[0]),
    .b(decodeur_SEPT_segm_1_a[1]), .e(decodeur_SEPT_segm_1_p[3]), .d(decodeur_SEPT_segm_1_p[2]),
    .c(decodeur_SEPT_segm_1_p[1]), .dp(decodeur_SEPT_segm_1_p[0]));

  // Notes on the sheet:
  //   MODE
endmodule

module Horloge (
  input  MRST,
  input  clk,
  input  longA,
  input  FallA,
  input  FallB,
  output [9:0] ms,
  output [5:0] Seconds,
  output [5:0] Minutes,
  output [4:0] Hours,
  output wrtMode
);

  wire and_1_out, and_2_out, and_3_out, and_4_out, and_5_out, and_6_out, and_7_out, and_8_out, and_9_out,
       and_10_out, and_11_out, and_12_out, and_13_out, and_14_out, and_15_out, and_16_out, and_17_out,
       and_18_out, and_19_out, and_20_out, and_21_out, and_22_out, and_23_out, and_24_out, counter8bit_1_o0,
       counter8bit_1_o1, counter8bit_1_o2, counter8bit_1_ovrf, counter8bit_4_o0, counter8bit_4_o1,
       counter8bit_4_o2, counter8bit_4_o3, counter8bit_4_o4, counter8bit_4_o5, counter8bit_6_o0,
       counter8bit_6_o1, counter8bit_6_o2, counter8bit_6_o3, counter8bit_6_o4, d_ff_1_q, d_ff_2_q, d_ff_3_q,
       d_ff_4_q, d_ff_5_q, d_ff_6_q, not_1_out, or_1_out, or_2_out, or_3_out, or_4_out, or_5_out, or_6_out,
       t_ff_2_q;

  and and_1 (and_1_out, wrtMode, FallA);
  and and_2 (and_2_out, wrtMode, FallB);
  T_Flip_Flop t_ff_1 (.T(longA), .clk(clk), .Q(wrtMode), .reset(MRST), .preset(1'b0));  // open: Qn
  T_Flip_Flop t_ff_2 (.T(and_1_out), .clk(clk), .Q(t_ff_2_q), .reset(MRST), .preset(1'b0));  // open: Qn
  and and_3 (and_3_out, counter8bit_4_o5, counter8bit_4_o4, counter8bit_4_o3, counter8bit_4_o2, ~counter8bit_4_o1, ~counter8bit_4_o0);  // AND_Gate
  and and_4 (and_4_out, counter8bit_6_o4, counter8bit_6_o3, ~counter8bit_6_o2, ~counter8bit_6_o1, ~counter8bit_6_o0);  // AND_Gate
  and and_5 (and_5_out, t_ff_2_q, and_2_out);
  or or_1 (or_1_out, and_3_out, MRST);
  counter8bit counter8bit_4 (
    .EN(and_5_out), .clk(clk), .rst(or_1_out), .WRITE(1'b0), .I7(1'b0), .I6(1'b0), .I5(1'b0), .I4(1'b0),
    .I3(1'b0), .I2(1'b0), .I1(1'b0), .I0(1'b0), .O5(counter8bit_4_o5), .O4(counter8bit_4_o4),
    .O3(counter8bit_4_o3), .O2(counter8bit_4_o2), .O1(counter8bit_4_o1), .O0(counter8bit_4_o0));  // open: OVRF, O7, O6
  and and_6 (and_6_out, not_1_out, and_2_out);
  or or_2 (or_2_out, and_4_out, MRST);
  counter8bit counter8bit_6 (
    .EN(and_6_out), .clk(clk), .rst(or_2_out), .WRITE(1'b0), .I7(1'b0), .I6(1'b0), .I5(1'b0), .I4(1'b0),
    .I3(1'b0), .I2(1'b0), .I1(1'b0), .I0(1'b0), .O4(counter8bit_6_o4), .O3(counter8bit_6_o3),
    .O2(counter8bit_6_o2), .O1(counter8bit_6_o1), .O0(counter8bit_6_o0));  // open: OVRF, O7, O6, O5
  not not_1 (not_1_out, t_ff_2_q);
  or or_3 (or_3_out, MRST, and_20_out);
  or or_4 (or_4_out, MRST, and_7_out);
  or or_5 (or_5_out, MRST, and_8_out);
  or or_6 (or_6_out, MRST, and_9_out);
  and and_7 (and_7_out, Seconds[5], Seconds[4], Seconds[3], Seconds[2], ~Seconds[1], ~Seconds[0]);  // AND_Gate
  and and_8 (and_8_out, Minutes[5], Minutes[4], Minutes[3], Minutes[2], ~Minutes[1], ~Minutes[0]);  // AND_Gate
  and and_9 (and_9_out, Hours[4], Hours[3], ~Hours[2], ~Hours[1], ~Hours[0]);  // AND_Gate
  and and_10 (and_10_out, counter8bit_1_o2, counter8bit_1_o1, counter8bit_1_o0);
  and and_11 (and_11_out, ~wrtMode, 1'b1);  // AND_Gate
  counter8bit counter8bit_1 (
    .EN(and_11_out), .clk(clk), .rst(or_3_out), .WRITE(1'b0), .I7(1'b0), .I6(1'b0), .I5(1'b0), .I4(1'b0),
    .I3(1'b0), .I2(1'b0), .I1(1'b0), .I0(1'b0), .OVRF(counter8bit_1_ovrf), .O7(ms[4]), .O6(ms[3]),
    .O5(ms[2]), .O4(ms[1]), .O3(ms[0]), .O2(counter8bit_1_o2), .O1(counter8bit_1_o1), .O0(counter8bit_1_o0));
  counter8bit counter8bit_3 (
    .EN(and_22_out), .clk(clk), .rst(or_4_out), .WRITE(1'b0), .I7(1'b0), .I6(1'b0), .I5(1'b0), .I4(1'b0),
    .I3(1'b0), .I2(1'b0), .I1(1'b0), .I0(1'b0), .O5(Seconds[5]), .O4(Seconds[4]), .O3(Seconds[3]),
    .O2(Seconds[2]), .O1(Seconds[1]), .O0(Seconds[0]));  // open: OVRF, O7, O6
  and and_12 (and_12_out, Seconds[0], Seconds[1], ~Seconds[2], and_21_out, Seconds[3], Seconds[4], Seconds[5]);  // AND_Gate
  counter8bit counter8bit_5 (
    .EN(and_23_out), .clk(clk), .rst(or_5_out), .WRITE(wrtMode), .I7(1'b0), .I6(1'b0), .I5(counter8bit_4_o5),
    .I4(counter8bit_4_o4), .I3(counter8bit_4_o3), .I2(counter8bit_4_o2), .I1(counter8bit_4_o1),
    .I0(counter8bit_4_o0), .O5(Minutes[5]), .O4(Minutes[4]), .O3(Minutes[3]), .O2(Minutes[2]),
    .O1(Minutes[1]), .O0(Minutes[0]));  // open: OVRF, O7, O6
  and and_13 (and_13_out, Minutes[0], Minutes[1], ~Minutes[2], and_12_out, Minutes[3], Minutes[4], Minutes[5]);  // AND_Gate
  counter8bit counter8bit_7 (
    .EN(and_24_out), .clk(clk), .rst(or_6_out), .WRITE(wrtMode), .I7(1'b0), .I6(1'b0), .I5(1'b0),
    .I4(counter8bit_6_o4), .I3(counter8bit_6_o3), .I2(counter8bit_6_o2), .I1(counter8bit_6_o1),
    .I0(counter8bit_6_o0), .O4(Hours[4]), .O3(Hours[3]), .O2(Hours[2]), .O1(Hours[1]), .O0(Hours[0]));  // open: OVRF, O7, O6, O5
  and and_14 (and_14_out, d_ff_4_q, ~and_21_out);  // AND_Gate
  D_Flip_Flop d_ff_1 (.D(and_15_out), .clk(clk), .Q(d_ff_1_q), .preset(1'b0), .reset(and_14_out));  // open: Qn
  and and_15 (and_15_out, ~d_ff_4_q, and_21_out);  // AND_Gate
  D_Flip_Flop d_ff_2 (.D(and_16_out), .clk(clk), .Q(d_ff_2_q), .preset(1'b0), .reset(and_17_out));  // open: Qn
  and and_16 (and_16_out, ~d_ff_5_q, and_12_out);  // AND_Gate
  and and_17 (and_17_out, d_ff_5_q, ~and_12_out);  // AND_Gate
  D_Flip_Flop d_ff_3 (.D(and_18_out), .clk(clk), .Q(d_ff_3_q), .preset(1'b0), .reset(and_19_out));  // open: Qn
  and and_18 (and_18_out, ~d_ff_6_q, and_13_out);  // AND_Gate
  and and_19 (and_19_out, d_ff_6_q, ~and_13_out);  // AND_Gate
  counter8bit counter8bit_2 (
    .EN(counter8bit_1_ovrf), .clk(clk), .rst(or_3_out), .WRITE(1'b0), .I7(1'b0), .I6(1'b0), .I5(1'b0),
    .I4(1'b0), .I3(1'b0), .I2(1'b0), .I1(1'b0), .I0(1'b0), .O4(ms[9]), .O3(ms[8]), .O2(ms[7]), .O1(ms[6]),
    .O0(ms[5]));  // open: OVRF, O7, O6, O5
  and and_20 (and_20_out, ms[0], ~ms[1], ~ms[2], ms[3], ~ms[4], ms[5], ms[6], ms[7], ms[8], ms[9]);  // AND_Gate
  D_Flip_Flop d_ff_4 (.D(d_ff_1_q), .clk(clk), .Q(d_ff_4_q), .preset(1'b0), .reset(and_14_out));  // open: Qn
  D_Flip_Flop d_ff_5 (.D(d_ff_2_q), .clk(clk), .Q(d_ff_5_q), .preset(1'b0), .reset(and_17_out));  // open: Qn
  D_Flip_Flop d_ff_6 (.D(d_ff_3_q), .clk(clk), .Q(d_ff_6_q), .preset(1'b0), .reset(and_19_out));  // open: Qn
  and and_21 (and_21_out, ~ms[0], ~ms[1], ~ms[2], ms[3], ~ms[4], ms[5], ms[6], ms[7], ms[8], ms[9], and_10_out);  // AND_Gate
  and and_22 (and_22_out, d_ff_1_q, ~d_ff_4_q);  // AND_Gate
  and and_23 (and_23_out, d_ff_2_q, ~d_ff_5_q);  // AND_Gate
  and and_24 (and_24_out, d_ff_3_q, ~d_ff_6_q);  // AND_Gate
endmodule

module ones (
  input  Input_1,
  input  Input_2,
  input  Input_3,
  input  Input_4,
  input  Input_5,
  input  Input_6,
  output Output_1,
  output Output_2,
  output Output_3,
  output Output_4,
  output Output_5,
  output Output_6
);

  wire and_1_out, and_2_out, and_3_out, and_4_out, and_5_out, and_6_out, and_7_out, and_8_out, and_9_out,
       and_10_out, and_11_out, and_12_out, and_13_out, and_14_out, and_15_out, and_16_out, and_17_out,
       and_18_out, and_19_out, and_20_out, and_21_out, and_22_out, and_23_out, and_24_out, not_1_out,
       not_2_out, not_3_out, not_4_out, not_5_out, not_6_out, not_7_out, not_8_out, not_9_out, not_10_out,
       not_11_out, not_12_out, not_13_out, not_14_out, not_15_out, not_16_out, not_17_out, not_18_out,
       not_19_out, not_20_out, not_21_out, not_22_out, not_23_out, not_24_out, not_25_out, not_26_out,
       not_27_out, not_28_out, not_29_out, not_30_out, not_31_out, not_32_out, not_33_out, not_34_out,
       not_35_out, not_36_out, not_37_out, not_38_out, not_39_out, not_40_out, not_41_out, not_42_out,
       not_43_out, not_44_out, not_45_out, not_46_out, not_47_out, not_48_out, not_49_out, not_50_out,
       not_51_out, not_52_out, not_53_out, not_54_out;

  not not_1 (not_1_out, Input_1);
  not not_2 (not_2_out, Input_2);
  not not_3 (not_3_out, Input_4);
  not not_4 (not_4_out, Input_5);
  not not_5 (not_5_out, Input_1);
  not not_6 (not_6_out, Input_3);
  not not_7 (not_7_out, Input_4);
  not not_8 (not_8_out, Input_1);
  not not_9 (not_9_out, Input_5);
  not not_10 (not_10_out, Input_2);
  not not_11 (not_11_out, Input_3);
  not not_12 (not_12_out, Input_3);
  not not_13 (not_13_out, Input_4);
  not not_14 (not_14_out, Input_5);
  not not_15 (not_15_out, Input_4);
  not not_16 (not_16_out, Input_2);
  not not_17 (not_17_out, Input_3);
  not not_18 (not_18_out, Input_5);
  not not_19 (not_19_out, Input_1);
  not not_20 (not_20_out, Input_2);
  not not_21 (not_21_out, Input_1);
  not not_22 (not_22_out, Input_4);
  not not_23 (not_23_out, Input_5);
  not not_24 (not_24_out, Input_1);
  not not_25 (not_25_out, Input_4);
  not not_26 (not_26_out, Input_4);
  not not_27 (not_27_out, Input_5);
  not not_28 (not_28_out, Input_2);
  not not_29 (not_29_out, Input_3);
  not not_30 (not_30_out, Input_4);
  not not_31 (not_31_out, Input_2);
  not not_32 (not_32_out, Input_3);
  not not_33 (not_33_out, Input_1);
  not not_34 (not_34_out, Input_2);
  not not_35 (not_35_out, Input_3);
  not not_36 (not_36_out, Input_1);
  not not_37 (not_37_out, Input_3);
  not not_38 (not_38_out, Input_1);
  not not_39 (not_39_out, Input_2);
  not not_40 (not_40_out, Input_5);
  not not_41 (not_41_out, Input_1);
  not not_42 (not_42_out, Input_3);
  not not_43 (not_43_out, Input_4);
  not not_44 (not_44_out, Input_5);
  not not_45 (not_45_out, Input_1);
  not not_46 (not_46_out, Input_4);
  not not_47 (not_47_out, Input_2);
  not not_48 (not_48_out, Input_3);
  not not_49 (not_49_out, Input_5);
  not not_50 (not_50_out, Input_3);
  not not_51 (not_51_out, Input_5);
  not not_52 (not_52_out, Input_2);
  not not_53 (not_53_out, Input_4);
  not not_54 (not_54_out, Input_5);
  and and_1 (and_1_out, not_1_out, not_2_out, Input_3, not_3_out, not_4_out);
  and and_2 (and_2_out, not_5_out, Input_2, not_6_out, not_7_out, Input_5);
  and and_3 (and_3_out, not_8_out, Input_2, Input_3, Input_4, not_9_out);
  and and_4 (and_4_out, Input_1, not_10_out, not_11_out, Input_4, Input_5);
  and and_5 (and_5_out, Input_1, Input_2, not_12_out, not_13_out, not_14_out);
  and and_6 (and_6_out, Input_1, Input_2, Input_3, not_15_out, Input_5);
  and and_7 (and_7_out, not_16_out, not_17_out, Input_4, not_18_out);
  and and_8 (and_8_out, not_19_out, not_20_out, Input_4, Input_5);
  and and_9 (and_9_out, not_21_out, Input_2, not_22_out, not_23_out);
  and and_10 (and_10_out, not_24_out, Input_2, Input_3, not_25_out);
  and and_11 (and_11_out, Input_2, Input_3, not_26_out, not_27_out);
  and and_12 (and_12_out, Input_1, not_28_out, not_29_out, not_30_out, Input_5);
  and and_13 (and_13_out, Input_1, not_31_out, Input_3, Input_4);
  and and_14 (and_14_out, Input_1, Input_2, not_32_out, Input_4, Input_5);
  and and_15 (and_15_out, not_33_out, not_34_out, not_35_out, Input_5);
  and and_16 (and_16_out, not_36_out, not_37_out, Input_4, Input_5);
  and and_17 (and_17_out, not_38_out, not_39_out, Input_3, Input_4, not_40_out);
  and and_18 (and_18_out, not_41_out, Input_2, not_42_out, not_43_out, not_44_out);
  and and_19 (and_19_out, not_45_out, Input_2, Input_3, not_46_out, Input_5);
  and and_20 (and_20_out, Input_1, not_47_out, not_48_out, not_49_out);
  and and_21 (and_21_out, Input_1, not_50_out, Input_4, not_51_out);
  and and_22 (and_22_out, Input_1, not_52_out, Input_3, Input_5);
  and and_23 (and_23_out, Input_1, Input_3, Input_4, Input_5);
  and and_24 (and_24_out, Input_1, Input_2, Input_3, not_53_out, not_54_out);
  or or_1 (Output_3, and_1_out, and_2_out, and_3_out, and_4_out, and_5_out, and_6_out);
  or or_2 (Output_4, and_7_out, and_8_out, and_9_out, and_10_out, and_11_out, and_12_out, and_13_out, and_14_out);
  or or_3 (Output_5, and_15_out, and_16_out, and_17_out, and_18_out, and_19_out, and_20_out, and_21_out, and_22_out, and_23_out, and_24_out);

  assign Output_1 = 1'b0;
  assign Output_2 = 1'b0;
  assign Output_6 = Input_6;
endmodule

module tens (
  input  Input_1,
  input  Input_2,
  input  Input_3,
  input  Input_4,
  input  Input_5,
  input  Input_6,
  output Output_1,
  output Output_2,
  output Output_3,
  output Output_4,
  output Output_5,
  output Output_6
);

  wire and_1_out, and_2_out, and_3_out, and_4_out, and_5_out, and_6_out, and_7_out, and_8_out, and_9_out,
       and_10_out, and_11_out, and_12_out, and_13_out, and_14_out, not_1_out, not_2_out, not_3_out,
       not_4_out, not_5_out, not_6_out, not_7_out, not_8_out, not_9_out, not_10_out, not_11_out, not_12_out,
       not_13_out, not_14_out, not_15_out, not_16_out, not_17_out;

  and and_1 (and_1_out, Input_1, Input_3);
  and and_2 (and_2_out, Input_1, Input_2);
  not not_1 (not_1_out, Input_1);
  and and_3 (and_3_out, not_1_out, Input_2, Input_4);
  not not_2 (not_2_out, Input_1);
  and and_4 (and_4_out, not_2_out, Input_2, Input_3);
  and and_5 (and_5_out, Input_2, Input_3, Input_4);
  not not_3 (not_3_out, Input_2);
  and and_6 (and_6_out, Input_1, not_3_out, not_4_out);
  not not_4 (not_4_out, Input_3);
  not not_5 (not_5_out, Input_1);
  not not_6 (not_6_out, Input_2);
  not not_7 (not_7_out, Input_1);
  not not_8 (not_8_out, Input_2);
  not not_9 (not_9_out, Input_1);
  not not_10 (not_10_out, Input_1);
  not not_11 (not_11_out, Input_3);
  not not_12 (not_12_out, Input_4);
  not not_13 (not_13_out, Input_2);
  not not_14 (not_14_out, Input_3);
  not not_15 (not_15_out, Input_3);
  not not_16 (not_16_out, Input_3);
  not not_17 (not_17_out, Input_4);
  or or_1 (Output_4, and_1_out, and_2_out);
  or or_2 (Output_5, and_3_out, and_4_out, and_5_out, and_6_out);
  and and_7 (and_7_out, not_5_out, not_6_out, Input_3, Input_5);
  and and_8 (and_8_out, not_7_out, not_8_out, Input_3, Input_4);
  and and_9 (and_9_out, not_9_out, Input_3, Input_4, Input_5);
  and and_10 (and_10_out, not_10_out, Input_2, not_11_out, not_12_out);
  and and_11 (and_11_out, Input_1, not_13_out, not_14_out);
  and and_12 (and_12_out, Input_1, not_15_out, Input_5);
  and and_13 (and_13_out, Input_1, not_16_out, Input_4);
  and and_14 (and_14_out, Input_1, Input_2, Input_3, not_17_out);
  or or_3 (Output_6, and_7_out, and_8_out, and_9_out, and_10_out, and_11_out, and_12_out, and_13_out, and_14_out);

  assign Output_1 = 1'b0;
  assign Output_2 = 1'b0;
  assign Output_3 = 1'b0;
endmodule

module rectifieurhorraire (
  input  bh0,
  input  bh1,
  input  bh2,
  input  bh3,
  input  bh4,
  input  sh0,
  input  sh1,
  input  sh2,
  input  sh3,
  input  sh4,
  output h0,
  output h1,
  output h2,
  output h3,
  output h4
);

  wire and_1_out, and_2_out, and_3_out, and_4_out, and_5_out, and_6_out, and_7_out, and_8_out, and_9_out,
       and_10_out, and_11_out, and_12_out, and_13_out, and_14_out, and_15_out, and_16_out, and_17_out,
       and_18_out, and_19_out, and_20_out, and_21_out, and_22_out, and_23_out, and_24_out, and_25_out,
       and_26_out, and_27_out, and_28_out, and_29_out, and_30_out, and_31_out, and_32_out, and_33_out,
       and_34_out, and_35_out, and_36_out, and_37_out, and_38_out, and_39_out, and_40_out, and_41_out,
       and_42_out, and_43_out, and_44_out, and_45_out, and_46_out, and_47_out, and_48_out, and_49_out,
       and_50_out, and_51_out, and_52_out, and_53_out, and_54_out, and_55_out, and_56_out, and_57_out,
       and_58_out, and_59_out, and_60_out, and_61_out, and_62_out, and_63_out, and_64_out, and_65_out,
       and_66_out, and_67_out, and_68_out, and_69_out, and_70_out, and_71_out, and_72_out, and_73_out,
       and_74_out, and_75_out, and_76_out, and_77_out, and_78_out, and_79_out, and_80_out, and_81_out,
       and_82_out, and_83_out, and_84_out, and_85_out, and_86_out, and_87_out, and_88_out, and_89_out,
       and_90_out, and_91_out, and_92_out, and_93_out, and_94_out, and_95_out, and_96_out, and_97_out,
       and_98_out, and_99_out, and_100_out, and_101_out, and_102_out, and_103_out, and_104_out, and_105_out,
       and_106_out, and_107_out, and_108_out, and_109_out, and_110_out, and_111_out, and_112_out,
       and_113_out, and_114_out, and_115_out, and_116_out, and_117_out, and_118_out, and_119_out,
       and_120_out, and_121_out, and_122_out, and_123_out, and_124_out, and_125_out, and_126_out,
       and_127_out, and_128_out, and_129_out, and_130_out, and_131_out, and_132_out, and_133_out,
       and_134_out, and_135_out, and_136_out, and_137_out, and_138_out, and_139_out, and_140_out,
       and_141_out, and_142_out, and_143_out, and_144_out, and_145_out, and_146_out, and_147_out,
       and_148_out, and_149_out, and_150_out, and_151_out, and_152_out, and_153_out, and_154_out,
       and_155_out, and_156_out, and_157_out, and_158_out, and_159_out, and_160_out, and_161_out,
       and_162_out, and_163_out, and_164_out, and_165_out, and_166_out, and_167_out, and_168_out,
       and_169_out, and_170_out, and_171_out, and_172_out, and_173_out, and_174_out, and_175_out,
       and_176_out, and_177_out, and_178_out, and_179_out, and_180_out, and_181_out, and_182_out,
       and_183_out, and_184_out, and_185_out, and_186_out, and_187_out, and_188_out, and_189_out,
       and_190_out, and_191_out, and_192_out, and_193_out, and_194_out, and_195_out, and_196_out,
       and_197_out, and_198_out, and_199_out, and_200_out, and_201_out, and_202_out, and_203_out,
       and_204_out, and_205_out, and_206_out, and_207_out, and_208_out, and_209_out, and_210_out,
       and_211_out, not_1_out, not_2_out, not_3_out, not_4_out, not_5_out, not_6_out, not_7_out, not_8_out,
       not_9_out, not_10_out, not_11_out, not_12_out, not_13_out, not_14_out, not_15_out, not_16_out,
       not_17_out, not_18_out, not_19_out, not_20_out, not_21_out, not_22_out, not_23_out, not_24_out,
       not_25_out, not_26_out, not_27_out, not_28_out, not_29_out, not_30_out, not_31_out, not_32_out,
       not_33_out, not_34_out, not_35_out, not_36_out, not_37_out, not_38_out, not_39_out, not_40_out,
       not_41_out, not_42_out, not_43_out, not_44_out, not_45_out, not_46_out, not_47_out, not_48_out,
       not_49_out, not_50_out, not_51_out, not_52_out, not_53_out, not_54_out, not_55_out, not_56_out,
       not_57_out, not_58_out, not_59_out, not_60_out, not_61_out, not_62_out, not_63_out, not_64_out,
       not_65_out, not_66_out, not_67_out, not_68_out, not_69_out, not_70_out, not_71_out, not_72_out,
       not_73_out, not_74_out, not_75_out, not_76_out, not_77_out, not_78_out, not_79_out, not_80_out,
       not_81_out, not_82_out, not_83_out, not_84_out, not_85_out, not_86_out, not_87_out, not_88_out,
       not_89_out, not_90_out, not_91_out, not_92_out, not_93_out, not_94_out, not_95_out, not_96_out,
       not_97_out, not_98_out, not_99_out, not_100_out, not_101_out, not_102_out, not_103_out, not_104_out,
       not_105_out, not_106_out, not_107_out, not_108_out, not_109_out, not_110_out, not_111_out,
       not_112_out, not_113_out, not_114_out, not_115_out, not_116_out, not_117_out, not_118_out,
       not_119_out, not_120_out, not_121_out, not_122_out, not_123_out, not_124_out, not_125_out,
       not_126_out, not_127_out, not_128_out, not_129_out, not_130_out, not_131_out, not_132_out,
       not_133_out, not_134_out, not_135_out, not_136_out, not_137_out, not_138_out, not_139_out,
       not_140_out, not_141_out, not_142_out, not_143_out, not_144_out, not_145_out, not_146_out,
       not_147_out, not_148_out, not_149_out, not_150_out, not_151_out, not_152_out, not_153_out,
       not_154_out, not_155_out, not_156_out, not_157_out, not_158_out, not_159_out, not_160_out,
       not_161_out, not_162_out, not_163_out, not_164_out, not_165_out, not_166_out, not_167_out,
       not_168_out, not_169_out, not_170_out, not_171_out, not_172_out, not_173_out, not_174_out,
       not_175_out, not_176_out, not_177_out, not_178_out, not_179_out, not_180_out, not_181_out,
       not_182_out, not_183_out, not_184_out, not_185_out, not_186_out, not_187_out, not_188_out,
       not_189_out, not_190_out, not_191_out, not_192_out, not_193_out, not_194_out, not_195_out,
       not_196_out, not_197_out, not_198_out, not_199_out, not_200_out, not_201_out, not_202_out,
       not_203_out, not_204_out, not_205_out, not_206_out, not_207_out, not_208_out, not_209_out,
       not_210_out, not_211_out, not_212_out, not_213_out, not_214_out, not_215_out, not_216_out,
       not_217_out, not_218_out, not_219_out, not_220_out, not_221_out, not_222_out, not_223_out,
       not_224_out, not_225_out, not_226_out, not_227_out, not_228_out, not_229_out, not_230_out,
       not_231_out, not_232_out, not_233_out, not_234_out, not_235_out, not_236_out, not_237_out,
       not_238_out, not_239_out, not_240_out, not_241_out, not_242_out, not_243_out, not_244_out,
       not_245_out, not_246_out, not_247_out, not_248_out, not_249_out, not_250_out, not_251_out,
       not_252_out, not_253_out, not_254_out, not_255_out, not_256_out, not_257_out, not_258_out,
       not_259_out, not_260_out, not_261_out, not_262_out, not_263_out, not_264_out, not_265_out,
       not_266_out, not_267_out, not_268_out, not_269_out, not_270_out, not_271_out, not_272_out,
       not_273_out, not_274_out, not_275_out, not_276_out, not_277_out, not_278_out, not_279_out,
       not_280_out, not_281_out, not_282_out, not_283_out, not_284_out, not_285_out, not_286_out,
       not_287_out, not_288_out, not_289_out, not_290_out, not_291_out, not_292_out, not_293_out,
       not_294_out, not_295_out, not_296_out, not_297_out, not_298_out, not_299_out, not_300_out,
       not_301_out, not_302_out, not_303_out, not_304_out, not_305_out, not_306_out, not_307_out,
       not_308_out, not_309_out, not_310_out, not_311_out, not_312_out, not_313_out, not_314_out,
       not_315_out, not_316_out, not_317_out, not_318_out, not_319_out, not_320_out, not_321_out,
       not_322_out, not_323_out, not_324_out, not_325_out, not_326_out, not_327_out, not_328_out,
       not_329_out, not_330_out, not_331_out, not_332_out, not_333_out, not_334_out, not_335_out,
       not_336_out, not_337_out, not_338_out, not_339_out, not_340_out, not_341_out, not_342_out,
       not_343_out, not_344_out, not_345_out, not_346_out, not_347_out, not_348_out, not_349_out,
       not_350_out, not_351_out, not_352_out, not_353_out, not_354_out, not_355_out, not_356_out,
       not_357_out, not_358_out, not_359_out, not_360_out, not_361_out, not_362_out, not_363_out,
       not_364_out, not_365_out, not_366_out, not_367_out, not_368_out, not_369_out, not_370_out,
       not_371_out, not_372_out, not_373_out, not_374_out, not_375_out, not_376_out, not_377_out,
       not_378_out, not_379_out, not_380_out, not_381_out, not_382_out, not_383_out, not_384_out,
       not_385_out, not_386_out, not_387_out, not_388_out, not_389_out, not_390_out, not_391_out,
       not_392_out, not_393_out, not_394_out, not_395_out, not_396_out, not_397_out, not_398_out,
       not_399_out, not_400_out, not_401_out, not_402_out, not_403_out, not_404_out, not_405_out,
       not_406_out, not_407_out, not_408_out, not_409_out, not_410_out, not_411_out, not_412_out,
       not_413_out, not_414_out, not_415_out, not_416_out, not_417_out, not_418_out, not_419_out,
       not_420_out, not_421_out, not_422_out, not_423_out, not_424_out, not_425_out, not_426_out,
       not_427_out, not_428_out, not_429_out, not_430_out, not_431_out, not_432_out, not_433_out,
       not_434_out, not_435_out, not_436_out, not_437_out, not_438_out, not_439_out, not_440_out,
       not_441_out, not_442_out, not_443_out, not_444_out, not_445_out, not_446_out, not_447_out,
       not_448_out, not_449_out, not_450_out, not_451_out, not_452_out, not_453_out, not_454_out,
       not_455_out, not_456_out, not_457_out, not_458_out, not_459_out, not_460_out, not_461_out,
       not_462_out, not_463_out, not_464_out, not_465_out, not_466_out, not_467_out, not_468_out,
       not_469_out, not_470_out, not_471_out, not_472_out, not_473_out, not_474_out, not_475_out,
       not_476_out, not_477_out, not_478_out, not_479_out, not_480_out, not_481_out, not_482_out,
       not_483_out, not_484_out, not_485_out, not_486_out, not_487_out, not_488_out, not_489_out,
       not_490_out, not_491_out, not_492_out, not_493_out, not_494_out, not_495_out, not_496_out,
       not_497_out, not_498_out, not_499_out, not_500_out, not_501_out, not_502_out, not_503_out,
       not_504_out, not_505_out, not_506_out, not_507_out, not_508_out, not_509_out, not_510_out,
       not_511_out, not_512_out, not_513_out, not_514_out, not_515_out, not_516_out, not_517_out,
       not_518_out, not_519_out, not_520_out, not_521_out, not_522_out, not_523_out, not_524_out,
       not_525_out, not_526_out, not_527_out, not_528_out, not_529_out, not_530_out, not_531_out,
       not_532_out, not_533_out, not_534_out, not_535_out, not_536_out, not_537_out, not_538_out,
       not_539_out, not_540_out, not_541_out, not_542_out, not_543_out, not_544_out, not_545_out,
       not_546_out, not_547_out, not_548_out, not_549_out, not_550_out, not_551_out, not_552_out,
       not_553_out, not_554_out, not_555_out, not_556_out, not_557_out, not_558_out, not_559_out,
       not_560_out, not_561_out, not_562_out, not_563_out, not_564_out, not_565_out, not_566_out,
       not_567_out, not_568_out, not_569_out, not_570_out, not_571_out, not_572_out, not_573_out,
       not_574_out, not_575_out, not_576_out, not_577_out, not_578_out, not_579_out, not_580_out,
       not_581_out, not_582_out, not_583_out, not_584_out, not_585_out, not_586_out, not_587_out,
       not_588_out, not_589_out, not_590_out, not_591_out, not_592_out, not_593_out, not_594_out,
       not_595_out, not_596_out, not_597_out, not_598_out, not_599_out, not_600_out, not_601_out,
       not_602_out, not_603_out, not_604_out, not_605_out, not_606_out, not_607_out, not_608_out,
       not_609_out, not_610_out, not_611_out, not_612_out, not_613_out, not_614_out, not_615_out,
       not_616_out, not_617_out, not_618_out, not_619_out, not_620_out, not_621_out, not_622_out,
       not_623_out, not_624_out, not_625_out, not_626_out, not_627_out, not_628_out, not_629_out,
       not_630_out, not_631_out, not_632_out, not_633_out, not_634_out, not_635_out, not_636_out,
       not_637_out, not_638_out, not_639_out, not_640_out, not_641_out, not_642_out, not_643_out,
       not_644_out, not_645_out, not_646_out, not_647_out, not_648_out, not_649_out, not_650_out,
       not_651_out, not_652_out, not_653_out, not_654_out, not_655_out, not_656_out, not_657_out,
       not_658_out, not_659_out, not_660_out, not_661_out, not_662_out, not_663_out, not_664_out,
       not_665_out, not_666_out, not_667_out, not_668_out, not_669_out, not_670_out, not_671_out,
       not_672_out, not_673_out, not_674_out, not_675_out, not_676_out, not_677_out, not_678_out,
       not_679_out, not_680_out, not_681_out, not_682_out, not_683_out, not_684_out, not_685_out,
       not_686_out, not_687_out, not_688_out, not_689_out, not_690_out, not_691_out, not_692_out,
       not_693_out, not_694_out, not_695_out, not_696_out, not_697_out, not_698_out, not_699_out,
       not_700_out, not_701_out, not_702_out, not_703_out, not_704_out, not_705_out, not_706_out,
       not_707_out, not_708_out, not_709_out, not_710_out, not_711_out, not_712_out, not_713_out,
       not_714_out, not_715_out, not_716_out, not_717_out, not_718_out, not_719_out, not_720_out,
       not_721_out, not_722_out, not_723_out, not_724_out, not_725_out, not_726_out, not_727_out,
       not_728_out, not_729_out, not_730_out, not_731_out, not_732_out, not_733_out, not_734_out,
       not_735_out, not_736_out, not_737_out, not_738_out, not_739_out, not_740_out, not_741_out,
       not_742_out, or_4_out, or_5_out, or_6_out, or_7_out, or_8_out, or_10_out, or_11_out;

  not not_1 (not_1_out, bh0);
  not not_2 (not_2_out, bh1);
  not not_3 (not_3_out, bh2);
  not not_4 (not_4_out, bh3);
  not not_5 (not_5_out, bh4);
  not not_6 (not_6_out, sh1);
  not not_7 (not_7_out, bh0);
  not not_8 (not_8_out, bh1);
  not not_9 (not_9_out, bh2);
  not not_10 (not_10_out, bh3);
  not not_11 (not_11_out, sh1);
  not not_12 (not_12_out, sh3);
  not not_13 (not_13_out, bh0);
  not not_14 (not_14_out, bh1);
  not not_15 (not_15_out, bh2);
  not not_16 (not_16_out, bh3);
  not not_17 (not_17_out, sh1);
  not not_18 (not_18_out, sh4);
  not not_19 (not_19_out, bh0);
  not not_20 (not_20_out, bh1);
  not not_21 (not_21_out, bh2);
  not not_22 (not_22_out, bh4);
  not not_23 (not_23_out, sh1);
  not not_24 (not_24_out, sh3);
  not not_25 (not_25_out, bh0);
  not not_26 (not_26_out, bh1);
  not not_27 (not_27_out, bh2);
  not not_28 (not_28_out, sh1);
  not not_29 (not_29_out, sh2);
  not not_30 (not_30_out, bh0);
  not not_31 (not_31_out, bh1);
  not not_32 (not_32_out, bh2);
  not not_33 (not_33_out, sh1);
  not not_34 (not_34_out, sh3);
  not not_35 (not_35_out, sh4);
  not not_36 (not_36_out, bh0);
  not not_37 (not_37_out, bh1);
  not not_38 (not_38_out, bh3);
  not not_39 (not_39_out, bh4);
  not not_40 (not_40_out, sh1);
  not not_41 (not_41_out, sh2);
  not not_42 (not_42_out, bh0);
  not not_43 (not_43_out, bh1);
  not not_44 (not_44_out, bh3);
  not not_45 (not_45_out, sh1);
  not not_46 (not_46_out, sh2);
  not not_47 (not_47_out, sh3);
  not not_48 (not_48_out, bh0);
  not not_49 (not_49_out, bh1);
  not not_50 (not_50_out, bh3);
  not not_51 (not_51_out, sh1);
  not not_52 (not_52_out, sh2);
  not not_53 (not_53_out, sh4);
  not not_54 (not_54_out, bh0);
  not not_55 (not_55_out, bh1);
  not not_56 (not_56_out, bh4);
  not not_57 (not_57_out, sh1);
  not not_58 (not_58_out, sh2);
  not not_59 (not_59_out, sh3);
  not not_60 (not_60_out, bh0);
  not not_61 (not_61_out, bh1);
  not not_62 (not_62_out, sh1);
  not not_63 (not_63_out, sh2);
  not not_64 (not_64_out, sh3);
  not not_65 (not_65_out, sh4);
  not not_66 (not_66_out, bh0);
  not not_67 (not_67_out, bh1);
  not not_68 (not_68_out, sh0);
  not not_69 (not_69_out, bh0);
  not not_70 (not_70_out, bh1);
  not not_71 (not_71_out, sh0);
  not not_72 (not_72_out, bh0);
  not not_73 (not_73_out, bh1);
  not not_74 (not_74_out, sh0);
  not not_75 (not_75_out, bh0);
  not not_76 (not_76_out, bh1);
  not not_77 (not_77_out, sh0);
  not not_78 (not_78_out, bh0);
  not not_79 (not_79_out, bh1);
  not not_80 (not_80_out, sh0);
  not not_81 (not_81_out, bh0);
  not not_82 (not_82_out, bh1);
  not not_83 (not_83_out, sh0);
  not not_84 (not_84_out, bh0);
  not not_85 (not_85_out, bh1);
  not not_86 (not_86_out, sh0);
  not not_87 (not_87_out, bh0);
  not not_88 (not_88_out, bh2);
  not not_89 (not_89_out, bh3);
  not not_90 (not_90_out, bh4);
  not not_91 (not_91_out, sh0);
  not not_92 (not_92_out, bh0);
  not not_93 (not_93_out, bh2);
  not not_94 (not_94_out, bh3);
  not not_95 (not_95_out, sh0);
  not not_96 (not_96_out, sh3);
  not not_97 (not_97_out, bh0);
  not not_98 (not_98_out, bh2);
  not not_99 (not_99_out, bh3);
  not not_100 (not_100_out, sh0);
  not not_101 (not_101_out, sh4);
  not not_102 (not_102_out, bh0);
  not not_103 (not_103_out, bh2);
  not not_104 (not_104_out, bh4);
  not not_105 (not_105_out, sh0);
  not not_106 (not_106_out, sh3);
  not not_107 (not_107_out, bh0);
  not not_108 (not_108_out, bh2);
  not not_109 (not_109_out, sh0);
  not not_110 (not_110_out, sh2);
  not not_111 (not_111_out, bh0);
  not not_112 (not_112_out, bh2);
  not not_113 (not_113_out, sh0);
  not not_114 (not_114_out, sh3);
  not not_115 (not_115_out, sh4);
  not not_116 (not_116_out, bh0);
  not not_117 (not_117_out, bh3);
  not not_118 (not_118_out, bh4);
  not not_119 (not_119_out, sh0);
  not not_120 (not_120_out, sh2);
  not not_121 (not_121_out, bh0);
  not not_122 (not_122_out, bh3);
  not not_123 (not_123_out, sh0);
  not not_124 (not_124_out, sh2);
  not not_125 (not_125_out, sh3);
  not not_126 (not_126_out, bh0);
  not not_127 (not_127_out, bh3);
  not not_128 (not_128_out, sh0);
  not not_129 (not_129_out, sh2);
  not not_130 (not_130_out, sh4);
  not not_131 (not_131_out, bh0);
  not not_132 (not_132_out, bh4);
  not not_133 (not_133_out, sh0);
  not not_134 (not_134_out, sh2);
  not not_135 (not_135_out, sh3);
  not not_136 (not_136_out, bh0);
  not not_137 (not_137_out, sh0);
  not not_138 (not_138_out, sh2);
  not not_139 (not_139_out, sh3);
  not not_140 (not_140_out, sh4);
  not not_141 (not_141_out, bh0);
  not not_142 (not_142_out, sh0);
  not not_143 (not_143_out, sh1);
  not not_144 (not_144_out, bh0);
  not not_145 (not_145_out, bh0);
  not not_146 (not_146_out, sh0);
  not not_147 (not_147_out, sh1);
  not not_148 (not_148_out, bh0);
  not not_149 (not_149_out, bh0);
  not not_150 (not_150_out, sh0);
  not not_151 (not_151_out, sh1);
  not not_152 (not_152_out, bh0);
  not not_153 (not_153_out, bh0);
  not not_154 (not_154_out, sh0);
  not not_155 (not_155_out, sh1);
  not not_156 (not_156_out, bh0);
  not not_157 (not_157_out, bh0);
  not not_158 (not_158_out, sh0);
  not not_159 (not_159_out, sh1);
  not not_160 (not_160_out, bh0);
  not not_161 (not_161_out, bh0);
  not not_162 (not_162_out, sh0);
  not not_163 (not_163_out, sh1);
  not not_164 (not_164_out, bh0);
  not not_165 (not_165_out, bh0);
  not not_166 (not_166_out, sh0);
  not not_167 (not_167_out, sh1);
  not not_168 (not_168_out, bh0);
  not not_169 (not_169_out, bh1);
  not not_170 (not_170_out, bh2);
  not not_171 (not_171_out, bh3);
  not not_172 (not_172_out, bh4);
  not not_173 (not_173_out, sh0);
  not not_174 (not_174_out, sh1);
  not not_175 (not_175_out, bh1);
  not not_176 (not_176_out, bh2);
  not not_177 (not_177_out, bh3);
  not not_178 (not_178_out, sh0);
  not not_179 (not_179_out, sh1);
  not not_180 (not_180_out, sh3);
  not not_181 (not_181_out, bh1);
  not not_182 (not_182_out, bh2);
  not not_183 (not_183_out, bh3);
  not not_184 (not_184_out, sh0);
  not not_185 (not_185_out, sh1);
  not not_186 (not_186_out, sh4);
  not not_187 (not_187_out, bh1);
  not not_188 (not_188_out, bh2);
  not not_189 (not_189_out, bh4);
  not not_190 (not_190_out, sh0);
  not not_191 (not_191_out, sh1);
  not not_192 (not_192_out, sh3);
  not not_193 (not_193_out, bh1);
  not not_194 (not_194_out, bh2);
  not not_195 (not_195_out, sh0);
  not not_196 (not_196_out, sh1);
  not not_197 (not_197_out, sh2);
  not not_198 (not_198_out, bh1);
  not not_199 (not_199_out, bh2);
  not not_200 (not_200_out, sh0);
  not not_201 (not_201_out, sh1);
  not not_202 (not_202_out, sh3);
  not not_203 (not_203_out, sh4);
  not not_204 (not_204_out, bh1);
  not not_205 (not_205_out, bh3);
  not not_206 (not_206_out, bh4);
  not not_207 (not_207_out, sh0);
  not not_208 (not_208_out, sh1);
  not not_209 (not_209_out, sh2);
  not not_210 (not_210_out, bh1);
  not not_211 (not_211_out, bh3);
  not not_212 (not_212_out, sh0);
  not not_213 (not_213_out, sh1);
  not not_214 (not_214_out, sh2);
  not not_215 (not_215_out, sh3);
  not not_216 (not_216_out, bh1);
  not not_217 (not_217_out, bh3);
  not not_218 (not_218_out, sh0);
  not not_219 (not_219_out, sh1);
  not not_220 (not_220_out, sh2);
  not not_221 (not_221_out, sh4);
  not not_222 (not_222_out, bh1);
  not not_223 (not_223_out, bh4);
  not not_224 (not_224_out, sh0);
  not not_225 (not_225_out, sh1);
  not not_226 (not_226_out, sh2);
  not not_227 (not_227_out, sh3);
  not not_228 (not_228_out, bh1);
  not not_229 (not_229_out, sh0);
  not not_230 (not_230_out, sh1);
  not not_231 (not_231_out, sh2);
  not not_232 (not_232_out, sh3);
  not not_233 (not_233_out, sh4);
  not not_234 (not_234_out, bh1);
  not not_235 (not_235_out, bh2);
  not not_236 (not_236_out, bh3);
  not not_237 (not_237_out, bh4);
  not not_238 (not_238_out, bh1);
  not not_239 (not_239_out, bh2);
  not not_240 (not_240_out, bh3);
  not not_241 (not_241_out, sh3);
  not not_242 (not_242_out, bh1);
  not not_243 (not_243_out, bh2);
  not not_244 (not_244_out, bh3);
  not not_245 (not_245_out, sh4);
  not not_246 (not_246_out, bh1);
  not not_247 (not_247_out, bh2);
  not not_248 (not_248_out, bh4);
  not not_249 (not_249_out, sh3);
  not not_250 (not_250_out, bh1);
  not not_251 (not_251_out, bh2);
  not not_252 (not_252_out, sh2);
  not not_253 (not_253_out, bh1);
  not not_254 (not_254_out, bh2);
  not not_255 (not_255_out, sh3);
  not not_256 (not_256_out, sh4);
  not not_257 (not_257_out, bh1);
  not not_258 (not_258_out, bh3);
  not not_259 (not_259_out, bh4);
  not not_260 (not_260_out, sh2);
  not not_261 (not_261_out, bh1);
  not not_262 (not_262_out, bh3);
  not not_263 (not_263_out, sh2);
  not not_264 (not_264_out, sh3);
  not not_265 (not_265_out, bh1);
  not not_266 (not_266_out, bh3);
  not not_267 (not_267_out, sh2);
  not not_268 (not_268_out, sh4);
  not not_269 (not_269_out, bh1);
  not not_270 (not_270_out, bh4);
  not not_271 (not_271_out, sh2);
  not not_272 (not_272_out, sh3);
  not not_273 (not_273_out, bh1);
  not not_274 (not_274_out, sh2);
  not not_275 (not_275_out, sh3);
  not not_276 (not_276_out, sh4);
  not not_277 (not_277_out, bh1);
  not not_278 (not_278_out, sh1);
  not not_279 (not_279_out, bh1);
  not not_280 (not_280_out, sh1);
  not not_281 (not_281_out, bh1);
  not not_282 (not_282_out, sh1);
  not not_283 (not_283_out, bh1);
  not not_284 (not_284_out, sh1);
  not not_285 (not_285_out, bh1);
  not not_286 (not_286_out, sh1);
  not not_287 (not_287_out, bh1);
  not not_288 (not_288_out, sh1);
  not not_289 (not_289_out, bh1);
  not not_290 (not_290_out, sh1);
  not not_291 (not_291_out, bh2);
  not not_292 (not_292_out, bh3);
  not not_293 (not_293_out, bh4);
  not not_294 (not_294_out, sh1);
  not not_295 (not_295_out, bh2);
  not not_296 (not_296_out, bh3);
  not not_297 (not_297_out, sh1);
  not not_298 (not_298_out, sh3);
  not not_299 (not_299_out, bh2);
  not not_300 (not_300_out, bh3);
  not not_301 (not_301_out, sh1);
  not not_302 (not_302_out, sh4);
  not not_303 (not_303_out, bh2);
  not not_304 (not_304_out, bh4);
  not not_305 (not_305_out, sh1);
  not not_306 (not_306_out, sh3);
  not not_307 (not_307_out, bh2);
  not not_308 (not_308_out, sh1);
  not not_309 (not_309_out, sh2);
  not not_310 (not_310_out, bh2);
  not not_311 (not_311_out, sh1);
  not not_312 (not_312_out, sh3);
  not not_313 (not_313_out, sh4);
  not not_314 (not_314_out, bh3);
  not not_315 (not_315_out, bh4);
  not not_316 (not_316_out, sh1);
  not not_317 (not_317_out, sh2);
  not not_318 (not_318_out, bh3);
  not not_319 (not_319_out, sh1);
  not not_320 (not_320_out, sh2);
  not not_321 (not_321_out, sh3);
  not not_322 (not_322_out, bh3);
  not not_323 (not_323_out, sh1);
  not not_324 (not_324_out, sh2);
  not not_325 (not_325_out, sh4);
  not not_326 (not_326_out, bh4);
  not not_327 (not_327_out, sh1);
  not not_328 (not_328_out, sh2);
  not not_329 (not_329_out, sh3);
  not not_330 (not_330_out, sh1);
  not not_331 (not_331_out, sh2);
  not not_332 (not_332_out, sh3);
  not not_333 (not_333_out, sh4);
  not not_334 (not_334_out, sh0);
  not not_335 (not_335_out, sh0);
  not not_336 (not_336_out, sh0);
  not not_337 (not_337_out, sh0);
  not not_338 (not_338_out, sh0);
  not not_339 (not_339_out, sh0);
  not not_340 (not_340_out, sh0);
  not not_341 (not_341_out, bh0);
  not not_342 (not_342_out, bh1);
  not not_343 (not_343_out, bh2);
  not not_344 (not_344_out, bh3);
  not not_345 (not_345_out, bh4);
  not not_346 (not_346_out, sh0);
  not not_347 (not_347_out, bh0);
  not not_348 (not_348_out, bh1);
  not not_349 (not_349_out, bh2);
  not not_350 (not_350_out, bh3);
  not not_351 (not_351_out, sh0);
  not not_352 (not_352_out, sh3);
  not not_353 (not_353_out, bh0);
  not not_354 (not_354_out, bh1);
  not not_355 (not_355_out, bh2);
  not not_356 (not_356_out, bh3);
  not not_357 (not_357_out, sh0);
  not not_358 (not_358_out, sh4);
  not not_359 (not_359_out, bh0);
  not not_360 (not_360_out, bh1);
  not not_361 (not_361_out, bh2);
  not not_362 (not_362_out, bh4);
  not not_363 (not_363_out, sh0);
  not not_364 (not_364_out, sh3);
  not not_365 (not_365_out, bh0);
  not not_366 (not_366_out, bh1);
  not not_367 (not_367_out, bh2);
  not not_368 (not_368_out, sh0);
  not not_369 (not_369_out, sh2);
  not not_370 (not_370_out, bh0);
  not not_371 (not_371_out, bh1);
  not not_372 (not_372_out, bh2);
  not not_373 (not_373_out, sh0);
  not not_374 (not_374_out, sh3);
  not not_375 (not_375_out, sh4);
  not not_376 (not_376_out, bh0);
  not not_377 (not_377_out, bh1);
  not not_378 (not_378_out, bh3);
  not not_379 (not_379_out, bh4);
  not not_380 (not_380_out, sh0);
  not not_381 (not_381_out, sh2);
  not not_382 (not_382_out, bh0);
  not not_383 (not_383_out, bh1);
  not not_384 (not_384_out, bh3);
  not not_385 (not_385_out, sh0);
  not not_386 (not_386_out, sh2);
  not not_387 (not_387_out, sh3);
  not not_388 (not_388_out, bh0);
  not not_389 (not_389_out, bh1);
  not not_390 (not_390_out, bh3);
  not not_391 (not_391_out, sh0);
  not not_392 (not_392_out, sh2);
  not not_393 (not_393_out, sh4);
  not not_394 (not_394_out, bh0);
  not not_395 (not_395_out, bh1);
  not not_396 (not_396_out, bh4);
  not not_397 (not_397_out, sh0);
  not not_398 (not_398_out, sh2);
  not not_399 (not_399_out, sh3);
  not not_400 (not_400_out, bh0);
  not not_401 (not_401_out, bh1);
  not not_402 (not_402_out, sh0);
  not not_403 (not_403_out, sh2);
  not not_404 (not_404_out, sh3);
  not not_405 (not_405_out, sh4);
  not not_406 (not_406_out, bh0);
  not not_407 (not_407_out, bh1);
  not not_408 (not_408_out, sh0);
  not not_409 (not_409_out, sh1);
  not not_410 (not_410_out, bh0);
  not not_411 (not_411_out, bh1);
  not not_412 (not_412_out, bh0);
  not not_413 (not_413_out, bh1);
  not not_414 (not_414_out, sh0);
  not not_415 (not_415_out, sh1);
  not not_416 (not_416_out, bh0);
  not not_417 (not_417_out, bh1);
  not not_418 (not_418_out, bh0);
  not not_419 (not_419_out, bh1);
  not not_420 (not_420_out, sh0);
  not not_421 (not_421_out, sh1);
  not not_422 (not_422_out, bh0);
  not not_423 (not_423_out, bh1);
  not not_424 (not_424_out, bh0);
  not not_425 (not_425_out, bh1);
  not not_426 (not_426_out, sh0);
  not not_427 (not_427_out, sh1);
  not not_428 (not_428_out, bh0);
  not not_429 (not_429_out, bh1);
  not not_430 (not_430_out, bh0);
  not not_431 (not_431_out, bh1);
  not not_432 (not_432_out, sh0);
  not not_433 (not_433_out, sh1);
  not not_434 (not_434_out, bh0);
  not not_435 (not_435_out, bh1);
  not not_436 (not_436_out, bh0);
  not not_437 (not_437_out, bh1);
  not not_438 (not_438_out, sh0);
  not not_439 (not_439_out, sh1);
  not not_440 (not_440_out, bh0);
  not not_441 (not_441_out, bh1);
  not not_442 (not_442_out, bh0);
  not not_443 (not_443_out, bh1);
  not not_444 (not_444_out, sh0);
  not not_445 (not_445_out, sh1);
  not not_446 (not_446_out, bh0);
  not not_447 (not_447_out, bh1);
  not not_448 (not_448_out, bh0);
  not not_449 (not_449_out, bh2);
  not not_450 (not_450_out, bh3);
  not not_451 (not_451_out, bh4);
  not not_452 (not_452_out, sh0);
  not not_453 (not_453_out, sh1);
  not not_454 (not_454_out, bh0);
  not not_455 (not_455_out, bh2);
  not not_456 (not_456_out, bh3);
  not not_457 (not_457_out, sh0);
  not not_458 (not_458_out, sh1);
  not not_459 (not_459_out, sh3);
  not not_460 (not_460_out, bh0);
  not not_461 (not_461_out, bh2);
  not not_462 (not_462_out, bh3);
  not not_463 (not_463_out, sh0);
  not not_464 (not_464_out, sh1);
  not not_465 (not_465_out, sh4);
  not not_466 (not_466_out, bh0);
  not not_467 (not_467_out, bh2);
  not not_468 (not_468_out, bh4);
  not not_469 (not_469_out, sh0);
  not not_470 (not_470_out, sh1);
  not not_471 (not_471_out, sh3);
  not not_472 (not_472_out, bh0);
  not not_473 (not_473_out, bh2);
  not not_474 (not_474_out, sh0);
  not not_475 (not_475_out, sh1);
  not not_476 (not_476_out, sh2);
  not not_477 (not_477_out, bh0);
  not not_478 (not_478_out, bh2);
  not not_479 (not_479_out, sh0);
  not not_480 (not_480_out, sh1);
  not not_481 (not_481_out, sh3);
  not not_482 (not_482_out, sh4);
  not not_483 (not_483_out, bh0);
  not not_484 (not_484_out, bh3);
  not not_485 (not_485_out, bh4);
  not not_486 (not_486_out, sh0);
  not not_487 (not_487_out, sh1);
  not not_488 (not_488_out, sh2);
  not not_489 (not_489_out, bh0);
  not not_490 (not_490_out, bh3);
  not not_491 (not_491_out, sh0);
  not not_492 (not_492_out, sh1);
  not not_493 (not_493_out, sh2);
  not not_494 (not_494_out, sh3);
  not not_495 (not_495_out, bh0);
  not not_496 (not_496_out, bh3);
  not not_497 (not_497_out, sh0);
  not not_498 (not_498_out, sh1);
  not not_499 (not_499_out, sh2);
  not not_500 (not_500_out, sh4);
  not not_501 (not_501_out, bh0);
  not not_502 (not_502_out, bh4);
  not not_503 (not_503_out, sh0);
  not not_504 (not_504_out, sh1);
  not not_505 (not_505_out, sh2);
  not not_506 (not_506_out, sh3);
  not not_507 (not_507_out, bh0);
  not not_508 (not_508_out, sh0);
  not not_509 (not_509_out, sh1);
  not not_510 (not_510_out, sh2);
  not not_511 (not_511_out, sh3);
  not not_512 (not_512_out, sh4);
  not not_513 (not_513_out, bh0);
  not not_514 (not_514_out, bh2);
  not not_515 (not_515_out, bh3);
  not not_516 (not_516_out, bh4);
  not not_517 (not_517_out, bh0);
  not not_518 (not_518_out, bh2);
  not not_519 (not_519_out, bh3);
  not not_520 (not_520_out, sh3);
  not not_521 (not_521_out, bh0);
  not not_522 (not_522_out, bh2);
  not not_523 (not_523_out, bh3);
  not not_524 (not_524_out, sh4);
  not not_525 (not_525_out, bh0);
  not not_526 (not_526_out, bh2);
  not not_527 (not_527_out, bh4);
  not not_528 (not_528_out, sh3);
  not not_529 (not_529_out, bh0);
  not not_530 (not_530_out, bh2);
  not not_531 (not_531_out, sh2);
  not not_532 (not_532_out, bh0);
  not not_533 (not_533_out, bh2);
  not not_534 (not_534_out, sh3);
  not not_535 (not_535_out, sh4);
  not not_536 (not_536_out, bh0);
  not not_537 (not_537_out, bh3);
  not not_538 (not_538_out, bh4);
  not not_539 (not_539_out, sh2);
  not not_540 (not_540_out, bh0);
  not not_541 (not_541_out, bh3);
  not not_542 (not_542_out, sh2);
  not not_543 (not_543_out, sh3);
  not not_544 (not_544_out, bh0);
  not not_545 (not_545_out, bh3);
  not not_546 (not_546_out, sh2);
  not not_547 (not_547_out, sh4);
  not not_548 (not_548_out, bh0);
  not not_549 (not_549_out, bh4);
  not not_550 (not_550_out, sh2);
  not not_551 (not_551_out, sh3);
  not not_552 (not_552_out, bh0);
  not not_553 (not_553_out, sh2);
  not not_554 (not_554_out, sh3);
  not not_555 (not_555_out, sh4);
  not not_556 (not_556_out, bh0);
  not not_557 (not_557_out, sh1);
  not not_558 (not_558_out, bh0);
  not not_559 (not_559_out, sh1);
  not not_560 (not_560_out, bh0);
  not not_561 (not_561_out, sh1);
  not not_562 (not_562_out, bh0);
  not not_563 (not_563_out, sh1);
  not not_564 (not_564_out, bh0);
  not not_565 (not_565_out, sh1);
  not not_566 (not_566_out, bh0);
  not not_567 (not_567_out, sh1);
  not not_568 (not_568_out, bh0);
  not not_569 (not_569_out, sh1);
  not not_570 (not_570_out, bh1);
  not not_571 (not_571_out, bh2);
  not not_572 (not_572_out, bh3);
  not not_573 (not_573_out, bh4);
  not not_574 (not_574_out, sh1);
  not not_575 (not_575_out, bh1);
  not not_576 (not_576_out, bh2);
  not not_577 (not_577_out, bh3);
  not not_578 (not_578_out, sh1);
  not not_579 (not_579_out, sh3);
  not not_580 (not_580_out, bh1);
  not not_581 (not_581_out, bh2);
  not not_582 (not_582_out, bh3);
  not not_583 (not_583_out, sh1);
  not not_584 (not_584_out, sh4);
  not not_585 (not_585_out, bh1);
  not not_586 (not_586_out, bh2);
  not not_587 (not_587_out, bh4);
  not not_588 (not_588_out, sh1);
  not not_589 (not_589_out, sh3);
  not not_590 (not_590_out, bh1);
  not not_591 (not_591_out, bh2);
  not not_592 (not_592_out, sh1);
  not not_593 (not_593_out, sh2);
  not not_594 (not_594_out, bh1);
  not not_595 (not_595_out, bh2);
  not not_596 (not_596_out, sh1);
  not not_597 (not_597_out, sh3);
  not not_598 (not_598_out, sh4);
  not not_599 (not_599_out, bh1);
  not not_600 (not_600_out, bh3);
  not not_601 (not_601_out, bh4);
  not not_602 (not_602_out, sh1);
  not not_603 (not_603_out, sh2);
  not not_604 (not_604_out, bh1);
  not not_605 (not_605_out, bh3);
  not not_606 (not_606_out, sh1);
  not not_607 (not_607_out, sh2);
  not not_608 (not_608_out, sh3);
  not not_609 (not_609_out, bh1);
  not not_610 (not_610_out, bh3);
  not not_611 (not_611_out, sh1);
  not not_612 (not_612_out, sh2);
  not not_613 (not_613_out, sh4);
  not not_614 (not_614_out, bh1);
  not not_615 (not_615_out, bh4);
  not not_616 (not_616_out, sh1);
  not not_617 (not_617_out, sh2);
  not not_618 (not_618_out, sh3);
  not not_619 (not_619_out, bh1);
  not not_620 (not_620_out, sh1);
  not not_621 (not_621_out, sh2);
  not not_622 (not_622_out, sh3);
  not not_623 (not_623_out, sh4);
  not not_624 (not_624_out, bh1);
  not not_625 (not_625_out, sh0);
  not not_626 (not_626_out, bh1);
  not not_627 (not_627_out, sh0);
  not not_628 (not_628_out, bh1);
  not not_629 (not_629_out, sh0);
  not not_630 (not_630_out, bh1);
  not not_631 (not_631_out, sh0);
  not not_632 (not_632_out, bh1);
  not not_633 (not_633_out, sh0);
  not not_634 (not_634_out, bh1);
  not not_635 (not_635_out, sh0);
  not not_636 (not_636_out, bh1);
  not not_637 (not_637_out, sh0);
  not not_638 (not_638_out, bh2);
  not not_639 (not_639_out, bh3);
  not not_640 (not_640_out, bh4);
  not not_641 (not_641_out, sh0);
  not not_642 (not_642_out, bh2);
  not not_643 (not_643_out, bh3);
  not not_644 (not_644_out, sh0);
  not not_645 (not_645_out, sh3);
  not not_646 (not_646_out, bh2);
  not not_647 (not_647_out, bh3);
  not not_648 (not_648_out, sh0);
  not not_649 (not_649_out, sh4);
  not not_650 (not_650_out, bh2);
  not not_651 (not_651_out, bh4);
  not not_652 (not_652_out, sh0);
  not not_653 (not_653_out, sh3);
  not not_654 (not_654_out, bh2);
  not not_655 (not_655_out, sh0);
  not not_656 (not_656_out, sh2);
  not not_657 (not_657_out, bh2);
  not not_658 (not_658_out, sh0);
  not not_659 (not_659_out, sh3);
  not not_660 (not_660_out, sh4);
  not not_661 (not_661_out, bh3);
  not not_662 (not_662_out, bh4);
  not not_663 (not_663_out, sh0);
  not not_664 (not_664_out, sh2);
  not not_665 (not_665_out, bh3);
  not not_666 (not_666_out, sh0);
  not not_667 (not_667_out, sh2);
  not not_668 (not_668_out, sh3);
  not not_669 (not_669_out, bh3);
  not not_670 (not_670_out, sh0);
  not not_671 (not_671_out, sh2);
  not not_672 (not_672_out, sh4);
  not not_673 (not_673_out, bh4);
  not not_674 (not_674_out, sh0);
  not not_675 (not_675_out, sh2);
  not not_676 (not_676_out, sh3);
  not not_677 (not_677_out, sh0);
  not not_678 (not_678_out, sh2);
  not not_679 (not_679_out, sh3);
  not not_680 (not_680_out, sh4);
  not not_681 (not_681_out, sh0);
  not not_682 (not_682_out, sh1);
  not not_683 (not_683_out, sh0);
  not not_684 (not_684_out, sh1);
  not not_685 (not_685_out, sh0);
  not not_686 (not_686_out, sh1);
  not not_687 (not_687_out, sh0);
  not not_688 (not_688_out, sh1);
  not not_689 (not_689_out, sh0);
  not not_690 (not_690_out, sh1);
  not not_691 (not_691_out, sh0);
  not not_692 (not_692_out, sh1);
  not not_693 (not_693_out, sh0);
  not not_694 (not_694_out, sh1);
  not not_695 (not_695_out, bh2);
  not not_696 (not_696_out, bh3);
  not not_697 (not_697_out, bh4);
  not not_698 (not_698_out, bh2);
  not not_699 (not_699_out, bh3);
  not not_700 (not_700_out, sh3);
  not not_701 (not_701_out, bh2);
  not not_702 (not_702_out, bh3);
  not not_703 (not_703_out, sh4);
  not not_704 (not_704_out, bh2);
  not not_705 (not_705_out, bh4);
  not not_706 (not_706_out, sh3);
  not not_707 (not_707_out, bh2);
  not not_708 (not_708_out, sh3);
  not not_709 (not_709_out, sh4);
  not not_710 (not_710_out, bh2);
  not not_711 (not_711_out, sh2);
  not not_712 (not_712_out, bh2);
  not not_713 (not_713_out, sh2);
  not not_714 (not_714_out, bh2);
  not not_715 (not_715_out, sh2);
  not not_716 (not_716_out, bh3);
  not not_717 (not_717_out, bh4);
  not not_718 (not_718_out, sh2);
  not not_719 (not_719_out, bh3);
  not not_720 (not_720_out, sh2);
  not not_721 (not_721_out, sh3);
  not not_722 (not_722_out, bh3);
  not not_723 (not_723_out, sh2);
  not not_724 (not_724_out, sh4);
  not not_725 (not_725_out, bh4);
  not not_726 (not_726_out, sh2);
  not not_727 (not_727_out, sh3);
  not not_728 (not_728_out, sh2);
  not not_729 (not_729_out, sh3);
  not not_730 (not_730_out, sh4);
  not not_731 (not_731_out, bh3);
  not not_732 (not_732_out, bh4);
  not not_733 (not_733_out, bh3);
  not not_734 (not_734_out, sh4);
  not not_735 (not_735_out, bh3);
  not not_736 (not_736_out, sh3);
  not not_737 (not_737_out, bh4);
  not not_738 (not_738_out, sh3);
  not not_739 (not_739_out, sh3);
  not not_740 (not_740_out, sh4);
  not not_741 (not_741_out, bh4);
  not not_742 (not_742_out, sh4);
  and and_1 (and_1_out, not_1_out, not_2_out, not_3_out, not_4_out, not_5_out, sh0, not_6_out);
  and and_2 (and_2_out, not_7_out, not_8_out, not_9_out, not_10_out, sh0, not_11_out, not_12_out);
  and and_3 (and_3_out, not_13_out, not_14_out, not_15_out, not_16_out, sh0, not_17_out, not_18_out);
  and and_4 (and_4_out, not_19_out, not_20_out, not_21_out, not_22_out, sh0, not_23_out, not_24_out);
  and and_5 (and_5_out, not_25_out, not_26_out, not_27_out, sh0, not_28_out, not_29_out);
  and and_6 (and_6_out, not_30_out, not_31_out, not_32_out, sh0, not_33_out, not_34_out, not_35_out);
  and and_7 (and_7_out, not_36_out, not_37_out, not_38_out, not_39_out, sh0, not_40_out, not_41_out);
  and and_8 (and_8_out, not_42_out, not_43_out, not_44_out, sh0, not_45_out, not_46_out, not_47_out);
  and and_9 (and_9_out, not_48_out, not_49_out, not_50_out, sh0, not_51_out, not_52_out, not_53_out);
  and and_10 (and_10_out, not_54_out, not_55_out, not_56_out, sh0, not_57_out, not_58_out, not_59_out);
  and and_11 (and_11_out, not_60_out, not_61_out, sh0, not_62_out, not_63_out, not_64_out, not_65_out);
  and and_12 (and_12_out, not_66_out, not_67_out, bh4, not_68_out, sh1, sh2, sh3, sh4);
  and and_13 (and_13_out, not_69_out, not_70_out, bh3, not_71_out, sh1, sh2, sh3);
  and and_14 (and_14_out, not_72_out, not_73_out, bh3, bh4, not_74_out, sh1, sh2, sh4);
  and and_15 (and_15_out, not_75_out, not_76_out, bh2, not_77_out, sh1, sh2);
  and and_16 (and_16_out, not_78_out, not_79_out, bh2, bh4, not_80_out, sh1, sh3, sh4);
  and and_17 (and_17_out, not_81_out, not_82_out, bh2, bh3, not_83_out, sh1, sh3);
  and and_18 (and_18_out, not_84_out, not_85_out, bh2, bh3, bh4, not_86_out, sh1, sh4);
  and and_19 (and_19_out, not_87_out, bh1, not_88_out, not_89_out, not_90_out, not_91_out, sh1);
  and and_20 (and_20_out, not_92_out, bh1, not_93_out, not_94_out, not_95_out, sh1, not_96_out);
  and and_21 (and_21_out, not_97_out, bh1, not_98_out, not_99_out, not_100_out, sh1, not_101_out);
  and and_22 (and_22_out, not_102_out, bh1, not_103_out, not_104_out, not_105_out, sh1, not_106_out);
  and and_23 (and_23_out, not_107_out, bh1, not_108_out, not_109_out, sh1, not_110_out);
  and and_24 (and_24_out, not_111_out, bh1, not_112_out, not_113_out, sh1, not_114_out, not_115_out);
  and and_25 (and_25_out, not_116_out, bh1, not_117_out, not_118_out, not_119_out, sh1, not_120_out);
  and and_26 (and_26_out, not_121_out, bh1, not_122_out, not_123_out, sh1, not_124_out, not_125_out);
  and and_27 (and_27_out, not_126_out, bh1, not_127_out, not_128_out, sh1, not_129_out, not_130_out);
  and and_28 (and_28_out, not_131_out, bh1, not_132_out, not_133_out, sh1, not_134_out, not_135_out);
  and and_29 (and_29_out, not_136_out, bh1, not_137_out, sh1, not_138_out, not_139_out, not_140_out);
  and and_30 (and_30_out, not_141_out, bh1, bh4, not_142_out, not_143_out, sh2, sh3, sh4);
  and and_31 (and_31_out, not_144_out, bh1, bh4, sh0, sh1, sh2, sh3, sh4);
  and and_32 (and_32_out, not_145_out, bh1, bh3, not_146_out, not_147_out, sh2, sh3);
  and and_33 (and_33_out, not_148_out, bh1, bh3, sh0, sh1, sh2, sh3);
  and and_34 (and_34_out, not_149_out, bh1, bh3, bh4, not_150_out, not_151_out, sh2, sh4);
  and and_35 (and_35_out, not_152_out, bh1, bh3, bh4, sh0, sh1, sh2, sh4);
  and and_36 (and_36_out, not_153_out, bh1, bh2, not_154_out, not_155_out, sh2);
  and and_37 (and_37_out, not_156_out, bh1, bh2, sh0, sh1, sh2);
  and and_38 (and_38_out, not_157_out, bh1, bh2, bh4, not_158_out, not_159_out, sh3, sh4);
  and and_39 (and_39_out, not_160_out, bh1, bh2, bh4, sh0, sh1, sh3, sh4);
  and and_40 (and_40_out, not_161_out, bh1, bh2, bh3, not_162_out, not_163_out, sh3);
  and and_41 (and_41_out, not_164_out, bh1, bh2, bh3, sh0, sh1, sh3);
  and and_42 (and_42_out, not_165_out, bh1, bh2, bh3, bh4, not_166_out, not_167_out, sh4);
  and and_43 (and_43_out, not_168_out, bh1, bh2, bh3, bh4, sh0, sh1, sh4);
  and and_44 (and_44_out, bh0, not_169_out, not_170_out, not_171_out, not_172_out, not_173_out, not_174_out);
  and and_45 (and_45_out, bh0, not_175_out, not_176_out, not_177_out, not_178_out, not_179_out, not_180_out);
  and and_46 (and_46_out, bh0, not_181_out, not_182_out, not_183_out, not_184_out, not_185_out, not_186_out);
  and and_47 (and_47_out, bh0, not_187_out, not_188_out, not_189_out, not_190_out, not_191_out, not_192_out);
  and and_48 (and_48_out, bh0, not_193_out, not_194_out, not_195_out, not_196_out, not_197_out);
  and and_49 (and_49_out, bh0, not_198_out, not_199_out, not_200_out, not_201_out, not_202_out, not_203_out);
  and and_50 (and_50_out, bh0, not_204_out, not_205_out, not_206_out, not_207_out, not_208_out, not_209_out);
  and and_51 (and_51_out, bh0, not_210_out, not_211_out, not_212_out, not_213_out, not_214_out, not_215_out);
  and and_52 (and_52_out, bh0, not_216_out, not_217_out, not_218_out, not_219_out, not_220_out, not_221_out);
  and and_53 (and_53_out, bh0, not_222_out, not_223_out, not_224_out, not_225_out, not_226_out, not_227_out);
  and and_54 (and_54_out, bh0, not_228_out, not_229_out, not_230_out, not_231_out, not_232_out, not_233_out);
  and and_55 (and_55_out, bh0, not_234_out, not_235_out, not_236_out, not_237_out, sh0, sh1);
  and and_56 (and_56_out, bh0, not_238_out, not_239_out, not_240_out, sh0, sh1, not_241_out);
  and and_57 (and_57_out, bh0, not_242_out, not_243_out, not_244_out, sh0, sh1, not_245_out);
  and and_58 (and_58_out, bh0, not_246_out, not_247_out, not_248_out, sh0, sh1, not_249_out);
  and and_59 (and_59_out, bh0, not_250_out, not_251_out, sh0, sh1, not_252_out);
  and and_60 (and_60_out, bh0, not_253_out, not_254_out, sh0, sh1, not_255_out, not_256_out);
  and and_61 (and_61_out, bh0, not_257_out, not_258_out, not_259_out, sh0, sh1, not_260_out);
  and and_62 (and_62_out, bh0, not_261_out, not_262_out, sh0, sh1, not_263_out, not_264_out);
  and and_63 (and_63_out, bh0, not_265_out, not_266_out, sh0, sh1, not_267_out, not_268_out);
  and and_64 (and_64_out, bh0, not_269_out, not_270_out, sh0, sh1, not_271_out, not_272_out);
  and and_65 (and_65_out, bh0, not_273_out, sh0, sh1, not_274_out, not_275_out, not_276_out);
  and and_66 (and_66_out, bh0, not_277_out, bh4, sh0, not_278_out, sh2, sh3, sh4);
  and and_67 (and_67_out, bh0, not_279_out, bh3, sh0, not_280_out, sh2, sh3);
  and and_68 (and_68_out, bh0, not_281_out, bh3, bh4, sh0, not_282_out, sh2, sh4);
  and and_69 (and_69_out, bh0, not_283_out, bh2, sh0, not_284_out, sh2);
  and and_70 (and_70_out, bh0, not_285_out, bh2, bh4, sh0, not_286_out, sh3, sh4);
  and and_71 (and_71_out, bh0, not_287_out, bh2, bh3, sh0, not_288_out, sh3);
  and and_72 (and_72_out, bh0, not_289_out, bh2, bh3, bh4, sh0, not_290_out, sh4);
  and and_73 (and_73_out, bh0, bh1, not_291_out, not_292_out, not_293_out, sh0, not_294_out);
  and and_74 (and_74_out, bh0, bh1, not_295_out, not_296_out, sh0, not_297_out, not_298_out);
  and and_75 (and_75_out, bh0, bh1, not_299_out, not_300_out, sh0, not_301_out, not_302_out);
  and and_76 (and_76_out, bh0, bh1, not_303_out, not_304_out, sh0, not_305_out, not_306_out);
  and and_77 (and_77_out, bh0, bh1, not_307_out, sh0, not_308_out, not_309_out);
  and and_78 (and_78_out, bh0, bh1, not_310_out, sh0, not_311_out, not_312_out, not_313_out);
  and and_79 (and_79_out, bh0, bh1, not_314_out, not_315_out, sh0, not_316_out, not_317_out);
  and and_80 (and_80_out, bh0, bh1, not_318_out, sh0, not_319_out, not_320_out, not_321_out);
  and and_81 (and_81_out, bh0, bh1, not_322_out, sh0, not_323_out, not_324_out, not_325_out);
  and and_82 (and_82_out, bh0, bh1, not_326_out, sh0, not_327_out, not_328_out, not_329_out);
  and and_83 (and_83_out, bh0, bh1, sh0, not_330_out, not_331_out, not_332_out, not_333_out);
  and and_84 (and_84_out, bh0, bh1, bh4, not_334_out, sh1, sh2, sh3, sh4);
  and and_85 (and_85_out, bh0, bh1, bh3, not_335_out, sh1, sh2, sh3);
  and and_86 (and_86_out, bh0, bh1, bh3, bh4, not_336_out, sh1, sh2, sh4);
  and and_87 (and_87_out, bh0, bh1, bh2, not_337_out, sh1, sh2);
  and and_88 (and_88_out, bh0, bh1, bh2, bh4, not_338_out, sh1, sh3, sh4);
  and and_89 (and_89_out, bh0, bh1, bh2, bh3, not_339_out, sh1, sh3);
  and and_90 (and_90_out, bh0, bh1, bh2, bh3, bh4, not_340_out, sh1, sh4);
  and and_91 (and_91_out, not_341_out, not_342_out, not_343_out, not_344_out, not_345_out, not_346_out, sh1);
  and and_92 (and_92_out, not_347_out, not_348_out, not_349_out, not_350_out, not_351_out, sh1, not_352_out);
  and and_93 (and_93_out, not_353_out, not_354_out, not_355_out, not_356_out, not_357_out, sh1, not_358_out);
  and and_94 (and_94_out, not_359_out, not_360_out, not_361_out, not_362_out, not_363_out, sh1, not_364_out);
  and and_95 (and_95_out, not_365_out, not_366_out, not_367_out, not_368_out, sh1, not_369_out);
  and and_96 (and_96_out, not_370_out, not_371_out, not_372_out, not_373_out, sh1, not_374_out, not_375_out);
  and and_97 (and_97_out, not_376_out, not_377_out, not_378_out, not_379_out, not_380_out, sh1, not_381_out);
  and and_98 (and_98_out, not_382_out, not_383_out, not_384_out, not_385_out, sh1, not_386_out, not_387_out);
  and and_99 (and_99_out, not_388_out, not_389_out, not_390_out, not_391_out, sh1, not_392_out, not_393_out);
  and and_100 (and_100_out, not_394_out, not_395_out, not_396_out, not_397_out, sh1, not_398_out, not_399_out);
  and and_101 (and_101_out, not_400_out, not_401_out, not_402_out, sh1, not_403_out, not_404_out, not_405_out);
  and and_102 (and_102_out, not_406_out, not_407_out, bh4, not_408_out, not_409_out, sh2, sh3, sh4);
  and and_103 (and_103_out, not_410_out, not_411_out, bh4, sh0, sh1, sh2, sh3, sh4);
  and and_104 (and_104_out, not_412_out, not_413_out, bh3, not_414_out, not_415_out, sh2, sh3);
  and and_105 (and_105_out, not_416_out, not_417_out, bh3, sh0, sh1, sh2, sh3);
  and and_106 (and_106_out, not_418_out, not_419_out, bh3, bh4, not_420_out, not_421_out, sh2, sh4);
  and and_107 (and_107_out, not_422_out, not_423_out, bh3, bh4, sh0, sh1, sh2, sh4);
  and and_108 (and_108_out, not_424_out, not_425_out, bh2, not_426_out, not_427_out, sh2);
  and and_109 (and_109_out, not_428_out, not_429_out, bh2, sh0, sh1, sh2);
  and and_110 (and_110_out, not_430_out, not_431_out, bh2, bh4, not_432_out, not_433_out, sh3, sh4);
  and and_111 (and_111_out, not_434_out, not_435_out, bh2, bh4, sh0, sh1, sh3, sh4);
  and and_112 (and_112_out, not_436_out, not_437_out, bh2, bh3, not_438_out, not_439_out, sh3);
  and and_113 (and_113_out, not_440_out, not_441_out, bh2, bh3, sh0, sh1, sh3);
  and and_114 (and_114_out, not_442_out, not_443_out, bh2, bh3, bh4, not_444_out, not_445_out, sh4);
  and and_115 (and_115_out, not_446_out, not_447_out, bh2, bh3, bh4, sh0, sh1, sh4);
  and and_116 (and_116_out, not_448_out, bh1, not_449_out, not_450_out, not_451_out, not_452_out, not_453_out);
  and and_117 (and_117_out, not_454_out, bh1, not_455_out, not_456_out, not_457_out, not_458_out, not_459_out);
  and and_118 (and_118_out, not_460_out, bh1, not_461_out, not_462_out, not_463_out, not_464_out, not_465_out);
  and and_119 (and_119_out, not_466_out, bh1, not_467_out, not_468_out, not_469_out, not_470_out, not_471_out);
  and and_120 (and_120_out, not_472_out, bh1, not_473_out, not_474_out, not_475_out, not_476_out);
  and and_121 (and_121_out, not_477_out, bh1, not_478_out, not_479_out, not_480_out, not_481_out, not_482_out);
  and and_122 (and_122_out, not_483_out, bh1, not_484_out, not_485_out, not_486_out, not_487_out, not_488_out);
  and and_123 (and_123_out, not_489_out, bh1, not_490_out, not_491_out, not_492_out, not_493_out, not_494_out);
  and and_124 (and_124_out, not_495_out, bh1, not_496_out, not_497_out, not_498_out, not_499_out, not_500_out);
  and and_125 (and_125_out, not_501_out, bh1, not_502_out, not_503_out, not_504_out, not_505_out, not_506_out);
  and and_126 (and_126_out, not_507_out, bh1, not_508_out, not_509_out, not_510_out, not_511_out, not_512_out);
  and and_127 (and_127_out, not_513_out, bh1, not_514_out, not_515_out, not_516_out, sh0, sh1);
  and and_128 (and_128_out, not_517_out, bh1, not_518_out, not_519_out, sh0, sh1, not_520_out);
  and and_129 (and_129_out, not_521_out, bh1, not_522_out, not_523_out, sh0, sh1, not_524_out);
  and and_130 (and_130_out, not_525_out, bh1, not_526_out, not_527_out, sh0, sh1, not_528_out);
  and and_131 (and_131_out, not_529_out, bh1, not_530_out, sh0, sh1, not_531_out);
  and and_132 (and_132_out, not_532_out, bh1, not_533_out, sh0, sh1, not_534_out, not_535_out);
  and and_133 (and_133_out, not_536_out, bh1, not_537_out, not_538_out, sh0, sh1, not_539_out);
  and and_134 (and_134_out, not_540_out, bh1, not_541_out, sh0, sh1, not_542_out, not_543_out);
  and and_135 (and_135_out, not_544_out, bh1, not_545_out, sh0, sh1, not_546_out, not_547_out);
  and and_136 (and_136_out, not_548_out, bh1, not_549_out, sh0, sh1, not_550_out, not_551_out);
  and and_137 (and_137_out, not_552_out, bh1, sh0, sh1, not_553_out, not_554_out, not_555_out);
  and and_138 (and_138_out, not_556_out, bh1, bh4, sh0, not_557_out, sh2, sh3, sh4);
  and and_139 (and_139_out, not_558_out, bh1, bh3, sh0, not_559_out, sh2, sh3);
  and and_140 (and_140_out, not_560_out, bh1, bh3, bh4, sh0, not_561_out, sh2, sh4);
  and and_141 (and_141_out, not_562_out, bh1, bh2, sh0, not_563_out, sh2);
  and and_142 (and_142_out, not_564_out, bh1, bh2, bh4, sh0, not_565_out, sh3, sh4);
  and and_143 (and_143_out, not_566_out, bh1, bh2, bh3, sh0, not_567_out, sh3);
  and and_144 (and_144_out, not_568_out, bh1, bh2, bh3, bh4, sh0, not_569_out, sh4);
  and and_145 (and_145_out, bh0, not_570_out, not_571_out, not_572_out, not_573_out, sh0, not_574_out);
  and and_146 (and_146_out, bh0, not_575_out, not_576_out, not_577_out, sh0, not_578_out, not_579_out);
  and and_147 (and_147_out, bh0, not_580_out, not_581_out, not_582_out, sh0, not_583_out, not_584_out);
  and and_148 (and_148_out, bh0, not_585_out, not_586_out, not_587_out, sh0, not_588_out, not_589_out);
  and and_149 (and_149_out, bh0, not_590_out, not_591_out, sh0, not_592_out, not_593_out);
  and and_150 (and_150_out, bh0, not_594_out, not_595_out, sh0, not_596_out, not_597_out, not_598_out);
  and and_151 (and_151_out, bh0, not_599_out, not_600_out, not_601_out, sh0, not_602_out, not_603_out);
  and and_152 (and_152_out, bh0, not_604_out, not_605_out, sh0, not_606_out, not_607_out, not_608_out);
  and and_153 (and_153_out, bh0, not_609_out, not_610_out, sh0, not_611_out, not_612_out, not_613_out);
  and and_154 (and_154_out, bh0, not_614_out, not_615_out, sh0, not_616_out, not_617_out, not_618_out);
  and and_155 (and_155_out, bh0, not_619_out, sh0, not_620_out, not_621_out, not_622_out, not_623_out);
  and and_156 (and_156_out, bh0, not_624_out, bh4, not_625_out, sh1, sh2, sh3, sh4);
  and and_157 (and_157_out, bh0, not_626_out, bh3, not_627_out, sh1, sh2, sh3);
  and and_158 (and_158_out, bh0, not_628_out, bh3, bh4, not_629_out, sh1, sh2, sh4);
  and and_159 (and_159_out, bh0, not_630_out, bh2, not_631_out, sh1, sh2);
  and and_160 (and_160_out, bh0, not_632_out, bh2, bh4, not_633_out, sh1, sh3, sh4);
  and and_161 (and_161_out, bh0, not_634_out, bh2, bh3, not_635_out, sh1, sh3);
  and and_162 (and_162_out, bh0, not_636_out, bh2, bh3, bh4, not_637_out, sh1, sh4);
  and and_163 (and_163_out, bh0, bh1, not_638_out, not_639_out, not_640_out, not_641_out, sh1);
  and and_164 (and_164_out, bh0, bh1, not_642_out, not_643_out, not_644_out, sh1, not_645_out);
  and and_165 (and_165_out, bh0, bh1, not_646_out, not_647_out, not_648_out, sh1, not_649_out);
  and and_166 (and_166_out, bh0, bh1, not_650_out, not_651_out, not_652_out, sh1, not_653_out);
  and and_167 (and_167_out, bh0, bh1, not_654_out, not_655_out, sh1, not_656_out);
  and and_168 (and_168_out, bh0, bh1, not_657_out, not_658_out, sh1, not_659_out, not_660_out);
  and and_169 (and_169_out, bh0, bh1, not_661_out, not_662_out, not_663_out, sh1, not_664_out);
  and and_170 (and_170_out, bh0, bh1, not_665_out, not_666_out, sh1, not_667_out, not_668_out);
  and and_171 (and_171_out, bh0, bh1, not_669_out, not_670_out, sh1, not_671_out, not_672_out);
  and and_172 (and_172_out, bh0, bh1, not_673_out, not_674_out, sh1, not_675_out, not_676_out);
  and and_173 (and_173_out, bh0, bh1, not_677_out, sh1, not_678_out, not_679_out, not_680_out);
  and and_174 (and_174_out, bh0, bh1, bh4, not_681_out, not_682_out, sh2, sh3, sh4);
  and and_175 (and_175_out, bh0, bh1, bh4, sh0, sh1, sh2, sh3, sh4);
  and and_176 (and_176_out, bh0, bh1, bh3, not_683_out, not_684_out, sh2, sh3);
  and and_177 (and_177_out, bh0, bh1, bh3, sh0, sh1, sh2, sh3);
  and and_178 (and_178_out, bh0, bh1, bh3, bh4, not_685_out, not_686_out, sh2, sh4);
  and and_179 (and_179_out, bh0, bh1, bh3, bh4, sh0, sh1, sh2, sh4);
  and and_180 (and_180_out, bh0, bh1, bh2, not_687_out, not_688_out, sh2);
  and and_181 (and_181_out, bh0, bh1, bh2, sh0, sh1, sh2);
  and and_182 (and_182_out, bh0, bh1, bh2, bh4, not_689_out, not_690_out, sh3, sh4);
  and and_183 (and_183_out, bh0, bh1, bh2, bh4, sh0, sh1, sh3, sh4);
  and and_184 (and_184_out, bh0, bh1, bh2, bh3, not_691_out, not_692_out, sh3);
  and and_185 (and_185_out, bh0, bh1, bh2, bh3, sh0, sh1, sh3);
  and and_186 (and_186_out, bh0, bh1, bh2, bh3, bh4, not_693_out, not_694_out, sh4);
  and and_187 (and_187_out, bh0, bh1, bh2, bh3, bh4, sh0, sh1, sh4);
  and and_188 (and_188_out, not_695_out, not_696_out, not_697_out, sh2);
  and and_189 (and_189_out, not_698_out, not_699_out, sh2, not_700_out);
  and and_190 (and_190_out, not_701_out, not_702_out, sh2, not_703_out);
  and and_191 (and_191_out, not_704_out, not_705_out, sh2, not_706_out);
  and and_192 (and_192_out, not_707_out, sh2, not_708_out, not_709_out);
  and and_193 (and_193_out, not_710_out, bh4, not_711_out, sh3, sh4);
  and and_194 (and_194_out, not_712_out, bh3, not_713_out, sh3);
  and and_195 (and_195_out, not_714_out, bh3, bh4, not_715_out, sh4);
  and and_196 (and_196_out, bh2, not_716_out, not_717_out, not_718_out);
  and and_197 (and_197_out, bh2, not_719_out, not_720_out, not_721_out);
  and and_198 (and_198_out, bh2, not_722_out, not_723_out, not_724_out);
  and and_199 (and_199_out, bh2, not_725_out, not_726_out, not_727_out);
  and and_200 (and_200_out, bh2, not_728_out, not_729_out, not_730_out);
  and and_201 (and_201_out, bh2, bh4, sh2, sh3, sh4);
  and and_202 (and_202_out, bh2, bh3, sh2, sh3);
  and and_203 (and_203_out, bh2, bh3, bh4, sh2, sh4);
  and and_204 (and_204_out, not_731_out, not_732_out, sh3);
  and and_205 (and_205_out, not_733_out, sh3, not_734_out);
  and and_206 (and_206_out, not_735_out, bh4, not_736_out, sh4);
  and and_207 (and_207_out, bh3, not_737_out, not_738_out);
  and and_208 (and_208_out, bh3, not_739_out, not_740_out);
  and and_209 (and_209_out, bh3, bh4, sh3, sh4);
  and and_210 (and_210_out, not_741_out, sh4);
  or or_1 (h4, and_210_out, and_211_out);
  and and_211 (and_211_out, bh4, not_742_out);
  or or_2 (h2, and_188_out, and_189_out, and_190_out, and_191_out, and_192_out, and_193_out, and_194_out, and_195_out, and_196_out, and_197_out, and_198_out, and_199_out, and_200_out, and_201_out, and_202_out, and_203_out);
  or or_3 (h3, and_204_out, and_205_out, and_206_out, and_207_out, and_208_out, and_209_out);
  or or_4 (or_4_out, and_91_out, and_92_out, and_93_out, and_94_out, and_95_out, and_96_out, and_97_out, and_98_out, and_99_out, and_100_out, and_101_out, and_102_out, and_103_out, and_104_out, and_105_out, and_106_out, and_107_out, and_108_out, and_109_out, and_110_out, and_111_out, and_112_out, and_113_out, and_114_out, and_115_out);
  or or_5 (or_5_out, and_116_out, and_117_out, and_118_out, and_119_out, and_120_out, and_121_out, and_122_out, and_123_out, and_124_out, and_125_out, and_126_out, and_127_out, and_128_out, and_129_out, and_130_out, and_131_out, and_132_out, and_133_out, and_134_out, and_135_out, and_136_out, and_137_out, and_138_out, and_139_out);
  or or_6 (or_6_out, and_140_out, and_141_out, and_142_out, and_143_out, and_144_out, and_145_out, and_146_out, and_147_out, and_148_out, and_149_out, and_150_out, and_151_out, and_152_out, and_153_out, and_154_out, and_155_out, and_156_out, and_157_out, and_158_out, and_159_out, and_160_out, and_161_out, and_162_out, and_163_out);
  or or_7 (or_7_out, and_164_out, and_165_out, and_166_out, and_167_out, and_168_out, and_169_out, and_170_out, and_171_out, and_172_out, and_173_out, and_174_out, and_175_out, and_176_out, and_177_out, and_178_out, and_179_out, and_180_out, and_181_out, and_182_out, and_183_out, and_184_out, and_185_out, and_186_out, and_187_out);
  or or_8 (or_8_out, and_1_out, and_2_out, and_3_out, and_4_out, and_5_out, and_6_out, and_7_out, and_8_out, and_9_out, and_10_out, and_11_out, and_12_out, and_13_out, and_14_out, and_15_out, and_16_out, and_17_out, and_18_out, and_19_out, and_20_out, and_21_out, and_22_out, and_23_out, and_24_out, and_25_out, and_26_out, and_27_out, and_28_out, and_29_out, and_30_out);
  or or_9 (h0, or_8_out, or_10_out, or_11_out);
  or or_10 (or_10_out, and_31_out, and_32_out, and_33_out, and_34_out, and_35_out, and_36_out, and_37_out, and_38_out, and_39_out, and_40_out, and_41_out, and_42_out, and_43_out, and_44_out, and_45_out, and_46_out, and_47_out, and_48_out, and_49_out, and_50_out, and_51_out, and_52_out, and_53_out, and_54_out, and_55_out, and_56_out, and_57_out, and_58_out, and_59_out, and_60_out);
  or or_11 (or_11_out, and_61_out, and_62_out, and_63_out, and_64_out, and_65_out, and_66_out, and_67_out, and_68_out, and_69_out, and_70_out, and_71_out, and_72_out, and_73_out, and_74_out, and_75_out, and_76_out, and_77_out, and_78_out, and_79_out, and_80_out, and_81_out, and_82_out, and_83_out, and_84_out, and_85_out, and_86_out, and_87_out, and_88_out, and_89_out, and_90_out);
  or or_12 (h1, or_4_out, or_5_out, or_6_out, or_7_out);
endmodule

module decalhorraire (
  input  rst,
  input  button,
  input  clk,
  output [5:0] hour1,
  output [5:0] hour0,
  output [5:0] min1,
  output [5:0] min0,
  output [5:0] sec1,
  output [5:0] sec0,
  output [4:0] hour_shift
);

  wire and_1_out, and_2_out, and_3_out, and_4_out, and_5_out, t_ff_1_q, t_ff_2_q;
  wire [5:0] selcomp_1_output_bus_1, selcomp_2_output_bus_1, selcomp_3_output_bus_1, selcomp_4_output_bus_1,
       selcomp_5_output_bus_1, selcomp_6_output_bus_1, selcomp_7_output_bus_1, selcomp_8_output_bus_1,
       selcomp_9_output_bus_1, selcomp_10_output_bus_1, selcomp_11_output_bus_1, selcomp_12_output_bus_1;

  T_Flip_Flop t_ff_1 (.T(button), .clk(clk), .Q(t_ff_1_q), .reset(rst));  // open: Qn, preset
  and and_1 (and_1_out, button, t_ff_1_q);
  T_Flip_Flop t_ff_2 (.T(and_1_out), .clk(clk), .Q(t_ff_2_q), .reset(rst));  // open: Qn, preset
  and and_2 (and_2_out, t_ff_1_q, ~t_ff_2_q);  // AND_Gate
  and and_3 (and_3_out, ~t_ff_1_q, ~t_ff_2_q);  // AND_Gate
  and and_4 (and_4_out, t_ff_1_q, t_ff_2_q);
  and and_5 (and_5_out, ~t_ff_1_q, t_ff_2_q);  // AND_Gate
  selcomp selcomp_1 (
    .en(and_3_out), .Input_1(1'b1), .Input_2(1'b0), .Input_3(1'b0), .Input_4(1'b0), .Input_5(1'b1),
    .Input_6(1'b0), .Output_bus_1(selcomp_1_output_bus_1));
  selcomp selcomp_2 (
    .en(and_3_out), .Input_1(1'b1), .Input_2(1'b1), .Input_3(1'b1), .Input_4(1'b0), .Input_5(1'b1),
    .Input_6(1'b0), .Output_bus_1(selcomp_2_output_bus_1));
  selcomp selcomp_3 (
    .en(and_3_out), .Input_1(1'b0), .Input_2(1'b1), .Input_3(1'b1), .Input_4(1'b1), .Input_5(1'b1),
    .Input_6(1'b0), .Output_bus_1(selcomp_3_output_bus_1));
  selcomp selcomp_4 (
    .en(and_2_out), .Input_1(1'b0), .Input_2(1'b1), .Input_3(1'b0), .Input_4(1'b1), .Input_5(1'b1),
    .Input_6(1'b0), .Output_bus_1(selcomp_4_output_bus_1));
  selcomp selcomp_5 (
    .en(and_2_out), .Input_1(1'b0), .Input_2(1'b0), .Input_3(1'b1), .Input_4(1'b1), .Input_5(1'b1),
    .Input_6(1'b0), .Output_bus_1(selcomp_5_output_bus_1));
  selcomp selcomp_6 (
    .en(and_2_out), .Input_1(1'b1), .Input_2(1'b0), .Input_3(1'b1), .Input_4(1'b1), .Input_5(1'b1),
    .Input_6(1'b0), .Output_bus_1(selcomp_6_output_bus_1));
  selcomp selcomp_7 (
    .en(and_5_out), .Input_1(1'b1), .Input_2(1'b1), .Input_3(1'b1), .Input_4(1'b0), .Input_5(1'b1),
    .Input_6(1'b0), .Output_bus_1(selcomp_7_output_bus_1));
  selcomp selcomp_8 (
    .en(and_5_out), .Input_1(1'b1), .Input_2(1'b0), .Input_3(1'b1), .Input_4(1'b1), .Input_5(1'b1),
    .Input_6(1'b0), .Output_bus_1(selcomp_8_output_bus_1));
  selcomp selcomp_9 (
    .en(and_5_out), .Input_1(1'b1), .Input_2(1'b0), .Input_3(1'b1), .Input_4(1'b1), .Input_5(1'b0),
    .Input_6(1'b0), .Output_bus_1(selcomp_9_output_bus_1));
  selcomp selcomp_10 (
    .en(and_4_out), .Input_1(1'b0), .Input_2(1'b0), .Input_3(1'b0), .Input_4(1'b1), .Input_5(1'b1),
    .Input_6(1'b0), .Output_bus_1(selcomp_10_output_bus_1));
  selcomp selcomp_11 (
    .en(and_4_out), .Input_1(1'b1), .Input_2(1'b0), .Input_3(1'b0), .Input_4(1'b0), .Input_5(1'b0),
    .Input_6(1'b1), .Output_bus_1(selcomp_11_output_bus_1));
  selcomp selcomp_12 (
    .en(and_4_out), .Input_1(1'b1), .Input_2(1'b0), .Input_3(1'b1), .Input_4(1'b1), .Input_5(1'b0),
    .Input_6(1'b0), .Output_bus_1(selcomp_12_output_bus_1));
  shift shift_1 (
    .c1(and_4_out), .c2(and_5_out), .c3(and_2_out), .c4(and_3_out), .b0(hour_shift[0]), .b1(hour_shift[1]),
    .b2(hour_shift[2]), .b3(hour_shift[3]), .b4(hour_shift[4]));
  tens tens_1 (
    .Input_1(1'b0), .Input_2(hour_shift[4]), .Input_3(hour_shift[3]), .Input_4(hour_shift[2]),
    .Input_5(hour_shift[1]), .Input_6(hour_shift[0]), .Output_1(sec1[5]), .Output_2(sec1[4]),
    .Output_3(sec1[3]), .Output_4(sec1[2]), .Output_5(sec1[1]), .Output_6(sec1[0]));
  ones ones_1 (
    .Input_1(1'b0), .Input_2(hour_shift[4]), .Input_3(hour_shift[3]), .Input_4(hour_shift[2]),
    .Input_5(hour_shift[1]), .Input_6(hour_shift[0]), .Output_1(sec0[5]), .Output_2(sec0[4]),
    .Output_3(sec0[3]), .Output_4(sec0[2]), .Output_5(sec0[1]), .Output_6(sec0[0]));
  assign hour1 = selcomp_1_output_bus_1 | selcomp_4_output_bus_1 | selcomp_7_output_bus_1 | selcomp_10_output_bus_1;  // OR_Gate or_1, 6 bits wide
  assign hour0 = selcomp_2_output_bus_1 | selcomp_5_output_bus_1 | selcomp_8_output_bus_1 | selcomp_11_output_bus_1;  // OR_Gate or_2, 6 bits wide
  assign min1 = selcomp_3_output_bus_1 | selcomp_6_output_bus_1 | selcomp_9_output_bus_1 | selcomp_12_output_bus_1;  // OR_Gate or_3, 6 bits wide

  assign min0 = 6'b001010;

  // Notes on the sheet:
  //   londre
  //   moscou
  //   ldn
  //   mscu
  //   new-york
  //   nyk
  //   paris
  //   moscou
  //   MSC
  //   Greenwitch
  //   GRW
  //   prs
  //   newyork
  //   NYC
endmodule

module selcomp (
  input  en,
  input  Input_1,
  input  Input_2,
  input  Input_3,
  input  Input_4,
  input  Input_5,
  input  Input_6,
  output [5:0] Output_bus_1
);

  and and_1 (Output_bus_1[0], en, Input_1);
  and and_2 (Output_bus_1[1], en, Input_2);
  and and_3 (Output_bus_1[2], en, Input_3);
  and and_4 (Output_bus_1[3], en, Input_4);
  and and_5 (Output_bus_1[4], en, Input_5);
  and and_6 (Output_bus_1[5], en, Input_6);
endmodule

module shift (
  input  c1,
  input  c2,
  input  c3,
  input  c4,
  output b0,
  output b1,
  output b2,
  output b3,
  output b4
);

  wire not_2_out, not_3_out;

  not not_1 (b0, c4);
  not not_2 (not_2_out, c3);
  not not_3 (not_3_out, c4);
  and and_1 (b1, not_2_out, not_3_out);

  assign b2 = 1'b0;
  assign b3 = 1'b0;
  assign b4 = c1;
endmodule

module smartbutton (
  input  button,
  input  clk,
  output fall,
  output Tlong,
  output long
);

  wire and_1_out, and_2_out, and_3_out, and_4_out, and_5_out, and_6_out, and_7_out, and_8_out, and_9_out,
       and_10_out, and_11_out, and_12_out, and_13_out, and_14_out, d_ff_1_q, d_ff_2_q, d_ff_3_q, d_ff_4_q,
       t_ff_1_q, t_ff_2_q, t_ff_3_q, t_ff_4_q, t_ff_5_q, t_ff_6_q, t_ff_7_q, t_ff_8_q, t_ff_9_q, t_ff_10_q,
       t_ff_11_q, t_ff_12_q, t_ff_13_q;

  T_Flip_Flop t_ff_1 (.T(button), .clk(clk), .Q(t_ff_1_q), .reset(and_2_out));  // open: Qn, preset
  D_Flip_Flop d_ff_1 (.D(button), .clk(clk), .Q(d_ff_1_q));  // open: Qn, preset, reset
  and and_1 (and_1_out, button, t_ff_1_q);
  D_Flip_Flop d_ff_2 (.D(d_ff_1_q), .clk(clk), .Q(d_ff_2_q));  // open: Qn, preset, reset
  T_Flip_Flop t_ff_2 (.T(and_1_out), .clk(clk), .Q(t_ff_2_q), .reset(and_2_out));  // open: Qn, preset
  and and_2 (and_2_out, ~d_ff_1_q, d_ff_2_q);  // AND_Gate
  T_Flip_Flop t_ff_3 (.T(and_3_out), .clk(clk), .Q(t_ff_3_q), .reset(and_2_out));  // open: Qn, preset
  and and_3 (and_3_out, and_1_out, t_ff_2_q);
  T_Flip_Flop t_ff_4 (.T(and_4_out), .clk(clk), .Q(t_ff_4_q), .reset(and_2_out));  // open: Qn, preset
  and and_4 (and_4_out, and_3_out, t_ff_3_q);
  T_Flip_Flop t_ff_5 (.T(and_5_out), .clk(clk), .Q(t_ff_5_q), .reset(and_2_out));  // open: Qn, preset
  and and_5 (and_5_out, and_4_out, t_ff_4_q);
  and and_6 (and_6_out, and_5_out, t_ff_5_q);
  T_Flip_Flop t_ff_6 (.T(and_6_out), .clk(clk), .Q(t_ff_6_q), .reset(and_2_out));  // open: Qn, preset
  T_Flip_Flop t_ff_7 (.T(and_7_out), .clk(clk), .Q(t_ff_7_q), .reset(and_2_out));  // open: Qn, preset
  and and_7 (and_7_out, and_6_out, t_ff_6_q);
  T_Flip_Flop t_ff_8 (.T(and_8_out), .clk(clk), .Q(t_ff_8_q), .reset(and_2_out));  // open: Qn, preset
  and and_8 (and_8_out, and_7_out, t_ff_7_q);
  T_Flip_Flop t_ff_9 (.T(and_9_out), .clk(clk), .Q(t_ff_9_q), .reset(and_2_out));  // open: Qn, preset
  and and_9 (and_9_out, and_8_out, t_ff_8_q);
  and and_10 (and_10_out, and_9_out, t_ff_9_q);
  T_Flip_Flop t_ff_10 (.T(and_10_out), .clk(clk), .Q(t_ff_10_q), .reset(and_2_out));  // open: Qn, preset
  T_Flip_Flop t_ff_11 (.T(and_11_out), .clk(clk), .Q(t_ff_11_q), .reset(and_2_out));  // open: Qn, preset
  and and_11 (and_11_out, and_10_out, t_ff_10_q);
  T_Flip_Flop t_ff_12 (.T(and_12_out), .clk(clk), .Q(t_ff_12_q), .reset(and_2_out));  // open: Qn, preset
  and and_12 (and_12_out, and_11_out, t_ff_11_q);
  T_Flip_Flop t_ff_13 (.T(and_13_out), .clk(clk), .Q(t_ff_13_q), .reset(and_2_out));  // open: Qn, preset
  and and_13 (and_13_out, and_12_out, t_ff_12_q);
  and and_14 (and_14_out, t_ff_13_q, ~long);  // AND_Gate
  D_Flip_Flop d_ff_3 (.D(and_14_out), .clk(clk), .Q(d_ff_3_q));  // open: Qn, preset, reset
  D_Flip_Flop d_ff_4 (.D(d_ff_3_q), .clk(clk), .Q(d_ff_4_q));  // open: Qn, preset, reset
  and and_15 (Tlong, d_ff_3_q, ~d_ff_4_q);  // AND_Gate
  T_Flip_Flop t_ff_14 (.T(Tlong), .clk(clk), .Q(long), .reset(and_2_out));  // open: Qn, preset
  and and_16 (fall, and_2_out, ~long);  // AND_Gate
endmodule

module ModHorloge (
  input  mrst,
  input  clk,
  input  LongA,
  input  ButtA,
  input  ButtB,
  input  [4:0] shift,
  output [5:0] s0,
  output [5:0] s1,
  output [5:0] m0,
  output [5:0] m1,
  output [5:0] h0,
  output [5:0] h1,
  output [5:0] Hours,
  output [5:0] minutes
);

  wire Horloge_1_wrtmode;
  wire [4:0] Horloge_1_hours;
  wire [5:0] Horloge_1_seconds, ones_1_output_6, tens_1_output_6;

  Horloge Horloge_1 (
    .MRST(mrst), .clk(clk), .longA(LongA), .FallA(ButtA), .FallB(ButtB), .Seconds(Horloge_1_seconds),
    .Minutes(minutes), .Hours(Horloge_1_hours), .wrtMode(Horloge_1_wrtmode));  // open: ms
  rectifieurhorraire rectifieurhorraire_1 (
    .bh0(Horloge_1_hours[4]), .bh1(Horloge_1_hours[3]), .bh2(Horloge_1_hours[2]), .bh3(Horloge_1_hours[1]),
    .bh4(Horloge_1_hours[0]), .sh0(shift[4]), .sh1(shift[3]), .sh2(shift[2]), .sh3(shift[1]), .sh4(shift[0]),
    .h0(Hours[4]), .h1(Hours[3]), .h2(Hours[2]), .h3(Hours[1]), .h4(Hours[0]));
  ones ones_1 (
    .Input_1(Horloge_1_seconds[5]), .Input_2(Horloge_1_seconds[4]), .Input_3(Horloge_1_seconds[3]),
    .Input_4(Horloge_1_seconds[2]), .Input_5(Horloge_1_seconds[1]), .Input_6(Horloge_1_seconds[0]),
    .Output_1(ones_1_output_6[5]), .Output_2(ones_1_output_6[4]), .Output_3(ones_1_output_6[3]),
    .Output_4(ones_1_output_6[2]), .Output_5(ones_1_output_6[1]), .Output_6(ones_1_output_6[0]));
  tens tens_1 (
    .Input_1(Horloge_1_seconds[5]), .Input_2(Horloge_1_seconds[4]), .Input_3(Horloge_1_seconds[3]),
    .Input_4(Horloge_1_seconds[2]), .Input_5(Horloge_1_seconds[1]), .Input_6(Horloge_1_seconds[0]),
    .Output_1(tens_1_output_6[5]), .Output_2(tens_1_output_6[4]), .Output_3(tens_1_output_6[3]),
    .Output_4(tens_1_output_6[2]), .Output_5(tens_1_output_6[1]), .Output_6(tens_1_output_6[0]));
  ones ones_2 (
    .Input_1(minutes[5]), .Input_2(minutes[4]), .Input_3(minutes[3]), .Input_4(minutes[2]),
    .Input_5(minutes[1]), .Input_6(minutes[0]), .Output_1(m0[5]), .Output_2(m0[4]), .Output_3(m0[3]),
    .Output_4(m0[2]), .Output_5(m0[1]), .Output_6(m0[0]));
  tens tens_2 (
    .Input_1(minutes[5]), .Input_2(minutes[4]), .Input_3(minutes[3]), .Input_4(minutes[2]),
    .Input_5(minutes[1]), .Input_6(minutes[0]), .Output_1(m1[5]), .Output_2(m1[4]), .Output_3(m1[3]),
    .Output_4(m1[2]), .Output_5(m1[1]), .Output_6(m1[0]));
  ones ones_3 (
    .Input_1(1'b0), .Input_2(Hours[4]), .Input_3(Hours[3]), .Input_4(Hours[2]), .Input_5(Hours[1]),
    .Input_6(Hours[0]), .Output_1(h0[5]), .Output_2(h0[4]), .Output_3(h0[3]), .Output_4(h0[2]),
    .Output_5(h0[1]), .Output_6(h0[0]));
  tens tens_3 (
    .Input_1(1'b0), .Input_2(Hours[4]), .Input_3(Hours[3]), .Input_4(Hours[2]), .Input_5(Hours[1]),
    .Input_6(Hours[0]), .Output_1(h1[5]), .Output_2(h1[4]), .Output_3(h1[3]), .Output_4(h1[2]),
    .Output_5(h1[1]), .Output_6(h1[0]));
  Multiplexer #(.width(6), .enable("false")) multiplexer_1 (
    .in0(ones_1_output_6), .in1(6'b011101), .out(s0), .sel(Horloge_1_wrtmode));
  Multiplexer #(.width(6), .enable("false")) multiplexer_2 (
    .in0(tens_1_output_6), .in1(6'b011110), .out(s1), .sel(Horloge_1_wrtmode));

  assign Hours[5] = 1'b0;
endmodule
module counter8bit (
  input  EN,
  input  clk,
  input  rst,
  input  WRITE,
  input  I7,
  input  I6,
  input  I5,
  input  I4,
  input  I3,
  input  I2,
  input  I1,
  input  I0,
  output OVRF,
  output O7,
  output O6,
  output O5,
  output O4,
  output O3,
  output O2,
  output O1,
  output O0
);

  wire and_1_out, and_2_out, and_3_out, and_4_out, and_5_out, and_6_out, and_7_out, and_8_out, and_9_out,
       and_10_out, and_11_out, and_12_out, and_13_out, and_14_out, and_15_out, and_16_out, and_17_out,
       and_18_out, and_19_out, and_20_out, and_21_out, and_22_out, and_24_out, not_1_out, not_2_out,
       not_3_out, not_4_out, not_5_out, not_6_out, not_7_out, not_8_out, or_1_out, or_2_out, or_3_out,
       or_4_out, or_5_out, or_6_out, or_7_out, or_8_out;

  T_Flip_Flop t_ff_1 (.T(EN), .clk(clk), .Q(O0), .reset(or_1_out), .preset(and_2_out));  // open: Qn
  and and_1 (and_1_out, EN, O0);
  or or_1 (or_1_out, rst, and_3_out);
  and and_2 (and_2_out, WRITE, I0);
  and and_3 (and_3_out, WRITE, not_1_out);
  not not_1 (not_1_out, I0);
  T_Flip_Flop t_ff_2 (.T(and_1_out), .clk(clk), .Q(O1), .reset(or_2_out), .preset(and_4_out));  // open: Qn
  or or_2 (or_2_out, rst, and_5_out);
  and and_4 (and_4_out, WRITE, I1);
  and and_5 (and_5_out, WRITE, not_2_out);
  not not_2 (not_2_out, I1);
  and and_6 (and_6_out, and_1_out, O1);
  T_Flip_Flop t_ff_3 (.T(and_6_out), .clk(clk), .Q(O2), .reset(or_3_out), .preset(and_9_out));  // open: Qn
  or or_3 (or_3_out, rst, and_7_out);
  and and_7 (and_7_out, WRITE, not_3_out);
  not not_3 (not_3_out, I2);
  and and_8 (and_8_out, and_6_out, O2);
  T_Flip_Flop t_ff_4 (.T(and_8_out), .clk(clk), .Q(O3), .reset(or_4_out), .preset(and_12_out));  // open: Qn
  or or_4 (or_4_out, rst, and_10_out);
  and and_9 (and_9_out, WRITE, I2);
  and and_10 (and_10_out, WRITE, not_4_out);
  and and_11 (and_11_out, and_8_out, O3);
  T_Flip_Flop t_ff_5 (.T(and_11_out), .clk(clk), .Q(O4), .reset(or_5_out), .preset(and_15_out));  // open: Qn
  and and_12 (and_12_out, WRITE, I3);
  not not_4 (not_4_out, I3);
  and and_13 (and_13_out, and_11_out, O4);
  or or_5 (or_5_out, rst, and_14_out);
  and and_14 (and_14_out, WRITE, not_5_out);
  and and_15 (and_15_out, WRITE, I4);
  not not_5 (not_5_out, I4);
  T_Flip_Flop t_ff_6 (.T(and_13_out), .clk(clk), .Q(O5), .reset(or_6_out), .preset(and_16_out));  // open: Qn
  or or_6 (or_6_out, rst, and_17_out);
  and and_16 (and_16_out, WRITE, I5);
  and and_17 (and_17_out, WRITE, not_6_out);
  not not_6 (not_6_out, I5);
  and and_18 (and_18_out, and_13_out, O5);
  T_Flip_Flop t_ff_7 (.T(and_18_out), .clk(clk), .Q(O6), .reset(or_7_out), .preset(and_21_out));  // open: Qn
  or or_7 (or_7_out, rst, and_19_out);
  and and_19 (and_19_out, WRITE, not_7_out);
  not not_7 (not_7_out, I6);
  and and_20 (and_20_out, and_18_out, O6);
  T_Flip_Flop t_ff_8 (.T(and_20_out), .clk(clk), .Q(O7), .reset(or_8_out), .preset(and_24_out));  // open: Qn
  or or_8 (or_8_out, rst, and_22_out);
  and and_21 (and_21_out, WRITE, I6);
  and and_22 (and_22_out, WRITE, not_8_out);
  and and_23 (OVRF, and_20_out, O7);
  and and_24 (and_24_out, WRITE, I7);
  not not_8 (not_8_out, I7);
endmodule

module decodeur_SEPT_segm (
  input  i0,
  input  i1,
  input  i2,
  input  i3,
  input  i4,
  input  i5,
  output a,
  output b,
  output c,
  output d,
  output e,
  output f,
  output g,
  output p
);

  wire and_1_out, and_2_out, and_3_out, and_4_out, and_5_out, and_6_out, and_7_out, and_8_out, and_9_out,
       and_10_out, and_11_out, and_12_out, and_13_out, and_14_out, and_15_out, and_16_out, and_17_out,
       and_18_out, and_19_out, and_20_out, and_21_out, and_22_out, and_23_out, and_24_out, and_25_out,
       and_26_out, and_27_out, and_28_out, and_29_out, and_30_out, and_31_out, and_32_out, and_33_out,
       and_34_out, and_35_out, and_36_out, and_37_out, and_38_out, and_39_out, and_40_out, and_41_out,
       and_42_out, and_43_out, and_44_out, and_45_out, and_46_out, and_47_out, and_48_out, and_49_out,
       and_50_out, and_51_out, and_52_out, and_53_out, and_54_out, and_55_out, and_56_out, and_57_out,
       and_58_out, and_59_out, and_60_out, and_61_out, and_62_out, and_63_out, and_64_out, and_65_out,
       and_66_out, and_67_out, and_68_out, and_69_out, and_70_out, and_71_out, and_72_out, and_73_out,
       and_74_out, and_75_out, and_76_out, and_77_out, and_78_out, and_79_out, and_80_out, and_81_out,
       and_82_out, and_83_out, and_84_out, not_1_out, not_2_out, not_3_out, not_4_out, not_5_out, not_6_out,
       not_7_out, not_8_out, not_9_out, not_10_out, not_11_out, not_12_out, not_13_out, not_14_out,
       not_15_out, not_16_out, not_17_out, not_18_out, not_19_out, not_20_out, not_21_out, not_22_out,
       not_23_out, not_24_out, not_25_out, not_26_out, not_27_out, not_28_out, not_29_out, not_30_out,
       not_31_out, not_32_out, not_33_out, not_34_out, not_35_out, not_36_out, not_37_out, not_38_out,
       not_39_out, not_40_out, not_41_out, not_42_out, not_43_out, not_44_out, not_45_out, not_46_out,
       not_47_out, not_48_out, not_49_out, not_50_out, not_51_out, not_52_out, not_53_out, not_54_out,
       not_55_out, not_56_out, not_57_out, not_58_out, not_59_out, not_60_out, not_61_out, not_62_out,
       not_63_out, not_64_out, not_65_out, not_66_out, not_67_out, not_68_out, not_69_out, not_70_out,
       not_71_out, not_72_out, not_73_out, not_74_out, not_75_out, not_76_out, not_77_out, not_78_out,
       not_79_out, not_80_out, not_81_out, not_82_out, not_83_out, not_84_out, not_85_out, not_86_out,
       not_87_out, not_88_out, not_89_out, not_90_out, not_91_out, not_92_out, not_93_out, not_94_out,
       not_95_out, not_96_out, not_97_out, not_98_out, not_99_out, not_100_out, not_101_out, not_102_out,
       not_103_out, not_104_out, not_105_out, not_106_out, not_107_out, not_108_out, not_109_out,
       not_110_out, not_111_out, not_112_out, not_113_out, not_114_out, not_115_out, not_116_out,
       not_117_out, not_118_out, not_119_out, not_120_out, not_121_out, not_122_out, not_123_out,
       not_124_out, not_125_out, not_126_out, not_127_out, not_128_out, not_129_out, not_130_out,
       not_131_out, not_132_out, not_133_out, not_134_out, not_135_out, not_136_out, not_137_out,
       not_138_out, not_139_out, not_140_out, not_141_out, not_142_out, not_143_out, not_144_out,
       not_145_out, not_146_out, not_147_out, not_148_out, not_149_out, not_150_out, not_151_out,
       not_152_out, not_153_out, not_154_out, not_155_out, not_156_out, not_157_out, not_158_out,
       not_159_out, not_160_out, not_161_out, not_162_out, not_163_out, not_164_out, not_165_out,
       not_166_out, not_167_out, not_168_out, not_169_out, not_170_out, not_171_out, not_172_out,
       not_173_out, not_174_out, not_175_out, not_176_out, not_177_out, not_178_out, not_179_out,
       not_180_out, not_181_out, not_182_out, not_183_out, not_184_out, not_185_out, not_186_out,
       not_187_out, not_188_out, not_189_out, not_190_out, not_191_out, not_192_out, not_193_out,
       not_194_out, not_195_out, not_196_out, not_197_out, not_198_out, not_199_out, not_200_out,
       not_201_out, not_202_out, not_203_out, not_204_out, not_205_out, not_206_out, not_207_out,
       not_208_out, not_209_out, not_210_out, not_211_out, not_212_out, not_213_out, not_214_out, not_215_out;

  not not_1 (not_1_out, i0);
  not not_2 (not_2_out, i1);
  not not_3 (not_3_out, i3);
  not not_4 (not_4_out, i4);
  not not_5 (not_5_out, i5);
  not not_6 (not_6_out, i0);
  not not_7 (not_7_out, i1);
  not not_8 (not_8_out, i2);
  not not_9 (not_9_out, i0);
  not not_10 (not_10_out, i2);
  not not_11 (not_11_out, i0);
  not not_12 (not_12_out, i4);
  not not_13 (not_13_out, i0);
  not not_14 (not_14_out, i1);
  not not_15 (not_15_out, i1);
  not not_16 (not_16_out, i4);
  not not_17 (not_17_out, i0);
  not not_18 (not_18_out, i2);
  not not_19 (not_19_out, i3);
  not not_20 (not_20_out, i4);
  not not_21 (not_21_out, i3);
  not not_22 (not_22_out, i1);
  not not_23 (not_23_out, i3);
  not not_24 (not_24_out, i5);
  not not_25 (not_25_out, i4);
  not not_26 (not_26_out, i3);
  not not_27 (not_27_out, i4);
  not not_28 (not_28_out, i5);
  not not_29 (not_29_out, i0);
  not not_30 (not_30_out, i1);
  not not_31 (not_31_out, i2);
  not not_32 (not_32_out, i3);
  not not_33 (not_33_out, i1);
  not not_34 (not_34_out, i3);
  not not_35 (not_35_out, i4);
  not not_36 (not_36_out, i1);
  not not_37 (not_37_out, i2);
  not not_38 (not_38_out, i3);
  not not_39 (not_39_out, i0);
  not not_40 (not_40_out, i2);
  not not_41 (not_41_out, i4);
  not not_42 (not_42_out, i5);
  not not_43 (not_43_out, i0);
  not not_44 (not_44_out, i2);
  not not_45 (not_45_out, i0);
  not not_46 (not_46_out, i3);
  not not_47 (not_47_out, i0);
  not not_48 (not_48_out, i1);
  not not_49 (not_49_out, i5);
  not not_50 (not_50_out, i0);
  not not_51 (not_51_out, i3);
  not not_52 (not_52_out, i5);
  not not_53 (not_53_out, i3);
  not not_54 (not_54_out, i4);
  not not_55 (not_55_out, i3);
  not not_56 (not_56_out, i5);
  not not_57 (not_57_out, i0);
  not not_58 (not_58_out, i1);
  not not_59 (not_59_out, i4);
  not not_60 (not_60_out, i5);
  not not_61 (not_61_out, i1);
  not not_62 (not_62_out, i2);
  not not_63 (not_63_out, i3);
  not not_64 (not_64_out, i4);
  not not_65 (not_65_out, i0);
  not not_66 (not_66_out, i1);
  not not_67 (not_67_out, i2);
  not not_68 (not_68_out, i0);
  not not_69 (not_69_out, i2);
  not not_70 (not_70_out, i4);
  not not_71 (not_71_out, i0);
  not not_72 (not_72_out, i1);
  not not_73 (not_73_out, i2);
  not not_74 (not_74_out, i0);
  not not_75 (not_75_out, i2);
  not not_76 (not_76_out, i4);
  not not_77 (not_77_out, i0);
  not not_78 (not_78_out, i3);
  not not_79 (not_79_out, i4);
  not not_80 (not_80_out, i3);
  not not_81 (not_81_out, i1);
  not not_82 (not_82_out, i5);
  not not_83 (not_83_out, i2);
  not not_84 (not_84_out, i3);
  not not_85 (not_85_out, i5);
  not not_86 (not_86_out, i0);
  not not_87 (not_87_out, i1);
  not not_88 (not_88_out, i2);
  not not_89 (not_89_out, i3);
  not not_90 (not_90_out, i5);
  not not_91 (not_91_out, i1);
  not not_92 (not_92_out, i2);
  not not_93 (not_93_out, i3);
  not not_94 (not_94_out, i1);
  not not_95 (not_95_out, i2);
  not not_96 (not_96_out, i5);
  not not_97 (not_97_out, i0);
  not not_98 (not_98_out, i1);
  not not_99 (not_99_out, i4);
  not not_100 (not_100_out, i0);
  not not_101 (not_101_out, i1);
  not not_102 (not_102_out, i4);
  not not_103 (not_103_out, i4);
  not not_104 (not_104_out, i0);
  not not_105 (not_105_out, i0);
  not not_106 (not_106_out, i3);
  not not_107 (not_107_out, i4);
  not not_108 (not_108_out, i0);
  not not_109 (not_109_out, i2);
  not not_110 (not_110_out, i5);
  not not_111 (not_111_out, i1);
  not not_112 (not_112_out, i2);
  not not_113 (not_113_out, i3);
  not not_114 (not_114_out, i1);
  not not_115 (not_115_out, i2);
  not not_116 (not_116_out, i5);
  not not_117 (not_117_out, i2);
  not not_118 (not_118_out, i3);
  not not_119 (not_119_out, i0);
  not not_120 (not_120_out, i2);
  not not_121 (not_121_out, i3);
  not not_122 (not_122_out, i5);
  not not_123 (not_123_out, i0);
  not not_124 (not_124_out, i3);
  not not_125 (not_125_out, i4);
  not not_126 (not_126_out, i5);
  not not_127 (not_127_out, i0);
  not not_128 (not_128_out, i2);
  not not_129 (not_129_out, i5);
  not not_130 (not_130_out, i0);
  not not_131 (not_131_out, i1);
  not not_132 (not_132_out, i0);
  not not_133 (not_133_out, i1);
  not not_134 (not_134_out, i0);
  not not_135 (not_135_out, i2);
  not not_136 (not_136_out, i0);
  not not_137 (not_137_out, i3);
  not not_138 (not_138_out, i4);
  not not_139 (not_139_out, i0);
  not not_140 (not_140_out, i5);
  not not_141 (not_141_out, i4);
  not not_142 (not_142_out, i5);
  not not_143 (not_143_out, i1);
  not not_144 (not_144_out, i2);
  not not_145 (not_145_out, i3);
  not not_146 (not_146_out, i4);
  not not_147 (not_147_out, i0);
  not not_148 (not_148_out, i1);
  not not_149 (not_149_out, i4);
  not not_150 (not_150_out, i5);
  not not_151 (not_151_out, i1);
  not not_152 (not_152_out, i2);
  not not_153 (not_153_out, i3);
  not not_154 (not_154_out, i4);
  not not_155 (not_155_out, i5);
  not not_156 (not_156_out, i0);
  not not_157 (not_157_out, i1);
  not not_158 (not_158_out, i2);
  not not_159 (not_159_out, i5);
  not not_160 (not_160_out, i0);
  not not_161 (not_161_out, i1);
  not not_162 (not_162_out, i4);
  not not_163 (not_163_out, i0);
  not not_164 (not_164_out, i1);
  not not_165 (not_165_out, i0);
  not not_166 (not_166_out, i2);
  not not_167 (not_167_out, i3);
  not not_168 (not_168_out, i0);
  not not_169 (not_169_out, i2);
  not not_170 (not_170_out, i0);
  not not_171 (not_171_out, i3);
  not not_172 (not_172_out, i0);
  not not_173 (not_173_out, i5);
  not not_174 (not_174_out, i4);
  not not_175 (not_175_out, i1);
  not not_176 (not_176_out, i3);
  not not_177 (not_177_out, i5);
  not not_178 (not_178_out, i1);
  not not_179 (not_179_out, i2);
  not not_180 (not_180_out, i3);
  not not_181 (not_181_out, i0);
  not not_182 (not_182_out, i1);
  not not_183 (not_183_out, i2);
  not not_184 (not_184_out, i4);
  not not_185 (not_185_out, i0);
  not not_186 (not_186_out, i1);
  not not_187 (not_187_out, i5);
  not not_188 (not_188_out, i1);
  not not_189 (not_189_out, i2);
  not not_190 (not_190_out, i4);
  not not_191 (not_191_out, i5);
  not not_192 (not_192_out, i0);
  not not_193 (not_193_out, i3);
  not not_194 (not_194_out, i4);
  not not_195 (not_195_out, i0);
  not not_196 (not_196_out, i3);
  not not_197 (not_197_out, i0);
  not not_198 (not_198_out, i5);
  not not_199 (not_199_out, i0);
  not not_200 (not_200_out, i1);
  not not_201 (not_201_out, i0);
  not not_202 (not_202_out, i3);
  not not_203 (not_203_out, i5);
  not not_204 (not_204_out, i0);
  not not_205 (not_205_out, i4);
  not not_206 (not_206_out, i1);
  not not_207 (not_207_out, i3);
  not not_208 (not_208_out, i1);
  not not_209 (not_209_out, i2);
  not not_210 (not_210_out, i5);
  not not_211 (not_211_out, i1);
  not not_212 (not_212_out, i2);
  not not_213 (not_213_out, i4);
  not not_214 (not_214_out, i3);
  not not_215 (not_215_out, i4);
  and and_1 (and_1_out, not_1_out, not_2_out, not_3_out, not_4_out, not_5_out);
  and and_2 (and_2_out, not_6_out, not_7_out, not_8_out, i4);
  and and_3 (and_3_out, not_9_out, not_10_out, i3, i5);
  and and_4 (and_4_out, not_11_out, i3, not_12_out, i5);
  and and_5 (and_5_out, not_13_out, not_14_out, i2, i5);
  and and_6 (and_6_out, not_15_out, i2, not_16_out, i5);
  and and_7 (and_7_out, not_17_out, i1, not_18_out, not_19_out, not_20_out);
  and and_8 (and_8_out, i1, i2, not_21_out, i4);
  and and_9 (and_9_out, i0, not_22_out, not_23_out, i4, not_24_out);
  and and_10 (and_10_out, i0, i2, i3, not_25_out);
  and and_11 (and_11_out, i0, i1, not_26_out, not_27_out, not_28_out);
  and and_12 (and_12_out, not_29_out, not_30_out, not_31_out, not_32_out);
  and and_13 (and_13_out, not_33_out, not_34_out, not_35_out);
  and and_14 (and_14_out, not_36_out, not_37_out, not_38_out, i5);
  and and_15 (and_15_out, not_39_out, not_40_out, i3, not_41_out, not_42_out);
  and and_16 (and_16_out, not_43_out, not_44_out, i3, i4, i5);
  and and_17 (and_17_out, not_45_out, i2, not_46_out, i4, i5);
  and and_18 (and_18_out, not_47_out, not_48_out, i2, i3, i4, not_49_out);
  and and_19 (and_19_out, not_50_out, i1, not_51_out, i4, not_52_out);
  and and_20 (and_20_out, i0, not_53_out, not_54_out, i5);
  and and_21 (and_21_out, i0, i2, not_55_out, not_56_out);
  and and_22 (and_22_out, i0, i2, i3, i4, i5);
  and and_23 (and_23_out, not_57_out, not_58_out, not_59_out, not_60_out);
  and and_24 (and_24_out, not_61_out, not_62_out, not_63_out, not_64_out);
  and and_25 (and_25_out, not_65_out, not_66_out, not_67_out, i5);
  and and_26 (and_26_out, not_68_out, not_69_out, not_70_out, i5);
  and and_27 (and_27_out, not_71_out, not_72_out, not_73_out, i3);
  and and_28 (and_28_out, not_74_out, not_75_out, i3, not_76_out);
  and and_29 (and_29_out, not_77_out, i2, not_78_out, not_79_out);
  and and_30 (and_30_out, i2, not_80_out, i5);
  and and_31 (and_31_out, not_81_out, i2, i3, i4, not_82_out);
  and and_32 (and_32_out, i1, not_83_out, not_84_out, i4, not_85_out);
  and and_33 (and_33_out, not_86_out, i1, i3, i5);
  and and_34 (and_34_out, not_87_out, not_88_out, not_89_out, not_90_out);
  and and_35 (and_35_out, not_91_out, not_92_out, not_93_out, i4);
  and and_36 (and_36_out, not_94_out, not_95_out, i4, not_96_out);
  and and_37 (and_37_out, not_97_out, not_98_out, i3, not_99_out, i5);
  and and_38 (and_38_out, not_100_out, not_101_out, i2, not_102_out);
  and and_39 (and_39_out, i2, i3, not_103_out, i5);
  and and_40 (and_40_out, not_104_out, i2, i3, i4);
  and and_41 (and_41_out, not_105_out, i1, not_106_out, not_107_out, i5);
  and and_42 (and_42_out, not_108_out, i1, not_109_out, i3, not_110_out);
  and and_43 (and_43_out, i0, not_111_out, not_112_out, not_113_out);
  and and_44 (and_44_out, i0, not_114_out, not_115_out, not_116_out);
  and and_45 (and_45_out, i0, not_117_out, not_118_out, i4, i5);
  and and_46 (and_46_out, not_119_out, not_120_out, not_121_out, not_122_out);
  and and_47 (and_47_out, not_123_out, not_124_out, not_125_out, not_126_out);
  and and_48 (and_48_out, not_127_out, not_128_out, i4, not_129_out);
  and and_49 (and_49_out, not_130_out, not_131_out, i2, i4, i5);
  and and_50 (and_50_out, not_132_out, not_133_out, i2, i3);
  and and_51 (and_51_out, i2, i3, i4, i5);
  and and_52 (and_52_out, not_134_out, i1, not_135_out);
  and and_53 (and_53_out, not_136_out, i1, not_137_out, not_138_out);
  and and_54 (and_54_out, not_139_out, i1, not_140_out);
  and and_55 (and_55_out, i1, i3, not_141_out, not_142_out);
  and and_56 (and_56_out, i0, not_143_out, not_144_out, not_145_out, not_146_out, i5);
  and and_57 (and_57_out, not_147_out, not_148_out, not_149_out, not_150_out);
  and and_58 (and_58_out, not_151_out, not_152_out, not_153_out, not_154_out, not_155_out);
  and and_59 (and_59_out, not_156_out, not_157_out, not_158_out, i3, not_159_out);
  and and_60 (and_60_out, not_160_out, not_161_out, i3, not_162_out);
  and and_61 (and_61_out, not_163_out, not_164_out, i2, i5);
  and and_62 (and_62_out, not_165_out, i1, not_166_out, not_167_out);
  and and_63 (and_63_out, not_168_out, i1, not_169_out, i4);
  and and_64 (and_64_out, not_170_out, i1, not_171_out, i4);
  and and_65 (and_65_out, not_172_out, i1, i4, not_173_out);
  and and_66 (and_66_out, i1, i3, not_174_out, i5);
  and and_67 (and_67_out, i0, not_175_out, not_176_out, i5);
  and and_68 (and_68_out, i0, i2, i4, not_177_out);
  and and_69 (and_69_out, not_178_out, not_179_out, not_180_out, i4);
  and and_70 (and_70_out, not_181_out, not_182_out, not_183_out, i3, not_184_out);
  and and_71 (and_71_out, not_185_out, not_186_out, i3, not_187_out);
  and and_72 (and_72_out, not_188_out, not_189_out, i3, not_190_out, not_191_out);
  and and_73 (and_73_out, not_192_out, i2, not_193_out, not_194_out);
  and and_74 (and_74_out, not_195_out, i2, not_196_out, i5);
  and and_75 (and_75_out, not_197_out, i2, i3, not_198_out);
  and and_76 (and_76_out, not_199_out, not_200_out, i2, i3, i4);
  and and_77 (and_77_out, not_201_out, i1, not_202_out, not_203_out);
  and and_78 (and_78_out, not_204_out, i1, i3, not_205_out, i5);
  and and_79 (and_79_out, i0, not_206_out, not_207_out, i4);
  and and_80 (and_80_out, i0, not_208_out, not_209_out, i4, i5);
  and and_81 (and_81_out, i0, i1, i3, i4, not_210_out);
  and and_82 (and_82_out, i0, not_211_out, not_212_out, i3, not_213_out, i5);
  and and_83 (and_83_out, i0, i2, not_214_out, not_215_out);
  and and_84 (and_84_out, i0, i1, i3, i4, i5);
  or or_1 (a, and_1_out, and_2_out, and_3_out, and_4_out, and_5_out, and_6_out, and_7_out, and_8_out, and_9_out, and_10_out, and_11_out);
  or or_2 (b, and_12_out, and_13_out, and_14_out, and_15_out, and_16_out, and_17_out, and_18_out, and_19_out, and_20_out, and_21_out, and_22_out);
  or or_3 (c, and_23_out, and_24_out, and_25_out, and_26_out, and_27_out, and_28_out, and_29_out, and_30_out, and_31_out, and_32_out, and_33_out);
  or or_4 (d, and_34_out, and_35_out, and_36_out, and_37_out, and_38_out, and_39_out, and_40_out, and_41_out, and_42_out, and_43_out, and_44_out, and_45_out);
  or or_5 (e, and_46_out, and_47_out, and_48_out, and_49_out, and_50_out, and_51_out, and_52_out, and_53_out, and_54_out, and_55_out, and_56_out);
  or or_6 (f, and_57_out, and_58_out, and_59_out, and_60_out, and_61_out, and_62_out, and_63_out, and_64_out, and_65_out, and_66_out, and_67_out, and_68_out);
  or or_7 (g, and_69_out, and_70_out, and_71_out, and_72_out, and_73_out, and_74_out, and_75_out, and_76_out, and_77_out, and_78_out, and_79_out, and_80_out, and_81_out);
  or or_8 (p, and_82_out, and_83_out, and_84_out);
endmodule

module chrono (
  input  rst,
  input  clk,
  input  FallA,
  input  fallB,
  output [5:0] h0,
  output [5:0] h1,
  output [5:0] m0,
  output [5:0] m1,
  output [5:0] s0,
  output [5:0] s1
);

  wire and_1_out, and_2_out, and_3_out, and_4_out, and_5_out, and_6_out, and_7_out, and_8_out,
       counter8bit_1_o0, counter8bit_1_o1, counter8bit_1_o2, counter8bit_1_ovrf, d_ff_1_q, d_ff_2_q,
       d_ff_3_q, d_ff_4_q, or_1_out, or_2_out, or_3_out, t_ff_1_q;
  wire [5:0] counter8bit_3_o0, counter8bit_4_o0;
  wire [9:0] counter8bit_1_o3;

  T_Flip_Flop t_ff_1 (.T(FallA), .clk(clk), .Q(t_ff_1_q), .reset(rst));  // open: Qn, preset
  and and_1 (and_1_out, counter8bit_1_o2, counter8bit_1_o1, counter8bit_1_o0);
  counter8bit counter8bit_1 (
    .EN(t_ff_1_q), .clk(clk), .rst(or_1_out), .WRITE(1'b0), .I7(1'b0), .I6(1'b0), .I5(1'b0), .I4(1'b0),
    .I3(1'b0), .I2(1'b0), .I1(1'b0), .I0(1'b0), .OVRF(counter8bit_1_ovrf), .O7(counter8bit_1_o3[4]),
    .O6(counter8bit_1_o3[3]), .O5(counter8bit_1_o3[2]), .O4(counter8bit_1_o3[1]), .O3(counter8bit_1_o3[0]),
    .O2(counter8bit_1_o2), .O1(counter8bit_1_o1), .O0(counter8bit_1_o0));
  or or_1 (or_1_out, and_2_out, rst, fallB);
  and and_2 (and_2_out, counter8bit_1_o3[0], ~counter8bit_1_o3[1], ~counter8bit_1_o3[2], counter8bit_1_o3[3], ~counter8bit_1_o3[4], counter8bit_1_o3[5], counter8bit_1_o3[6], counter8bit_1_o3[7], counter8bit_1_o3[8], counter8bit_1_o3[9]);  // AND_Gate
  D_Flip_Flop d_ff_1 (.D(and_3_out), .clk(clk), .Q(d_ff_1_q));  // open: Qn, preset, reset
  counter8bit counter8bit_2 (
    .EN(counter8bit_1_ovrf), .clk(clk), .rst(or_1_out), .WRITE(1'b0), .I7(1'b0), .I6(1'b0), .I5(1'b0),
    .I4(1'b0), .I3(1'b0), .I2(1'b0), .I1(1'b0), .I0(1'b0), .O4(counter8bit_1_o3[9]),
    .O3(counter8bit_1_o3[8]), .O2(counter8bit_1_o3[7]), .O1(counter8bit_1_o3[6]), .O0(counter8bit_1_o3[5]));  // open: OVRF, O7, O6, O5
  D_Flip_Flop d_ff_2 (.D(d_ff_1_q), .clk(clk), .Q(d_ff_2_q));  // open: Qn, preset, reset
  and and_3 (and_3_out, ~counter8bit_1_o3[0], ~counter8bit_1_o3[1], ~counter8bit_1_o3[2], counter8bit_1_o3[3], ~counter8bit_1_o3[4], counter8bit_1_o3[5], counter8bit_1_o3[6], counter8bit_1_o3[7], counter8bit_1_o3[8], counter8bit_1_o3[9], and_1_out);  // AND_Gate
  and and_4 (and_4_out, d_ff_1_q, ~d_ff_2_q);  // AND_Gate
  ones ones_1 (
    .Input_1(counter8bit_4_o0[5]), .Input_2(counter8bit_4_o0[4]), .Input_3(counter8bit_4_o0[3]),
    .Input_4(counter8bit_4_o0[2]), .Input_5(counter8bit_4_o0[1]), .Input_6(counter8bit_4_o0[0]),
    .Output_1(h0[5]), .Output_2(h0[4]), .Output_3(h0[3]), .Output_4(h0[2]), .Output_5(h0[1]), .Output_6(h0[0]));
  tens tens_1 (
    .Input_1(counter8bit_4_o0[5]), .Input_2(counter8bit_4_o0[4]), .Input_3(counter8bit_4_o0[3]),
    .Input_4(counter8bit_4_o0[2]), .Input_5(counter8bit_4_o0[1]), .Input_6(counter8bit_4_o0[0]),
    .Output_1(h1[5]), .Output_2(h1[4]), .Output_3(h1[3]), .Output_4(h1[2]), .Output_5(h1[1]), .Output_6(h1[0]));
  ones ones_2 (
    .Input_1(counter8bit_3_o0[5]), .Input_2(counter8bit_3_o0[4]), .Input_3(counter8bit_3_o0[3]),
    .Input_4(counter8bit_3_o0[2]), .Input_5(counter8bit_3_o0[1]), .Input_6(counter8bit_3_o0[0]),
    .Output_1(m0[5]), .Output_2(m0[4]), .Output_3(m0[3]), .Output_4(m0[2]), .Output_5(m0[1]), .Output_6(m0[0]));
  tens tens_2 (
    .Input_1(counter8bit_3_o0[5]), .Input_2(counter8bit_3_o0[4]), .Input_3(counter8bit_3_o0[3]),
    .Input_4(counter8bit_3_o0[2]), .Input_5(counter8bit_3_o0[1]), .Input_6(counter8bit_3_o0[0]),
    .Output_1(m1[5]), .Output_2(m1[4]), .Output_3(m1[3]), .Output_4(m1[2]), .Output_5(m1[1]), .Output_6(m1[0]));
  tens tens_3 (
    .Input_1(counter8bit_1_o3[5]), .Input_2(counter8bit_1_o3[4]), .Input_3(counter8bit_1_o3[3]),
    .Input_4(counter8bit_1_o3[2]), .Input_5(counter8bit_1_o3[1]), .Input_6(counter8bit_1_o3[0]),
    .Output_1(s0[5]), .Output_2(s0[4]), .Output_3(s0[3]), .Output_4(s0[2]), .Output_5(s0[1]), .Output_6(s0[0]));
  hundreds hundreds_1 (
    .a9(counter8bit_1_o3[9]), .a8(counter8bit_1_o3[8]), .a7(counter8bit_1_o3[7]), .a6(counter8bit_1_o3[6]),
    .a5(counter8bit_1_o3[5]), .a4(counter8bit_1_o3[4]), .a3(counter8bit_1_o3[3]), .a2(counter8bit_1_o3[2]),
    .a1(counter8bit_1_o3[1]), .a0(counter8bit_1_o3[0]), .o3(s1[3]), .o2(s1[2]), .o1(s1[1]), .o0(s1[0]));
  and and_5 (and_5_out, counter8bit_3_o0[5], counter8bit_3_o0[4], counter8bit_3_o0[3], counter8bit_3_o0[2], ~counter8bit_3_o0[1], ~counter8bit_3_o0[0]);  // AND_Gate
  D_Flip_Flop d_ff_3 (.D(and_6_out), .clk(clk), .Q(d_ff_3_q));  // open: Qn, preset, reset
  or or_2 (or_2_out, and_5_out, rst, fallB);
  and and_6 (and_6_out, counter8bit_3_o0[0], counter8bit_3_o0[1], ~counter8bit_3_o0[2], and_3_out, counter8bit_3_o0[3], counter8bit_3_o0[4], counter8bit_3_o0[5]);  // AND_Gate
  D_Flip_Flop d_ff_4 (.D(d_ff_3_q), .clk(clk), .Q(d_ff_4_q));  // open: Qn, preset, reset
  counter8bit counter8bit_3 (
    .EN(and_4_out), .clk(clk), .rst(or_2_out), .WRITE(1'b0), .I7(1'b0), .I6(1'b0), .I5(1'b0), .I4(1'b0),
    .I3(1'b0), .I2(1'b0), .I1(1'b0), .I0(1'b0), .O5(counter8bit_3_o0[5]), .O4(counter8bit_3_o0[4]),
    .O3(counter8bit_3_o0[3]), .O2(counter8bit_3_o0[2]), .O1(counter8bit_3_o0[1]), .O0(counter8bit_3_o0[0]));  // open: OVRF, O7, O6
  and and_7 (and_7_out, d_ff_3_q, ~d_ff_4_q);  // AND_Gate
  and and_8 (and_8_out, counter8bit_4_o0[5], counter8bit_4_o0[4], counter8bit_4_o0[3], counter8bit_4_o0[2], ~counter8bit_4_o0[1], ~counter8bit_4_o0[0]);  // AND_Gate
  or or_3 (or_3_out, and_8_out, rst, fallB);
  counter8bit counter8bit_4 (
    .EN(and_7_out), .clk(clk), .rst(or_3_out), .WRITE(1'b0), .I7(1'b0), .I6(1'b0), .I5(1'b0), .I4(1'b0),
    .I3(1'b0), .I2(1'b0), .I1(1'b0), .I0(1'b0), .O5(counter8bit_4_o0[5]), .O4(counter8bit_4_o0[4]),
    .O3(counter8bit_4_o0[3]), .O2(counter8bit_4_o0[2]), .O1(counter8bit_4_o0[1]), .O0(counter8bit_4_o0[0]));  // open: OVRF, O7, O6

  assign s1[5:4] = 2'b00;
endmodule

module hundreds (
  input  a9,
  input  a8,
  input  a7,
  input  a6,
  input  a5,
  input  a4,
  input  a3,
  input  a2,
  input  a1,
  input  a0,
  output o3,
  output o2,
  output o1,
  output o0
);

  wire and_1_out, and_2_out, and_3_out, and_4_out, and_5_out, and_6_out, and_7_out, and_8_out, and_9_out,
       and_10_out, and_11_out, and_12_out, and_13_out, and_14_out, and_15_out, and_16_out, and_17_out,
       and_18_out, and_19_out, and_20_out, and_21_out, and_22_out, and_23_out, and_24_out, and_25_out,
       and_26_out, and_27_out, and_28_out, and_29_out, and_30_out, and_31_out, and_32_out, and_33_out,
       and_34_out, and_35_out, and_36_out, and_37_out, and_38_out, not_1_out, not_2_out, not_3_out,
       not_4_out, not_5_out, not_6_out, not_7_out, not_8_out, not_9_out, not_10_out, not_11_out, not_12_out,
       not_13_out, not_14_out, not_15_out, not_16_out, not_17_out, not_18_out, not_19_out, not_20_out,
       not_21_out, not_22_out, not_23_out, not_24_out, not_25_out, not_26_out, not_27_out, not_28_out,
       not_29_out, not_30_out, not_31_out, not_32_out, not_33_out, not_34_out, not_35_out, not_36_out,
       not_37_out, not_38_out, not_39_out, not_40_out, not_41_out, not_42_out, not_43_out, not_44_out,
       not_45_out, not_46_out, not_47_out, not_48_out, not_49_out, not_50_out, not_51_out, not_52_out,
       not_53_out, not_54_out, not_55_out, not_56_out, not_57_out, not_58_out, not_59_out, not_60_out,
       not_61_out, not_62_out, not_63_out, not_64_out;

  and and_1 (and_1_out, a9, a8, a5);
  and and_2 (and_2_out, a9, a8, a6);
  and and_3 (and_3_out, a9, a8, a7);
  not not_1 (not_1_out, a9);
  not not_2 (not_2_out, a9);
  not not_3 (not_3_out, a9);
  not not_4 (not_4_out, a8);
  not not_5 (not_5_out, a7);
  not not_6 (not_6_out, a6);
  not not_7 (not_7_out, a5);
  not not_8 (not_8_out, a8);
  not not_9 (not_9_out, a8);
  not not_10 (not_10_out, a8);
  not not_11 (not_11_out, a9);
  not not_12 (not_12_out, a7);
  not not_13 (not_13_out, a9);
  not not_14 (not_14_out, a6);
  not not_15 (not_15_out, a5);
  not not_16 (not_16_out, a4);
  not not_17 (not_17_out, a7);
  not not_18 (not_18_out, a6);
  not not_19 (not_19_out, a5);
  not not_20 (not_20_out, a8);
  not not_21 (not_21_out, a8);
  not not_22 (not_22_out, a8);
  not not_23 (not_23_out, a9);
  not not_24 (not_24_out, a7);
  not not_25 (not_25_out, a9);
  not not_26 (not_26_out, a7);
  not not_27 (not_27_out, a9);
  not not_28 (not_28_out, a7);
  not not_29 (not_29_out, a9);
  not not_30 (not_30_out, a8);
  not not_31 (not_31_out, a6);
  not not_32 (not_32_out, a9);
  not not_33 (not_33_out, a8);
  not not_34 (not_34_out, a5);
  not not_35 (not_35_out, a4);
  not not_36 (not_36_out, a3);
  not not_37 (not_37_out, a9);
  not not_38 (not_38_out, a6);
  not not_39 (not_39_out, a5);
  not not_40 (not_40_out, a4);
  not not_41 (not_41_out, a9);
  not not_42 (not_42_out, a7);
  not not_43 (not_43_out, a9);
  not not_44 (not_44_out, a7);
  not not_45 (not_45_out, a9);
  not not_46 (not_46_out, a7);
  not not_47 (not_47_out, a9);
  not not_48 (not_48_out, a9);
  not not_49 (not_49_out, a8);
  not not_50 (not_50_out, a7);
  not not_51 (not_51_out, a6);
  not not_52 (not_52_out, a8);
  not not_53 (not_53_out, a7);
  not not_54 (not_54_out, a5);
  not not_55 (not_55_out, a4);
  not not_56 (not_56_out, a8);
  not not_57 (not_57_out, a7);
  not not_58 (not_58_out, a5);
  not not_59 (not_59_out, a3);
  not not_60 (not_60_out, a7);
  not not_61 (not_61_out, a6);
  not not_62 (not_62_out, a5);
  not not_63 (not_63_out, a6);
  not not_64 (not_64_out, a5);
  or or_1 (o3, and_1_out, and_2_out, and_3_out);
  and and_4 (and_4_out, not_1_out, a8, a7, a4);
  and and_5 (and_5_out, not_2_out, a8, a7, a5);
  and and_6 (and_6_out, not_3_out, a8, a7, a6);
  and and_7 (and_7_out, a9, not_4_out);
  and and_8 (and_8_out, a9, not_5_out, not_6_out, not_7_out);
  and and_9 (and_9_out, not_8_out, a7, a6, a3);
  and and_10 (and_10_out, not_9_out, a7, a6, a4);
  and and_11 (and_11_out, not_10_out, a7, a6, a5);
  and and_12 (and_12_out, not_11_out, a8, not_12_out);
  and and_13 (and_13_out, not_13_out, a8, not_14_out, not_15_out, not_16_out);
  and and_14 (and_14_out, a8, not_17_out, not_18_out, not_19_out);
  and and_15 (and_15_out, a9, not_20_out, a6, a4, a3);
  and and_16 (and_16_out, a9, not_21_out, a6, a5);
  and and_17 (and_17_out, a9, not_22_out, a7);
  and and_18 (and_18_out, not_23_out, not_24_out, a6, a5, a2);
  and and_19 (and_19_out, not_25_out, not_26_out, a6, a5, a3);
  and and_20 (and_20_out, not_27_out, not_28_out, a6, a5, a4);
  and and_21 (and_21_out, not_29_out, not_30_out, a7, not_31_out);
  and and_22 (and_22_out, not_32_out, not_33_out, a7, not_34_out, not_35_out, not_36_out);
  and and_23 (and_23_out, not_37_out, a7, not_38_out, not_39_out, not_40_out);
  and and_24 (and_24_out, not_41_out, a8, not_42_out, a5, a3, a2);
  and and_25 (and_25_out, not_43_out, a8, not_44_out, a5, a4);
  and and_26 (and_26_out, not_45_out, a8, not_46_out, a6);
  and and_27 (and_27_out, not_47_out, a8, a6, a5, a4, a2);
  and and_28 (and_28_out, not_48_out, a8, a6, a5, a4, a3);
  and and_29 (and_29_out, a9, not_49_out, not_50_out, not_51_out);
  and and_30 (and_30_out, a9, not_52_out, not_53_out, not_54_out, not_55_out);
  and and_31 (and_31_out, a9, not_56_out, not_57_out, not_58_out, not_59_out);
  and and_32 (and_32_out, a9, not_60_out, not_61_out, not_62_out);
  and and_33 (and_33_out, a9, a7, a5, a4, a3, a2);
  and and_34 (and_34_out, a9, a7, a6);
  and and_35 (and_35_out, a9, a8, not_63_out, not_64_out, a4);
  and and_36 (and_36_out, a9, a8, a7, a2);
  and and_37 (and_37_out, a9, a8, a7, a3);
  and and_38 (and_38_out, a9, a8, a7, a5);
  or or_2 (o2, and_4_out, and_5_out, and_6_out, and_7_out, and_8_out);
  or or_3 (o1, and_9_out, and_10_out, and_11_out, and_12_out, and_13_out, and_14_out, and_15_out, and_16_out, and_17_out);
  or or_4 (o0, and_18_out, and_19_out, and_20_out, and_21_out, and_22_out, and_23_out, and_24_out, and_25_out, and_26_out, and_27_out, and_28_out, and_29_out, and_30_out, and_31_out, and_32_out, and_33_out, and_34_out, and_35_out, and_36_out, and_37_out, and_38_out);
endmodule

module primary (
  input  TlongB,
  input  clk,
  input  rst,
  output [2:0] choice
);

  wire primFSM_1_d0, primFSM_1_d1, primFSM_1_d2;

  primFSM primFSM_1 (
    .en(TlongB), .q2(choice[2]), .q1(choice[1]), .q0(choice[0]), .d2(primFSM_1_d2), .d1(primFSM_1_d1),
    .d0(primFSM_1_d0));
  D_Flip_Flop d_ff_1 (.D(primFSM_1_d0), .clk(clk), .Q(choice[0]), .preset(1'b0), .reset(rst));  // open: Qn
  D_Flip_Flop d_ff_2 (.D(primFSM_1_d1), .clk(clk), .Q(choice[1]), .preset(1'b0), .reset(rst));  // open: Qn
  D_Flip_Flop d_ff_3 (.D(primFSM_1_d2), .clk(clk), .Q(choice[2]), .preset(1'b0), .reset(rst));  // open: Qn
endmodule

module primFSM (
  input  en,
  input  q2,
  input  q1,
  input  q0,
  output d2,
  output d1,
  output d0
);

  wire and_1_out, and_2_out, and_3_out, and_4_out, and_5_out, and_6_out, and_7_out, and_8_out, not_1_out,
       not_2_out, not_3_out, not_4_out, not_5_out, not_6_out, not_7_out;

  not not_1 (not_1_out, en);
  not not_2 (not_2_out, en);
  not not_3 (not_3_out, q0);
  not not_4 (not_4_out, q1);
  not not_5 (not_5_out, en);
  not not_6 (not_6_out, q2);
  not not_7 (not_7_out, q0);
  and and_1 (and_1_out, not_1_out, q2);
  and and_2 (and_2_out, q2, q0);
  and and_3 (and_3_out, en, q1, q0);
  and and_4 (and_4_out, not_2_out, q1);
  and and_5 (and_5_out, q1, not_3_out);
  and and_6 (and_6_out, en, not_4_out, q0);
  and and_7 (and_7_out, not_5_out, q0);
  and and_8 (and_8_out, en, not_6_out, not_7_out);
  or or_1 (d2, and_1_out, and_2_out, and_3_out);
  or or_2 (d1, and_4_out, and_5_out, and_6_out);
  or or_3 (d0, and_7_out, and_8_out);
endmodule

module mod60 (
  input  EN,
  input  dir,
  input  CLK,
  input  mrst,
  output [5:0] count,
  output ovrf,
  output undf,
  output zero
);

  wire d_ff_7_q, d_ff_8_q, d_ff_9_q, d_ff_10_q, updown60_1_d0, updown60_1_d1, updown60_1_d2, updown60_1_d3,
       updown60_1_d4, updown60_1_d5, updown60_1_ovrf, updown60_1_undf;

  updown60 updown60_1 (
    .EN(EN), .DIR(dir), .Q5(count[5]), .Q4(count[4]), .Q3(count[3]), .Q2(count[2]), .Q1(count[1]),
    .Q0(count[0]), .D5(updown60_1_d5), .D4(updown60_1_d4), .D3(updown60_1_d3), .D2(updown60_1_d2),
    .D1(updown60_1_d1), .D0(updown60_1_d0), .OVRF(updown60_1_ovrf), .UNDF(updown60_1_undf));
  D_Flip_Flop d_ff_1 (.D(updown60_1_d0), .clk(CLK), .Q(count[0]), .preset(mrst));  // open: Qn, reset
  D_Flip_Flop d_ff_2 (.D(updown60_1_d1), .clk(CLK), .Q(count[1]), .reset(mrst));  // open: Qn, preset
  D_Flip_Flop d_ff_3 (.D(updown60_1_d2), .clk(CLK), .Q(count[2]), .reset(mrst));  // open: Qn, preset
  D_Flip_Flop d_ff_4 (.D(updown60_1_d3), .clk(CLK), .Q(count[3]), .reset(mrst));  // open: Qn, preset
  D_Flip_Flop d_ff_5 (.D(updown60_1_d4), .clk(CLK), .Q(count[4]), .reset(mrst));  // open: Qn, preset
  D_Flip_Flop d_ff_6 (.D(updown60_1_d5), .clk(CLK), .Q(count[5]), .reset(mrst));  // open: Qn, preset
  D_Flip_Flop d_ff_7 (.D(updown60_1_ovrf), .clk(CLK), .Q(d_ff_7_q), .reset(mrst));  // open: Qn, preset
  D_Flip_Flop d_ff_8 (.D(updown60_1_undf), .clk(CLK), .Q(d_ff_8_q), .reset(mrst));  // open: Qn, preset
  and and_1 (zero, ~count[0], ~count[1], ~count[2], ~count[3], ~count[4], ~count[5]);  // AND_Gate
  D_Flip_Flop d_ff_9 (.D(d_ff_7_q), .clk(CLK), .Q(d_ff_9_q), .reset(mrst));  // open: Qn, preset
  D_Flip_Flop d_ff_10 (.D(d_ff_8_q), .clk(CLK), .Q(d_ff_10_q), .reset(mrst));  // open: Qn, preset
  and and_2 (ovrf, d_ff_7_q, ~d_ff_9_q);  // AND_Gate
  and and_3 (undf, d_ff_8_q, ~d_ff_10_q);  // AND_Gate
endmodule

module cndt (
  input  rst,
  input  clk,
  input  change,
  input  choice,
  input  inc,
  output [5:0] s0,
  output [5:0] s1,
  output [5:0] m0,
  output [5:0] m1,
  output [5:0] h0,
  output [5:0] h1,
  output zero,
  output buzzReady
);

  wire and_1_out, and_2_out, and_3_out, and_4_out, and_5_out, and_6_out, and_7_out, and_8_out, and_9_out,
       and_10_out, and_11_out, and_12_out, and_13_out, and_14_out, and_15_out, and_16_out, and_17_out,
       and_18_out, and_19_out, clock_1_out, counter8bit_1_o0, counter8bit_1_o1, counter8bit_1_o2,
       counter8bit_1_o3, counter8bit_1_o4, counter8bit_1_o5, counter8bit_1_o6, counter8bit_1_o7,
       counter8bit_1_ovrf, counter8bit_2_o0, counter8bit_2_o1, counter8bit_2_o2, counter8bit_2_o3,
       counter8bit_2_o4, d_ff_1_q, d_ff_2_q, d_ff_3_q, d_ff_4_q, mod24_1_zero, mod60_1_zero, mod60_2_zero,
       or_1_out, or_3_out, or_4_out, or_5_out, shift3_1_output_1, shift3_1_output_2, shift3_1_output_3,
       t_ff_1_q, t_ff_2_q, t_ff_2_qn;
  wire [4:0] mod24_1_hour;
  wire [5:0] mod60_1_count, mod60_2_count;

  T_Flip_Flop t_ff_1 (.T(and_1_out), .clk(clock_1_out), .Q(t_ff_1_q), .reset(rst));  // open: Qn, preset
  and and_1 (and_1_out, ~t_ff_2_q, inc);  // AND_Gate
  Clock clock_1 (.out(clock_1_out));
  T_Flip_Flop t_ff_2 (.T(change), .clk(clock_1_out), .Q(t_ff_2_q), .Qn(t_ff_2_qn), .preset(rst));  // open: reset
  and and_2 (and_2_out, t_ff_2_q, choice);
  and and_3 (and_3_out, t_ff_2_q, inc);
  and and_4 (and_4_out, ~t_ff_2_q, ~zero, t_ff_1_q);  // AND_Gate
  or or_1 (or_1_out, t_ff_2_q, and_15_out);
  shift3 shift3_1 (
    .EN(and_2_out), .rst(rst), .clk(clock_1_out), .Output_1(shift3_1_output_1), .Output_2(shift3_1_output_2),
    .Output_3(shift3_1_output_3));
  and and_5 (and_5_out, counter8bit_1_o2, counter8bit_1_o1, counter8bit_1_o0);
  and and_6 (and_6_out, and_3_out, shift3_1_output_1);
  and and_7 (and_7_out, and_3_out, shift3_1_output_2);
  and and_8 (and_8_out, and_3_out, shift3_1_output_3);
  counter8bit counter8bit_1 (
    .EN(and_4_out), .clk(clock_1_out), .rst(or_1_out), .WRITE(1'b0), .I7(1'b0), .I6(1'b0), .I5(1'b0),
    .I4(1'b0), .I3(1'b0), .I2(1'b0), .I1(1'b0), .I0(1'b0), .OVRF(counter8bit_1_ovrf), .O7(counter8bit_1_o7),
    .O6(counter8bit_1_o6), .O5(counter8bit_1_o5), .O4(counter8bit_1_o4), .O3(counter8bit_1_o3),
    .O2(counter8bit_1_o2), .O1(counter8bit_1_o1), .O0(counter8bit_1_o0));
  and and_9 (and_9_out, ~t_ff_2_q, and_18_out);  // AND_Gate
  and and_10 (and_10_out, and_6_out, t_ff_2_q);
  and and_11 (and_11_out, ~t_ff_2_q, and_16_out);  // AND_Gate
  and and_12 (and_12_out, and_7_out, t_ff_2_q);
  and and_13 (and_13_out, ~t_ff_2_q, and_17_out);  // AND_Gate
  and and_14 (and_14_out, and_8_out, t_ff_2_q);
  D_Flip_Flop d_ff_1 (.D(and_19_out), .clk(clock_1_out), .Q(d_ff_1_q), .reset(rst));  // open: Qn, preset
  or or_2 (zero, and_19_out, d_ff_1_q, d_ff_2_q, d_ff_3_q, d_ff_4_q);
  counter8bit counter8bit_2 (
    .EN(counter8bit_1_ovrf), .clk(clock_1_out), .rst(or_1_out), .WRITE(1'b0), .I7(1'b0), .I6(1'b0),
    .I5(1'b0), .I4(1'b0), .I3(1'b0), .I2(1'b0), .I1(1'b0), .I0(1'b0), .O4(counter8bit_2_o4),
    .O3(counter8bit_2_o3), .O2(counter8bit_2_o2), .O1(counter8bit_2_o1), .O0(counter8bit_2_o0));  // open: OVRF, O7, O6, O5
  and and_15 (and_15_out, counter8bit_1_o3, ~counter8bit_1_o4, ~counter8bit_1_o5, counter8bit_1_o6, ~counter8bit_1_o7, counter8bit_2_o0, counter8bit_2_o1, counter8bit_2_o2, counter8bit_2_o3, counter8bit_2_o4);  // AND_Gate
  or or_3 (or_3_out, and_9_out, and_10_out);
  and and_16 (and_16_out, and_18_out, mod60_1_zero);
  or or_4 (or_4_out, and_11_out, and_12_out);
  and and_17 (and_17_out, mod60_2_zero, and_16_out);
  or or_5 (or_5_out, and_13_out, and_14_out);
  D_Flip_Flop d_ff_2 (.D(d_ff_1_q), .clk(clock_1_out), .Q(d_ff_2_q), .reset(rst));  // open: Qn, preset
  and and_18 (and_18_out, ~counter8bit_1_o3, ~counter8bit_1_o4, ~counter8bit_1_o5, counter8bit_1_o6, ~counter8bit_1_o7, counter8bit_2_o0, counter8bit_2_o1, counter8bit_2_o2, counter8bit_2_o3, counter8bit_2_o4, and_5_out);  // AND_Gate
  D_Flip_Flop d_ff_3 (.D(d_ff_2_q), .clk(clock_1_out), .Q(d_ff_3_q), .reset(rst));  // open: Qn, preset
  mod60 mod60_1 (
    .EN(or_3_out), .dir(t_ff_2_qn), .CLK(clock_1_out), .mrst(rst), .count(mod60_1_count), .zero(mod60_1_zero));  // open: ovrf, undf
  mod60 mod60_2 (
    .EN(or_4_out), .dir(t_ff_2_qn), .CLK(clock_1_out), .mrst(rst), .count(mod60_2_count), .zero(mod60_2_zero));  // open: ovrf, undf
  mod24 mod24_1 (
    .en(or_5_out), .dir(t_ff_2_qn), .clk(clock_1_out), .rst(rst), .hour(mod24_1_hour), .zero(mod24_1_zero));  // open: ovrf, undf
  D_Flip_Flop d_ff_4 (.D(d_ff_3_q), .clk(clock_1_out), .Q(d_ff_4_q), .reset(rst));  // open: Qn, preset
  and and_19 (and_19_out, mod24_1_zero, mod60_2_zero, mod60_1_zero);
  ones ones_1 (
    .Input_1(mod60_1_count[5]), .Input_2(mod60_1_count[4]), .Input_3(mod60_1_count[3]),
    .Input_4(mod60_1_count[2]), .Input_5(mod60_1_count[1]), .Input_6(mod60_1_count[0]), .Output_1(s0[5]),
    .Output_2(s0[4]), .Output_3(s0[3]), .Output_4(s0[2]), .Output_5(s0[1]), .Output_6(s0[0]));
  tens tens_1 (
    .Input_1(mod60_1_count[5]), .Input_2(mod60_1_count[4]), .Input_3(mod60_1_count[3]),
    .Input_4(mod60_1_count[2]), .Input_5(mod60_1_count[1]), .Input_6(mod60_1_count[0]), .Output_1(s1[5]),
    .Output_2(s1[4]), .Output_3(s1[3]), .Output_4(s1[2]), .Output_5(s1[1]), .Output_6(s1[0]));
  ones ones_2 (
    .Input_1(mod60_2_count[5]), .Input_2(mod60_2_count[4]), .Input_3(mod60_2_count[3]),
    .Input_4(mod60_2_count[2]), .Input_5(mod60_2_count[1]), .Input_6(mod60_2_count[0]), .Output_1(m0[5]),
    .Output_2(m0[4]), .Output_3(m0[3]), .Output_4(m0[2]), .Output_5(m0[1]), .Output_6(m0[0]));
  tens tens_2 (
    .Input_1(mod60_2_count[5]), .Input_2(mod60_2_count[4]), .Input_3(mod60_2_count[3]),
    .Input_4(mod60_2_count[2]), .Input_5(mod60_2_count[1]), .Input_6(mod60_2_count[0]), .Output_1(m1[5]),
    .Output_2(m1[4]), .Output_3(m1[3]), .Output_4(m1[2]), .Output_5(m1[1]), .Output_6(m1[0]));
  ones ones_3 (
    .Input_1(1'b0), .Input_2(mod24_1_hour[4]), .Input_3(mod24_1_hour[3]), .Input_4(mod24_1_hour[2]),
    .Input_5(mod24_1_hour[1]), .Input_6(mod24_1_hour[0]), .Output_1(h0[5]), .Output_2(h0[4]),
    .Output_3(h0[3]), .Output_4(h0[2]), .Output_5(h0[1]), .Output_6(h0[0]));
  tens tens_3 (
    .Input_1(1'b0), .Input_2(mod24_1_hour[4]), .Input_3(mod24_1_hour[3]), .Input_4(mod24_1_hour[2]),
    .Input_5(mod24_1_hour[1]), .Input_6(mod24_1_hour[0]), .Output_1(h1[5]), .Output_2(h1[4]),
    .Output_3(h1[3]), .Output_4(h1[2]), .Output_5(h1[1]), .Output_6(h1[0]));
  and and_20 (buzzReady, ~t_ff_2_q, t_ff_1_q);  // AND_Gate
endmodule

module updown60 (
  input  EN,
  input  DIR,
  input  Q5,
  input  Q4,
  input  Q3,
  input  Q2,
  input  Q1,
  input  Q0,
  output D5,
  output D4,
  output D3,
  output D2,
  output D1,
  output D0,
  output OVRF,
  output UNDF
);

  wire and_1_out, and_2_out, and_3_out, and_4_out, and_5_out, and_6_out, and_7_out, and_8_out, and_9_out,
       and_10_out, and_11_out, and_12_out, and_13_out, and_14_out, and_15_out, and_16_out, and_17_out,
       and_18_out, and_19_out, and_20_out, and_21_out, and_22_out, and_23_out, and_24_out, and_25_out,
       and_26_out, and_27_out, and_28_out, and_29_out, and_30_out, and_31_out, and_32_out, and_33_out,
       and_34_out, and_35_out, and_36_out, and_37_out, and_38_out, and_39_out, and_40_out, and_41_out,
       and_42_out, and_43_out, and_44_out, and_45_out, and_46_out, and_47_out, and_48_out, and_49_out,
       and_50_out, and_51_out, and_52_out, not_1_out, not_2_out, not_3_out, not_4_out, not_5_out, not_6_out,
       not_7_out, not_8_out, not_9_out, not_10_out, not_11_out, not_12_out, not_13_out, not_14_out,
       not_15_out, not_16_out, not_17_out, not_18_out, not_19_out, not_20_out, not_21_out, not_22_out,
       not_23_out, not_24_out, not_25_out, not_26_out, not_27_out, not_28_out, not_29_out, not_30_out,
       not_31_out, not_32_out, not_33_out, not_34_out, not_35_out, not_36_out, not_37_out, not_38_out,
       not_39_out, not_40_out, not_41_out, not_42_out, not_43_out, not_44_out, not_45_out, not_46_out,
       not_47_out, not_48_out, not_49_out, not_50_out, not_51_out, not_52_out, not_53_out, not_54_out,
       not_55_out, not_56_out, not_57_out, not_58_out, not_59_out, not_60_out, not_61_out, not_62_out,
       not_63_out, not_64_out, not_65_out, not_66_out, not_67_out, not_68_out, not_69_out, not_70_out,
       not_71_out, not_72_out, not_73_out, not_74_out, not_75_out, not_76_out, not_77_out, not_78_out,
       not_79_out, not_80_out, not_81_out, not_82_out, not_83_out, not_84_out, not_85_out, not_86_out,
       not_87_out, not_88_out, not_89_out, not_90_out, not_91_out, not_92_out, not_93_out, not_94_out,
       not_95_out;

  not not_1 (not_1_out, DIR);
  not not_2 (not_2_out, Q5);
  not not_3 (not_3_out, Q4);
  not not_4 (not_4_out, Q3);
  not not_5 (not_5_out, Q2);
  not not_6 (not_6_out, Q1);
  not not_7 (not_7_out, Q0);
  not not_8 (not_8_out, EN);
  not not_9 (not_9_out, DIR);
  not not_10 (not_10_out, Q3);
  not not_11 (not_11_out, Q3);
  not not_12 (not_12_out, Q3);
  not not_13 (not_13_out, Q3);
  not not_14 (not_14_out, Q5);
  not not_15 (not_15_out, Q2);
  not not_16 (not_16_out, Q1);
  not not_17 (not_17_out, Q0);
  not not_18 (not_18_out, DIR);
  not not_19 (not_19_out, Q4);
  not not_20 (not_20_out, Q4);
  not not_21 (not_21_out, Q3);
  not not_22 (not_22_out, Q2);
  not not_23 (not_23_out, Q1);
  not not_24 (not_24_out, Q0);
  not not_25 (not_25_out, EN);
  not not_26 (not_26_out, DIR);
  not not_27 (not_27_out, Q5);
  not not_28 (not_28_out, Q2);
  not not_29 (not_29_out, DIR);
  not not_30 (not_30_out, Q4);
  not not_31 (not_31_out, Q2);
  not not_32 (not_32_out, DIR);
  not not_33 (not_33_out, Q1);
  not not_34 (not_34_out, Q5);
  not not_35 (not_35_out, Q2);
  not not_36 (not_36_out, Q4);
  not not_37 (not_37_out, Q2);
  not not_38 (not_38_out, Q5);
  not not_39 (not_39_out, Q2);
  not not_40 (not_40_out, Q4);
  not not_41 (not_41_out, Q2);
  not not_42 (not_42_out, Q0);
  not not_43 (not_43_out, Q1);
  not not_44 (not_44_out, DIR);
  not not_45 (not_45_out, Q3);
  not not_46 (not_46_out, Q3);
  not not_47 (not_47_out, Q2);
  not not_48 (not_48_out, Q1);
  not not_49 (not_49_out, Q0);
  not not_50 (not_50_out, EN);
  not not_51 (not_51_out, DIR);
  not not_52 (not_52_out, Q1);
  not not_53 (not_53_out, Q0);
  not not_54 (not_54_out, DIR);
  not not_55 (not_55_out, Q5);
  not not_56 (not_56_out, Q2);
  not not_57 (not_57_out, DIR);
  not not_58 (not_58_out, Q4);
  not not_59 (not_59_out, Q2);
  not not_60 (not_60_out, DIR);
  not not_61 (not_61_out, Q3);
  not not_62 (not_62_out, Q2);
  not not_63 (not_63_out, Q2);
  not not_64 (not_64_out, Q1);
  not not_65 (not_65_out, Q0);
  not not_66 (not_66_out, Q2);
  not not_67 (not_67_out, Q1);
  not not_68 (not_68_out, Q0);
  not not_69 (not_69_out, Q2);
  not not_70 (not_70_out, Q1);
  not not_71 (not_71_out, Q0);
  not not_72 (not_72_out, EN);
  not not_73 (not_73_out, DIR);
  not not_74 (not_74_out, Q0);
  not not_75 (not_75_out, DIR);
  not not_76 (not_76_out, Q1);
  not not_77 (not_77_out, Q1);
  not not_78 (not_78_out, Q0);
  not not_79 (not_79_out, EN);
  not not_80 (not_80_out, Q0);
  not not_81 (not_81_out, DIR);
  not not_82 (not_82_out, Q5);
  not not_83 (not_83_out, Q4);
  not not_84 (not_84_out, Q3);
  not not_85 (not_85_out, Q2);
  not not_86 (not_86_out, Q1);
  not not_87 (not_87_out, EN);
  and and_1 (and_1_out, not_87_out, Q5);
  not not_88 (not_88_out, DIR);
  and and_2 (and_2_out, not_88_out, Q5, not_89_out);
  not not_89 (not_89_out, Q4);
  not not_90 (not_90_out, DIR);
  and and_3 (and_3_out, not_90_out, Q5, not_91_out);
  not not_91 (not_91_out, Q0);
  not not_92 (not_92_out, Q4);
  and and_4 (and_4_out, Q5, not_92_out, Q0);
  and and_5 (and_5_out, Q5, Q2);
  not not_93 (not_93_out, Q4);
  and and_6 (and_6_out, Q5, not_93_out, Q3);
  and and_7 (and_7_out, Q5, Q3, not_94_out);
  not not_94 (not_94_out, Q1);
  and and_8 (and_8_out, Q5, Q4, not_95_out);
  not not_95 (not_95_out, Q3);
  and and_9 (and_9_out, DIR, Q5, Q1);
  and and_10 (and_10_out, EN, not_1_out, Q4, Q3, Q2, Q1, Q0);
  and and_11 (and_11_out, EN, DIR, not_2_out, not_3_out, not_4_out, not_5_out, not_6_out, not_7_out);
  and and_12 (and_12_out, not_8_out, Q4);
  and and_13 (and_13_out, not_9_out, Q4, not_10_out);
  and and_14 (and_14_out, Q4, not_11_out, Q0);
  and and_15 (and_15_out, Q4, not_12_out, Q1);
  and and_16 (and_16_out, Q4, not_13_out, Q2);
  and and_17 (and_17_out, not_14_out, Q4, Q3, not_15_out);
  and and_18 (and_18_out, Q4, Q3, not_16_out);
  and and_19 (and_19_out, Q4, Q3, not_17_out);
  and and_20 (and_20_out, DIR, Q4, Q3);
  and and_21 (and_21_out, EN, not_18_out, not_19_out, Q3, Q2, Q1, Q0);
  and and_22 (and_22_out, EN, DIR, not_20_out, not_21_out, not_22_out, not_23_out, not_24_out);
  and and_23 (and_23_out, not_25_out, Q3);
  and and_24 (and_24_out, not_26_out, not_27_out, Q3, not_28_out);
  and and_25 (and_25_out, not_29_out, not_30_out, Q3, not_31_out);
  and and_26 (and_26_out, not_32_out, Q3, not_33_out);
  and and_27 (and_27_out, not_34_out, Q3, not_35_out, Q0);
  and and_28 (and_28_out, not_36_out, Q3, not_37_out, Q0);
  and and_29 (and_29_out, not_38_out, Q3, not_39_out, Q1);
  and and_30 (and_30_out, not_40_out, Q3, not_41_out, Q1);
  and and_31 (and_31_out, Q3, Q1, not_42_out);
  and and_32 (and_32_out, Q3, Q2, not_43_out);
  and and_33 (and_33_out, DIR, Q3, Q0);
  and and_34 (and_34_out, EN, not_44_out, not_45_out, Q2, Q1, Q0);
  and and_35 (and_35_out, EN, DIR, not_46_out, not_47_out, not_48_out, not_49_out);
  and and_36 (and_36_out, not_50_out, Q2);
  and and_37 (and_37_out, not_51_out, Q2, not_52_out);
  and and_38 (and_38_out, Q2, Q1, not_53_out);
  and and_39 (and_39_out, DIR, Q2, Q0);
  and and_40 (and_40_out, EN, not_54_out, not_55_out, not_56_out, Q1, Q0);
  and and_41 (and_41_out, EN, not_57_out, not_58_out, not_59_out, Q1, Q0);
  and and_42 (and_42_out, EN, not_60_out, not_61_out, not_62_out, Q1, Q0);
  and and_43 (and_43_out, EN, DIR, Q3, not_63_out, not_64_out, not_65_out);
  and and_44 (and_44_out, EN, DIR, Q4, not_66_out, not_67_out, not_68_out);
  and and_45 (and_45_out, EN, DIR, Q5, not_69_out, not_70_out, not_71_out);
  and and_46 (and_46_out, not_72_out, Q1);
  and and_47 (and_47_out, not_73_out, Q1, not_74_out);
  and and_48 (and_48_out, DIR, Q1, Q0);
  and and_49 (and_49_out, EN, not_75_out, not_76_out, Q0);
  and and_50 (and_50_out, EN, DIR, not_77_out, not_78_out);
  and and_51 (and_51_out, not_79_out, Q0);
  and and_52 (and_52_out, EN, not_80_out);
  and and_53 (OVRF, EN, not_81_out, Q5, Q4, Q3, Q1, Q0);
  and and_54 (UNDF, EN, DIR, not_82_out, not_83_out, not_84_out, not_85_out, not_86_out, Q0);
  or or_1 (D1, and_46_out, and_47_out, and_48_out, and_49_out, and_50_out);
  or or_2 (D0, and_51_out, and_52_out);
  or or_3 (D5, and_1_out, and_2_out, and_3_out, and_4_out, and_5_out, and_6_out, and_7_out, and_8_out, and_9_out, and_10_out, and_11_out);
  or or_4 (D4, and_12_out, and_13_out, and_14_out, and_15_out, and_16_out, and_17_out, and_18_out, and_19_out, and_20_out, and_21_out, and_22_out);
  or or_5 (D3, and_23_out, and_24_out, and_25_out, and_26_out, and_27_out, and_28_out, and_29_out, and_30_out, and_31_out, and_32_out, and_33_out, and_34_out, and_35_out);
  or or_6 (D2, and_36_out, and_37_out, and_38_out, and_39_out, and_40_out, and_41_out, and_42_out, and_43_out, and_44_out, and_45_out);
endmodule

module shift3 (
  input  EN,
  input  rst,
  input  clk,
  output Output_1,
  output Output_2,
  output Output_3
);

  wire and_1_out, and_2_out, and_3_out, and_4_out, d_ff_1_q, d_ff_2_q, not_1_out, not_2_out, not_3_out,
       not_4_out, or_1_out, or_2_out;

  not not_1 (not_1_out, EN);
  not not_2 (not_2_out, EN);
  not not_3 (not_3_out, d_ff_2_q);
  not not_4 (not_4_out, d_ff_1_q);
  and and_1 (and_1_out, not_1_out, d_ff_2_q);
  and and_2 (and_2_out, EN, d_ff_1_q);
  and and_3 (and_3_out, not_2_out, d_ff_1_q);
  and and_4 (and_4_out, EN, not_3_out, not_4_out);
  or or_1 (or_1_out, and_1_out, and_2_out);
  or or_2 (or_2_out, and_3_out, and_4_out);
  D_Flip_Flop d_ff_1 (.D(or_2_out), .clk(clk), .Q(d_ff_1_q), .reset(rst));  // open: Qn, preset
  D_Flip_Flop d_ff_2 (.D(or_1_out), .clk(clk), .Q(d_ff_2_q));  // open: Qn, preset, reset
  and and_5 (Output_1, ~d_ff_1_q, ~d_ff_2_q);  // AND_Gate
  and and_6 (Output_2, d_ff_1_q, ~d_ff_2_q);  // AND_Gate
  and and_7 (Output_3, ~d_ff_1_q, d_ff_2_q);  // AND_Gate
endmodule

module mod24 (
  input  en,
  input  dir,
  input  clk,
  input  rst,
  output [4:0] hour,
  output ovrf,
  output undf,
  output zero
);

  wire base24_1_d0, base24_1_d1, base24_1_d2, base24_1_d3, base24_1_d4, base24_1_ovrf, base24_1_undf,
       d_ff_6_q, d_ff_7_q, d_ff_8_q, d_ff_9_q;

  and and_1 (zero, ~hour[0], ~hour[1], ~hour[2], ~hour[3], ~hour[4]);  // AND_Gate
  base24 base24_1 (
    .EN(en), .DIR(dir), .Q4(hour[4]), .Q3(hour[3]), .Q2(hour[2]), .Q1(hour[1]), .Q0(hour[0]),
    .D4(base24_1_d4), .D3(base24_1_d3), .D2(base24_1_d2), .D1(base24_1_d1), .D0(base24_1_d0),
    .OVRF(base24_1_ovrf), .UNDF(base24_1_undf));
  D_Flip_Flop d_ff_1 (.D(base24_1_d0), .clk(clk), .Q(hour[0]), .reset(rst));  // open: Qn, preset
  D_Flip_Flop d_ff_2 (.D(base24_1_d1), .clk(clk), .Q(hour[1]), .reset(rst));  // open: Qn, preset
  D_Flip_Flop d_ff_3 (.D(base24_1_d2), .clk(clk), .Q(hour[2]), .reset(rst));  // open: Qn, preset
  D_Flip_Flop d_ff_4 (.D(base24_1_d3), .clk(clk), .Q(hour[3]), .reset(rst));  // open: Qn, preset
  D_Flip_Flop d_ff_5 (.D(base24_1_d4), .clk(clk), .Q(hour[4]), .reset(rst));  // open: Qn, preset
  D_Flip_Flop d_ff_6 (.D(base24_1_ovrf), .clk(clk), .Q(d_ff_6_q), .reset(rst));  // open: Qn, preset
  D_Flip_Flop d_ff_7 (.D(base24_1_undf), .clk(clk), .Q(d_ff_7_q), .reset(rst));  // open: Qn, preset
  D_Flip_Flop d_ff_8 (.D(d_ff_6_q), .clk(clk), .Q(d_ff_8_q), .reset(rst));  // open: Qn, preset
  D_Flip_Flop d_ff_9 (.D(d_ff_7_q), .clk(clk), .Q(d_ff_9_q), .reset(rst));  // open: Qn, preset
  and and_2 (ovrf, d_ff_6_q, ~d_ff_8_q);  // AND_Gate
  and and_3 (undf, d_ff_7_q, ~d_ff_9_q);  // AND_Gate
endmodule

module base24 (
  input  EN,
  input  DIR,
  input  Q4,
  input  Q3,
  input  Q2,
  input  Q1,
  input  Q0,
  output D4,
  output D3,
  output D2,
  output D1,
  output D0,
  output OVRF,
  output UNDF
);

  wire and_1_out, and_2_out, and_3_out, and_4_out, and_5_out, and_6_out, and_7_out, and_8_out, and_9_out,
       and_10_out, and_11_out, and_12_out, and_13_out, and_14_out, and_15_out, and_16_out, and_17_out,
       and_18_out, and_19_out, and_20_out, and_21_out, and_22_out, and_23_out, and_24_out, and_25_out,
       and_26_out, and_27_out, and_28_out, and_29_out, not_1_out, not_2_out, not_3_out, not_4_out, not_5_out,
       not_6_out, not_7_out, not_8_out, not_9_out, not_10_out, not_11_out, not_12_out, not_13_out,
       not_14_out, not_15_out, not_16_out, not_17_out, not_18_out, not_19_out, not_20_out, not_21_out,
       not_22_out, not_23_out, not_24_out, not_25_out, not_26_out, not_27_out, not_28_out, not_29_out,
       not_30_out, not_31_out, not_32_out, not_33_out, not_34_out, not_35_out, not_36_out, not_37_out,
       not_38_out, not_39_out, not_40_out, not_41_out, not_42_out, not_43_out, not_44_out, not_45_out,
       not_46_out, not_47_out, not_48_out, not_49_out, not_50_out;

  not not_1 (not_1_out, EN);
  not not_2 (not_2_out, DIR);
  not not_3 (not_3_out, Q2);
  not not_4 (not_4_out, DIR);
  not not_5 (not_5_out, Q0);
  not not_6 (not_6_out, Q2);
  not not_7 (not_7_out, Q1);
  not not_8 (not_8_out, DIR);
  not not_9 (not_9_out, Q4);
  not not_10 (not_10_out, Q3);
  not not_11 (not_11_out, Q2);
  not not_12 (not_12_out, Q1);
  not not_13 (not_13_out, Q0);
  not not_14 (not_14_out, EN);
  not not_15 (not_15_out, DIR);
  not not_16 (not_16_out, Q2);
  not not_17 (not_17_out, DIR);
  not not_18 (not_18_out, Q0);
  not not_19 (not_19_out, Q2);
  not not_20 (not_20_out, Q1);
  not not_21 (not_21_out, DIR);
  not not_22 (not_22_out, Q4);
  not not_23 (not_23_out, Q3);
  not not_24 (not_24_out, Q2);
  not not_25 (not_25_out, Q1);
  not not_26 (not_26_out, Q0);
  not not_27 (not_27_out, EN);
  not not_28 (not_28_out, DIR);
  not not_29 (not_29_out, Q1);
  not not_30 (not_30_out, Q0);
  not not_31 (not_31_out, DIR);
  not not_32 (not_32_out, Q2);
  not not_33 (not_33_out, Q2);
  not not_34 (not_34_out, Q1);
  not not_35 (not_35_out, Q0);
  not not_36 (not_36_out, EN);
  not not_37 (not_37_out, DIR);
  not not_38 (not_38_out, Q0);
  not not_39 (not_39_out, DIR);
  not not_40 (not_40_out, Q1);
  not not_41 (not_41_out, Q1);
  not not_42 (not_42_out, Q0);
  not not_43 (not_43_out, EN);
  not not_44 (not_44_out, Q0);
  not not_45 (not_45_out, DIR);
  not not_46 (not_46_out, Q4);
  not not_47 (not_47_out, Q3);
  not not_48 (not_48_out, Q2);
  not not_49 (not_49_out, Q1);
  not not_50 (not_50_out, Q0);
  and and_1 (and_1_out, not_1_out, Q4);
  and and_2 (and_2_out, not_2_out, Q4, not_3_out);
  and and_3 (and_3_out, not_4_out, Q4, not_5_out);
  and and_4 (and_4_out, Q4, not_6_out, Q0);
  and and_5 (and_5_out, Q4, Q2, not_7_out);
  and and_6 (and_6_out, DIR, Q4, Q1);
  and and_7 (and_7_out, EN, not_8_out, Q3, Q2, Q1, Q0);
  and and_8 (and_8_out, EN, DIR, not_9_out, not_10_out, not_11_out, not_12_out, not_13_out);
  and and_9 (and_9_out, not_14_out, Q3);
  and and_10 (and_10_out, not_15_out, Q3, not_16_out);
  and and_11 (and_11_out, not_17_out, Q3, not_18_out);
  and and_12 (and_12_out, Q3, not_19_out, Q0);
  and and_13 (and_13_out, Q3, Q2, not_20_out);
  and and_14 (and_14_out, DIR, Q3, Q1);
  and and_15 (and_15_out, EN, not_21_out, not_22_out, not_23_out, Q2, Q1, Q0);
  and and_16 (and_16_out, EN, DIR, Q4, not_24_out, not_25_out, not_26_out);
  and and_17 (and_17_out, not_27_out, Q2);
  and and_18 (and_18_out, not_28_out, Q2, not_29_out);
  and and_19 (and_19_out, Q2, Q1, not_30_out);
  and and_20 (and_20_out, DIR, Q2, Q0);
  and and_21 (and_21_out, EN, not_31_out, not_32_out, Q1, Q0);
  and and_22 (and_22_out, EN, DIR, not_33_out, not_34_out, not_35_out);
  and and_23 (and_23_out, not_36_out, Q1);
  and and_24 (and_24_out, not_37_out, Q1, not_38_out);
  and and_25 (and_25_out, DIR, Q1, Q0);
  and and_26 (and_26_out, EN, not_39_out, not_40_out, Q0);
  and and_27 (and_27_out, EN, DIR, not_41_out, not_42_out);
  and and_28 (and_28_out, not_43_out, Q0);
  and and_29 (and_29_out, EN, not_44_out);
  and and_30 (OVRF, EN, not_45_out, Q4, Q2, Q1, Q0);
  and and_31 (UNDF, EN, DIR, not_46_out, not_47_out, not_48_out, not_49_out, not_50_out);
  or or_1 (D4, and_1_out, and_2_out, and_3_out, and_4_out, and_5_out, and_6_out, and_7_out, and_8_out);
  or or_2 (D3, and_9_out, and_10_out, and_11_out, and_12_out, and_13_out, and_14_out, and_15_out, and_16_out);
  or or_3 (D2, and_17_out, and_18_out, and_19_out, and_20_out, and_21_out, and_22_out);
  or or_4 (D1, and_23_out, and_24_out, and_25_out, and_26_out, and_27_out);
  or or_5 (D0, and_28_out, and_29_out);
endmodule

module nav (
  input  [2:0] pos,
  input  longB,
  input  [5:0] h1,
  input  [5:0] h0,
  input  [5:0] m1,
  input  [5:0] m0,
  input  [5:0] s1,
  input  [5:0] s0,
  output [5:0] hour1,
  output [5:0] hour0,
  output [5:0] min1,
  output [5:0] min0,
  output [5:0] sec1,
  output [5:0] sec0
);

  wire not_1_out;
  wire [5:0] multiplexer_1_out, multiplexer_2_out, multiplexer_3_out, multiplexer_4_out, multiplexer_5_out,
       multiplexer_6_out;

  not not_1 (not_1_out, longB);
  Multiplexer #(.select(3), .width(6), .enable("false")) multiplexer_1 (
    .in0(6'b011110), .in1(6'b001011), .in2(6'b011110), .in3(6'b001101), .in4(6'b001101), .in5(6'b001010),
    .in6(6'b001010), .in7(6'b001010), .out(multiplexer_1_out), .sel(pos));
  Multiplexer #(.select(3), .width(6), .enable("false")) multiplexer_2 (
    .in0(6'b010011), .in1(6'b010110), .in2(6'b100111), .in3(6'b010010), .in4(6'b011000), .in5(6'b001010),
    .in6(6'b001010), .in7(6'b001010), .out(multiplexer_2_out), .sel(pos));
  Multiplexer #(.select(3), .width(6), .enable("false")) multiplexer_3 (
    .in0(6'b010111), .in1(6'b001011), .in2(6'b100100), .in3(6'b011100), .in4(6'b011110), .in5(6'b001010),
    .in6(6'b001010), .in7(6'b001010), .out(multiplexer_3_out), .sel(pos));
  Multiplexer #(.select(3), .width(6), .enable("false")) multiplexer_4 (
    .in0(6'b001111), .in1(6'b011100), .in2(6'b011001), .in3(6'b011001), .in4(6'b001110), .in5(6'b001010),
    .in6(6'b001010), .in7(6'b001010), .out(multiplexer_4_out), .sel(pos));
  Multiplexer #(.select(3), .width(6), .enable("false")) multiplexer_5 (
    .in0(6'b001010), .in1(6'b010111), .in2(6'b011000), .in3(6'b011000), .in4(6'b001010), .in5(6'b001010),
    .in6(6'b001010), .in7(6'b001010), .out(multiplexer_5_out), .sel(pos));
  Multiplexer #(.select(3), .width(6), .enable("false")) multiplexer_6 (
    .in0(6'b001010), .in1(6'b001010), .in2(6'b001111), .in3(6'b011001), .in4(6'b001010), .in5(6'b001010),
    .in6(6'b001010), .in7(6'b001010), .out(multiplexer_6_out), .sel(pos));
  Multiplexer #(.width(6), .enable("false")) multiplexer_7 (
    .in0(multiplexer_1_out), .in1(h1), .out(hour1), .sel(not_1_out));
  Multiplexer #(.width(6), .enable("false")) multiplexer_8 (
    .in0(multiplexer_2_out), .in1(h0), .out(hour0), .sel(not_1_out));
  Multiplexer #(.width(6), .enable("false")) multiplexer_9 (
    .in0(multiplexer_3_out), .in1(m1), .out(min1), .sel(not_1_out));
  Multiplexer #(.width(6), .enable("false")) multiplexer_10 (
    .in0(multiplexer_4_out), .in1(m0), .out(min0), .sel(not_1_out));
  Multiplexer #(.width(6), .enable("false")) multiplexer_11 (
    .in0(multiplexer_5_out), .in1(s1), .out(sec1), .sel(not_1_out));
  Multiplexer #(.width(6), .enable("false")) multiplexer_12 (
    .in0(multiplexer_6_out), .in1(s0), .out(sec0), .sel(not_1_out));
endmodule

module generator (
  input  EN,
  input  clk,
  input  rst,
  input  E4,
  input  F4,
  input  G4,
  input  A4,
  input  B4,
  input  C5,
  input  D5,
  input  E5,
  output sig
);

  wire and_1_out, and_2_out, and_3_out, and_4_out, and_5_out, and_6_out, and_7_out, and_8_out, and_9_out,
       and_10_out, and_11_out, and_12_out, and_13_out, and_14_out, and_15_out, and_16_out, and_17_out,
       and_18_out, and_19_out, and_20_out, and_21_out, or_1_out, or_2_out, t_ff_1_q, t_ff_2_q, t_ff_3_q,
       t_ff_4_q, t_ff_5_q, t_ff_6_q, t_ff_7_q, t_ff_9_q, t_ff_10_q, t_ff_11_q, t_ff_12_q, t_ff_13_q,
       t_ff_14_q;

  or or_1 (or_1_out, rst, or_2_out);
  and and_1 (and_1_out, EN, t_ff_1_q);
  T_Flip_Flop t_ff_1 (.T(EN), .clk(clk), .Q(t_ff_1_q), .reset(or_1_out), .preset(1'b0));  // open: Qn
  and and_2 (and_2_out, ~t_ff_12_q, ~t_ff_11_q, ~t_ff_10_q, ~t_ff_9_q, ~t_ff_7_q, ~t_ff_6_q, ~t_ff_5_q, ~t_ff_4_q, ~t_ff_3_q, ~t_ff_2_q, ~t_ff_1_q);  // AND_Gate
  and and_3 (and_3_out, and_1_out, t_ff_2_q);
  T_Flip_Flop t_ff_2 (.T(and_1_out), .clk(clk), .Q(t_ff_2_q), .reset(or_1_out), .preset(1'b0));  // open: Qn
  and and_4 (and_4_out, and_3_out, t_ff_3_q);
  T_Flip_Flop t_ff_3 (.T(and_3_out), .clk(clk), .Q(t_ff_3_q), .reset(or_1_out), .preset(1'b0));  // open: Qn
  and and_5 (and_5_out, and_4_out, t_ff_4_q);
  T_Flip_Flop t_ff_4 (.T(and_4_out), .clk(clk), .Q(t_ff_4_q), .reset(or_1_out), .preset(1'b0));  // open: Qn
  and and_6 (and_6_out, t_ff_6_q, t_ff_5_q, ~t_ff_4_q, ~t_ff_3_q, ~t_ff_2_q, ~t_ff_1_q, E4);  // AND_Gate
  and and_7 (and_7_out, t_ff_6_q, ~t_ff_5_q, t_ff_4_q, t_ff_3_q, t_ff_2_q, ~t_ff_1_q, F4);  // AND_Gate
  and and_8 (and_8_out, t_ff_6_q, ~t_ff_5_q, t_ff_4_q, ~t_ff_3_q, ~t_ff_2_q, t_ff_1_q, G4);  // AND_Gate
  and and_9 (and_9_out, t_ff_6_q, ~t_ff_5_q, ~t_ff_4_q, t_ff_3_q, ~t_ff_2_q, ~t_ff_1_q, A4);  // AND_Gate
  and and_10 (and_10_out, t_ff_6_q, ~t_ff_5_q, ~t_ff_4_q, ~t_ff_3_q, ~t_ff_2_q, ~t_ff_1_q, B4);  // AND_Gate
  and and_11 (and_11_out, ~t_ff_6_q, t_ff_5_q, t_ff_4_q, t_ff_3_q, t_ff_2_q, t_ff_1_q, C5);  // AND_Gate
  and and_12 (and_12_out, ~t_ff_6_q, t_ff_5_q, t_ff_4_q, t_ff_3_q, ~t_ff_2_q, ~t_ff_1_q, D5);  // AND_Gate
  and and_13 (and_13_out, ~t_ff_6_q, t_ff_5_q, t_ff_4_q, ~t_ff_3_q, ~t_ff_2_q, ~t_ff_1_q, E5);  // AND_Gate
  and and_14 (and_14_out, and_5_out, t_ff_5_q);
  T_Flip_Flop t_ff_5 (.T(and_5_out), .clk(clk), .Q(t_ff_5_q), .reset(or_1_out), .preset(1'b0));  // open: Qn
  or or_2 (or_2_out, and_6_out, and_7_out, and_8_out, and_9_out, and_10_out, and_11_out, and_12_out, and_13_out);
  and and_15 (and_15_out, and_14_out, t_ff_6_q);
  T_Flip_Flop t_ff_6 (.T(and_14_out), .clk(clk), .Q(t_ff_6_q), .reset(or_1_out), .preset(1'b0));  // open: Qn
  and and_16 (and_16_out, and_15_out, t_ff_7_q);
  T_Flip_Flop t_ff_7 (.T(and_15_out), .clk(clk), .Q(t_ff_7_q), .reset(or_1_out), .preset(1'b0));  // open: Qn
  T_Flip_Flop t_ff_8 (.T(and_2_out), .clk(clk), .Q(sig));  // open: Qn, reset, preset
  and and_17 (and_17_out, and_16_out, t_ff_9_q);
  T_Flip_Flop t_ff_9 (.T(and_16_out), .clk(clk), .Q(t_ff_9_q), .reset(or_1_out), .preset(1'b0));  // open: Qn
  and and_18 (and_18_out, and_17_out, t_ff_10_q);
  T_Flip_Flop t_ff_10 (.T(and_17_out), .clk(clk), .Q(t_ff_10_q), .reset(or_1_out), .preset(1'b0));  // open: Qn
  and and_19 (and_19_out, and_18_out, t_ff_11_q);
  T_Flip_Flop t_ff_11 (.T(and_18_out), .clk(clk), .Q(t_ff_11_q), .reset(or_1_out), .preset(1'b0));  // open: Qn
  and and_20 (and_20_out, and_19_out, t_ff_12_q);
  T_Flip_Flop t_ff_12 (.T(and_19_out), .clk(clk), .Q(t_ff_12_q), .reset(or_1_out), .preset(1'b0));  // open: Qn
  and and_21 (and_21_out, and_20_out, t_ff_13_q);
  T_Flip_Flop t_ff_13 (.T(and_20_out), .clk(clk), .Q(t_ff_13_q), .reset(or_1_out), .preset(1'b0));  // open: Qn
  T_Flip_Flop t_ff_14 (.T(and_21_out), .clk(clk), .Q(t_ff_14_q), .reset(or_1_out), .preset(1'b0));  // open: Qn
endmodule

module partition (
  input  en,
  input  clk,
  input  rst,
  output gnd,
  output sgn
);

  wire and_1_out, and_2_out, and_3_out, and_4_out, and_5_out, and_6_out, and_7_out, and_8_out, and_9_out,
       and_10_out, and_11_out, and_12_out, and_13_out, and_14_out, and_15_out, d_ff_1_q, d_ff_2_q, d_ff_3_q,
       d_ff_4_q, d_ff_5_q, d_ff_6_q, or_1_out, or_2_out, score_1_a4, score_1_b4, score_1_c5, score_1_d5,
       score_1_e4, score_1_e5, score_1_f4, score_1_g4, t_ff_1_q, t_ff_2_q, t_ff_3_q, t_ff_4_q, t_ff_5_q,
       t_ff_6_q, t_ff_7_q, t_ff_8_q, t_ff_9_q, t_ff_10_q, t_ff_11_q, t_ff_12_q, t_ff_13_q, timing_1_d0,
       timing_1_d1, timing_1_d2, timing_1_d3, timing_1_d4;

  D_Flip_Flop d_ff_1 (.D(en), .clk(clk), .Q(d_ff_1_q), .reset(rst));  // open: Qn, preset
  or or_1 (or_1_out, rst, and_1_out);
  and and_1 (and_1_out, ~t_ff_11_q, t_ff_10_q, t_ff_9_q, t_ff_8_q, t_ff_7_q, t_ff_6_q, ~t_ff_5_q, t_ff_4_q, ~t_ff_3_q, ~t_ff_2_q, ~t_ff_1_q);  // AND_Gate
  and and_2 (and_2_out, ~d_ff_1_q, en);  // AND_Gate
  T_Flip_Flop t_ff_1 (.T(en), .clk(clk), .Q(t_ff_1_q), .reset(or_1_out), .preset(1'b0));  // open: Qn
  or or_2 (or_2_out, rst, and_2_out);
  and and_3 (and_3_out, en, t_ff_1_q);
  T_Flip_Flop t_ff_2 (.T(and_3_out), .clk(clk), .Q(t_ff_2_q), .reset(or_1_out), .preset(1'b0));  // open: Qn
  and and_4 (and_4_out, and_3_out, t_ff_2_q);
  T_Flip_Flop t_ff_3 (.T(and_4_out), .clk(clk), .Q(t_ff_3_q), .reset(or_1_out), .preset(1'b0));  // open: Qn
  and and_5 (and_5_out, ~t_ff_1_q, ~t_ff_3_q, ~t_ff_8_q, ~t_ff_4_q, ~t_ff_5_q, ~t_ff_6_q, ~t_ff_7_q, ~t_ff_13_q, ~t_ff_2_q, ~t_ff_9_q, ~t_ff_10_q, ~t_ff_11_q, ~t_ff_12_q);  // AND_Gate
  and and_6 (and_6_out, and_4_out, t_ff_3_q);
  T_Flip_Flop t_ff_4 (.T(and_6_out), .clk(clk), .Q(t_ff_4_q), .reset(or_1_out), .preset(1'b0));  // open: Qn
  timing timing_1 (
    .en(and_5_out), .q4(d_ff_6_q), .q3(d_ff_5_q), .q2(d_ff_4_q), .q1(d_ff_3_q), .q0(d_ff_2_q),
    .d4(timing_1_d4), .d3(timing_1_d3), .d2(timing_1_d2), .d1(timing_1_d1), .d0(timing_1_d0));
  and and_7 (and_7_out, and_6_out, t_ff_4_q);
  T_Flip_Flop t_ff_5 (.T(and_7_out), .clk(clk), .Q(t_ff_5_q), .reset(or_1_out), .preset(1'b0));  // open: Qn
  D_Flip_Flop d_ff_2 (.D(timing_1_d0), .clk(clk), .Q(d_ff_2_q), .reset(or_2_out));  // open: Qn, preset
  and and_8 (and_8_out, and_7_out, t_ff_5_q);
  T_Flip_Flop t_ff_6 (.T(and_8_out), .clk(clk), .Q(t_ff_6_q), .reset(or_1_out), .preset(1'b0));  // open: Qn
  D_Flip_Flop d_ff_3 (.D(timing_1_d1), .clk(clk), .Q(d_ff_3_q), .reset(or_2_out));  // open: Qn, preset
  and and_9 (and_9_out, and_8_out, t_ff_6_q);
  T_Flip_Flop t_ff_7 (.T(and_9_out), .clk(clk), .Q(t_ff_7_q), .reset(or_1_out), .preset(1'b0));  // open: Qn
  D_Flip_Flop d_ff_4 (.D(timing_1_d2), .clk(clk), .Q(d_ff_4_q), .reset(or_2_out));  // open: Qn, preset
  and and_10 (and_10_out, and_9_out, t_ff_7_q);
  T_Flip_Flop t_ff_8 (.T(and_10_out), .clk(clk), .Q(t_ff_8_q), .reset(or_1_out), .preset(1'b0));  // open: Qn
  D_Flip_Flop d_ff_5 (.D(timing_1_d3), .clk(clk), .Q(d_ff_5_q), .reset(or_2_out));  // open: Qn, preset
  and and_11 (and_11_out, and_10_out, t_ff_8_q);
  T_Flip_Flop t_ff_9 (.T(and_11_out), .clk(clk), .Q(t_ff_9_q), .reset(or_1_out), .preset(1'b0));  // open: Qn
  D_Flip_Flop d_ff_6 (.D(timing_1_d4), .clk(clk), .Q(d_ff_6_q), .reset(or_2_out));  // open: Qn, preset
  and and_12 (and_12_out, and_11_out, t_ff_9_q);
  T_Flip_Flop t_ff_10 (.T(and_12_out), .clk(clk), .Q(t_ff_10_q), .reset(or_1_out), .preset(1'b0));  // open: Qn
  and and_13 (and_13_out, and_12_out, t_ff_10_q);
  T_Flip_Flop t_ff_11 (.T(and_13_out), .clk(clk), .Q(t_ff_11_q), .reset(or_1_out), .preset(1'b0));  // open: Qn
  and and_14 (and_14_out, and_13_out, t_ff_11_q);
  T_Flip_Flop t_ff_12 (.T(and_14_out), .clk(clk), .Q(t_ff_12_q), .reset(or_1_out), .preset(1'b0));  // open: Qn
  and and_15 (and_15_out, and_14_out, t_ff_12_q);
  T_Flip_Flop t_ff_13 (.T(and_15_out), .clk(clk), .Q(t_ff_13_q), .reset(or_1_out), .preset(1'b0));  // open: Qn
  score score_1 (
    .en(en), .i4(d_ff_6_q), .i3(d_ff_5_q), .i2(d_ff_4_q), .i1(d_ff_3_q), .i0(d_ff_2_q), .e4(score_1_e4),
    .f4(score_1_f4), .g4(score_1_g4), .a4(score_1_a4), .b4(score_1_b4), .c5(score_1_c5), .d5(score_1_d5),
    .e5(score_1_e5));
  generator generator_1 (
    .EN(en), .clk(clk), .rst(or_2_out), .E4(score_1_e4), .F4(score_1_f4), .G4(score_1_g4), .A4(score_1_a4),
    .B4(score_1_b4), .C5(score_1_c5), .D5(score_1_d5), .E5(score_1_e5), .sig(sgn));

  assign gnd = 1'b0;
endmodule

module timing (
  input  en,
  input  q4,
  input  q3,
  input  q2,
  input  q1,
  input  q0,
  output d4,
  output d3,
  output d2,
  output d1,
  output d0
);

  wire and_1_out, and_2_out, and_3_out, and_4_out, and_5_out, and_6_out, and_7_out, and_8_out, and_9_out,
       and_10_out, and_11_out, and_12_out, and_13_out, and_14_out, and_15_out, and_16_out, and_17_out,
       and_18_out, and_19_out, and_20_out, and_21_out, and_22_out, and_23_out, and_24_out, and_25_out,
       not_1_out, not_2_out, not_3_out, not_4_out, not_5_out, not_6_out, not_7_out, not_8_out, not_9_out,
       not_10_out, not_11_out, not_12_out, not_13_out, not_14_out, not_15_out, not_16_out, not_17_out,
       not_18_out, not_19_out, not_20_out, not_21_out, not_22_out, not_23_out, not_24_out, not_25_out,
       not_26_out, not_27_out, not_28_out, not_29_out, not_30_out, not_31_out, not_32_out, not_33_out,
       not_34_out, not_35_out;

  not not_1 (not_1_out, en);
  not not_2 (not_2_out, q3);
  not not_3 (not_3_out, q2);
  not not_4 (not_4_out, q1);
  not not_5 (not_5_out, q4);
  not not_6 (not_6_out, en);
  not not_7 (not_7_out, q4);
  not not_8 (not_8_out, q0);
  not not_9 (not_9_out, q2);
  not not_10 (not_10_out, q1);
  not not_11 (not_11_out, q3);
  not not_12 (not_12_out, en);
  not not_13 (not_13_out, q4);
  not not_14 (not_14_out, q0);
  not not_15 (not_15_out, q3);
  not not_16 (not_16_out, q0);
  not not_17 (not_17_out, q1);
  not not_18 (not_18_out, q2);
  not not_19 (not_19_out, en);
  and and_1 (and_1_out, not_19_out, q1);
  not not_20 (not_20_out, q4);
  and and_2 (and_2_out, not_20_out, q1, not_21_out);
  not not_21 (not_21_out, q0);
  not not_22 (not_22_out, q3);
  and and_3 (and_3_out, not_22_out, q1, not_23_out);
  not not_23 (not_23_out, q0);
  not not_24 (not_24_out, q2);
  and and_4 (and_4_out, not_24_out, q1, not_25_out);
  not not_25 (not_25_out, q0);
  not not_26 (not_26_out, q1);
  and and_5 (and_5_out, en, not_26_out, q0);
  not not_27 (not_27_out, en);
  and and_6 (and_6_out, not_27_out, q0);
  and and_7 (and_7_out, en, not_28_out, not_29_out);
  not not_28 (not_28_out, q4);
  not not_29 (not_29_out, q0);
  and and_8 (and_8_out, en, not_30_out, not_31_out);
  not not_30 (not_30_out, q3);
  not not_31 (not_31_out, q0);
  and and_9 (and_9_out, en, not_32_out, not_33_out);
  not not_32 (not_32_out, q2);
  not not_33 (not_33_out, q0);
  and and_10 (and_10_out, en, not_34_out, not_35_out);
  not not_34 (not_34_out, q1);
  not not_35 (not_35_out, q0);
  and and_11 (and_11_out, not_1_out, q4);
  and and_12 (and_12_out, q4, not_2_out);
  and and_13 (and_13_out, q4, not_3_out);
  and and_14 (and_14_out, q4, not_4_out);
  and and_15 (and_15_out, en, not_5_out, q3, q2, q1, q0);
  and and_16 (and_16_out, not_6_out, q3);
  and and_17 (and_17_out, not_7_out, q3, not_8_out);
  and and_18 (and_18_out, q3, not_9_out);
  and and_19 (and_19_out, q3, not_10_out);
  and and_20 (and_20_out, en, not_11_out, q2, q1, q0);
  and and_21 (and_21_out, not_12_out, q2);
  and and_22 (and_22_out, not_13_out, q2, not_14_out);
  and and_23 (and_23_out, not_15_out, q2, not_16_out);
  and and_24 (and_24_out, q2, not_17_out);
  and and_25 (and_25_out, en, not_18_out, q1, q0);
  or or_1 (d1, and_1_out, and_2_out, and_3_out, and_4_out, and_5_out);
  or or_2 (d0, and_6_out, and_7_out, and_8_out, and_9_out, and_10_out);
  or or_3 (d4, and_11_out, and_12_out, and_13_out, and_14_out, and_15_out);
  or or_4 (d3, and_16_out, and_17_out, and_18_out, and_19_out, and_20_out);
  or or_5 (d2, and_21_out, and_22_out, and_23_out, and_24_out, and_25_out);
endmodule

module score (
  input  en,
  input  i4,
  input  i3,
  input  i2,
  input  i1,
  input  i0,
  output e4,
  output f4,
  output g4,
  output a4,
  output b4,
  output c5,
  output d5,
  output e5
);

  wire and_1_out, and_2_out, and_3_out, and_4_out, and_5_out, and_6_out, and_7_out, and_8_out, and_9_out,
       and_10_out, and_11_out, and_12_out, and_13_out, not_1_out, not_2_out, not_3_out, not_4_out, not_5_out,
       not_6_out, not_7_out, not_8_out, not_9_out, not_10_out, not_11_out, not_12_out, not_13_out,
       not_14_out, not_15_out, not_16_out, not_17_out, not_18_out, not_19_out, not_20_out, not_21_out,
       not_22_out, not_23_out, not_24_out, not_25_out, not_26_out, not_27_out, not_28_out, not_29_out;

  not not_1 (not_1_out, i4);
  not not_2 (not_2_out, i3);
  not not_3 (not_3_out, i4);
  not not_4 (not_4_out, i2);
  not not_5 (not_5_out, i2);
  not not_6 (not_6_out, i1);
  not not_7 (not_7_out, i0);
  not not_8 (not_8_out, i4);
  not not_9 (not_9_out, i3);
  not not_10 (not_10_out, i1);
  not not_11 (not_11_out, i3);
  not not_12 (not_12_out, i2);
  not not_13 (not_13_out, i2);
  not not_14 (not_14_out, i0);
  not not_15 (not_15_out, i2);
  not not_16 (not_16_out, i1);
  not not_17 (not_17_out, i4);
  not not_18 (not_18_out, i3);
  not not_19 (not_19_out, i2);
  not not_20 (not_20_out, i3);
  not not_21 (not_21_out, i2);
  not not_22 (not_22_out, i1);
  not not_23 (not_23_out, i2);
  not not_24 (not_24_out, i1);
  not not_25 (not_25_out, i0);
  not not_26 (not_26_out, i3);
  not not_27 (not_27_out, i0);
  not not_28 (not_28_out, i3);
  not not_29 (not_29_out, i1);
  and and_1 (and_1_out, en, not_1_out, not_2_out, i2, i1);
  and and_2 (and_2_out, en, not_3_out, i3, not_4_out);
  and and_3 (and_3_out, en, i3, not_5_out, i1, i0);
  and and_4 (and_4_out, en, i3, i2, not_6_out);
  and and_5 (and_5_out, en, i4, i3, i2, not_7_out);
  and and_6 (and_6_out, en, not_8_out, not_9_out, i2, not_10_out);
  and and_7 (and_7_out, en, i4, not_11_out, not_12_out, i1);
  and and_8 (and_8_out, en, i4, not_13_out, i1, not_14_out);
  and and_9 (and_9_out, en, i4, i3, not_15_out, not_16_out, i0);
  and and_10 (and_10_out, en, not_17_out, not_18_out, not_19_out);
  and and_11 (and_11_out, en, not_20_out, not_21_out, not_22_out);
  and and_12 (and_12_out, en, i4, not_23_out, not_24_out, not_25_out);
  and and_13 (and_13_out, en, i4, not_26_out, i2, i1, not_27_out);
  and and_14 (d5, en, i4, not_28_out, i2, not_29_out);
  or or_1 (e4, and_1_out, and_2_out, and_3_out, and_4_out, and_5_out);
  or or_2 (a4, and_6_out, and_7_out, and_8_out, and_9_out);
  or or_3 (b4, and_10_out, and_11_out, and_12_out, and_13_out);

  assign c5 = 1'b0;
  assign e5 = 1'b0;
  assign f4 = 1'b0;
  assign g4 = 1'b0;
endmodule

module Alarm (
  input  LongA,
  input  rst,
  input  clk,
  input  A,
  input  B,
  input  [5:0] hour,
  input  [5:0] min,
  output [5:0] s0,
  output [5:0] s1,
  output [5:0] min0,
  output [5:0] min1,
  output [5:0] hour0,
  output [5:0] hour1,
  output buzzer
);

  wire and_1_out, and_2_out, Compare_1_same, Compare_2_same, t_ff_1_q, t_ff_2_q;
  wire [4:0] mod24_1_hour;
  wire [5:0] mod60_1_count;

  T_Flip_Flop t_ff_1 (.T(LongA), .clk(clk), .Q(t_ff_1_q), .reset(rst));  // open: Qn, preset
  T_Flip_Flop t_ff_2 (.T(A), .clk(clk), .Q(t_ff_2_q));  // open: Qn, reset, preset
  and and_1 (and_1_out, t_ff_2_q, B);
  and and_2 (and_2_out, t_ff_2_q, B);
  mod60 mod60_1 (.EN(and_1_out), .dir(1'b0), .CLK(clk), .mrst(rst), .count(mod60_1_count));  // open: ovrf, undf, zero
  mod24 mod24_1 (.en(and_2_out), .dir(1'b0), .clk(clk), .rst(rst), .hour(mod24_1_hour));  // open: ovrf, undf, zero
  Compare Compare_1 (.inA(mod60_1_count), .inB(min), .same(Compare_1_same));
  Compare Compare_2 (.inA({1'b0, mod24_1_hour}), .inB(hour), .same(Compare_2_same));
  Multiplexer #(.width(6), .enable("false")) multiplexer_1 (.in0(6'b010000), .in1(6'b011000), .out(s0), .sel(t_ff_1_q));
  and and_3 (buzzer, t_ff_1_q, Compare_1_same, Compare_2_same);
  ones ones_1 (
    .Input_1(mod60_1_count[5]), .Input_2(mod60_1_count[4]), .Input_3(mod60_1_count[3]),
    .Input_4(mod60_1_count[2]), .Input_5(mod60_1_count[1]), .Input_6(mod60_1_count[0]), .Output_1(min0[5]),
    .Output_2(min0[4]), .Output_3(min0[3]), .Output_4(min0[2]), .Output_5(min0[1]), .Output_6(min0[0]));
  tens tens_1 (
    .Input_1(mod60_1_count[5]), .Input_2(mod60_1_count[4]), .Input_3(mod60_1_count[3]),
    .Input_4(mod60_1_count[2]), .Input_5(mod60_1_count[1]), .Input_6(mod60_1_count[0]), .Output_1(min1[5]),
    .Output_2(min1[4]), .Output_3(min1[3]), .Output_4(min1[2]), .Output_5(min1[1]), .Output_6(min1[0]));
  ones ones_2 (
    .Input_1(1'b0), .Input_2(mod24_1_hour[4]), .Input_3(mod24_1_hour[3]), .Input_4(mod24_1_hour[2]),
    .Input_5(mod24_1_hour[1]), .Input_6(mod24_1_hour[0]), .Output_1(hour0[5]), .Output_2(hour0[4]),
    .Output_3(hour0[3]), .Output_4(hour0[2]), .Output_5(hour0[1]), .Output_6(hour0[0]));
  tens tens_2 (
    .Input_1(1'b0), .Input_2(mod24_1_hour[4]), .Input_3(mod24_1_hour[3]), .Input_4(mod24_1_hour[2]),
    .Input_5(mod24_1_hour[1]), .Input_6(mod24_1_hour[0]), .Output_1(hour1[5]), .Output_2(hour1[4]),
    .Output_3(hour1[3]), .Output_4(hour1[2]), .Output_5(hour1[1]), .Output_6(hour1[0]));

  assign s1 = 6'b011001;
endmodule

module Compare (
  input  [5:0] inA,
  input  [5:0] inB,
  output same
);

  wire xnor_1_out, xnor_2_out, xnor_3_out, xnor_4_out, xnor_5_out, xnor_6_out;

  xnor xnor_1 (xnor_1_out, inA[0], inB[0]);
  xnor xnor_2 (xnor_2_out, inA[1], inB[1]);
  xnor xnor_3 (xnor_3_out, inA[2], inB[2]);
  xnor xnor_4 (xnor_4_out, inA[3], inB[3]);
  xnor xnor_5 (xnor_5_out, inA[4], inB[4]);
  xnor xnor_6 (xnor_6_out, inA[5], inB[5]);
  and and_1 (same, xnor_1_out, xnor_2_out, xnor_3_out, xnor_4_out, xnor_5_out, xnor_6_out);
endmodule
