// Logisim project alarme_BIS_DIPSWITCH.circ as structural Verilog: 16 circuits, main circuit main
module main (
  output [3:0] nbr1,
  output [3:0] nbr2,
  output [3:0] nbr3,
  output [3:0] nbr4,
  output [3:0] nbr5,
  output [3:0] nbr6
);

  wire Button_1_out, DipSwitch_1_sw1, DipSwitch_1_sw2, DipSwitch_1_sw3, DipSwitch_1_sw4, DipSwitch_1_sw5,
       DipSwitch_1_sw6;

  Button Button_1 (.out(Button_1_out));
  DipSwitch #(.number(6)) DipSwitch_1 (
    .sw1(DipSwitch_1_sw1), .sw2(DipSwitch_1_sw2), .sw3(DipSwitch_1_sw3), .sw4(DipSwitch_1_sw4),
    .sw5(DipSwitch_1_sw5), .sw6(DipSwitch_1_sw6));
  seven_seg_controller seven_seg_controller_1 (.Input_1(Button_1_out), .en(DipSwitch_1_sw1), .one(nbr1));
  sec_2 sec_2_1 (.Input_2(Button_1_out), .en(DipSwitch_1_sw2), .ten(nbr2));
  seven_seg_controller seven_seg_controller_2 (.Input_1(Button_1_out), .en(DipSwitch_1_sw3), .one(nbr3));
  sec_2 sec_2_2 (.Input_2(Button_1_out), .en(DipSwitch_1_sw4), .ten(nbr4));
  hour1 hour1_1 (.inputt(Button_1_out), .en(DipSwitch_1_sw5), .hour2(nbr6), .hour1(nbr5));
  hour_2 hour_2_1 (.Input_2(Button_1_out), .en(DipSwitch_1_sw6), .hour1(nbr5[3:2]), .hour2(nbr6));
endmodule

module seven_seg_controller (
  input  Input_1,
  input  en,
  output [3:0] one
);

  wire and_1_out, and_2_out, clock_1_out, d_ff_1_q, d_ff_2_q, d_ff_3_q, d_ff_4_q, fonction_a_1_a,
       fonction_b_1_b, fonction_c_1_c, fonction_d_1_d, fonction_e_1_e, fonction_f_1_f, fonction_g_1_g,
       not_1_out, not_2_out, t_ff_1_qn, t_ff_2_qn, t_ff_3_qn;

  Clock clock_1 (.out(clock_1_out));
  D_Flip_Flop d_ff_1 (.D(Input_1), .clk(clock_1_out), .Q(d_ff_1_q));  // open: Qn, preset, reset
  D_Flip_Flop d_ff_2 (.D(d_ff_1_q), .clk(clock_1_out), .Q(d_ff_2_q));  // open: Qn, preset, reset
  D_Flip_Flop d_ff_3 (.D(d_ff_2_q), .clk(clock_1_out), .Q(d_ff_3_q));  // open: Qn, preset, reset
  and and_1 (and_1_out, d_ff_1_q, d_ff_2_q, d_ff_3_q, d_ff_4_q);
  D_Flip_Flop d_ff_4 (.D(d_ff_3_q), .clk(clock_1_out), .Q(d_ff_4_q));  // open: Qn, preset, reset
  T_Flip_Flop t_ff_1 (.T(en), .clk(and_1_out), .Q(one[0]), .Qn(t_ff_1_qn), .reset(and_2_out), .preset(1'b0));
  T_Flip_Flop t_ff_2 (.T(en), .clk(t_ff_1_qn), .Q(one[1]), .Qn(t_ff_2_qn), .reset(and_2_out), .preset(1'b0));
  T_Flip_Flop t_ff_3 (.T(en), .clk(t_ff_2_qn), .Q(one[2]), .Qn(t_ff_3_qn), .reset(and_2_out), .preset(1'b0));
  T_Flip_Flop t_ff_4 (.T(en), .clk(t_ff_3_qn), .Q(one[3]), .reset(and_2_out), .preset(1'b0));  // open: Qn
  not not_1 (not_1_out, one[0]);
  not not_2 (not_2_out, one[2]);
  and and_2 (and_2_out, not_1_out, one[1], not_2_out, one[3]);
  fonction_a fonction_a_1 (.W(one[3]), .X(one[2]), .Y(one[1]), .Z(one[0]), .a(fonction_a_1_a));
  fonction_b fonction_b_1 (.W(one[3]), .X(one[2]), .Y(one[1]), .Z(one[0]), .b(fonction_b_1_b));
  fonction_c fonction_c_1 (.W(one[3]), .X(one[2]), .Y(one[1]), .Z(one[0]), .c(fonction_c_1_c));
  fonction_d fonction_d_1 (.W(one[3]), .X(one[2]), .Y(one[1]), .Z(one[0]), .d(fonction_d_1_d));
  fonction_e fonction_e_1 (.W(one[3]), .X(one[2]), .Y(one[1]), .Z(one[0]), .e(fonction_e_1_e));
  fonction_f fonction_f_1 (.W(one[3]), .X(one[2]), .Y(one[1]), .Z(one[0]), .f(fonction_f_1_f));
  fonction_g fonction_g_1 (.W(one[3]), .X(one[2]), .Y(one[1]), .Z(one[0]), .g(fonction_g_1_g));
  _7_Segment_Display L_7_Segment_Display_1 (
    .g(fonction_g_1_g), .f(fonction_f_1_f), .a(fonction_a_1_a), .b(fonction_b_1_b), .e(fonction_e_1_e),
    .d(fonction_d_1_d), .c(fonction_c_1_c), .dp(en));
endmodule

module fonction_a (
  input  W,
  input  X,
  input  Y,
  input  Z,
  output a
);

  wire and_1_out, and_2_out, and_3_out, and_4_out, not_1_out, not_2_out, not_3_out, not_4_out, or_1_out;

  not not_1 (not_1_out, W);
  not not_2 (not_2_out, X);
  not not_3 (not_3_out, Y);
  not not_4 (not_4_out, Z);
  and and_1 (and_1_out, not_1_out, not_2_out, not_3_out, Z);
  and and_2 (and_2_out, not_1_out, X, not_3_out, not_4_out);
  and and_3 (and_3_out, W, not_2_out, Y, Z);
  and and_4 (and_4_out, W, X, not_3_out, Z);
  or or_1 (or_1_out, and_1_out, and_2_out, and_3_out, and_4_out);
  not not_5 (a, or_1_out);
endmodule

module fonction_b (
  input  W,
  input  X,
  input  Y,
  input  Z,
  output b
);

  wire and_1_out, and_2_out, and_3_out, and_4_out, and_5_out, not_1_out, not_2_out, not_3_out, not_4_out;

  not not_1 (not_1_out, W);
  not not_2 (not_2_out, X);
  not not_3 (not_3_out, Y);
  not not_4 (not_4_out, Z);
  and and_1 (and_1_out, not_1_out, not_2_out);
  and and_2 (and_2_out, not_2_out, not_4_out);
  and and_3 (and_3_out, not_1_out, not_3_out, not_4_out);
  and and_4 (and_4_out, not_1_out, Y, Z);
  and and_5 (and_5_out, W, not_3_out, Z);
  or or_1 (b, and_1_out, and_2_out, and_3_out, and_4_out, and_5_out);
endmodule

module fonction_c (
  input  W,
  input  X,
  input  Y,
  input  Z,
  output c
);

  wire and_1_out, and_2_out, and_3_out, not_1_out, not_2_out, not_3_out, not_4_out, or_1_out;

  not not_1 (not_1_out, W);
  not not_2 (not_2_out, X);
  not not_3 (not_3_out, Y);
  not not_4 (not_4_out, Z);
  and and_1 (and_1_out, W, X, not_4_out);
  and and_2 (and_2_out, W, X, Y);
  and and_3 (and_3_out, not_1_out, not_2_out, Y, not_4_out);
  not not_5 (c, or_1_out);
  or or_1 (or_1_out, and_1_out, and_2_out, and_3_out);
endmodule

module fonction_d (
  input  W,
  input  X,
  input  Y,
  input  Z,
  output d
);

  wire and_1_out, and_2_out, and_3_out, and_4_out, and_5_out, not_1_out, not_2_out, not_3_out, not_4_out;

  not not_1 (not_1_out, W);
  not not_2 (not_2_out, X);
  not not_3 (not_3_out, Y);
  not not_4 (not_4_out, Z);
  and and_1 (and_1_out, W, not_3_out);
  and and_2 (and_2_out, X, Y, not_4_out);
  and and_3 (and_3_out, not_2_out, Y, Z);
  and and_4 (and_4_out, not_1_out, not_2_out, not_4_out);
  and and_5 (and_5_out, X, not_3_out, Z);
  or or_1 (d, and_1_out, and_2_out, and_3_out, and_4_out, and_5_out);
endmodule

module fonction_e (
  input  W,
  input  X,
  input  Y,
  input  Z,
  output e
);

  wire and_1_out, and_2_out, and_3_out, and_4_out, not_1_out, not_2_out, not_3_out, not_4_out;

  not not_1 (not_1_out, W);
  not not_2 (not_2_out, X);
  not not_3 (not_3_out, Y);
  not not_4 (not_4_out, Z);
  and and_1 (and_1_out, W, X);
  and and_2 (and_2_out, W, Y);
  and and_3 (and_3_out, not_2_out, not_4_out);
  and and_4 (and_4_out, Y, not_4_out);
  or or_1 (e, and_1_out, and_2_out, and_3_out, and_4_out);
endmodule

module fonction_f (
  input  W,
  input  X,
  input  Y,
  input  Z,
  output f
);

  wire and_1_out, and_2_out, and_3_out, and_4_out, not_1_out, not_2_out, not_3_out, not_4_out, or_1_out;

  not not_1 (not_1_out, W);
  not not_2 (not_2_out, X);
  not not_3 (not_3_out, Y);
  not not_4 (not_4_out, Z);
  and and_1 (and_1_out, W, X, not_3_out, Z);
  and and_2 (and_2_out, not_1_out, Y, Z);
  and and_3 (and_3_out, not_1_out, not_2_out, Y);
  and and_4 (and_4_out, not_1_out, not_2_out, Z);
  or or_1 (or_1_out, and_1_out, and_2_out, and_3_out, and_4_out);
  not not_5 (f, or_1_out);
endmodule

module fonction_g (
  input  W,
  input  X,
  input  Y,
  input  Z,
  output g
);

  wire and_1_out, and_2_out, and_3_out, not_1_out, not_2_out, not_3_out, not_4_out, or_1_out;

  not not_1 (not_1_out, W);
  not not_2 (not_2_out, X);
  not not_3 (not_3_out, Y);
  not not_4 (not_4_out, Z);
  and and_1 (and_1_out, not_1_out, not_2_out, not_3_out);
  and and_2 (and_2_out, W, X, not_3_out, not_4_out);
  and and_3 (and_3_out, not_1_out, X, Y, Z);
  or or_1 (or_1_out, and_1_out, and_2_out, and_3_out);
  not not_5 (g, or_1_out);
endmodule

module fonction_a_nor (
  input  W,
  input  X,
  input  Y,
  input  Z,
  output a
);

  wire nor_1_out, nor_2_out, nor_3_out, nor_4_out, nor_5_out, nor_6_out, nor_7_out, nor_8_out;

  nor nor_1 (nor_1_out, W, 1'b0);
  nor nor_2 (nor_2_out, X, 1'b0);
  nor nor_3 (nor_3_out, Y, 1'b0);
  nor nor_4 (nor_4_out, Z, 1'b0);
  nor nor_5 (nor_5_out, W, X, Y, nor_4_out);
  nor nor_6 (nor_6_out, W, nor_2_out, Y, Z);
  nor nor_7 (nor_7_out, nor_1_out, X, nor_3_out, nor_4_out);
  nor nor_8 (nor_8_out, nor_1_out, nor_2_out, Y, nor_4_out);
  nor nor_9 (a, nor_5_out, nor_6_out, nor_7_out, nor_8_out);
endmodule

module fonction_b_nand (
  input  W,
  input  X,
  input  Y,
  input  Z,
  output b
);

  wire nand_1_out, nand_2_out, nand_3_out, nand_4_out, nand_5_out, nand_6_out, nand_7_out, nand_8_out,
       nand_9_out;

  nand nand_1 (nand_1_out, W, W);
  nand nand_2 (nand_2_out, X, X);
  nand nand_3 (nand_3_out, Y, Y);
  nand nand_4 (nand_4_out, Z, Z);
  nand nand_5 (nand_5_out, nand_1_out, nand_2_out);
  nand nand_6 (nand_6_out, nand_2_out, nand_4_out);
  nand nand_7 (nand_7_out, nand_1_out, nand_3_out, nand_4_out);
  nand nand_8 (nand_8_out, nand_1_out, Y, Z);
  nand nand_9 (nand_9_out, W, nand_3_out, Z);
  nand nand_10 (b, nand_5_out, nand_6_out, nand_7_out, nand_8_out, nand_9_out);
endmodule

module fonction_c_or_xor (
  input  W,
  input  X,
  input  Y,
  input  Z,
  output c
);

  wire or_1_out, or_2_out, or_3_out, or_4_out, xor_1_out, xor_2_out, xor_3_out, xor_4_out, xor_5_out,
       xor_6_out, xor_7_out;

  xor xor_1 (xor_1_out, W, 1'b1);
  xor xor_2 (xor_2_out, X, 1'b1);
  xor xor_3 (xor_3_out, Y, 1'b1);
  xor xor_4 (xor_4_out, Z, 1'b1);
  or or_1 (or_1_out, xor_1_out, xor_2_out, Z);
  or or_2 (or_2_out, xor_1_out, xor_2_out, xor_3_out);
  or or_3 (or_3_out, W, X, xor_3_out, Z);
  xor xor_5 (xor_5_out, or_1_out, 1'b1);
  xor xor_6 (xor_6_out, or_2_out, 1'b1);
  xor xor_7 (xor_7_out, or_3_out, 1'b1);
  or or_4 (or_4_out, xor_5_out, xor_6_out, xor_7_out);
  xor xor_8 (c, 1'b1, or_4_out);
endmodule

module fonction_e_forme_conjunctive (
  input  W,
  input  X,
  input  Y,
  input  Z,
  output e
);

  wire not_1_out, not_2_out, not_3_out, not_4_out, or_1_out, or_2_out, or_3_out, or_4_out;

  not not_1 (not_1_out, W);
  not not_2 (not_2_out, X);
  not not_3 (not_3_out, Y);
  not not_4 (not_4_out, Z);
  or or_1 (or_1_out, not_1_out, not_2_out);
  or or_2 (or_2_out, not_1_out, not_3_out);
  or or_3 (or_3_out, W, Z);
  or or_4 (or_4_out, not_2_out, Z);
  nand nand_1 (e, or_1_out, or_2_out, or_3_out, or_4_out);
endmodule

module sec_2 (
  input  Input_2,
  input  en,
  output [3:0] ten
);

  wire and_1_out, and_2_out, clock_1_out, d_ff_1_q, d_ff_2_q, d_ff_3_q, d_ff_4_q, fonction_a_1_a,
       fonction_b_1_b, fonction_c_1_c, fonction_d_1_d, fonction_e_1_e, fonction_f_1_f, fonction_g_1_g,
       t_ff_1_qn, t_ff_2_qn, t_ff_3_qn;

  Clock clock_1 (.out(clock_1_out));
  D_Flip_Flop d_ff_1 (.D(Input_2), .clk(clock_1_out), .Q(d_ff_1_q));  // open: Qn, preset, reset
  D_Flip_Flop d_ff_2 (.D(d_ff_1_q), .clk(clock_1_out), .Q(d_ff_2_q));  // open: Qn, preset, reset
  D_Flip_Flop d_ff_3 (.D(d_ff_2_q), .clk(clock_1_out), .Q(d_ff_3_q));  // open: Qn, preset, reset
  and and_1 (and_1_out, d_ff_1_q, d_ff_2_q, d_ff_3_q, d_ff_4_q);
  D_Flip_Flop d_ff_4 (.D(d_ff_3_q), .clk(clock_1_out), .Q(d_ff_4_q));  // open: Qn, preset, reset
  T_Flip_Flop t_ff_1 (.T(en), .clk(and_1_out), .Q(ten[0]), .Qn(t_ff_1_qn), .reset(and_2_out), .preset(1'b0));
  T_Flip_Flop t_ff_2 (.T(en), .clk(t_ff_1_qn), .Q(ten[1]), .Qn(t_ff_2_qn), .reset(and_2_out), .preset(1'b0));
  T_Flip_Flop t_ff_3 (.T(en), .clk(t_ff_2_qn), .Q(ten[2]), .Qn(t_ff_3_qn), .reset(and_2_out), .preset(1'b0));
  T_Flip_Flop t_ff_4 (.T(en), .clk(t_ff_3_qn), .Q(ten[3]), .reset(and_2_out), .preset(1'b0));  // open: Qn
  and and_2 (and_2_out, ten[1], ten[2]);
  fonction_a fonction_a_1 (.W(ten[3]), .X(ten[2]), .Y(ten[1]), .Z(ten[0]), .a(fonction_a_1_a));
  fonction_b fonction_b_1 (.W(ten[3]), .X(ten[2]), .Y(ten[1]), .Z(ten[0]), .b(fonction_b_1_b));
  fonction_c fonction_c_1 (.W(ten[3]), .X(ten[2]), .Y(ten[1]), .Z(ten[0]), .c(fonction_c_1_c));
  fonction_d fonction_d_1 (.W(ten[3]), .X(ten[2]), .Y(ten[1]), .Z(ten[0]), .d(fonction_d_1_d));
  fonction_e fonction_e_1 (.W(ten[3]), .X(ten[2]), .Y(ten[1]), .Z(ten[0]), .e(fonction_e_1_e));
  fonction_f fonction_f_1 (.W(ten[3]), .X(ten[2]), .Y(ten[1]), .Z(ten[0]), .f(fonction_f_1_f));
  fonction_g fonction_g_1 (.W(ten[3]), .X(ten[2]), .Y(ten[1]), .Z(ten[0]), .g(fonction_g_1_g));
  _7_Segment_Display L_7_Segment_Display_1 (
    .g(fonction_g_1_g), .f(fonction_f_1_f), .a(fonction_a_1_a), .b(fonction_b_1_b), .e(fonction_e_1_e),
    .d(fonction_d_1_d), .c(fonction_c_1_c), .dp(en));
endmodule

module hour_2 (
  input  Input_2,
  input  en,
  input  [1:0] hour1,
  output [3:0] hour2
);

  wire and_1_out, and_2_out, and_3_out, clock_1_out, d_ff_1_q, d_ff_2_q, d_ff_3_q, d_ff_4_q, fonction_a_1_a,
       fonction_b_1_b, fonction_c_1_c, fonction_d_1_d, fonction_e_1_e, fonction_f_1_f, fonction_g_1_g,
       or_1_out, or_2_out, or_3_out, or_4_out, t_ff_1_qn, t_ff_2_qn, t_ff_3_qn;

  Clock clock_1 (.out(clock_1_out));
  D_Flip_Flop d_ff_1 (.D(Input_2), .clk(clock_1_out), .Q(d_ff_1_q));  // open: Qn, preset, reset
  D_Flip_Flop d_ff_2 (.D(d_ff_1_q), .clk(clock_1_out), .Q(d_ff_2_q));  // open: Qn, preset, reset
  and and_1 (and_1_out, d_ff_1_q, d_ff_2_q, d_ff_3_q, d_ff_4_q);
  D_Flip_Flop d_ff_3 (.D(d_ff_2_q), .clk(clock_1_out), .Q(d_ff_3_q));  // open: Qn, preset, reset
  D_Flip_Flop d_ff_4 (.D(d_ff_3_q), .clk(clock_1_out), .Q(d_ff_4_q));  // open: Qn, preset, reset
  T_Flip_Flop t_ff_1 (.T(en), .clk(and_1_out), .Q(hour2[0]), .Qn(t_ff_1_qn), .reset(or_3_out), .preset(1'b0));
  T_Flip_Flop t_ff_2 (.T(en), .clk(t_ff_1_qn), .Q(hour2[1]), .Qn(t_ff_2_qn), .reset(or_2_out), .preset(1'b0));
  T_Flip_Flop t_ff_3 (.T(en), .clk(t_ff_2_qn), .Q(hour2[2]), .Qn(t_ff_3_qn), .reset(or_2_out), .preset(1'b0));
  T_Flip_Flop t_ff_4 (.T(en), .clk(t_ff_3_qn), .Q(hour2[3]), .reset(or_4_out), .preset(1'b0));  // open: Qn
  or or_1 (or_1_out, hour1[0], hour1[1]);
  or or_2 (or_2_out, and_3_out, and_2_out);
  or or_3 (or_3_out, and_3_out, and_2_out);
  or or_4 (or_4_out, and_2_out, and_3_out);
  and and_2 (and_2_out, hour2[0], hour2[1], ~hour2[2], ~hour2[3], en);  // AND_Gate
  fonction_a fonction_a_1 (.W(hour2[3]), .X(hour2[2]), .Y(hour2[1]), .Z(hour2[0]), .a(fonction_a_1_a));
  fonction_b fonction_b_1 (.W(hour2[3]), .X(hour2[2]), .Y(hour2[1]), .Z(hour2[0]), .b(fonction_b_1_b));
  fonction_c fonction_c_1 (.W(hour2[3]), .X(hour2[2]), .Y(hour2[1]), .Z(hour2[0]), .c(fonction_c_1_c));
  fonction_d fonction_d_1 (.W(hour2[3]), .X(hour2[2]), .Y(hour2[1]), .Z(hour2[0]), .d(fonction_d_1_d));
  fonction_e fonction_e_1 (.W(hour2[3]), .X(hour2[2]), .Y(hour2[1]), .Z(hour2[0]), .e(fonction_e_1_e));
  fonction_f fonction_f_1 (.W(hour2[3]), .X(hour2[2]), .Y(hour2[1]), .Z(hour2[0]), .f(fonction_f_1_f));
  fonction_g fonction_g_1 (.W(hour2[3]), .X(hour2[2]), .Y(hour2[1]), .Z(hour2[0]), .g(fonction_g_1_g));
  _7_Segment_Display L_7_Segment_Display_1 (
    .g(fonction_g_1_g), .f(fonction_f_1_f), .a(fonction_a_1_a), .b(fonction_b_1_b), .e(fonction_e_1_e),
    .d(fonction_d_1_d), .c(fonction_c_1_c), .dp(en));
  and and_3 (and_3_out, ~hour2[0], hour2[1], ~hour2[2], ~hour2[3], or_1_out, en);  // AND_Gate
endmodule

module hour1 (
  input  inputt,
  input  en,
  input  [3:0] hour2,
  output [3:0] hour1
);

  wire and_1_out, and_2_out, and_3_out, and_4_out, clock_1_out, d_ff_1_q, d_ff_2_q, d_ff_3_q, d_ff_4_q,
       fonction_a_1_a, fonction_b_1_b, fonction_c_1_c, fonction_d_1_d, fonction_e_1_e, fonction_f_1_f,
       fonction_g_1_g, or_1_out, or_2_out, or_3_out, t_ff_1_qn, t_ff_2_qn, t_ff_3_qn;

  Clock clock_1 (.out(clock_1_out));
  D_Flip_Flop d_ff_1 (.D(inputt), .clk(clock_1_out), .Q(d_ff_1_q));  // open: Qn, preset, reset
  D_Flip_Flop d_ff_2 (.D(d_ff_1_q), .clk(clock_1_out), .Q(d_ff_2_q));  // open: Qn, preset, reset
  and and_1 (and_1_out, d_ff_1_q, d_ff_2_q, d_ff_3_q, d_ff_4_q);
  D_Flip_Flop d_ff_3 (.D(d_ff_2_q), .clk(clock_1_out), .Q(d_ff_3_q));  // open: Qn, preset, reset
  D_Flip_Flop d_ff_4 (.D(d_ff_3_q), .clk(clock_1_out), .Q(d_ff_4_q));  // open: Qn, preset, reset
  T_Flip_Flop t_ff_1 (.T(en), .clk(and_1_out), .Q(hour1[0]), .Qn(t_ff_1_qn), .reset(or_1_out), .preset(1'b0));
  T_Flip_Flop t_ff_2 (.T(en), .clk(t_ff_1_qn), .Q(hour1[1]), .Qn(t_ff_2_qn), .reset(or_2_out), .preset(1'b0));
  T_Flip_Flop t_ff_3 (.T(en), .clk(t_ff_2_qn), .Q(hour1[2]), .Qn(t_ff_3_qn), .reset(or_2_out), .preset(1'b0));
  T_Flip_Flop t_ff_4 (.T(en), .clk(t_ff_3_qn), .Q(hour1[3]), .reset(or_3_out), .preset(1'b0));  // open: Qn
  and and_2 (and_2_out, ~hour2[0], hour2[1], ~hour2[2], ~hour2[3]);  // AND_Gate
  or or_1 (or_1_out, and_4_out, and_3_out);
  or or_2 (or_2_out, and_3_out, and_4_out);
  or or_3 (or_3_out, and_3_out, and_4_out);
  and and_3 (and_3_out, ~hour1[0], hour1[1], ~hour1[2], hour1[3], en);  // AND_Gate
  and and_4 (and_4_out, ~hour1[0], ~hour1[1], hour1[2], ~hour1[3], and_2_out, en);  // AND_Gate
  fonction_c fonction_c_1 (.W(hour1[3]), .X(hour1[2]), .Y(hour1[1]), .Z(hour1[0]), .c(fonction_c_1_c));
  fonction_a fonction_a_1 (.W(hour1[3]), .X(hour1[2]), .Y(hour1[1]), .Z(hour1[0]), .a(fonction_a_1_a));
  fonction_b fonction_b_1 (.W(hour1[3]), .X(hour1[2]), .Y(hour1[1]), .Z(hour1[0]), .b(fonction_b_1_b));
  fonction_d fonction_d_1 (.W(hour1[3]), .X(hour1[2]), .Y(hour1[1]), .Z(hour1[0]), .d(fonction_d_1_d));
  fonction_e fonction_e_1 (.W(hour1[3]), .X(hour1[2]), .Y(hour1[1]), .Z(hour1[0]), .e(fonction_e_1_e));
  fonction_f fonction_f_1 (.W(hour1[3]), .X(hour1[2]), .Y(hour1[1]), .Z(hour1[0]), .f(fonction_f_1_f));
  fonction_g fonction_g_1 (.W(hour1[3]), .X(hour1[2]), .Y(hour1[1]), .Z(hour1[0]), .g(fonction_g_1_g));
  _7_Segment_Display L_7_Segment_Display_1 (
    .g(fonction_g_1_g), .f(fonction_f_1_f), .a(fonction_a_1_a), .b(fonction_b_1_b), .e(fonction_e_1_e),
    .d(fonction_d_1_d), .c(fonction_c_1_c), .dp(en));
endmodule
