// Logisim project ctd_gated_clock.circ as structural Verilog: 10 circuits, main circuit main
module main (
  input  [5:0] in_1,
  input  SET,
  input  EN,
  input  [5:0] in_4,
  input  [5:0] in_5
);

  wire and_1_out, button_1_out, clock_1_out, comp_1_ending, d_ff_1_q, d_ff_1_qn, debouncer_1_out_3,
       dec7seg_1_out_7, dec7seg_1_out_8, dec7seg_1_out_9, dec7seg_1_out_10, dec7seg_1_out_11,
       dec7seg_1_out_12, dec7seg_1_out_13, dec7seg_1_out_14, dec7seg_2_out_7, dec7seg_2_out_8,
       dec7seg_2_out_9, dec7seg_2_out_10, dec7seg_2_out_11, dec7seg_2_out_12, dec7seg_2_out_13,
       dec7seg_2_out_14, dec7seg_3_out_7, dec7seg_3_out_8, dec7seg_3_out_9, dec7seg_3_out_10,
       dec7seg_3_out_11, dec7seg_3_out_12, dec7seg_3_out_13, dec7seg_3_out_14, dec7seg_4_out_7,
       dec7seg_4_out_8, dec7seg_4_out_9, dec7seg_4_out_10, dec7seg_4_out_11, dec7seg_4_out_12,
       dec7seg_4_out_13, dec7seg_4_out_14, dec7seg_5_out_7, dec7seg_5_out_8, dec7seg_5_out_9,
       dec7seg_5_out_10, dec7seg_5_out_11, dec7seg_5_out_12, dec7seg_5_out_13, dec7seg_5_out_14,
       dec7seg_6_out_7, dec7seg_6_out_8, dec7seg_6_out_9, dec7seg_6_out_10, dec7seg_6_out_11,
       dec7seg_6_out_12, dec7seg_6_out_13, dec7seg_6_out_14, min_1_under_m, one_1_out_7, one_1_out_8,
       one_1_out_9, one_1_out_10, one_1_out_11, one_1_out_12, one_2_out_7, one_2_out_8, one_2_out_9,
       one_2_out_10, one_2_out_11, one_2_out_12, one_3_out_7, one_3_out_8, one_3_out_9, one_3_out_10,
       one_3_out_11, one_3_out_12, sec_1_under_f, ten_1_out_7, ten_1_out_8, ten_1_out_9, ten_1_out_10,
       ten_1_out_11, ten_1_out_12, ten_2_out_7, ten_2_out_8, ten_2_out_9, ten_2_out_10, ten_2_out_11,
       ten_2_out_12, ten_3_out_7, ten_3_out_8, ten_3_out_9, ten_3_out_10, ten_3_out_11, ten_3_out_12,
       xor_1_out;
  wire [5:0] hour_1_hour, min_1_min, sec_1_sec;
  wire [16:0] adder_1_out, adder_2_out, multiplier_1_out, multiplier_2_out;

  Clock clock_1 (.out(clock_1_out));
  and and_1 (and_1_out, EN, d_ff_1_q);
  Button button_1 (.out(button_1_out));
  Multiplier #(.width(17)) multiplier_1 (
    .a({{11{1'b0}}, in_5}), .b(17'he10), .out(multiplier_1_out));  // open: cin, cout
  Multiplier #(.width(17)) multiplier_2 (
    .a({{11{1'b0}}, in_4}), .b(17'h3c), .out(multiplier_2_out));  // open: cin, cout
  sec sec_1 (
    .SEC_IN(in_1), .SET(SET), .EN(EN), .RST(and_1_out), .CLK(clock_1_out), .SEC(sec_1_sec),
    .UNDER_F(sec_1_under_f));
  xor xor_1 (xor_1_out, d_ff_1_q, EN);
  Adder #(.width(17)) adder_1 (.a({{11{1'b0}}, in_1}), .b(multiplier_2_out), .out(adder_1_out));  // open: cin, cout
  debouncer debouncer_1 (.button(button_1_out), .CLK(clock_1_out), .out_3(debouncer_1_out_3));
  min min_1 (
    .in_1(in_4), .SET(SET), .UNDER_F(sec_1_under_f), .EN(EN), .RST(and_1_out), .CLK(clock_1_out),
    .MIN(min_1_min), .UNDER_M(min_1_under_m));
  Adder #(.width(17)) adder_2 (.a(adder_1_out), .b(multiplier_1_out), .out(adder_2_out));  // open: cin, cout
  comp comp_1 (
    .en_comp(xor_1_out), .tps(adder_2_out), .CLK(clock_1_out), .RST_BUTTON(debouncer_1_out_3),
    .ending(comp_1_ending));
  ten ten_1 (
    .in_1(sec_1_sec[5]), .in_2(sec_1_sec[4]), .in_3(sec_1_sec[3]), .in_4(sec_1_sec[2]), .in_5(sec_1_sec[1]),
    .in_6(sec_1_sec[0]), .out_7(ten_1_out_7), .out_8(ten_1_out_8), .out_9(ten_1_out_9),
    .out_10(ten_1_out_10), .out_11(ten_1_out_11), .out_12(ten_1_out_12));
  D_Flip_Flop d_ff_1 (
    .D(d_ff_1_qn), .clk(comp_1_ending), .Q(d_ff_1_q), .Qn(d_ff_1_qn), .reset(debouncer_1_out_3));  // open: preset
  hour hour_1 (
    .in_1(in_5), .SET(SET), .UNDER_F(sec_1_under_f), .UNDER_M(min_1_under_m), .EN(EN), .RST(and_1_out),
    .CLK(clock_1_out), .HOUR(hour_1_hour));  // open: UNDER_H
  dec7seg dec7seg_1 (
    .in_1(ten_1_out_7), .in_2(ten_1_out_8), .in_3(ten_1_out_9), .in_4(ten_1_out_10), .in_5(ten_1_out_11),
    .in_6(ten_1_out_12), .out_7(dec7seg_1_out_7), .out_8(dec7seg_1_out_8), .out_9(dec7seg_1_out_9),
    .out_10(dec7seg_1_out_10), .out_11(dec7seg_1_out_11), .out_12(dec7seg_1_out_12),
    .out_13(dec7seg_1_out_13), .out_14(dec7seg_1_out_14));
  ten ten_2 (
    .in_1(min_1_min[5]), .in_2(min_1_min[4]), .in_3(min_1_min[3]), .in_4(min_1_min[2]), .in_5(min_1_min[1]),
    .in_6(min_1_min[0]), .out_7(ten_2_out_7), .out_8(ten_2_out_8), .out_9(ten_2_out_9),
    .out_10(ten_2_out_10), .out_11(ten_2_out_11), .out_12(ten_2_out_12));
  _7_Segment_Display u_7_segment_display_1 (
    .g(dec7seg_1_out_13), .f(dec7seg_1_out_12), .a(dec7seg_1_out_7), .b(dec7seg_1_out_8),
    .e(dec7seg_1_out_11), .d(dec7seg_1_out_10), .c(dec7seg_1_out_9), .dp(dec7seg_1_out_14));
  dec7seg dec7seg_2 (
    .in_1(ten_2_out_7), .in_2(ten_2_out_8), .in_3(ten_2_out_9), .in_4(ten_2_out_10), .in_5(ten_2_out_11),
    .in_6(ten_2_out_12), .out_7(dec7seg_2_out_7), .out_8(dec7seg_2_out_8), .out_9(dec7seg_2_out_9),
    .out_10(dec7seg_2_out_10), .out_11(dec7seg_2_out_11), .out_12(dec7seg_2_out_12),
    .out_13(dec7seg_2_out_13), .out_14(dec7seg_2_out_14));
  ten ten_3 (
    .in_1(hour_1_hour[5]), .in_2(hour_1_hour[4]), .in_3(hour_1_hour[3]), .in_4(hour_1_hour[2]),
    .in_5(hour_1_hour[1]), .in_6(hour_1_hour[0]), .out_7(ten_3_out_7), .out_8(ten_3_out_8),
    .out_9(ten_3_out_9), .out_10(ten_3_out_10), .out_11(ten_3_out_11), .out_12(ten_3_out_12));
  _7_Segment_Display u_7_segment_display_2 (
    .g(dec7seg_2_out_13), .f(dec7seg_2_out_12), .a(dec7seg_2_out_7), .b(dec7seg_2_out_8),
    .e(dec7seg_2_out_11), .d(dec7seg_2_out_10), .c(dec7seg_2_out_9), .dp(dec7seg_2_out_14));
  dec7seg dec7seg_3 (
    .in_1(ten_3_out_7), .in_2(ten_3_out_8), .in_3(ten_3_out_9), .in_4(ten_3_out_10), .in_5(ten_3_out_11),
    .in_6(ten_3_out_12), .out_7(dec7seg_3_out_7), .out_8(dec7seg_3_out_8), .out_9(dec7seg_3_out_9),
    .out_10(dec7seg_3_out_10), .out_11(dec7seg_3_out_11), .out_12(dec7seg_3_out_12),
    .out_13(dec7seg_3_out_13), .out_14(dec7seg_3_out_14));
  one one_1 (
    .in_1(sec_1_sec[5]), .in_2(sec_1_sec[4]), .in_3(sec_1_sec[3]), .in_4(sec_1_sec[2]), .in_5(sec_1_sec[1]),
    .in_6(sec_1_sec[0]), .out_7(one_1_out_7), .out_8(one_1_out_8), .out_9(one_1_out_9),
    .out_10(one_1_out_10), .out_11(one_1_out_11), .out_12(one_1_out_12));
  _7_Segment_Display u_7_segment_display_3 (
    .g(dec7seg_3_out_13), .f(dec7seg_3_out_12), .a(dec7seg_3_out_7), .b(dec7seg_3_out_8),
    .e(dec7seg_3_out_11), .d(dec7seg_3_out_10), .c(dec7seg_3_out_9), .dp(dec7seg_3_out_14));
  dec7seg dec7seg_4 (
    .in_1(one_1_out_7), .in_2(one_1_out_8), .in_3(one_1_out_9), .in_4(one_1_out_10), .in_5(one_1_out_11),
    .in_6(one_1_out_12), .out_7(dec7seg_4_out_7), .out_8(dec7seg_4_out_8), .out_9(dec7seg_4_out_9),
    .out_10(dec7seg_4_out_10), .out_11(dec7seg_4_out_11), .out_12(dec7seg_4_out_12),
    .out_13(dec7seg_4_out_13), .out_14(dec7seg_4_out_14));
  one one_2 (
    .in_1(min_1_min[5]), .in_2(min_1_min[4]), .in_3(min_1_min[3]), .in_4(min_1_min[2]), .in_5(min_1_min[1]),
    .in_6(min_1_min[0]), .out_7(one_2_out_7), .out_8(one_2_out_8), .out_9(one_2_out_9),
    .out_10(one_2_out_10), .out_11(one_2_out_11), .out_12(one_2_out_12));
  _7_Segment_Display u_7_segment_display_4 (
    .g(dec7seg_4_out_13), .f(dec7seg_4_out_12), .a(dec7seg_4_out_7), .b(dec7seg_4_out_8),
    .e(dec7seg_4_out_11), .d(dec7seg_4_out_10), .c(dec7seg_4_out_9), .dp(dec7seg_4_out_14));
  dec7seg dec7seg_5 (
    .in_1(one_2_out_7), .in_2(one_2_out_8), .in_3(one_2_out_9), .in_4(one_2_out_10), .in_5(one_2_out_11),
    .in_6(one_2_out_12), .out_7(dec7seg_5_out_7), .out_8(dec7seg_5_out_8), .out_9(dec7seg_5_out_9),
    .out_10(dec7seg_5_out_10), .out_11(dec7seg_5_out_11), .out_12(dec7seg_5_out_12),
    .out_13(dec7seg_5_out_13), .out_14(dec7seg_5_out_14));
  one one_3 (
    .in_1(hour_1_hour[5]), .in_2(hour_1_hour[4]), .in_3(hour_1_hour[3]), .in_4(hour_1_hour[2]),
    .in_5(hour_1_hour[1]), .in_6(hour_1_hour[0]), .out_7(one_3_out_7), .out_8(one_3_out_8),
    .out_9(one_3_out_9), .out_10(one_3_out_10), .out_11(one_3_out_11), .out_12(one_3_out_12));
  _7_Segment_Display u_7_segment_display_5 (
    .g(dec7seg_5_out_13), .f(dec7seg_5_out_12), .a(dec7seg_5_out_7), .b(dec7seg_5_out_8),
    .e(dec7seg_5_out_11), .d(dec7seg_5_out_10), .c(dec7seg_5_out_9), .dp(dec7seg_5_out_14));
  dec7seg dec7seg_6 (
    .in_1(one_3_out_7), .in_2(one_3_out_8), .in_3(one_3_out_9), .in_4(one_3_out_10), .in_5(one_3_out_11),
    .in_6(one_3_out_12), .out_7(dec7seg_6_out_7), .out_8(dec7seg_6_out_8), .out_9(dec7seg_6_out_9),
    .out_10(dec7seg_6_out_10), .out_11(dec7seg_6_out_11), .out_12(dec7seg_6_out_12),
    .out_13(dec7seg_6_out_13), .out_14(dec7seg_6_out_14));
  _7_Segment_Display u_7_segment_display_6 (
    .g(dec7seg_6_out_13), .f(dec7seg_6_out_12), .a(dec7seg_6_out_7), .b(dec7seg_6_out_8),
    .e(dec7seg_6_out_11), .d(dec7seg_6_out_10), .c(dec7seg_6_out_9), .dp(dec7seg_6_out_14));
endmodule

module sec (
  input  [5:0] SEC_IN,
  input  SET,
  input  EN,
  input  RST,
  input  CLK,
  output [5:0] SEC,
  output UNDER_F
);

  wire and_1_out, and_2_out, and_3_out, and_4_out, and_5_out, and_6_out, and_7_out, and_8_out, and_9_out,
       and_10_out, and_11_out, and_12_out, and_13_out, and_14_out, and_15_out, and_16_out, and_17_out,
       and_19_out, and_20_out, and_21_out, and_22_out, or_1_out, or_2_out, or_3_out, or_4_out, or_5_out,
       or_6_out, or_7_out, t_ff_1_qn, t_ff_2_qn, t_ff_3_qn, t_ff_4_qn, t_ff_5_qn, t_ff_6_qn;
  wire [0:0] and_24_out;
  wire [5:0] multiplexer_1_out;

  or or_1 (or_1_out, and_24_out[0], SET);
  Multiplexer #(.select(2), .width(6), .enable("false")) multiplexer_1 (
    .in0({6{1'b0}}), .in1(6'b111011), .in2(SEC_IN), .in3({6{1'b0}}), .out(multiplexer_1_out),
    .sel({SET, and_24_out[0]}));
  and and_1 (and_1_out, or_1_out, multiplexer_1_out[0]);
  T_Flip_Flop t_ff_1 (.T(EN), .clk(CLK), .Q(SEC[0]), .Qn(t_ff_1_qn), .reset(or_2_out), .preset(and_1_out));
  or or_2 (or_2_out, RST, and_9_out);
  T_Flip_Flop t_ff_2 (.T(and_2_out), .clk(CLK), .Q(SEC[1]), .Qn(t_ff_2_qn), .reset(or_5_out), .preset(and_10_out));
  and and_2 (and_2_out, t_ff_1_qn, EN);
  T_Flip_Flop t_ff_3 (.T(and_3_out), .clk(CLK), .Q(SEC[2]), .Qn(t_ff_3_qn), .reset(or_6_out), .preset(and_12_out));
  and and_3 (and_3_out, and_19_out, EN);
  T_Flip_Flop t_ff_4 (.T(and_4_out), .clk(CLK), .Q(SEC[3]), .Qn(t_ff_4_qn), .reset(or_7_out), .preset(and_15_out));
  and and_4 (and_4_out, and_20_out, EN);
  and and_5 (and_5_out, multiplexer_1_out[4], or_1_out);
  T_Flip_Flop t_ff_5 (.T(and_6_out), .clk(CLK), .Q(SEC[4]), .Qn(t_ff_5_qn), .reset(or_3_out), .preset(and_5_out));
  and and_6 (and_6_out, and_21_out, EN);
  or or_3 (or_3_out, RST, and_16_out);
  and and_7 (and_7_out, multiplexer_1_out[5], or_1_out);
  T_Flip_Flop t_ff_6 (.T(and_8_out), .clk(CLK), .Q(SEC[5]), .Qn(t_ff_6_qn), .reset(or_4_out), .preset(and_7_out));
  and and_8 (and_8_out, and_22_out, EN);
  or or_4 (or_4_out, RST, and_17_out);
  and and_9 (and_9_out, or_1_out, ~multiplexer_1_out[0]);  // AND_Gate
  and and_10 (and_10_out, or_1_out, multiplexer_1_out[1]);
  and and_11 (and_11_out, or_1_out, ~multiplexer_1_out[1]);  // AND_Gate
  or or_5 (or_5_out, RST, and_11_out);
  and and_12 (and_12_out, or_1_out, multiplexer_1_out[2]);
  and and_13 (and_13_out, or_1_out, ~multiplexer_1_out[2]);  // AND_Gate
  or or_6 (or_6_out, RST, and_13_out);
  and and_14 (and_14_out, or_1_out, ~multiplexer_1_out[3]);  // AND_Gate
  and and_15 (and_15_out, or_1_out, multiplexer_1_out[3]);
  or or_7 (or_7_out, RST, and_14_out);
  and and_16 (and_16_out, or_1_out, ~multiplexer_1_out[4]);  // AND_Gate
  and and_17 (and_17_out, or_1_out, ~multiplexer_1_out[5]);  // AND_Gate
  // AND_Gate and_18 has open pins: in0=t_ff_6_qn, in1=and_22_out, out=open
  and and_19 (and_19_out, t_ff_2_qn, t_ff_1_qn);
  and and_20 (and_20_out, t_ff_3_qn, and_19_out);
  and and_21 (and_21_out, t_ff_4_qn, and_20_out);
  and and_22 (and_22_out, t_ff_5_qn, and_21_out);
  and and_23 (UNDER_F, ~SEC[0], ~SEC[1], ~SEC[2], ~SEC[3], ~SEC[4], ~SEC[5]);  // AND_Gate
  and and_24 (and_24_out[0], SEC[0], SEC[1], SEC[2], SEC[3], SEC[4], SEC[5]);
endmodule

module min (
  input  [5:0] in_1,
  input  SET,
  input  UNDER_F,
  input  EN,
  input  RST,
  input  CLK,
  output [5:0] MIN,
  output UNDER_M
);

  wire and_1_out, and_2_out, and_3_out, and_4_out, and_5_out, and_6_out, and_7_out, and_8_out, and_9_out,
       and_10_out, and_11_out, and_12_out, and_13_out, and_14_out, and_15_out, and_16_out, and_17_out,
       and_18_out, and_20_out, and_21_out, and_22_out, and_23_out, or_1_out, or_2_out, or_3_out, or_4_out,
       or_5_out, or_6_out, or_7_out, t_ff_1_qn, t_ff_2_qn, t_ff_3_qn, t_ff_4_qn, t_ff_5_qn, t_ff_6_qn;
  wire [0:0] and_25_out;
  wire [5:0] multiplexer_1_out;

  or or_1 (or_1_out, and_25_out[0], SET);
  Multiplexer #(.select(2), .width(6), .enable("false")) multiplexer_1 (
    .in0({6{1'b0}}), .in1(6'b111011), .in2(in_1), .in3({6{1'b0}}), .out(multiplexer_1_out),
    .sel({SET, and_25_out[0]}));
  and and_1 (and_1_out, or_1_out, multiplexer_1_out[0]);
  T_Flip_Flop t_ff_1 (.T(and_2_out), .clk(CLK), .Q(MIN[0]), .Qn(t_ff_1_qn), .reset(or_2_out), .preset(and_1_out));
  and and_2 (and_2_out, UNDER_F, EN);
  or or_2 (or_2_out, RST, and_10_out);
  T_Flip_Flop t_ff_2 (.T(and_3_out), .clk(CLK), .Q(MIN[1]), .Qn(t_ff_2_qn), .reset(or_5_out), .preset(and_11_out));
  and and_3 (and_3_out, t_ff_1_qn, UNDER_F, EN);
  T_Flip_Flop t_ff_3 (.T(and_4_out), .clk(CLK), .Q(MIN[2]), .Qn(t_ff_3_qn), .reset(or_6_out), .preset(and_13_out));
  and and_4 (and_4_out, and_20_out, UNDER_F, EN);
  T_Flip_Flop t_ff_4 (.T(and_5_out), .clk(CLK), .Q(MIN[3]), .Qn(t_ff_4_qn), .reset(or_7_out), .preset(and_16_out));
  and and_5 (and_5_out, and_21_out, UNDER_F, EN);
  and and_6 (and_6_out, multiplexer_1_out[4], or_1_out);
  T_Flip_Flop t_ff_5 (.T(and_7_out), .clk(CLK), .Q(MIN[4]), .Qn(t_ff_5_qn), .reset(or_3_out), .preset(and_6_out));
  and and_7 (and_7_out, and_22_out, UNDER_F, EN);
  or or_3 (or_3_out, RST, and_17_out);
  and and_8 (and_8_out, multiplexer_1_out[5], or_1_out);
  T_Flip_Flop t_ff_6 (.T(and_9_out), .clk(CLK), .Q(MIN[5]), .Qn(t_ff_6_qn), .reset(or_4_out), .preset(and_8_out));
  and and_9 (and_9_out, and_23_out, UNDER_F, EN);
  or or_4 (or_4_out, RST, and_18_out);
  and and_10 (and_10_out, or_1_out, ~multiplexer_1_out[0]);  // AND_Gate
  and and_11 (and_11_out, or_1_out, multiplexer_1_out[1]);
  and and_12 (and_12_out, or_1_out, ~multiplexer_1_out[1]);  // AND_Gate
  or or_5 (or_5_out, RST, and_12_out);
  and and_13 (and_13_out, or_1_out, multiplexer_1_out[2]);
  and and_14 (and_14_out, or_1_out, ~multiplexer_1_out[2]);  // AND_Gate
  or or_6 (or_6_out, RST, and_14_out);
  and and_15 (and_15_out, or_1_out, ~multiplexer_1_out[3]);  // AND_Gate
  and and_16 (and_16_out, or_1_out, multiplexer_1_out[3]);
  or or_7 (or_7_out, RST, and_15_out);
  and and_17 (and_17_out, or_1_out, ~multiplexer_1_out[4]);  // AND_Gate
  and and_18 (and_18_out, or_1_out, ~multiplexer_1_out[5]);  // AND_Gate
  // AND_Gate and_19 has open pins: in0=t_ff_6_qn, in1=and_23_out, out=open
  and and_20 (and_20_out, t_ff_2_qn, t_ff_1_qn);
  and and_21 (and_21_out, t_ff_3_qn, and_20_out);
  and and_22 (and_22_out, t_ff_4_qn, and_21_out);
  and and_23 (and_23_out, t_ff_5_qn, and_22_out);
  and and_24 (UNDER_M, ~MIN[0], ~MIN[1], ~MIN[2], ~MIN[3], ~MIN[4], ~MIN[5]);  // AND_Gate
  and and_25 (and_25_out[0], MIN[0], MIN[1], MIN[2], MIN[3], MIN[4], MIN[5]);
endmodule

module hour (
  input  [5:0] in_1,
  input  SET,
  input  UNDER_F,
  input  UNDER_M,
  input  EN,
  input  RST,
  input  CLK,
  output UNDER_H,
  output [5:0] HOUR
);

  wire and_1_out, and_2_out, and_3_out, and_4_out, and_5_out, and_6_out, and_7_out, and_8_out, and_9_out,
       and_10_out, and_11_out, and_12_out, and_13_out, and_14_out, and_15_out, and_16_out, and_17_out,
       and_18_out, and_19_out, and_21_out, and_22_out, and_23_out, and_24_out, or_1_out, or_2_out, or_3_out,
       or_4_out, or_5_out, or_6_out, or_7_out, t_ff_1_qn, t_ff_2_qn, t_ff_3_qn, t_ff_4_qn, t_ff_5_qn,
       t_ff_6_qn;
  wire [0:0] and_26_out;
  wire [5:0] multiplexer_1_out;

  Multiplexer #(.select(2), .width(6), .enable("false")) multiplexer_1 (
    .in0({6{1'b0}}), .in1({6{1'b0}}), .in2(in_1), .in3({6{1'b0}}), .out(multiplexer_1_out),
    .sel({SET, and_26_out[0]}));
  or or_1 (or_1_out, and_26_out[0], SET);
  and and_1 (and_1_out, UNDER_F, UNDER_M);
  and and_2 (and_2_out, or_1_out, multiplexer_1_out[0]);
  T_Flip_Flop t_ff_1 (.T(and_3_out), .clk(CLK), .Q(HOUR[0]), .Qn(t_ff_1_qn), .reset(or_2_out), .preset(and_2_out));
  and and_3 (and_3_out, and_1_out, EN);
  or or_2 (or_2_out, RST, and_11_out);
  T_Flip_Flop t_ff_2 (.T(and_4_out), .clk(CLK), .Q(HOUR[1]), .Qn(t_ff_2_qn), .reset(or_5_out), .preset(and_13_out));
  and and_4 (and_4_out, t_ff_1_qn, and_1_out, EN);
  T_Flip_Flop t_ff_3 (.T(and_5_out), .clk(CLK), .Q(HOUR[2]), .Qn(t_ff_3_qn), .reset(or_6_out), .preset(and_14_out));
  and and_5 (and_5_out, and_21_out, and_1_out, EN);
  T_Flip_Flop t_ff_4 (.T(and_6_out), .clk(CLK), .Q(HOUR[3]), .Qn(t_ff_4_qn), .reset(or_7_out), .preset(and_17_out));
  and and_6 (and_6_out, and_22_out, and_1_out, EN);
  and and_7 (and_7_out, multiplexer_1_out[4], or_1_out);
  T_Flip_Flop t_ff_5 (.T(and_8_out), .clk(CLK), .Q(HOUR[4]), .Qn(t_ff_5_qn), .reset(or_3_out), .preset(and_7_out));
  and and_8 (and_8_out, and_23_out, and_1_out, EN);
  or or_3 (or_3_out, RST, and_18_out);
  and and_9 (and_9_out, multiplexer_1_out[5], or_1_out);
  T_Flip_Flop t_ff_6 (.T(and_10_out), .clk(CLK), .Q(HOUR[5]), .Qn(t_ff_6_qn), .reset(or_4_out), .preset(and_9_out));
  and and_10 (and_10_out, and_24_out, and_1_out, EN);
  or or_4 (or_4_out, RST, and_19_out);
  and and_11 (and_11_out, or_1_out, ~multiplexer_1_out[0]);  // AND_Gate
  and and_12 (and_12_out, or_1_out, ~multiplexer_1_out[1]);  // AND_Gate
  and and_13 (and_13_out, or_1_out, multiplexer_1_out[1]);
  or or_5 (or_5_out, RST, and_12_out);
  and and_14 (and_14_out, or_1_out, multiplexer_1_out[2]);
  and and_15 (and_15_out, or_1_out, ~multiplexer_1_out[2]);  // AND_Gate
  or or_6 (or_6_out, RST, and_15_out);
  and and_16 (and_16_out, or_1_out, ~multiplexer_1_out[3]);  // AND_Gate
  and and_17 (and_17_out, or_1_out, multiplexer_1_out[3]);
  or or_7 (or_7_out, RST, and_16_out);
  and and_18 (and_18_out, or_1_out, ~multiplexer_1_out[4]);  // AND_Gate
  and and_19 (and_19_out, or_1_out, ~multiplexer_1_out[5]);  // AND_Gate
  // AND_Gate and_20 has open pins: in0=t_ff_6_qn, in1=and_24_out, out=open
  and and_21 (and_21_out, t_ff_2_qn, t_ff_1_qn);
  and and_22 (and_22_out, t_ff_3_qn, and_21_out);
  and and_23 (and_23_out, t_ff_4_qn, and_22_out);
  and and_24 (and_24_out, t_ff_5_qn, and_23_out);
  and and_25 (UNDER_H, ~HOUR[5], ~HOUR[4], ~HOUR[3], ~HOUR[2], ~HOUR[1], ~HOUR[0]);  // AND_Gate
  and and_26 (and_26_out[0], HOUR[0], HOUR[1], HOUR[2], HOUR[3], HOUR[4], HOUR[5]);
endmodule

module one (
  input  in_1,
  input  in_2,
  input  in_3,
  input  in_4,
  input  in_5,
  input  in_6,
  output out_7,
  output out_8,
  output out_9,
  output out_10,
  output out_11,
  output out_12
);

  wire and_1_out, and_2_out, and_3_out, and_4_out, and_5_out, and_6_out, and_7_out, and_8_out, and_9_out,
       and_10_out, and_11_out, and_12_out, and_13_out, and_14_out, and_15_out, and_16_out, and_17_out,
       and_18_out, and_19_out, and_20_out, and_21_out, and_22_out, and_23_out, and_24_out, not_1_out,
       not_2_out, not_3_out, not_4_out, not_5_out, not_6_out, not_7_out, not_8_out, not_9_out, not_10_out,
       not_11_out, not_12_out, not_13_out, not_14_out, not_15_out, not_16_out, not_17_out, not_18_out,
       not_19_out, not_20_out, not_21_out, not_22_out, not_23_out, not_24_out, not_25_out, not_26_out,
       not_27_out, not_28_out, not_29_out, not_30_out, not_31_out, not_32_out, not_33_out, not_34_out,
       not_35_out, not_36_out, not_37_out, not_38_out, not_39_out, not_40_out, not_41_out, not_42_out,
       not_43_out, not_44_out, not_45_out, not_46_out, not_47_out, not_48_out, not_49_out, not_50_out,
       not_51_out, not_52_out, not_53_out, not_54_out;

  not not_1 (not_1_out, in_1);
  not not_2 (not_2_out, in_2);
  not not_3 (not_3_out, in_4);
  not not_4 (not_4_out, in_5);
  not not_5 (not_5_out, in_1);
  not not_6 (not_6_out, in_3);
  not not_7 (not_7_out, in_4);
  not not_8 (not_8_out, in_1);
  not not_9 (not_9_out, in_5);
  not not_10 (not_10_out, in_2);
  not not_11 (not_11_out, in_3);
  not not_12 (not_12_out, in_3);
  not not_13 (not_13_out, in_4);
  not not_14 (not_14_out, in_5);
  not not_15 (not_15_out, in_4);
  not not_16 (not_16_out, in_2);
  not not_17 (not_17_out, in_3);
  not not_18 (not_18_out, in_5);
  not not_19 (not_19_out, in_1);
  not not_20 (not_20_out, in_2);
  not not_21 (not_21_out, in_1);
  not not_22 (not_22_out, in_4);
  not not_23 (not_23_out, in_5);
  not not_24 (not_24_out, in_1);
  not not_25 (not_25_out, in_4);
  not not_26 (not_26_out, in_4);
  not not_27 (not_27_out, in_5);
  not not_28 (not_28_out, in_2);
  not not_29 (not_29_out, in_3);
  not not_30 (not_30_out, in_4);
  not not_31 (not_31_out, in_2);
  not not_32 (not_32_out, in_3);
  not not_33 (not_33_out, in_1);
  not not_34 (not_34_out, in_2);
  not not_35 (not_35_out, in_3);
  not not_36 (not_36_out, in_1);
  not not_37 (not_37_out, in_3);
  not not_38 (not_38_out, in_1);
  not not_39 (not_39_out, in_2);
  not not_40 (not_40_out, in_5);
  not not_41 (not_41_out, in_1);
  not not_42 (not_42_out, in_3);
  not not_43 (not_43_out, in_4);
  not not_44 (not_44_out, in_5);
  not not_45 (not_45_out, in_1);
  not not_46 (not_46_out, in_4);
  not not_47 (not_47_out, in_2);
  not not_48 (not_48_out, in_3);
  not not_49 (not_49_out, in_5);
  not not_50 (not_50_out, in_3);
  not not_51 (not_51_out, in_5);
  not not_52 (not_52_out, in_2);
  not not_53 (not_53_out, in_4);
  not not_54 (not_54_out, in_5);
  and and_1 (and_1_out, not_1_out, not_2_out, in_3, not_3_out, not_4_out);
  and and_2 (and_2_out, not_5_out, in_2, not_6_out, not_7_out, in_5);
  and and_3 (and_3_out, not_8_out, in_2, in_3, in_4, not_9_out);
  and and_4 (and_4_out, in_1, not_10_out, not_11_out, in_4, in_5);
  and and_5 (and_5_out, in_1, in_2, not_12_out, not_13_out, not_14_out);
  and and_6 (and_6_out, in_1, in_2, in_3, not_15_out, in_5);
  and and_7 (and_7_out, not_16_out, not_17_out, in_4, not_18_out);
  and and_8 (and_8_out, not_19_out, not_20_out, in_4, in_5);
  and and_9 (and_9_out, not_21_out, in_2, not_22_out, not_23_out);
  and and_10 (and_10_out, not_24_out, in_2, in_3, not_25_out);
  and and_11 (and_11_out, in_2, in_3, not_26_out, not_27_out);
  and and_12 (and_12_out, in_1, not_28_out, not_29_out, not_30_out, in_5);
  and and_13 (and_13_out, in_1, not_31_out, in_3, in_4);
  and and_14 (and_14_out, in_1, in_2, not_32_out, in_4, in_5);
  and and_15 (and_15_out, not_33_out, not_34_out, not_35_out, in_5);
  and and_16 (and_16_out, not_36_out, not_37_out, in_4, in_5);
  and and_17 (and_17_out, not_38_out, not_39_out, in_3, in_4, not_40_out);
  and and_18 (and_18_out, not_41_out, in_2, not_42_out, not_43_out, not_44_out);
  and and_19 (and_19_out, not_45_out, in_2, in_3, not_46_out, in_5);
  and and_20 (and_20_out, in_1, not_47_out, not_48_out, not_49_out);
  and and_21 (and_21_out, in_1, not_50_out, in_4, not_51_out);
  and and_22 (and_22_out, in_1, not_52_out, in_3, in_5);
  and and_23 (and_23_out, in_1, in_3, in_4, in_5);
  and and_24 (and_24_out, in_1, in_2, in_3, not_53_out, not_54_out);
  or or_1 (out_9, and_1_out, and_2_out, and_3_out, and_4_out, and_5_out, and_6_out);
  or or_2 (out_10, and_7_out, and_8_out, and_9_out, and_10_out, and_11_out, and_12_out, and_13_out, and_14_out);
  or or_3 (out_11, and_15_out, and_16_out, and_17_out, and_18_out, and_19_out, and_20_out, and_21_out, and_22_out, and_23_out, and_24_out);

  assign out_7 = 1'b0;
  assign out_8 = 1'b0;
  assign out_12 = in_6;
endmodule

module ten (
  input  in_1,
  input  in_2,
  input  in_3,
  input  in_4,
  input  in_5,
  input  in_6,
  output out_7,
  output out_8,
  output out_9,
  output out_10,
  output out_11,
  output out_12
);

  wire and_1_out, and_2_out, and_3_out, and_4_out, and_5_out, and_6_out, and_7_out, and_8_out, and_9_out,
       and_10_out, and_11_out, and_12_out, and_13_out, and_14_out, not_1_out, not_2_out, not_3_out,
       not_4_out, not_5_out, not_6_out, not_7_out, not_8_out, not_9_out, not_10_out, not_11_out, not_12_out,
       not_13_out, not_14_out, not_15_out, not_16_out, not_17_out;

  and and_1 (and_1_out, in_1, in_3);
  and and_2 (and_2_out, in_1, in_2);
  not not_1 (not_1_out, in_1);
  and and_3 (and_3_out, not_1_out, in_2, in_4);
  not not_2 (not_2_out, in_1);
  and and_4 (and_4_out, not_2_out, in_2, in_3);
  and and_5 (and_5_out, in_2, in_3, in_4);
  and and_6 (and_6_out, in_1, not_3_out, not_4_out);
  not not_3 (not_3_out, in_2);
  not not_4 (not_4_out, in_3);
  not not_5 (not_5_out, in_1);
  not not_6 (not_6_out, in_2);
  not not_7 (not_7_out, in_1);
  not not_8 (not_8_out, in_2);
  not not_9 (not_9_out, in_1);
  not not_10 (not_10_out, in_1);
  not not_11 (not_11_out, in_3);
  not not_12 (not_12_out, in_4);
  not not_13 (not_13_out, in_2);
  not not_14 (not_14_out, in_3);
  not not_15 (not_15_out, in_3);
  not not_16 (not_16_out, in_3);
  not not_17 (not_17_out, in_4);
  or or_1 (out_10, and_1_out, and_2_out);
  or or_2 (out_11, and_3_out, and_4_out, and_5_out, and_6_out);
  and and_7 (and_7_out, not_5_out, not_6_out, in_3, in_5);
  and and_8 (and_8_out, not_7_out, not_8_out, in_3, in_4);
  and and_9 (and_9_out, not_9_out, in_3, in_4, in_5);
  and and_10 (and_10_out, not_10_out, in_2, not_11_out, not_12_out);
  and and_11 (and_11_out, in_1, not_13_out, not_14_out);
  and and_12 (and_12_out, in_1, not_15_out, in_5);
  and and_13 (and_13_out, in_1, not_16_out, in_4);
  and and_14 (and_14_out, in_1, in_2, in_3, not_17_out);
  or or_3 (out_12, and_7_out, and_8_out, and_9_out, and_10_out, and_11_out, and_12_out, and_13_out, and_14_out);

  assign out_7 = 1'b0;
  assign out_8 = 1'b0;
  assign out_9 = 1'b0;
endmodule

module dec7seg (
  input  in_1,
  input  in_2,
  input  in_3,
  input  in_4,
  input  in_5,
  input  in_6,
  output out_7,
  output out_8,
  output out_9,
  output out_10,
  output out_11,
  output out_12,
  output out_13,
  output out_14
);

  wire and_1_out, and_2_out, and_3_out, and_4_out, and_5_out, and_6_out, and_7_out, and_8_out, and_9_out,
       and_10_out, and_11_out, and_12_out, and_13_out, and_14_out, and_15_out, and_16_out, and_17_out,
       and_18_out, and_19_out, and_20_out, and_21_out, and_22_out, and_23_out, and_24_out, and_25_out,
       and_26_out, and_27_out, and_28_out, and_29_out, and_30_out, and_31_out, and_32_out, and_33_out,
       and_34_out, and_35_out, and_36_out, and_37_out, and_38_out, and_39_out, and_40_out, and_41_out,
       and_42_out, and_43_out, and_44_out, and_45_out, and_46_out, and_47_out, and_48_out, and_49_out,
       and_50_out, and_51_out, and_52_out, and_53_out, and_54_out, and_55_out, and_56_out, and_57_out,
       and_58_out, and_59_out, and_60_out, and_61_out, and_62_out, and_63_out, and_64_out, and_65_out,
       and_66_out, and_67_out, and_68_out, and_69_out, and_70_out, and_71_out, and_72_out, and_73_out,
       and_74_out, and_75_out, and_76_out, and_77_out, and_78_out, and_79_out, and_80_out, and_81_out,
       and_82_out, and_83_out, and_84_out, not_1_out, not_2_out, not_3_out, not_4_out, not_5_out, not_6_out,
       not_7_out, not_8_out, not_9_out, not_10_out, not_11_out, not_12_out, not_13_out, not_14_out,
       not_15_out, not_16_out, not_17_out, not_18_out, not_19_out, not_20_out, not_21_out, not_22_out,
       not_23_out, not_24_out, not_25_out, not_26_out, not_27_out, not_28_out, not_29_out, not_30_out,
       not_31_out, not_32_out, not_33_out, not_34_out, not_35_out, not_36_out, not_37_out, not_38_out,
       not_39_out, not_40_out, not_41_out, not_42_out, not_43_out, not_44_out, not_45_out, not_46_out,
       not_47_out, not_48_out, not_49_out, not_50_out, not_51_out, not_52_out, not_53_out, not_54_out,
       not_55_out, not_56_out, not_57_out, not_58_out, not_59_out, not_60_out, not_61_out, not_62_out,
       not_63_out, not_64_out, not_65_out, not_66_out, not_67_out, not_68_out, not_69_out, not_70_out,
       not_71_out, not_72_out, not_73_out, not_74_out, not_75_out, not_76_out, not_77_out, not_78_out,
       not_79_out, not_80_out, not_81_out, not_82_out, not_83_out, not_84_out, not_85_out, not_86_out,
       not_87_out, not_88_out, not_89_out, not_90_out, not_91_out, not_92_out, not_93_out, not_94_out,
       not_95_out, not_96_out, not_97_out, not_98_out, not_99_out, not_100_out, not_101_out, not_102_out,
       not_103_out, not_104_out, not_105_out, not_106_out, not_107_out, not_108_out, not_109_out,
       not_110_out, not_111_out, not_112_out, not_113_out, not_114_out, not_115_out, not_116_out,
       not_117_out, not_118_out, not_119_out, not_120_out, not_121_out, not_122_out, not_123_out,
       not_124_out, not_125_out, not_126_out, not_127_out, not_128_out, not_129_out, not_130_out,
       not_131_out, not_132_out, not_133_out, not_134_out, not_135_out, not_136_out, not_137_out,
       not_138_out, not_139_out, not_140_out, not_141_out, not_142_out, not_143_out, not_144_out,
       not_145_out, not_146_out, not_147_out, not_148_out, not_149_out, not_150_out, not_151_out,
       not_152_out, not_153_out, not_154_out, not_155_out, not_156_out, not_157_out, not_158_out,
       not_159_out, not_160_out, not_161_out, not_162_out, not_163_out, not_164_out, not_165_out,
       not_166_out, not_167_out, not_168_out, not_169_out, not_170_out, not_171_out, not_172_out,
       not_173_out, not_174_out, not_175_out, not_176_out, not_177_out, not_178_out, not_179_out,
       not_180_out, not_181_out, not_182_out, not_183_out, not_184_out, not_185_out, not_186_out,
       not_187_out, not_188_out, not_189_out, not_190_out, not_191_out, not_192_out, not_193_out,
       not_194_out, not_195_out, not_196_out, not_197_out, not_198_out, not_199_out, not_200_out,
       not_201_out, not_202_out, not_203_out, not_204_out, not_205_out, not_206_out, not_207_out,
       not_208_out, not_209_out, not_210_out, not_211_out, not_212_out, not_213_out, not_214_out,
       not_215_out, not_216_out, not_217_out, not_218_out, not_219_out, not_220_out, not_221_out;

  not not_1 (not_1_out, in_1);
  not not_2 (not_2_out, in_2);
  not not_3 (not_3_out, in_4);
  not not_4 (not_4_out, in_5);
  not not_5 (not_5_out, in_6);
  not not_6 (not_6_out, in_1);
  not not_7 (not_7_out, in_2);
  not not_8 (not_8_out, in_3);
  not not_9 (not_9_out, in_1);
  not not_10 (not_10_out, in_3);
  not not_11 (not_11_out, in_1);
  not not_12 (not_12_out, in_5);
  not not_13 (not_13_out, in_1);
  not not_14 (not_14_out, in_2);
  not not_15 (not_15_out, in_2);
  not not_16 (not_16_out, in_5);
  not not_17 (not_17_out, in_1);
  not not_18 (not_18_out, in_3);
  not not_19 (not_19_out, in_4);
  not not_20 (not_20_out, in_5);
  not not_21 (not_21_out, in_3);
  not not_22 (not_22_out, in_4);
  not not_23 (not_23_out, in_5);
  not not_24 (not_24_out, in_6);
  not not_25 (not_25_out, in_1);
  not not_26 (not_26_out, in_4);
  not not_27 (not_27_out, in_2);
  not not_28 (not_28_out, in_4);
  not not_29 (not_29_out, in_6);
  not not_30 (not_30_out, in_2);
  not not_31 (not_31_out, in_4);
  not not_32 (not_32_out, in_5);
  not not_33 (not_33_out, in_1);
  not not_34 (not_34_out, in_2);
  not not_35 (not_35_out, in_4);
  not not_36 (not_36_out, in_2);
  not not_37 (not_37_out, in_3);
  not not_38 (not_38_out, in_4);
  not not_39 (not_39_out, in_1);
  not not_40 (not_40_out, in_3);
  not not_41 (not_41_out, in_4);
  not not_42 (not_42_out, in_6);
  not not_43 (not_43_out, in_1);
  not not_44 (not_44_out, in_3);
  not not_45 (not_45_out, in_5);
  not not_46 (not_46_out, in_6);
  not not_47 (not_47_out, in_1);
  not not_48 (not_48_out, in_2);
  not not_49 (not_49_out, in_6);
  not not_50 (not_50_out, in_1);
  not not_51 (not_51_out, in_3);
  not not_52 (not_52_out, in_1);
  not not_53 (not_53_out, in_4);
  not not_54 (not_54_out, in_3);
  not not_55 (not_55_out, in_4);
  not not_56 (not_56_out, in_5);
  not not_57 (not_57_out, in_2);
  not not_58 (not_58_out, in_4);
  not not_59 (not_59_out, in_6);
  not not_60 (not_60_out, in_2);
  not not_61 (not_61_out, in_1);
  not not_62 (not_62_out, in_2);
  not not_63 (not_63_out, in_5);
  not not_64 (not_64_out, in_6);
  not not_65 (not_65_out, in_2);
  not not_66 (not_66_out, in_3);
  not not_67 (not_67_out, in_4);
  not not_68 (not_68_out, in_5);
  not not_69 (not_69_out, in_1);
  not not_70 (not_70_out, in_2);
  not not_71 (not_71_out, in_3);
  not not_72 (not_72_out, in_1);
  not not_73 (not_73_out, in_3);
  not not_74 (not_74_out, in_5);
  not not_75 (not_75_out, in_1);
  not not_76 (not_76_out, in_2);
  not not_77 (not_77_out, in_3);
  not not_78 (not_78_out, in_1);
  not not_79 (not_79_out, in_3);
  not not_80 (not_80_out, in_5);
  not not_81 (not_81_out, in_1);
  not not_82 (not_82_out, in_3);
  not not_83 (not_83_out, in_1);
  not not_84 (not_84_out, in_4);
  not not_85 (not_85_out, in_5);
  not not_86 (not_86_out, in_2);
  not not_87 (not_87_out, in_4);
  not not_88 (not_88_out, in_2);
  not not_89 (not_89_out, in_6);
  not not_90 (not_90_out, in_3);
  not not_91 (not_91_out, in_4);
  not not_92 (not_92_out, in_6);
  not not_93 (not_93_out, in_1);
  not not_94 (not_94_out, in_2);
  not not_95 (not_95_out, in_3);
  not not_96 (not_96_out, in_4);
  not not_97 (not_97_out, in_6);
  not not_98 (not_98_out, in_2);
  not not_99 (not_99_out, in_3);
  not not_100 (not_100_out, in_4);
  not not_101 (not_101_out, in_2);
  not not_102 (not_102_out, in_3);
  not not_103 (not_103_out, in_6);
  not not_104 (not_104_out, in_1);
  not not_105 (not_105_out, in_2);
  not not_106 (not_106_out, in_5);
  not not_107 (not_107_out, in_1);
  not not_108 (not_108_out, in_2);
  not not_109 (not_109_out, in_5);
  not not_110 (not_110_out, in_1);
  not not_111 (not_111_out, in_5);
  not not_112 (not_112_out, in_2);
  not not_113 (not_113_out, in_5);
  not not_114 (not_114_out, in_1);
  not not_115 (not_115_out, in_1);
  not not_116 (not_116_out, in_4);
  not not_117 (not_117_out, in_5);
  not not_118 (not_118_out, in_1);
  not not_119 (not_119_out, in_3);
  not not_120 (not_120_out, in_6);
  not not_121 (not_121_out, in_2);
  not not_122 (not_122_out, in_3);
  not not_123 (not_123_out, in_4);
  not not_124 (not_124_out, in_2);
  not not_125 (not_125_out, in_3);
  not not_126 (not_126_out, in_6);
  not not_127 (not_127_out, in_3);
  not not_128 (not_128_out, in_4);
  not not_129 (not_129_out, in_1);
  not not_130 (not_130_out, in_3);
  not not_131 (not_131_out, in_4);
  not not_132 (not_132_out, in_6);
  not not_133 (not_133_out, in_1);
  not not_134 (not_134_out, in_4);
  not not_135 (not_135_out, in_5);
  not not_136 (not_136_out, in_6);
  not not_137 (not_137_out, in_1);
  not not_138 (not_138_out, in_3);
  not not_139 (not_139_out, in_6);
  not not_140 (not_140_out, in_1);
  not not_141 (not_141_out, in_2);
  not not_142 (not_142_out, in_1);
  not not_143 (not_143_out, in_2);
  not not_144 (not_144_out, in_2);
  not not_145 (not_145_out, in_1);
  not not_146 (not_146_out, in_3);
  not not_147 (not_147_out, in_1);
  not not_148 (not_148_out, in_4);
  not not_149 (not_149_out, in_5);
  not not_150 (not_150_out, in_1);
  not not_151 (not_151_out, in_6);
  not not_152 (not_152_out, in_3);
  not not_153 (not_153_out, in_5);
  not not_154 (not_154_out, in_6);
  not not_155 (not_155_out, in_1);
  not not_156 (not_156_out, in_2);
  not not_157 (not_157_out, in_3);
  not not_158 (not_158_out, in_4);
  not not_159 (not_159_out, in_5);
  not not_160 (not_160_out, in_1);
  not not_161 (not_161_out, in_2);
  not not_162 (not_162_out, in_5);
  not not_163 (not_163_out, in_6);
  not not_164 (not_164_out, in_1);
  not not_165 (not_165_out, in_5);
  not not_166 (not_166_out, in_1);
  not not_167 (not_167_out, in_2);
  not not_168 (not_168_out, in_1);
  not not_169 (not_169_out, in_3);
  not not_170 (not_170_out, in_4);
  not not_171 (not_171_out, in_1);
  not not_172 (not_172_out, in_3);
  not not_173 (not_173_out, in_1);
  not not_174 (not_174_out, in_4);
  not not_175 (not_175_out, in_1);
  not not_176 (not_176_out, in_6);
  not not_177 (not_177_out, in_3);
  not not_178 (not_178_out, in_5);
  not not_179 (not_179_out, in_2);
  not not_180 (not_180_out, in_4);
  not not_181 (not_181_out, in_2);
  not not_182 (not_182_out, in_6);
  not not_183 (not_183_out, in_2);
  not not_184 (not_184_out, in_3);
  not not_185 (not_185_out, in_4);
  not not_186 (not_186_out, in_1);
  not not_187 (not_187_out, in_2);
  not not_188 (not_188_out, in_6);
  not not_189 (not_189_out, in_2);
  not not_190 (not_190_out, in_5);
  not not_191 (not_191_out, in_6);
  not not_192 (not_192_out, in_1);
  not not_193 (not_193_out, in_3);
  not not_194 (not_194_out, in_5);
  not not_195 (not_195_out, in_1);
  not not_196 (not_196_out, in_4);
  not not_197 (not_197_out, in_5);
  not not_198 (not_198_out, in_1);
  not not_199 (not_199_out, in_4);
  not not_200 (not_200_out, in_1);
  not not_201 (not_201_out, in_6);
  not not_202 (not_202_out, in_1);
  not not_203 (not_203_out, in_2);
  not not_204 (not_204_out, in_1);
  not not_205 (not_205_out, in_4);
  not not_206 (not_206_out, in_6);
  not not_207 (not_207_out, in_1);
  not not_208 (not_208_out, in_5);
  not not_209 (not_209_out, in_2);
  not not_210 (not_210_out, in_4);
  not not_211 (not_211_out, in_2);
  not not_212 (not_212_out, in_3);
  not not_213 (not_213_out, in_3);
  not not_214 (not_214_out, in_6);
  not not_215 (not_215_out, in_2);
  not not_216 (not_216_out, in_3);
  not not_217 (not_217_out, in_5);
  not not_218 (not_218_out, in_2);
  not not_219 (not_219_out, in_4);
  not not_220 (not_220_out, in_5);
  not not_221 (not_221_out, in_3);
  and and_1 (and_1_out, not_1_out, not_2_out, not_3_out, not_4_out, not_5_out);
  and and_2 (and_2_out, not_6_out, not_7_out, not_8_out, in_5);
  and and_3 (and_3_out, not_9_out, not_10_out, in_4, in_6);
  and and_4 (and_4_out, not_11_out, in_4, not_12_out, in_6);
  and and_5 (and_5_out, not_13_out, not_14_out, in_3, in_6);
  and and_6 (and_6_out, not_15_out, in_3, not_16_out, in_6);
  and and_7 (and_7_out, not_17_out, in_2, not_18_out, not_19_out, not_20_out);
  and and_8 (and_8_out, in_2, not_21_out, not_22_out, not_23_out, not_24_out);
  and and_9 (and_9_out, not_25_out, in_2, in_3, not_26_out, in_5);
  and and_10 (and_10_out, in_1, not_27_out, not_28_out, in_5, not_29_out);
  and and_11 (and_11_out, not_30_out, not_31_out, not_32_out);
  and and_12 (and_12_out, not_33_out, not_34_out, not_35_out, in_6);
  and and_13 (and_13_out, not_36_out, not_37_out, not_38_out, in_6);
  and and_14 (and_14_out, not_39_out, not_40_out, not_41_out, in_5, not_42_out);
  and and_15 (and_15_out, not_43_out, not_44_out, in_4, not_45_out, not_46_out);
  and and_16 (and_16_out, not_47_out, not_48_out, in_4, in_5, not_49_out);
  and and_17 (and_17_out, not_50_out, not_51_out, in_4, in_5, in_6);
  and and_18 (and_18_out, not_52_out, in_2, in_3, not_53_out, in_5);
  and and_19 (and_19_out, in_1, not_54_out, not_55_out, not_56_out, in_6);
  and and_20 (and_20_out, in_1, not_57_out, in_3, not_58_out, not_59_out);
  and and_21 (and_21_out, in_1, not_60_out, in_3, in_4, in_5, in_6);
  and and_22 (and_22_out, not_61_out, not_62_out, not_63_out, not_64_out);
  and and_23 (and_23_out, not_65_out, not_66_out, not_67_out, not_68_out);
  and and_24 (and_24_out, not_69_out, not_70_out, not_71_out, in_6);
  and and_25 (and_25_out, not_72_out, not_73_out, not_74_out, in_6);
  and and_26 (and_26_out, not_75_out, not_76_out, not_77_out, in_4);
  and and_27 (and_27_out, not_78_out, not_79_out, in_4, not_80_out);
  and and_28 (and_28_out, not_81_out, not_82_out, in_4, in_6);
  and and_29 (and_29_out, not_83_out, in_3, not_84_out, not_85_out);
  and and_30 (and_30_out, not_86_out, in_3, not_87_out, in_6);
  and and_31 (and_31_out, not_88_out, in_3, in_4, in_5, not_89_out);
  and and_32 (and_32_out, in_2, not_90_out, not_91_out, in_5, not_92_out);
  and and_33 (and_33_out, not_93_out, in_2, in_3, in_6);
  and and_34 (and_34_out, not_94_out, not_95_out, not_96_out, not_97_out);
  and and_35 (and_35_out, not_98_out, not_99_out, not_100_out, in_5);
  and and_36 (and_36_out, not_101_out, not_102_out, in_5, not_103_out);
  and and_37 (and_37_out, not_104_out, not_105_out, in_4, not_106_out, in_6);
  and and_38 (and_38_out, not_107_out, not_108_out, in_3, not_109_out);
  and and_39 (and_39_out, not_110_out, in_3, not_111_out, in_6);
  and and_40 (and_40_out, not_112_out, in_3, in_4, not_113_out, in_6);
  and and_41 (and_41_out, not_114_out, in_3, in_4, in_5);
  and and_42 (and_42_out, not_115_out, in_2, not_116_out, not_117_out, in_6);
  and and_43 (and_43_out, not_118_out, in_2, not_119_out, in_4, not_120_out);
  and and_44 (and_44_out, in_1, not_121_out, not_122_out, not_123_out);
  and and_45 (and_45_out, in_1, not_124_out, not_125_out, not_126_out);
  and and_46 (and_46_out, in_1, not_127_out, not_128_out, in_5, in_6);
  and and_47 (and_47_out, not_129_out, not_130_out, not_131_out, not_132_out);
  and and_48 (and_48_out, not_133_out, not_134_out, not_135_out, not_136_out);
  and and_49 (and_49_out, not_137_out, not_138_out, in_5, not_139_out);
  and and_50 (and_50_out, not_140_out, not_141_out, in_3, in_5, in_6);
  and and_51 (and_51_out, not_142_out, not_143_out, in_3, in_4);
  and and_52 (and_52_out, not_144_out, in_3, in_4, in_5, in_6);
  and and_53 (and_53_out, not_145_out, in_2, not_146_out);
  and and_54 (and_54_out, not_147_out, in_2, not_148_out, not_149_out);
  and and_55 (and_55_out, not_150_out, in_2, not_151_out);
  and and_56 (and_56_out, in_2, not_152_out, in_4, not_153_out, not_154_out);
  and and_57 (and_57_out, not_155_out, in_2, in_4, in_5);
  and and_58 (and_58_out, in_1, not_156_out, not_157_out, not_158_out, not_159_out);
  and and_59 (and_59_out, not_160_out, not_161_out, not_162_out, not_163_out);
  and and_60 (and_60_out, not_164_out, in_4, not_165_out, in_6);
  and and_61 (and_61_out, not_166_out, not_167_out, in_3, in_6);
  and and_62 (and_62_out, not_168_out, in_2, not_169_out, not_170_out);
  and and_63 (and_63_out, not_171_out, in_2, not_172_out, in_5);
  and and_64 (and_64_out, not_173_out, in_2, not_174_out, in_5);
  and and_65 (and_65_out, not_175_out, in_2, in_5, not_176_out);
  and and_66 (and_66_out, in_2, not_177_out, in_4, not_178_out, in_6);
  and and_67 (and_67_out, in_1, not_179_out, not_180_out, in_6);
  and and_68 (and_68_out, in_1, not_181_out, in_3, in_5, not_182_out);
  and and_69 (and_69_out, not_183_out, not_184_out, not_185_out, in_5);
  and and_70 (and_70_out, not_186_out, not_187_out, in_4, not_188_out);
  and and_71 (and_71_out, not_189_out, in_4, not_190_out, not_191_out);
  and and_72 (and_72_out, not_192_out, not_193_out, in_4, not_194_out, in_6);
  and and_73 (and_73_out, not_195_out, in_3, not_196_out, not_197_out);
  and and_74 (and_74_out, not_198_out, in_3, not_199_out, in_6);
  and and_75 (and_75_out, not_200_out, in_3, in_4, not_201_out);
  and and_76 (and_76_out, not_202_out, not_203_out, in_3, in_4, in_5);
  and and_77 (and_77_out, not_204_out, in_2, not_205_out, not_206_out);
  and and_78 (and_78_out, not_207_out, in_2, in_3, not_208_out);
  and and_79 (and_79_out, in_1, not_209_out, not_210_out, in_5);
  and and_80 (and_80_out, in_1, not_211_out, not_212_out, in_5, in_6);
  and and_81 (and_81_out, in_1, in_2, not_213_out, in_4, in_5, not_214_out);
  and and_82 (and_82_out, in_1, not_215_out, not_216_out, in_4, not_217_out, in_6);
  and and_83 (and_83_out, in_1, not_218_out, in_3, not_219_out, not_220_out);
  and and_84 (and_84_out, in_1, in_2, not_221_out, in_4, in_5, in_6);
  or or_1 (out_7, and_1_out, and_2_out, and_3_out, and_4_out, and_5_out, and_6_out, and_7_out, and_8_out, and_9_out, and_10_out);
  or or_2 (out_8, and_11_out, and_12_out, and_13_out, and_14_out, and_15_out, and_16_out, and_17_out, and_18_out, and_19_out, and_20_out, and_21_out);
  or or_3 (out_9, and_22_out, and_23_out, and_24_out, and_25_out, and_26_out, and_27_out, and_28_out, and_29_out, and_30_out, and_31_out, and_32_out, and_33_out);
  or or_4 (out_10, and_34_out, and_35_out, and_36_out, and_37_out, and_38_out, and_39_out, and_40_out, and_41_out, and_42_out, and_43_out, and_44_out, and_45_out, and_46_out);
  or or_5 (out_11, and_47_out, and_48_out, and_49_out, and_50_out, and_51_out, and_52_out, and_53_out, and_54_out, and_55_out, and_56_out, and_57_out, and_58_out);
  or or_6 (out_12, and_59_out, and_60_out, and_61_out, and_62_out, and_63_out, and_64_out, and_65_out, and_66_out, and_67_out, and_68_out);
  or or_7 (out_13, and_69_out, and_70_out, and_71_out, and_72_out, and_73_out, and_74_out, and_75_out, and_76_out, and_77_out, and_78_out, and_79_out, and_80_out, and_81_out);
  or or_8 (out_14, and_82_out, and_83_out, and_84_out);
endmodule

module comp (
  input  en_comp,
  input  [16:0] tps,
  input  CLK,
  input  RST_BUTTON,
  output ending
);

  wire or_1_out, t_ff_1_q, t_ff_1_qn, t_ff_2_q, t_ff_2_qn, t_ff_3_q, t_ff_3_qn, t_ff_4_q, t_ff_4_qn,
       t_ff_5_q, t_ff_5_qn, t_ff_6_q, t_ff_6_qn, t_ff_7_q, t_ff_7_qn, t_ff_8_q, t_ff_8_qn, t_ff_9_q,
       t_ff_9_qn, t_ff_10_q, t_ff_10_qn, t_ff_11_q, t_ff_11_qn, t_ff_12_q, t_ff_12_qn, t_ff_13_q, t_ff_13_qn,
       t_ff_14_q, t_ff_14_qn, t_ff_15_q, t_ff_15_qn, t_ff_16_q, t_ff_16_qn, t_ff_17_q, xnor_1_out,
       xnor_2_out, xnor_3_out, xnor_4_out, xnor_5_out, xnor_6_out, xnor_7_out, xnor_8_out, xnor_9_out,
       xnor_10_out, xnor_11_out, xnor_12_out, xnor_13_out, xnor_14_out, xnor_15_out, xnor_16_out, xnor_17_out;

  or or_1 (or_1_out, ending, RST_BUTTON);
  T_Flip_Flop t_ff_1 (.T(en_comp), .clk(CLK), .Q(t_ff_1_q), .Qn(t_ff_1_qn), .reset(or_1_out));  // open: preset
  T_Flip_Flop t_ff_2 (.T(en_comp), .clk(t_ff_1_qn), .Q(t_ff_2_q), .Qn(t_ff_2_qn), .reset(or_1_out));  // open: preset
  T_Flip_Flop t_ff_3 (.T(en_comp), .clk(t_ff_2_qn), .Q(t_ff_3_q), .Qn(t_ff_3_qn), .reset(or_1_out));  // open: preset
  T_Flip_Flop t_ff_4 (.T(en_comp), .clk(t_ff_3_qn), .Q(t_ff_4_q), .Qn(t_ff_4_qn), .reset(or_1_out));  // open: preset
  T_Flip_Flop t_ff_5 (.T(en_comp), .clk(t_ff_4_qn), .Q(t_ff_5_q), .Qn(t_ff_5_qn), .reset(or_1_out));  // open: preset
  T_Flip_Flop t_ff_6 (.T(en_comp), .clk(t_ff_5_qn), .Q(t_ff_6_q), .Qn(t_ff_6_qn), .reset(or_1_out));  // open: preset
  T_Flip_Flop t_ff_7 (.T(en_comp), .clk(t_ff_6_qn), .Q(t_ff_7_q), .Qn(t_ff_7_qn), .reset(or_1_out));  // open: preset
  T_Flip_Flop t_ff_8 (.T(en_comp), .clk(t_ff_7_qn), .Q(t_ff_8_q), .Qn(t_ff_8_qn), .reset(or_1_out));  // open: preset
  T_Flip_Flop t_ff_9 (.T(en_comp), .clk(t_ff_8_qn), .Q(t_ff_9_q), .Qn(t_ff_9_qn), .reset(or_1_out));  // open: preset
  T_Flip_Flop t_ff_10 (.T(en_comp), .clk(t_ff_9_qn), .Q(t_ff_10_q), .Qn(t_ff_10_qn), .reset(or_1_out));  // open: preset
  T_Flip_Flop t_ff_11 (
    .T(en_comp), .clk(t_ff_10_qn), .Q(t_ff_11_q), .Qn(t_ff_11_qn), .reset(or_1_out));  // open: preset
  T_Flip_Flop t_ff_12 (
    .T(en_comp), .clk(t_ff_11_qn), .Q(t_ff_12_q), .Qn(t_ff_12_qn), .reset(or_1_out));  // open: preset
  T_Flip_Flop t_ff_13 (
    .T(en_comp), .clk(t_ff_12_qn), .Q(t_ff_13_q), .Qn(t_ff_13_qn), .reset(or_1_out));  // open: preset
  T_Flip_Flop t_ff_14 (
    .T(en_comp), .clk(t_ff_13_qn), .Q(t_ff_14_q), .Qn(t_ff_14_qn), .reset(or_1_out));  // open: preset
  T_Flip_Flop t_ff_15 (
    .T(en_comp), .clk(t_ff_14_qn), .Q(t_ff_15_q), .Qn(t_ff_15_qn), .reset(or_1_out));  // open: preset
  T_Flip_Flop t_ff_16 (
    .T(en_comp), .clk(t_ff_15_qn), .Q(t_ff_16_q), .Qn(t_ff_16_qn), .reset(or_1_out));  // open: preset
  T_Flip_Flop t_ff_17 (.T(en_comp), .clk(t_ff_16_qn), .Q(t_ff_17_q), .reset(or_1_out));  // open: Qn, preset
  xnor xnor_1 (xnor_1_out, t_ff_17_q, tps[16]);
  xnor xnor_2 (xnor_2_out, t_ff_15_q, tps[14]);
  xnor xnor_3 (xnor_3_out, t_ff_16_q, tps[15]);
  xnor xnor_4 (xnor_4_out, t_ff_14_q, tps[13]);
  xnor xnor_5 (xnor_5_out, t_ff_13_q, tps[12]);
  xnor xnor_6 (xnor_6_out, t_ff_12_q, tps[11]);
  xnor xnor_7 (xnor_7_out, t_ff_11_q, tps[10]);
  xnor xnor_8 (xnor_8_out, t_ff_10_q, tps[9]);
  xnor xnor_9 (xnor_9_out, t_ff_9_q, tps[8]);
  xnor xnor_10 (xnor_10_out, t_ff_7_q, tps[6]);
  xnor xnor_11 (xnor_11_out, t_ff_8_q, tps[7]);
  xnor xnor_12 (xnor_12_out, t_ff_6_q, tps[5]);
  and and_1 (ending, xnor_1_out, xnor_3_out, xnor_2_out, xnor_7_out, xnor_8_out, xnor_9_out, xnor_11_out, xnor_10_out, xnor_12_out, xnor_13_out, xnor_14_out, xnor_15_out, xnor_16_out, xnor_17_out, xnor_6_out, xnor_5_out, xnor_4_out);
  xnor xnor_13 (xnor_13_out, t_ff_5_q, tps[4]);
  xnor xnor_14 (xnor_14_out, t_ff_4_q, tps[3]);
  xnor xnor_15 (xnor_15_out, t_ff_3_q, tps[2]);
  xnor xnor_16 (xnor_16_out, t_ff_2_q, tps[1]);
  xnor xnor_17 (xnor_17_out, t_ff_1_q, tps[0]);
endmodule

module debouncer (
  input  button,
  input  CLK,
  output out_3
);

  wire d_ff_1_q, d_ff_2_q, d_ff_3_q, d_ff_4_q;

  D_Flip_Flop d_ff_1 (.D(button), .clk(CLK), .Q(d_ff_1_q));  // open: Qn, preset, reset
  D_Flip_Flop d_ff_2 (.D(d_ff_1_q), .clk(CLK), .Q(d_ff_2_q));  // open: Qn, preset, reset
  and and_1 (out_3, d_ff_1_q, d_ff_2_q, d_ff_3_q, d_ff_4_q);
  D_Flip_Flop d_ff_3 (.D(d_ff_2_q), .clk(CLK), .Q(d_ff_3_q));  // open: Qn, preset, reset
  D_Flip_Flop d_ff_4 (.D(d_ff_3_q), .clk(CLK), .Q(d_ff_4_q));  // open: Qn, preset, reset

  // Notes on the sheet:
  //   Debouncer
endmodule

module countdown (
  input  [5:0] in_1,
  input  in_2,
  input  in_3,
  input  [5:0] in_4,
  input  [5:0] in_5
);

  wire and_1_out, button_1_out, clock_1_out, comp_1_ending, d_ff_1_q, d_ff_1_qn, debouncer_1_out_3,
       dec7seg_1_out_7, dec7seg_1_out_8, dec7seg_1_out_9, dec7seg_1_out_10, dec7seg_1_out_11,
       dec7seg_1_out_12, dec7seg_1_out_13, dec7seg_1_out_14, dec7seg_2_out_7, dec7seg_2_out_8,
       dec7seg_2_out_9, dec7seg_2_out_10, dec7seg_2_out_11, dec7seg_2_out_12, dec7seg_2_out_13,
       dec7seg_2_out_14, dec7seg_3_out_7, dec7seg_3_out_8, dec7seg_3_out_9, dec7seg_3_out_10,
       dec7seg_3_out_11, dec7seg_3_out_12, dec7seg_3_out_13, dec7seg_3_out_14, dec7seg_4_out_7,
       dec7seg_4_out_8, dec7seg_4_out_9, dec7seg_4_out_10, dec7seg_4_out_11, dec7seg_4_out_12,
       dec7seg_4_out_13, dec7seg_4_out_14, dec7seg_5_out_7, dec7seg_5_out_8, dec7seg_5_out_9,
       dec7seg_5_out_10, dec7seg_5_out_11, dec7seg_5_out_12, dec7seg_5_out_13, dec7seg_5_out_14,
       dec7seg_6_out_7, dec7seg_6_out_8, dec7seg_6_out_9, dec7seg_6_out_10, dec7seg_6_out_11,
       dec7seg_6_out_12, dec7seg_6_out_13, dec7seg_6_out_14, min_1_under_m, one_1_out_7, one_1_out_8,
       one_1_out_9, one_1_out_10, one_1_out_11, one_1_out_12, one_2_out_7, one_2_out_8, one_2_out_9,
       one_2_out_10, one_2_out_11, one_2_out_12, one_3_out_7, one_3_out_8, one_3_out_9, one_3_out_10,
       one_3_out_11, one_3_out_12, sec_1_under_f, ten_1_out_7, ten_1_out_8, ten_1_out_9, ten_1_out_10,
       ten_1_out_11, ten_1_out_12, ten_2_out_7, ten_2_out_8, ten_2_out_9, ten_2_out_10, ten_2_out_11,
       ten_2_out_12, ten_3_out_7, ten_3_out_8, ten_3_out_9, ten_3_out_10, ten_3_out_11, ten_3_out_12;
  wire [5:0] hour_1_hour, min_1_min, sec_1_sec;
  wire [16:0] adder_1_out, adder_2_out, multiplier_1_out, multiplier_2_out;

  Clock clock_1 (.out(clock_1_out));
  and and_1 (and_1_out, in_3, d_ff_1_q);
  Button button_1 (.out(button_1_out));
  Multiplier #(.width(17)) multiplier_1 (
    .a({{11{1'b0}}, in_5}), .b(17'he10), .out(multiplier_1_out));  // open: cin, cout
  Multiplier #(.width(17)) multiplier_2 (
    .a({{11{1'b0}}, in_4}), .b(17'h3c), .out(multiplier_2_out));  // open: cin, cout
  sec sec_1 (
    .SEC_IN(in_1), .SET(in_2), .EN(in_3), .RST(and_1_out), .CLK(clock_1_out), .SEC(sec_1_sec),
    .UNDER_F(sec_1_under_f));
  debouncer debouncer_1 (.button(button_1_out), .CLK(clock_1_out), .out_3(debouncer_1_out_3));
  Adder #(.width(17)) adder_1 (.a({{11{1'b0}}, in_1}), .b(multiplier_2_out), .out(adder_1_out));  // open: cin, cout
  min min_1 (
    .in_1(in_4), .SET(in_2), .UNDER_F(sec_1_under_f), .EN(in_3), .RST(and_1_out), .CLK(clock_1_out),
    .MIN(min_1_min), .UNDER_M(min_1_under_m));
  Adder #(.width(17)) adder_2 (.a(adder_1_out), .b(multiplier_1_out), .out(adder_2_out));  // open: cin, cout
  comp comp_1 (.en_comp(in_3), .tps(adder_2_out), .CLK(clock_1_out), .ending(comp_1_ending));  // open: RST_BUTTON
  ten ten_1 (
    .in_1(sec_1_sec[5]), .in_2(sec_1_sec[4]), .in_3(sec_1_sec[3]), .in_4(sec_1_sec[2]), .in_5(sec_1_sec[1]),
    .in_6(sec_1_sec[0]), .out_7(ten_1_out_7), .out_8(ten_1_out_8), .out_9(ten_1_out_9),
    .out_10(ten_1_out_10), .out_11(ten_1_out_11), .out_12(ten_1_out_12));
  D_Flip_Flop d_ff_1 (
    .D(d_ff_1_qn), .clk(comp_1_ending), .Q(d_ff_1_q), .Qn(d_ff_1_qn), .reset(debouncer_1_out_3));  // open: preset
  hour hour_1 (
    .in_1(in_5), .SET(in_2), .UNDER_F(sec_1_under_f), .UNDER_M(min_1_under_m), .EN(in_3), .RST(and_1_out),
    .CLK(clock_1_out), .HOUR(hour_1_hour));  // open: UNDER_H
  dec7seg dec7seg_1 (
    .in_1(ten_1_out_7), .in_2(ten_1_out_8), .in_3(ten_1_out_9), .in_4(ten_1_out_10), .in_5(ten_1_out_11),
    .in_6(ten_1_out_12), .out_7(dec7seg_1_out_7), .out_8(dec7seg_1_out_8), .out_9(dec7seg_1_out_9),
    .out_10(dec7seg_1_out_10), .out_11(dec7seg_1_out_11), .out_12(dec7seg_1_out_12),
    .out_13(dec7seg_1_out_13), .out_14(dec7seg_1_out_14));
  ten ten_2 (
    .in_1(min_1_min[5]), .in_2(min_1_min[4]), .in_3(min_1_min[3]), .in_4(min_1_min[2]), .in_5(min_1_min[1]),
    .in_6(min_1_min[0]), .out_7(ten_2_out_7), .out_8(ten_2_out_8), .out_9(ten_2_out_9),
    .out_10(ten_2_out_10), .out_11(ten_2_out_11), .out_12(ten_2_out_12));
  _7_Segment_Display u_7_segment_display_1 (
    .g(dec7seg_1_out_13), .f(dec7seg_1_out_12), .a(dec7seg_1_out_7), .b(dec7seg_1_out_8),
    .e(dec7seg_1_out_11), .d(dec7seg_1_out_10), .c(dec7seg_1_out_9), .dp(dec7seg_1_out_14));
  dec7seg dec7seg_2 (
    .in_1(ten_2_out_7), .in_2(ten_2_out_8), .in_3(ten_2_out_9), .in_4(ten_2_out_10), .in_5(ten_2_out_11),
    .in_6(ten_2_out_12), .out_7(dec7seg_2_out_7), .out_8(dec7seg_2_out_8), .out_9(dec7seg_2_out_9),
    .out_10(dec7seg_2_out_10), .out_11(dec7seg_2_out_11), .out_12(dec7seg_2_out_12),
    .out_13(dec7seg_2_out_13), .out_14(dec7seg_2_out_14));
  ten ten_3 (
    .in_1(hour_1_hour[5]), .in_2(hour_1_hour[4]), .in_3(hour_1_hour[3]), .in_4(hour_1_hour[2]),
    .in_5(hour_1_hour[1]), .in_6(hour_1_hour[0]), .out_7(ten_3_out_7), .out_8(ten_3_out_8),
    .out_9(ten_3_out_9), .out_10(ten_3_out_10), .out_11(ten_3_out_11), .out_12(ten_3_out_12));
  _7_Segment_Display u_7_segment_display_2 (
    .g(dec7seg_2_out_13), .f(dec7seg_2_out_12), .a(dec7seg_2_out_7), .b(dec7seg_2_out_8),
    .e(dec7seg_2_out_11), .d(dec7seg_2_out_10), .c(dec7seg_2_out_9), .dp(dec7seg_2_out_14));
  dec7seg dec7seg_3 (
    .in_1(ten_3_out_7), .in_2(ten_3_out_8), .in_3(ten_3_out_9), .in_4(ten_3_out_10), .in_5(ten_3_out_11),
    .in_6(ten_3_out_12), .out_7(dec7seg_3_out_7), .out_8(dec7seg_3_out_8), .out_9(dec7seg_3_out_9),
    .out_10(dec7seg_3_out_10), .out_11(dec7seg_3_out_11), .out_12(dec7seg_3_out_12),
    .out_13(dec7seg_3_out_13), .out_14(dec7seg_3_out_14));
  one one_1 (
    .in_1(sec_1_sec[5]), .in_2(sec_1_sec[4]), .in_3(sec_1_sec[3]), .in_4(sec_1_sec[2]), .in_5(sec_1_sec[1]),
    .in_6(sec_1_sec[0]), .out_7(one_1_out_7), .out_8(one_1_out_8), .out_9(one_1_out_9),
    .out_10(one_1_out_10), .out_11(one_1_out_11), .out_12(one_1_out_12));
  _7_Segment_Display u_7_segment_display_3 (
    .g(dec7seg_3_out_13), .f(dec7seg_3_out_12), .a(dec7seg_3_out_7), .b(dec7seg_3_out_8),
    .e(dec7seg_3_out_11), .d(dec7seg_3_out_10), .c(dec7seg_3_out_9), .dp(dec7seg_3_out_14));
  dec7seg dec7seg_4 (
    .in_1(one_1_out_7), .in_2(one_1_out_8), .in_3(one_1_out_9), .in_4(one_1_out_10), .in_5(one_1_out_11),
    .in_6(one_1_out_12), .out_7(dec7seg_4_out_7), .out_8(dec7seg_4_out_8), .out_9(dec7seg_4_out_9),
    .out_10(dec7seg_4_out_10), .out_11(dec7seg_4_out_11), .out_12(dec7seg_4_out_12),
    .out_13(dec7seg_4_out_13), .out_14(dec7seg_4_out_14));
  one one_2 (
    .in_1(min_1_min[5]), .in_2(min_1_min[4]), .in_3(min_1_min[3]), .in_4(min_1_min[2]), .in_5(min_1_min[1]),
    .in_6(min_1_min[0]), .out_7(one_2_out_7), .out_8(one_2_out_8), .out_9(one_2_out_9),
    .out_10(one_2_out_10), .out_11(one_2_out_11), .out_12(one_2_out_12));
  _7_Segment_Display u_7_segment_display_4 (
    .g(dec7seg_4_out_13), .f(dec7seg_4_out_12), .a(dec7seg_4_out_7), .b(dec7seg_4_out_8),
    .e(dec7seg_4_out_11), .d(dec7seg_4_out_10), .c(dec7seg_4_out_9), .dp(dec7seg_4_out_14));
  dec7seg dec7seg_5 (
    .in_1(one_2_out_7), .in_2(one_2_out_8), .in_3(one_2_out_9), .in_4(one_2_out_10), .in_5(one_2_out_11),
    .in_6(one_2_out_12), .out_7(dec7seg_5_out_7), .out_8(dec7seg_5_out_8), .out_9(dec7seg_5_out_9),
    .out_10(dec7seg_5_out_10), .out_11(dec7seg_5_out_11), .out_12(dec7seg_5_out_12),
    .out_13(dec7seg_5_out_13), .out_14(dec7seg_5_out_14));
  one one_3 (
    .in_1(hour_1_hour[5]), .in_2(hour_1_hour[4]), .in_3(hour_1_hour[3]), .in_4(hour_1_hour[2]),
    .in_5(hour_1_hour[1]), .in_6(hour_1_hour[0]), .out_7(one_3_out_7), .out_8(one_3_out_8),
    .out_9(one_3_out_9), .out_10(one_3_out_10), .out_11(one_3_out_11), .out_12(one_3_out_12));
  _7_Segment_Display u_7_segment_display_5 (
    .g(dec7seg_5_out_13), .f(dec7seg_5_out_12), .a(dec7seg_5_out_7), .b(dec7seg_5_out_8),
    .e(dec7seg_5_out_11), .d(dec7seg_5_out_10), .c(dec7seg_5_out_9), .dp(dec7seg_5_out_14));
  dec7seg dec7seg_6 (
    .in_1(one_3_out_7), .in_2(one_3_out_8), .in_3(one_3_out_9), .in_4(one_3_out_10), .in_5(one_3_out_11),
    .in_6(one_3_out_12), .out_7(dec7seg_6_out_7), .out_8(dec7seg_6_out_8), .out_9(dec7seg_6_out_9),
    .out_10(dec7seg_6_out_10), .out_11(dec7seg_6_out_11), .out_12(dec7seg_6_out_12),
    .out_13(dec7seg_6_out_13), .out_14(dec7seg_6_out_14));
  _7_Segment_Display u_7_segment_display_6 (
    .g(dec7seg_6_out_13), .f(dec7seg_6_out_12), .a(dec7seg_6_out_7), .b(dec7seg_6_out_8),
    .e(dec7seg_6_out_11), .d(dec7seg_6_out_10), .c(dec7seg_6_out_9), .dp(dec7seg_6_out_14));
endmodule
