// Logisim project decodeurSegment.circ as structural Verilog: 2 circuits, main circuit main
module main (
  input  in_1
);

  wire clock_1_out, decodeur_sept_segm_1_a, decodeur_sept_segm_1_b, decodeur_sept_segm_1_c,
       decodeur_sept_segm_1_d, decodeur_sept_segm_1_e, decodeur_sept_segm_1_f, decodeur_sept_segm_1_g,
       decodeur_sept_segm_1_p, not_1_out;
  wire [5:0] counter_1_q;

  Clock clock_1 (.out(clock_1_out));
  Counter #(.width(6), .max('h3f)) counter_1 (
    .clr(in_1), .load(not_1_out), .up(1'b1), .clk(clock_1_out), .Q(counter_1_q));  // open: count, D, carry
  not not_1 (not_1_out, 1'b1);
  decodeur_SEPT_segm decodeur_sept_segm_1 (
    .i0(counter_1_q[5]), .i1(counter_1_q[4]), .i2(counter_1_q[3]), .i3(counter_1_q[2]), .i4(counter_1_q[1]),
    .i5(counter_1_q[0]), .a(decodeur_sept_segm_1_a), .b(decodeur_sept_segm_1_b), .c(decodeur_sept_segm_1_c),
    .d(decodeur_sept_segm_1_d), .e(decodeur_sept_segm_1_e), .f(decodeur_sept_segm_1_f),
    .g(decodeur_sept_segm_1_g), .p(decodeur_sept_segm_1_p));
  _7_Segment_Display u_7_segment_display_1 (
    .g(decodeur_sept_segm_1_g), .f(decodeur_sept_segm_1_f), .a(decodeur_sept_segm_1_a),
    .b(decodeur_sept_segm_1_b), .e(decodeur_sept_segm_1_e), .d(decodeur_sept_segm_1_d),
    .c(decodeur_sept_segm_1_c), .dp(decodeur_sept_segm_1_p));
endmodule

module decodeur_SEPT_segm (
  input  i0,
  input  i1,
  input  i2,
  input  i3,
  input  i4,
  input  i5,
  output a,
  output b,
  output c,
  output d,
  output e,
  output f,
  output g,
  output p
);

  wire and_1_out, and_2_out, and_3_out, and_4_out, and_5_out, and_6_out, and_7_out, and_8_out, and_9_out,
       and_10_out, and_11_out, and_12_out, and_13_out, and_14_out, and_15_out, and_16_out, and_17_out,
       and_18_out, and_19_out, and_20_out, and_21_out, and_22_out, and_23_out, and_24_out, and_25_out,
       and_26_out, and_27_out, and_28_out, and_29_out, and_30_out, and_31_out, and_32_out, and_33_out,
       and_34_out, and_35_out, and_36_out, and_37_out, and_38_out, and_39_out, and_40_out, and_41_out,
       and_42_out, and_43_out, and_44_out, and_45_out, and_46_out, and_47_out, and_48_out, and_49_out,
       and_50_out, and_51_out, and_52_out, and_53_out, and_54_out, and_55_out, and_56_out, and_57_out,
       and_58_out, and_59_out, and_60_out, and_61_out, and_62_out, and_63_out, and_64_out, and_65_out,
       and_66_out, and_67_out, and_68_out, and_69_out, and_70_out, and_71_out, and_72_out, and_73_out,
       and_74_out, and_75_out, and_76_out, and_77_out, and_78_out, and_79_out, and_80_out, and_81_out,
       and_82_out, and_83_out, and_84_out, not_1_out, not_2_out, not_3_out, not_4_out, not_5_out, not_6_out,
       not_7_out, not_8_out, not_9_out, not_10_out, not_11_out, not_12_out, not_13_out, not_14_out,
       not_15_out, not_16_out, not_17_out, not_18_out, not_19_out, not_20_out, not_21_out, not_22_out,
       not_23_out, not_24_out, not_25_out, not_26_out, not_27_out, not_28_out, not_29_out, not_30_out,
       not_31_out, not_32_out, not_33_out, not_34_out, not_35_out, not_36_out, not_37_out, not_38_out,
       not_39_out, not_40_out, not_41_out, not_42_out, not_43_out, not_44_out, not_45_out, not_46_out,
       not_47_out, not_48_out, not_49_out, not_50_out, not_51_out, not_52_out, not_53_out, not_54_out,
       not_55_out, not_56_out, not_57_out, not_58_out, not_59_out, not_60_out, not_61_out, not_62_out,
       not_63_out, not_64_out, not_65_out, not_66_out, not_67_out, not_68_out, not_69_out, not_70_out,
       not_71_out, not_72_out, not_73_out, not_74_out, not_75_out, not_76_out, not_77_out, not_78_out,
       not_79_out, not_80_out, not_81_out, not_82_out, not_83_out, not_84_out, not_85_out, not_86_out,
       not_87_out, not_88_out, not_89_out, not_90_out, not_91_out, not_92_out, not_93_out, not_94_out,
       not_95_out, not_96_out, not_97_out, not_98_out, not_99_out, not_100_out, not_101_out, not_102_out,
       not_103_out, not_104_out, not_105_out, not_106_out, not_107_out, not_108_out, not_109_out,
       not_110_out, not_111_out, not_112_out, not_113_out, not_114_out, not_115_out, not_116_out,
       not_117_out, not_118_out, not_119_out, not_120_out, not_121_out, not_122_out, not_123_out,
       not_124_out, not_125_out, not_126_out, not_127_out, not_128_out, not_129_out, not_130_out,
       not_131_out, not_132_out, not_133_out, not_134_out, not_135_out, not_136_out, not_137_out,
       not_138_out, not_139_out, not_140_out, not_141_out, not_142_out, not_143_out, not_144_out,
       not_145_out, not_146_out, not_147_out, not_148_out, not_149_out, not_150_out, not_151_out,
       not_152_out, not_153_out, not_154_out, not_155_out, not_156_out, not_157_out, not_158_out,
       not_159_out, not_160_out, not_161_out, not_162_out, not_163_out, not_164_out, not_165_out,
       not_166_out, not_167_out, not_168_out, not_169_out, not_170_out, not_171_out, not_172_out,
       not_173_out, not_174_out, not_175_out, not_176_out, not_177_out, not_178_out, not_179_out,
       not_180_out, not_181_out, not_182_out, not_183_out, not_184_out, not_185_out, not_186_out,
       not_187_out, not_188_out, not_189_out, not_190_out, not_191_out, not_192_out, not_193_out,
       not_194_out, not_195_out, not_196_out, not_197_out, not_198_out, not_199_out, not_200_out,
       not_201_out, not_202_out, not_203_out, not_204_out, not_205_out, not_206_out, not_207_out,
       not_208_out, not_209_out, not_210_out, not_211_out, not_212_out, not_213_out, not_214_out, not_215_out;

  not not_1 (not_1_out, i0);
  not not_2 (not_2_out, i1);
  not not_3 (not_3_out, i3);
  not not_4 (not_4_out, i4);
  not not_5 (not_5_out, i5);
  not not_6 (not_6_out, i0);
  not not_7 (not_7_out, i1);
  not not_8 (not_8_out, i2);
  not not_9 (not_9_out, i0);
  not not_10 (not_10_out, i2);
  not not_11 (not_11_out, i0);
  not not_12 (not_12_out, i4);
  not not_13 (not_13_out, i0);
  not not_14 (not_14_out, i1);
  not not_15 (not_15_out, i1);
  not not_16 (not_16_out, i4);
  not not_17 (not_17_out, i0);
  not not_18 (not_18_out, i2);
  not not_19 (not_19_out, i3);
  not not_20 (not_20_out, i4);
  not not_21 (not_21_out, i3);
  not not_22 (not_22_out, i1);
  not not_23 (not_23_out, i3);
  not not_24 (not_24_out, i5);
  not not_25 (not_25_out, i4);
  not not_26 (not_26_out, i3);
  not not_27 (not_27_out, i4);
  not not_28 (not_28_out, i5);
  not not_29 (not_29_out, i0);
  not not_30 (not_30_out, i1);
  not not_31 (not_31_out, i2);
  not not_32 (not_32_out, i3);
  not not_33 (not_33_out, i1);
  not not_34 (not_34_out, i3);
  not not_35 (not_35_out, i4);
  not not_36 (not_36_out, i1);
  not not_37 (not_37_out, i2);
  not not_38 (not_38_out, i3);
  not not_39 (not_39_out, i0);
  not not_40 (not_40_out, i2);
  not not_41 (not_41_out, i4);
  not not_42 (not_42_out, i5);
  not not_43 (not_43_out, i0);
  not not_44 (not_44_out, i2);
  not not_45 (not_45_out, i0);
  not not_46 (not_46_out, i3);
  not not_47 (not_47_out, i0);
  not not_48 (not_48_out, i1);
  not not_49 (not_49_out, i5);
  not not_50 (not_50_out, i0);
  not not_51 (not_51_out, i3);
  not not_52 (not_52_out, i5);
  not not_53 (not_53_out, i3);
  not not_54 (not_54_out, i4);
  not not_55 (not_55_out, i3);
  not not_56 (not_56_out, i5);
  not not_57 (not_57_out, i0);
  not not_58 (not_58_out, i1);
  not not_59 (not_59_out, i4);
  not not_60 (not_60_out, i5);
  not not_61 (not_61_out, i1);
  not not_62 (not_62_out, i2);
  not not_63 (not_63_out, i3);
  not not_64 (not_64_out, i4);
  not not_65 (not_65_out, i0);
  not not_66 (not_66_out, i1);
  not not_67 (not_67_out, i2);
  not not_68 (not_68_out, i0);
  not not_69 (not_69_out, i2);
  not not_70 (not_70_out, i4);
  not not_71 (not_71_out, i0);
  not not_72 (not_72_out, i1);
  not not_73 (not_73_out, i2);
  not not_74 (not_74_out, i0);
  not not_75 (not_75_out, i2);
  not not_76 (not_76_out, i4);
  not not_77 (not_77_out, i0);
  not not_78 (not_78_out, i3);
  not not_79 (not_79_out, i4);
  not not_80 (not_80_out, i3);
  not not_81 (not_81_out, i1);
  not not_82 (not_82_out, i5);
  not not_83 (not_83_out, i2);
  not not_84 (not_84_out, i3);
  not not_85 (not_85_out, i5);
  not not_86 (not_86_out, i0);
  not not_87 (not_87_out, i1);
  not not_88 (not_88_out, i2);
  not not_89 (not_89_out, i3);
  not not_90 (not_90_out, i5);
  not not_91 (not_91_out, i1);
  not not_92 (not_92_out, i2);
  not not_93 (not_93_out, i3);
  not not_94 (not_94_out, i1);
  not not_95 (not_95_out, i2);
  not not_96 (not_96_out, i5);
  not not_97 (not_97_out, i0);
  not not_98 (not_98_out, i1);
  not not_99 (not_99_out, i4);
  not not_100 (not_100_out, i0);
  not not_101 (not_101_out, i1);
  not not_102 (not_102_out, i4);
  not not_103 (not_103_out, i4);
  not not_104 (not_104_out, i0);
  not not_105 (not_105_out, i0);
  not not_106 (not_106_out, i3);
  not not_107 (not_107_out, i4);
  not not_108 (not_108_out, i0);
  not not_109 (not_109_out, i2);
  not not_110 (not_110_out, i5);
  not not_111 (not_111_out, i1);
  not not_112 (not_112_out, i2);
  not not_113 (not_113_out, i3);
  not not_114 (not_114_out, i1);
  not not_115 (not_115_out, i2);
  not not_116 (not_116_out, i5);
  not not_117 (not_117_out, i2);
  not not_118 (not_118_out, i3);
  not not_119 (not_119_out, i0);
  not not_120 (not_120_out, i2);
  not not_121 (not_121_out, i3);
  not not_122 (not_122_out, i5);
  not not_123 (not_123_out, i0);
  not not_124 (not_124_out, i3);
  not not_125 (not_125_out, i4);
  not not_126 (not_126_out, i5);
  not not_127 (not_127_out, i0);
  not not_128 (not_128_out, i2);
  not not_129 (not_129_out, i5);
  not not_130 (not_130_out, i0);
  not not_131 (not_131_out, i1);
  not not_132 (not_132_out, i0);
  not not_133 (not_133_out, i1);
  not not_134 (not_134_out, i0);
  not not_135 (not_135_out, i2);
  not not_136 (not_136_out, i0);
  not not_137 (not_137_out, i3);
  not not_138 (not_138_out, i4);
  not not_139 (not_139_out, i0);
  not not_140 (not_140_out, i5);
  not not_141 (not_141_out, i4);
  not not_142 (not_142_out, i5);
  not not_143 (not_143_out, i1);
  not not_144 (not_144_out, i2);
  not not_145 (not_145_out, i3);
  not not_146 (not_146_out, i4);
  not not_147 (not_147_out, i0);
  not not_148 (not_148_out, i1);
  not not_149 (not_149_out, i4);
  not not_150 (not_150_out, i5);
  not not_151 (not_151_out, i1);
  not not_152 (not_152_out, i2);
  not not_153 (not_153_out, i3);
  not not_154 (not_154_out, i4);
  not not_155 (not_155_out, i5);
  not not_156 (not_156_out, i0);
  not not_157 (not_157_out, i1);
  not not_158 (not_158_out, i2);
  not not_159 (not_159_out, i5);
  not not_160 (not_160_out, i0);
  not not_161 (not_161_out, i1);
  not not_162 (not_162_out, i4);
  not not_163 (not_163_out, i0);
  not not_164 (not_164_out, i1);
  not not_165 (not_165_out, i0);
  not not_166 (not_166_out, i2);
  not not_167 (not_167_out, i3);
  not not_168 (not_168_out, i0);
  not not_169 (not_169_out, i2);
  not not_170 (not_170_out, i0);
  not not_171 (not_171_out, i3);
  not not_172 (not_172_out, i0);
  not not_173 (not_173_out, i5);
  not not_174 (not_174_out, i4);
  not not_175 (not_175_out, i1);
  not not_176 (not_176_out, i3);
  not not_177 (not_177_out, i5);
  not not_178 (not_178_out, i1);
  not not_179 (not_179_out, i2);
  not not_180 (not_180_out, i3);
  not not_181 (not_181_out, i0);
  not not_182 (not_182_out, i1);
  not not_183 (not_183_out, i2);
  not not_184 (not_184_out, i4);
  not not_185 (not_185_out, i0);
  not not_186 (not_186_out, i1);
  not not_187 (not_187_out, i5);
  not not_188 (not_188_out, i1);
  not not_189 (not_189_out, i2);
  not not_190 (not_190_out, i4);
  not not_191 (not_191_out, i5);
  not not_192 (not_192_out, i0);
  not not_193 (not_193_out, i3);
  not not_194 (not_194_out, i4);
  not not_195 (not_195_out, i0);
  not not_196 (not_196_out, i3);
  not not_197 (not_197_out, i0);
  not not_198 (not_198_out, i5);
  not not_199 (not_199_out, i0);
  not not_200 (not_200_out, i1);
  not not_201 (not_201_out, i0);
  not not_202 (not_202_out, i3);
  not not_203 (not_203_out, i5);
  not not_204 (not_204_out, i0);
  not not_205 (not_205_out, i4);
  not not_206 (not_206_out, i1);
  not not_207 (not_207_out, i3);
  not not_208 (not_208_out, i1);
  not not_209 (not_209_out, i2);
  not not_210 (not_210_out, i5);
  not not_211 (not_211_out, i1);
  not not_212 (not_212_out, i2);
  not not_213 (not_213_out, i4);
  not not_214 (not_214_out, i3);
  not not_215 (not_215_out, i4);
  and and_1 (and_1_out, not_1_out, not_2_out, not_3_out, not_4_out, not_5_out);
  and and_2 (and_2_out, not_6_out, not_7_out, not_8_out, i4);
  and and_3 (and_3_out, not_9_out, not_10_out, i3, i5);
  and and_4 (and_4_out, not_11_out, i3, not_12_out, i5);
  and and_5 (and_5_out, not_13_out, not_14_out, i2, i5);
  and and_6 (and_6_out, not_15_out, i2, not_16_out, i5);
  and and_7 (and_7_out, not_17_out, i1, not_18_out, not_19_out, not_20_out);
  and and_8 (and_8_out, i1, i2, not_21_out, i4);
  and and_9 (and_9_out, i0, not_22_out, not_23_out, i4, not_24_out);
  and and_10 (and_10_out, i0, i2, i3, not_25_out);
  and and_11 (and_11_out, i0, i1, not_26_out, not_27_out, not_28_out);
  and and_12 (and_12_out, not_29_out, not_30_out, not_31_out, not_32_out);
  and and_13 (and_13_out, not_33_out, not_34_out, not_35_out);
  and and_14 (and_14_out, not_36_out, not_37_out, not_38_out, i5);
  and and_15 (and_15_out, not_39_out, not_40_out, i3, not_41_out, not_42_out);
  and and_16 (and_16_out, not_43_out, not_44_out, i3, i4, i5);
  and and_17 (and_17_out, not_45_out, i2, not_46_out, i4, i5);
  and and_18 (and_18_out, not_47_out, not_48_out, i2, i3, i4, not_49_out);
  and and_19 (and_19_out, not_50_out, i1, not_51_out, i4, not_52_out);
  and and_20 (and_20_out, i0, not_53_out, not_54_out, i5);
  and and_21 (and_21_out, i0, i2, not_55_out, not_56_out);
  and and_22 (and_22_out, i0, i2, i3, i4, i5);
  and and_23 (and_23_out, not_57_out, not_58_out, not_59_out, not_60_out);
  and and_24 (and_24_out, not_61_out, not_62_out, not_63_out, not_64_out);
  and and_25 (and_25_out, not_65_out, not_66_out, not_67_out, i5);
  and and_26 (and_26_out, not_68_out, not_69_out, not_70_out, i5);
  and and_27 (and_27_out, not_71_out, not_72_out, not_73_out, i3);
  and and_28 (and_28_out, not_74_out, not_75_out, i3, not_76_out);
  and and_29 (and_29_out, not_77_out, i2, not_78_out, not_79_out);
  and and_30 (and_30_out, i2, not_80_out, i5);
  and and_31 (and_31_out, not_81_out, i2, i3, i4, not_82_out);
  and and_32 (and_32_out, i1, not_83_out, not_84_out, i4, not_85_out);
  and and_33 (and_33_out, not_86_out, i1, i3, i5);
  and and_34 (and_34_out, not_87_out, not_88_out, not_89_out, not_90_out);
  and and_35 (and_35_out, not_91_out, not_92_out, not_93_out, i4);
  and and_36 (and_36_out, not_94_out, not_95_out, i4, not_96_out);
  and and_37 (and_37_out, not_97_out, not_98_out, i3, not_99_out, i5);
  and and_38 (and_38_out, not_100_out, not_101_out, i2, not_102_out);
  and and_39 (and_39_out, i2, i3, not_103_out, i5);
  and and_40 (and_40_out, not_104_out, i2, i3, i4);
  and and_41 (and_41_out, not_105_out, i1, not_106_out, not_107_out, i5);
  and and_42 (and_42_out, not_108_out, i1, not_109_out, i3, not_110_out);
  and and_43 (and_43_out, i0, not_111_out, not_112_out, not_113_out);
  and and_44 (and_44_out, i0, not_114_out, not_115_out, not_116_out);
  and and_45 (and_45_out, i0, not_117_out, not_118_out, i4, i5);
  and and_46 (and_46_out, not_119_out, not_120_out, not_121_out, not_122_out);
  and and_47 (and_47_out, not_123_out, not_124_out, not_125_out, not_126_out);
  and and_48 (and_48_out, not_127_out, not_128_out, i4, not_129_out);
  and and_49 (and_49_out, not_130_out, not_131_out, i2, i4, i5);
  and and_50 (and_50_out, not_132_out, not_133_out, i2, i3);
  and and_51 (and_51_out, i2, i3, i4, i5);
  and and_52 (and_52_out, not_134_out, i1, not_135_out);
  and and_53 (and_53_out, not_136_out, i1, not_137_out, not_138_out);
  and and_54 (and_54_out, not_139_out, i1, not_140_out);
  and and_55 (and_55_out, i1, i3, not_141_out, not_142_out);
  and and_56 (and_56_out, i0, not_143_out, not_144_out, not_145_out, not_146_out, i5);
  and and_57 (and_57_out, not_147_out, not_148_out, not_149_out, not_150_out);
  and and_58 (and_58_out, not_151_out, not_152_out, not_153_out, not_154_out, not_155_out);
  and and_59 (and_59_out, not_156_out, not_157_out, not_158_out, i3, not_159_out);
  and and_60 (and_60_out, not_160_out, not_161_out, i3, not_162_out);
  and and_61 (and_61_out, not_163_out, not_164_out, i2, i5);
  and and_62 (and_62_out, not_165_out, i1, not_166_out, not_167_out);
  and and_63 (and_63_out, not_168_out, i1, not_169_out, i4);
  and and_64 (and_64_out, not_170_out, i1, not_171_out, i4);
  and and_65 (and_65_out, not_172_out, i1, i4, not_173_out);
  and and_66 (and_66_out, i1, i3, not_174_out, i5);
  and and_67 (and_67_out, i0, not_175_out, not_176_out, i5);
  and and_68 (and_68_out, i0, i2, i4, not_177_out);
  and and_69 (and_69_out, not_178_out, not_179_out, not_180_out, i4);
  and and_70 (and_70_out, not_181_out, not_182_out, not_183_out, i3, not_184_out);
  and and_71 (and_71_out, not_185_out, not_186_out, i3, not_187_out);
  and and_72 (and_72_out, not_188_out, not_189_out, i3, not_190_out, not_191_out);
  and and_73 (and_73_out, not_192_out, i2, not_193_out, not_194_out);
  and and_74 (and_74_out, not_195_out, i2, not_196_out, i5);
  and and_75 (and_75_out, not_197_out, i2, i3, not_198_out);
  and and_76 (and_76_out, not_199_out, not_200_out, i2, i3, i4);
  and and_77 (and_77_out, not_201_out, i1, not_202_out, not_203_out);
  and and_78 (and_78_out, not_204_out, i1, i3, not_205_out, i5);
  and and_79 (and_79_out, i0, not_206_out, not_207_out, i4);
  and and_80 (and_80_out, i0, not_208_out, not_209_out, i4, i5);
  and and_81 (and_81_out, i0, i1, i3, i4, not_210_out);
  and and_82 (and_82_out, i0, not_211_out, not_212_out, i3, not_213_out, i5);
  and and_83 (and_83_out, i0, i2, not_214_out, not_215_out);
  and and_84 (and_84_out, i0, i1, i3, i4, i5);
  or or_1 (a, and_1_out, and_2_out, and_3_out, and_4_out, and_5_out, and_6_out, and_7_out, and_8_out, and_9_out, and_10_out, and_11_out);
  or or_2 (b, and_12_out, and_13_out, and_14_out, and_15_out, and_16_out, and_17_out, and_18_out, and_19_out, and_20_out, and_21_out, and_22_out);
  or or_3 (c, and_23_out, and_24_out, and_25_out, and_26_out, and_27_out, and_28_out, and_29_out, and_30_out, and_31_out, and_32_out, and_33_out);
  or or_4 (d, and_34_out, and_35_out, and_36_out, and_37_out, and_38_out, and_39_out, and_40_out, and_41_out, and_42_out, and_43_out, and_44_out, and_45_out);
  or or_5 (e, and_46_out, and_47_out, and_48_out, and_49_out, and_50_out, and_51_out, and_52_out, and_53_out, and_54_out, and_55_out, and_56_out);
  or or_6 (f, and_57_out, and_58_out, and_59_out, and_60_out, and_61_out, and_62_out, and_63_out, and_64_out, and_65_out, and_66_out, and_67_out, and_68_out);
  or or_7 (g, and_69_out, and_70_out, and_71_out, and_72_out, and_73_out, and_74_out, and_75_out, and_76_out, and_77_out, and_78_out, and_79_out, and_80_out, and_81_out);
  or or_8 (p, and_82_out, and_83_out, and_84_out);
endmodule
