// Logisim project sonneriedesesmorts.circ as structural Verilog: 9 circuits, main circuit main
module main (
  output Output_1,
  output terre
);

  wire and_1_out, and_2_out, and_3_out, and_4_out, and_5_out, and_6_out, and_7_out, and_8_out, and_9_out,
       Button_1_out, clock_1_out, counter_1_carry, d_ff_1_q, d_ff_2_q, d_ff_3_q, d_ff_4_q, d_ff_5_qn,
       demultiplexer_1_out0, demultiplexer_1_out1, demultiplexer_1_out2, demultiplexer_1_out3,
       demultiplexer_1_out4, demultiplexer_1_out5, demultiplexer_1_out6, demultiplexer_1_out7,
       demultiplexer_1_out8, demultiplexer_1_out9, demultiplexer_1_out10, demultiplexer_1_out11,
       demultiplexer_1_out12, demultiplexer_1_out13, demultiplexer_1_out14, demultiplexer_1_out15,
       dipswitch_1_sw1, not_1_out, nul_1_output_1, nul_2_output_1, nul_3_output_1, nul_4_output_1,
       nul_5_output_1, nul_6_output_1, nul_7_output_1, nul_8_output_1, or_1_out, or_2_out, or_3_out,
       unit_control_1_ending;
  wire [3:0] unit_control_1_ad_freq;
  wire [5:0] counter_1_q;

  DipSwitch dipswitch_1 (.sw1(dipswitch_1_sw1));  // open: sw2, sw3, sw4, sw5, sw6, sw7, sw8
  Button Button_1 (.out(Button_1_out));
  Clock clock_1 (.out(clock_1_out));
  Counter #(.width(6), .max('h3f)) counter_1 (
    .clr(or_3_out), .load(1'b0), .up(1'b1), .clk(clock_1_out), .carry(counter_1_carry),
    .Q({counter_1_q[0], counter_1_q[1], counter_1_q[2], counter_1_q[3], counter_1_q[4], counter_1_q[5]}));  // open: count, D
  D_Flip_Flop d_ff_1 (.D(Button_1_out), .clk(clock_1_out), .Q(d_ff_1_q));  // open: Qn, preset, reset
  D_Flip_Flop d_ff_2 (.D(d_ff_1_q), .clk(clock_1_out), .Q(d_ff_2_q));  // open: Qn, preset, reset
  and and_1 (and_1_out, d_ff_1_q, d_ff_2_q, d_ff_3_q, d_ff_4_q);
  D_Flip_Flop d_ff_3 (.D(d_ff_2_q), .clk(clock_1_out), .Q(d_ff_3_q));  // open: Qn, preset, reset
  D_Flip_Flop d_ff_4 (.D(d_ff_3_q), .clk(clock_1_out), .Q(d_ff_4_q));  // open: Qn, preset, reset
  not not_1 (not_1_out, unit_control_1_ending);
  Demultiplexer #(.select(4), .enable("false")) demultiplexer_1 (
    .out0(demultiplexer_1_out0), .out1(demultiplexer_1_out1), .out2(demultiplexer_1_out2),
    .out3(demultiplexer_1_out3), .out4(demultiplexer_1_out4), .out5(demultiplexer_1_out5),
    .out6(demultiplexer_1_out6), .out7(demultiplexer_1_out7), .out8(demultiplexer_1_out8),
    .out9(demultiplexer_1_out9), .out10(demultiplexer_1_out10), .out11(demultiplexer_1_out11),
    .out12(demultiplexer_1_out12), .out13(demultiplexer_1_out13), .out14(demultiplexer_1_out14),
    .out15(demultiplexer_1_out15), .in(not_1_out), .sel(unit_control_1_ad_freq));
  and and_2 (and_2_out, ~counter_1_q[5], ~counter_1_q[4], counter_1_q[3], ~counter_1_q[2], counter_1_q[1], counter_1_q[0], demultiplexer_1_out0);  // AND_Gate
  and and_3 (and_3_out, counter_1_q[5], counter_1_q[4], counter_1_q[3], ~counter_1_q[2], ~counter_1_q[1], counter_1_q[0], demultiplexer_1_out1);  // AND_Gate
  and and_4 (and_4_out, counter_1_q[5], ~counter_1_q[4], counter_1_q[3], ~counter_1_q[2], ~counter_1_q[1], counter_1_q[0], demultiplexer_1_out2);  // AND_Gate
  and and_5 (and_5_out, counter_1_q[5], ~counter_1_q[4], ~counter_1_q[3], ~counter_1_q[2], ~counter_1_q[1], counter_1_q[0], demultiplexer_1_out3);  // AND_Gate
  and and_6 (and_6_out, counter_1_q[5], counter_1_q[4], ~counter_1_q[3], ~counter_1_q[2], ~counter_1_q[1], counter_1_q[0], demultiplexer_1_out4);  // AND_Gate
  unit_control unit_control_1 (
    .EN(and_1_out), .RST_DIP(dipswitch_1_sw1), .ad_freq(unit_control_1_ad_freq),
    .ending(unit_control_1_ending));
  and and_7 (and_7_out, counter_1_q[5], ~counter_1_q[4], ~counter_1_q[3], counter_1_q[2], ~counter_1_q[1], counter_1_q[0], demultiplexer_1_out5);  // AND_Gate
  and and_8 (and_8_out, ~counter_1_q[5], counter_1_q[4], ~counter_1_q[3], counter_1_q[2], counter_1_q[1], ~counter_1_q[0], demultiplexer_1_out7);  // AND_Gate
  and and_9 (and_9_out, counter_1_q[5], ~counter_1_q[4], counter_1_q[3], counter_1_q[2], counter_1_q[1], ~counter_1_q[0], demultiplexer_1_out6);  // AND_Gate
  ending nul_1 (.Input_bus_1(counter_1_q), .Input_1(demultiplexer_1_out8), .Output_1(nul_1_output_1));
  ending nul_2 (.Input_bus_1(counter_1_q), .Input_1(demultiplexer_1_out9), .Output_1(nul_2_output_1));
  ending nul_3 (.Input_bus_1(counter_1_q), .Input_1(demultiplexer_1_out10), .Output_1(nul_3_output_1));
  ending nul_4 (.Input_bus_1(counter_1_q), .Input_1(demultiplexer_1_out11), .Output_1(nul_4_output_1));
  ending nul_5 (.Input_bus_1(counter_1_q), .Input_1(demultiplexer_1_out12), .Output_1(nul_5_output_1));
  ending nul_6 (.Input_bus_1(counter_1_q), .Input_1(demultiplexer_1_out13), .Output_1(nul_6_output_1));
  ending nul_7 (.Input_bus_1(counter_1_q), .Input_1(demultiplexer_1_out14), .Output_1(nul_7_output_1));
  ending nul_8 (.Input_bus_1(counter_1_q), .Input_1(demultiplexer_1_out15), .Output_1(nul_8_output_1));
  or or_1 (or_1_out, and_2_out, and_3_out, and_4_out, and_5_out, and_6_out, and_7_out, and_8_out, and_9_out);
  or or_2 (or_2_out, nul_1_output_1, nul_2_output_1, nul_3_output_1, nul_4_output_1, nul_5_output_1, nul_6_output_1, nul_7_output_1, nul_8_output_1);
  or or_3 (or_3_out, or_1_out, or_2_out);
  D_Flip_Flop d_ff_5 (.D(d_ff_5_qn), .clk(or_3_out), .Q(Output_1), .Qn(d_ff_5_qn));  // open: preset, reset

  assign terre = 1'b0;

  // Notes on the sheet:
  //   Debouncer
  //   B
  //   E
  //   F
  //   G
  //   F_s
  //   D_s
  //   B_2
  //   A_2
endmodule

module cmt (
  input  set,
  input  CLK,
  input  reset,
  output [4:0] Output_bus_1
);

  wire and_1_out, and_2_out, and_3_out;

  T_Flip_Flop t_ff_1 (.T(set), .clk(CLK), .Q(Output_bus_1[0]), .reset(reset));  // open: Qn, preset
  T_Flip_Flop t_ff_2 (.T(Output_bus_1[0]), .clk(CLK), .Q(Output_bus_1[1]), .reset(reset));  // open: Qn, preset
  T_Flip_Flop t_ff_3 (.T(and_1_out), .clk(CLK), .Q(Output_bus_1[2]), .reset(reset));  // open: Qn, preset
  T_Flip_Flop t_ff_4 (.T(and_2_out), .clk(CLK), .Q(Output_bus_1[3]), .reset(reset));  // open: Qn, preset
  T_Flip_Flop t_ff_5 (.T(and_3_out), .clk(CLK), .Q(Output_bus_1[4]), .reset(reset));  // open: Qn, preset
  and and_1 (and_1_out, Output_bus_1[1], Output_bus_1[0]);
  and and_2 (and_2_out, Output_bus_1[2], and_1_out);
  and and_3 (and_3_out, Output_bus_1[3], and_2_out);
endmodule

module partition (
  input  [4:0] cmt_part,
  output [3:0] freq,
  output [10:0] tempo
);

  Multiplexer #(.select(5), .width(4), .enable("false")) multiplexer_1 (
    .in0(4'b0000), .in1(4'b1111), .in2(4'b0001), .in3(4'b1111), .in4(4'b0011), .in5(4'b1111), .in6(4'b0010),
    .in7(4'b1111), .in8(4'b0001), .in9(4'b1111), .in10(4'b0111), .in11(4'b1111), .in12(4'b0110),
    .in13(4'b1111), .in14(4'b0100), .in15(4'b1111), .in16(4'b0001), .in17(4'b1111), .in18(4'b0011),
    .in19(4'b1111), .in20(4'b0010), .in21(4'b1111), .in22(4'b0101), .in23(4'b1111), .in24(4'b0010),
    .in25(4'b1111), .in26(4'b0000), .in27(4'b1111), .in28(4'b0111), .in29(4'b1111), .in30(4'b0111),
    .in31(4'b1111), .out(freq), .sel(cmt_part));
  Multiplexer #(.select(5), .width(11), .enable("false")) multiplexer_2 (
    .in0(11'h190), .in1(11'h64), .in2(11'h258), .in3(11'h64), .in4(11'hc8), .in5(11'h64), .in6(11'h190),
    .in7(11'h64), .in8(11'h320), .in9(11'h64), .in10(11'h190), .in11(11'h64), .in12(11'h3e8), .in13(11'h64),
    .in14(11'h3e8), .in15(11'h64), .in16(11'h258), .in17(11'h64), .in18(11'hc8), .in19(11'h64),
    .in20(11'h190), .in21(11'h64), .in22(11'h320), .in23(11'h64), .in24(11'h190), .in25(11'h64),
    .in26(11'h3e8), .in27(11'h64), .in28(11'h400), .in29(11'h64), .in30(11'h400), .in31(11'h64), .out(tempo),
    .sel(cmt_part));

  // Notes on the sheet:
  //   0.6
  //   0.2
  //   0.8
  //   1
  //   0.4
endmodule

module fin (
  input  [10:0] Input_bus_1,
  output Output_1
);

  and and_1 (Output_1, ~Input_bus_1[0], ~Input_bus_1[1], ~Input_bus_1[2], ~Input_bus_1[3], ~Input_bus_1[4], ~Input_bus_1[5], ~Input_bus_1[6], ~Input_bus_1[7], ~Input_bus_1[8], ~Input_bus_1[9], Input_bus_1[10]);  // AND_Gate
endmodule

module cmt_tempo (
  input  en_tmpo,
  input  [10:0] tempo_bis,
  input  clk_tempo,
  output set_tmpo
);

  wire and_1_out, and_2_out, and_3_out, and_4_out, and_5_out, and_6_out, and_7_out, and_8_out, and_9_out,
       and_11_out, and_12_out, d_ff_1_q, t_ff_1_q, t_ff_2_q, t_ff_3_q, t_ff_4_q, t_ff_5_q, t_ff_6_q,
       t_ff_7_q, t_ff_8_q, t_ff_9_q, t_ff_10_q, t_ff_11_q, undriven, xnor_1_out, xnor_2_out, xnor_3_out,
       xnor_4_out, xnor_5_out, xnor_6_out, xnor_7_out, xnor_8_out, xnor_9_out, xnor_10_out, xnor_11_out,
       xnor_12_out, xnor_13_out, xnor_14_out, xnor_15_out, xnor_16_out, xnor_17_out, xnor_18_out,
       xnor_19_out, xnor_20_out, xnor_21_out, xnor_22_out;
  wire [10:0] subtractor_1_out;

  T_Flip_Flop t_ff_1 (.T(and_7_out), .clk(clk_tempo), .Q(t_ff_1_q), .reset(and_11_out));  // open: Qn, preset
  T_Flip_Flop t_ff_2 (.T(en_tmpo), .clk(clk_tempo), .Q(t_ff_2_q), .reset(and_11_out));  // open: Qn, preset
  T_Flip_Flop t_ff_3 (.T(t_ff_2_q), .clk(clk_tempo), .Q(t_ff_3_q), .reset(and_11_out));  // open: Qn, preset
  T_Flip_Flop t_ff_4 (.T(and_1_out), .clk(clk_tempo), .Q(t_ff_4_q), .reset(and_11_out));  // open: Qn, preset
  T_Flip_Flop t_ff_5 (.T(and_2_out), .clk(clk_tempo), .Q(t_ff_5_q), .reset(and_11_out), .preset(undriven));  // open: Qn
  T_Flip_Flop t_ff_6 (.T(and_3_out), .clk(clk_tempo), .Q(t_ff_6_q), .reset(and_11_out));  // open: Qn, preset
  T_Flip_Flop t_ff_7 (.T(and_4_out), .clk(clk_tempo), .Q(t_ff_7_q), .reset(and_11_out));  // open: Qn, preset
  T_Flip_Flop t_ff_8 (.T(and_5_out), .clk(clk_tempo), .Q(t_ff_8_q), .reset(and_11_out));  // open: Qn, preset
  T_Flip_Flop t_ff_9 (.T(and_6_out), .clk(clk_tempo), .Q(t_ff_9_q), .reset(and_11_out));  // open: Qn, preset
  T_Flip_Flop t_ff_10 (.T(and_8_out), .clk(clk_tempo), .Q(t_ff_10_q), .reset(and_11_out));  // open: Qn, preset
  T_Flip_Flop t_ff_11 (.T(and_9_out), .clk(clk_tempo), .Q(t_ff_11_q), .reset(and_11_out));  // open: Qn, preset
  and and_1 (and_1_out, t_ff_3_q, t_ff_2_q);
  and and_2 (and_2_out, t_ff_4_q, and_1_out);
  and and_3 (and_3_out, t_ff_5_q, and_2_out);
  and and_4 (and_4_out, t_ff_6_q, and_3_out);
  and and_5 (and_5_out, t_ff_7_q, and_4_out);
  and and_6 (and_6_out, t_ff_8_q, and_5_out);
  and and_7 (and_7_out, t_ff_9_q, and_6_out);
  and and_8 (and_8_out, t_ff_1_q, and_7_out);
  and and_9 (and_9_out, t_ff_10_q, and_8_out);
  // AND_Gate and_10 has open pins: in0=t_ff_11_q, in1=and_9_out, out=open
  xnor xnor_1 (xnor_1_out, t_ff_11_q, tempo_bis[10]);
  xnor xnor_2 (xnor_2_out, t_ff_10_q, tempo_bis[9]);
  xnor xnor_3 (xnor_3_out, t_ff_1_q, tempo_bis[8]);
  xnor xnor_4 (xnor_4_out, t_ff_8_q, tempo_bis[6]);
  xnor xnor_5 (xnor_5_out, t_ff_9_q, tempo_bis[7]);
  xnor xnor_6 (xnor_6_out, t_ff_7_q, tempo_bis[5]);
  and and_11 (and_11_out, xnor_1_out, xnor_2_out, xnor_3_out, xnor_5_out, xnor_4_out, xnor_6_out, xnor_7_out, xnor_9_out, xnor_8_out, xnor_10_out, xnor_11_out);
  xnor xnor_7 (xnor_7_out, t_ff_6_q, tempo_bis[4]);
  xnor xnor_8 (xnor_8_out, t_ff_4_q, tempo_bis[2]);
  xnor xnor_9 (xnor_9_out, t_ff_5_q, tempo_bis[3]);
  xnor xnor_10 (xnor_10_out, t_ff_3_q, tempo_bis[1]);
  D_Flip_Flop d_ff_1 (.D(and_12_out), .clk(clk_tempo), .Q(d_ff_1_q));  // open: Qn, preset, reset
  xnor xnor_11 (xnor_11_out, t_ff_2_q, tempo_bis[0]);
  or or_1 (set_tmpo, and_12_out, d_ff_1_q);
  Subtractor #(.width(11)) subtractor_1 (.a(tempo_bis), .b(11'h1), .out(subtractor_1_out));  // open: bin, bout
  xnor xnor_12 (xnor_12_out, t_ff_11_q, subtractor_1_out[10]);
  xnor xnor_13 (xnor_13_out, t_ff_1_q, subtractor_1_out[8]);
  xnor xnor_14 (xnor_14_out, t_ff_10_q, subtractor_1_out[9]);
  xnor xnor_15 (xnor_15_out, t_ff_9_q, subtractor_1_out[7]);
  xnor xnor_16 (xnor_16_out, t_ff_8_q, subtractor_1_out[6]);
  xnor xnor_17 (xnor_17_out, t_ff_7_q, subtractor_1_out[5]);
  xnor xnor_18 (xnor_18_out, t_ff_6_q, subtractor_1_out[4]);
  and and_12 (and_12_out, xnor_12_out, xnor_14_out, xnor_13_out, xnor_15_out, xnor_16_out, xnor_17_out, xnor_18_out, xnor_19_out, xnor_20_out, xnor_21_out, xnor_22_out);
  xnor xnor_19 (xnor_19_out, t_ff_5_q, subtractor_1_out[3]);
  xnor xnor_20 (xnor_20_out, t_ff_4_q, subtractor_1_out[2]);
  xnor xnor_21 (xnor_21_out, t_ff_3_q, subtractor_1_out[1]);
  xnor xnor_22 (xnor_22_out, t_ff_2_q, subtractor_1_out[0]);
endmodule

module ending (
  input  [5:0] Input_bus_1,
  input  Input_1,
  output Output_1
);

  and and_1 (Output_1, Input_bus_1[5], Input_bus_1[4], Input_bus_1[3], Input_bus_1[2], Input_bus_1[1], Input_bus_1[0], Input_1);
endmodule

module unit_control (
  input  EN,
  input  RST_DIP,
  output [3:0] ad_freq,
  output ending
);

  wire and_1_out, and_2_out, and_3_out, clock_1_out, cmt_tempo_1_set_tmpo, fin_1_output_1, not_1_out,
       not_2_out;
  wire [4:0] cmt_1_output_bus_1;
  wire [10:0] partition_1_tempo;

  Clock #(.highDuration(8), .lowDuration(8)) clock_1 (.out(clock_1_out));
  and and_1 (and_1_out, 1'b1, fin_1_output_1);
  not not_1 (not_1_out, EN);
  and and_2 (and_2_out, not_1_out, and_1_out);
  not not_2 (not_2_out, fin_1_output_1);
  cmt_tempo cmt_tempo_1 (
    .en_tmpo(not_2_out), .tempo_bis(partition_1_tempo), .clk_tempo(clock_1_out),
    .set_tmpo(cmt_tempo_1_set_tmpo));
  or or_1 (ending, RST_DIP, fin_1_output_1);
  cmt cmt_1 (.set(and_3_out), .CLK(clock_1_out), .reset(and_2_out), .Output_bus_1(cmt_1_output_bus_1));
  and and_3 (and_3_out, cmt_tempo_1_set_tmpo, ~fin_1_output_1);  // AND_Gate
  fin fin_1 (.Input_bus_1(partition_1_tempo), .Output_1(fin_1_output_1));
  partition partition_1 (.cmt_part(cmt_1_output_bus_1), .freq(ad_freq), .tempo(partition_1_tempo));
endmodule

module to_mute (
  input  [10:0] tempo,
  output muting
);

  and and_1 (muting, ~tempo[0], ~tempo[1], ~tempo[2], ~tempo[3], ~tempo[4], ~tempo[5], ~tempo[6], ~tempo[7], ~tempo[8], tempo[9], tempo[10]);  // AND_Gate
endmodule

module cmt_tempo2 (
  input  in_1,
  input  [10:0] in_2,
  input  in_3,
  output out_4
);

  wire and_1_out, and_2_out, d_ff_1_q, t_ff_1_q, t_ff_1_qn, t_ff_2_q, t_ff_2_qn, t_ff_3_q, t_ff_3_qn,
       t_ff_4_q, t_ff_4_qn, t_ff_5_q, t_ff_5_qn, t_ff_6_q, t_ff_6_qn, t_ff_7_q, t_ff_7_qn, t_ff_8_q,
       t_ff_8_qn, t_ff_9_q, t_ff_9_qn, t_ff_10_q, t_ff_10_qn, t_ff_11_q, xnor_1_out, xnor_2_out, xnor_3_out,
       xnor_4_out, xnor_5_out, xnor_6_out, xnor_7_out, xnor_8_out, xnor_9_out, xnor_10_out, xnor_11_out,
       xnor_12_out, xnor_13_out, xnor_14_out, xnor_15_out, xnor_16_out, xnor_17_out, xnor_18_out,
       xnor_19_out, xnor_20_out, xnor_21_out, xnor_22_out;
  wire [10:0] subtractor_1_out;

  T_Flip_Flop t_ff_1 (.T(in_1), .clk(in_3), .Q(t_ff_1_q), .Qn(t_ff_1_qn), .reset(and_1_out));  // open: preset
  T_Flip_Flop t_ff_2 (.T(in_1), .clk(t_ff_1_qn), .Q(t_ff_2_q), .Qn(t_ff_2_qn), .reset(and_1_out));  // open: preset
  T_Flip_Flop t_ff_3 (.T(in_1), .clk(t_ff_2_qn), .Q(t_ff_3_q), .Qn(t_ff_3_qn), .reset(and_1_out));  // open: preset
  T_Flip_Flop t_ff_4 (.T(in_1), .clk(t_ff_3_qn), .Q(t_ff_4_q), .Qn(t_ff_4_qn), .reset(and_1_out));  // open: preset
  T_Flip_Flop t_ff_5 (.T(in_1), .clk(t_ff_4_qn), .Q(t_ff_5_q), .Qn(t_ff_5_qn), .reset(and_1_out));  // open: preset
  T_Flip_Flop t_ff_6 (.T(in_1), .clk(t_ff_5_qn), .Q(t_ff_6_q), .Qn(t_ff_6_qn), .reset(and_1_out));  // open: preset
  T_Flip_Flop t_ff_7 (.T(in_1), .clk(t_ff_6_qn), .Q(t_ff_7_q), .Qn(t_ff_7_qn), .reset(and_1_out));  // open: preset
  T_Flip_Flop t_ff_8 (.T(in_1), .clk(t_ff_7_qn), .Q(t_ff_8_q), .Qn(t_ff_8_qn), .reset(and_1_out));  // open: preset
  T_Flip_Flop t_ff_9 (.T(in_1), .clk(t_ff_8_qn), .Q(t_ff_9_q), .Qn(t_ff_9_qn), .reset(and_1_out));  // open: preset
  T_Flip_Flop t_ff_10 (.T(in_1), .clk(t_ff_9_qn), .Q(t_ff_10_q), .Qn(t_ff_10_qn), .reset(and_1_out));  // open: preset
  T_Flip_Flop t_ff_11 (.T(in_1), .clk(t_ff_10_qn), .Q(t_ff_11_q), .reset(and_1_out));  // open: Qn, preset
  xnor xnor_1 (xnor_1_out, t_ff_11_q, in_2[10]);
  xnor xnor_2 (xnor_2_out, t_ff_10_q, in_2[9]);
  xnor xnor_3 (xnor_3_out, t_ff_9_q, in_2[8]);
  xnor xnor_4 (xnor_4_out, t_ff_8_q, in_2[7]);
  xnor xnor_5 (xnor_5_out, t_ff_7_q, in_2[6]);
  xnor xnor_6 (xnor_6_out, t_ff_6_q, in_2[5]);
  and and_1 (and_1_out, xnor_1_out, xnor_2_out, xnor_3_out, xnor_4_out, xnor_5_out, xnor_6_out, xnor_7_out, xnor_9_out, xnor_8_out, xnor_10_out, xnor_11_out);
  xnor xnor_7 (xnor_7_out, t_ff_5_q, in_2[4]);
  xnor xnor_8 (xnor_8_out, t_ff_3_q, in_2[2]);
  xnor xnor_9 (xnor_9_out, t_ff_4_q, in_2[3]);
  D_Flip_Flop d_ff_1 (.D(and_2_out), .clk(in_3), .Q(d_ff_1_q));  // open: Qn, preset, reset
  xnor xnor_10 (xnor_10_out, t_ff_2_q, in_2[1]);
  xnor xnor_11 (xnor_11_out, t_ff_1_q, in_2[0]);
  or or_1 (out_4, and_2_out, d_ff_1_q);
  Subtractor #(.width(11)) subtractor_1 (.a(in_2), .b(11'h1), .out(subtractor_1_out));  // open: bin, bout
  xnor xnor_12 (xnor_12_out, t_ff_11_q, subtractor_1_out[10]);
  xnor xnor_13 (xnor_13_out, t_ff_10_q, subtractor_1_out[9]);
  xnor xnor_14 (xnor_14_out, t_ff_9_q, subtractor_1_out[8]);
  xnor xnor_15 (xnor_15_out, t_ff_8_q, subtractor_1_out[7]);
  xnor xnor_16 (xnor_16_out, t_ff_7_q, subtractor_1_out[6]);
  xnor xnor_17 (xnor_17_out, t_ff_5_q, subtractor_1_out[4]);
  xnor xnor_18 (xnor_18_out, t_ff_6_q, subtractor_1_out[5]);
  and and_2 (and_2_out, xnor_12_out, xnor_13_out, xnor_14_out, xnor_15_out, xnor_16_out, xnor_18_out, xnor_17_out, xnor_19_out, xnor_20_out, xnor_21_out, xnor_22_out);
  xnor xnor_19 (xnor_19_out, t_ff_4_q, subtractor_1_out[3]);
  xnor xnor_20 (xnor_20_out, t_ff_3_q, subtractor_1_out[2]);
  xnor xnor_21 (xnor_21_out, t_ff_2_q, subtractor_1_out[1]);
  xnor xnor_22 (xnor_22_out, t_ff_1_q, subtractor_1_out[0]);
endmodule
