// Logisim project testbase60counter.circ as structural Verilog: 7 circuits, main circuit mod60
module mod60 (
  input  EN,
  input  dir,
  input  CLK,
  input  mrst,
  output [5:0] count,
  output ovrf,
  output undf
);

  wire d_ff_7_q, d_ff_8_q, d_ff_9_q, d_ff_10_q, updown60_1_d0, updown60_1_d1, updown60_1_d2, updown60_1_d3,
       updown60_1_d4, updown60_1_d5, updown60_1_ovrf, updown60_1_undf;

  updown60 updown60_1 (
    .EN(EN), .DIR(dir), .Q5(count[5]), .Q4(count[4]), .Q3(count[3]), .Q2(count[2]), .Q1(count[1]),
    .Q0(count[0]), .D5(updown60_1_d5), .D4(updown60_1_d4), .D3(updown60_1_d3), .D2(updown60_1_d2),
    .D1(updown60_1_d1), .D0(updown60_1_d0), .OVRF(updown60_1_ovrf), .UNDF(updown60_1_undf));
  D_Flip_Flop d_ff_1 (.D(updown60_1_d0), .clk(CLK), .Q(count[0]), .reset(mrst));  // open: Qn, preset
  D_Flip_Flop d_ff_2 (.D(updown60_1_d1), .clk(CLK), .Q(count[1]), .reset(mrst));  // open: Qn, preset
  D_Flip_Flop d_ff_3 (.D(updown60_1_d2), .clk(CLK), .Q(count[2]), .reset(mrst));  // open: Qn, preset
  D_Flip_Flop d_ff_4 (.D(updown60_1_d3), .clk(CLK), .Q(count[3]), .reset(mrst));  // open: Qn, preset
  D_Flip_Flop d_ff_5 (.D(updown60_1_d4), .clk(CLK), .Q(count[4]), .reset(mrst));  // open: Qn, preset
  D_Flip_Flop d_ff_6 (.D(updown60_1_d5), .clk(CLK), .Q(count[5]), .reset(mrst));  // open: Qn, preset
  D_Flip_Flop d_ff_7 (.D(updown60_1_ovrf), .clk(CLK), .Q(d_ff_7_q), .reset(mrst));  // open: Qn, preset
  D_Flip_Flop d_ff_8 (.D(updown60_1_undf), .clk(CLK), .Q(d_ff_8_q), .reset(mrst));  // open: Qn, preset
  D_Flip_Flop d_ff_9 (.D(d_ff_7_q), .clk(CLK), .Q(d_ff_9_q), .reset(mrst));  // open: Qn, preset
  D_Flip_Flop d_ff_10 (.D(d_ff_8_q), .clk(CLK), .Q(d_ff_10_q), .reset(mrst));  // open: Qn, preset
  and and_1 (ovrf, d_ff_7_q, ~d_ff_9_q);  // AND_Gate
  and and_2 (undf, d_ff_8_q, ~d_ff_10_q);  // AND_Gate
endmodule

module en60base (
  input  EN,
  input  q5,
  input  q4,
  input  q3,
  input  q2,
  input  q1,
  input  q0,
  output d5,
  output d4,
  output d3,
  output d2,
  output d1,
  output d0,
  output ovr
);

  wire and_1_out, and_2_out, and_3_out, and_4_out, and_5_out, and_6_out, and_7_out, and_8_out, and_9_out,
       and_10_out, and_11_out, and_12_out, and_13_out, and_14_out, and_15_out, and_16_out, and_17_out,
       and_18_out, and_19_out, and_20_out, and_21_out, and_22_out, and_23_out, and_24_out, and_25_out,
       and_26_out, and_27_out, and_28_out, and_29_out, and_30_out, and_31_out, and_32_out, and_33_out,
       and_34_out, and_35_out, and_36_out, and_37_out, and_38_out, and_39_out, and_40_out, and_41_out,
       and_42_out, and_43_out, and_44_out, and_45_out, and_46_out, and_47_out, and_48_out, and_49_out,
       and_50_out, and_51_out, and_52_out, and_53_out, and_54_out, and_55_out, and_56_out, and_57_out,
       and_58_out, and_59_out, not_1_out, not_2_out, not_3_out, not_4_out, not_5_out, not_6_out, not_7_out,
       not_8_out, not_9_out, not_10_out, not_11_out, not_12_out, not_13_out, not_14_out, not_15_out,
       not_16_out, not_17_out, not_18_out, not_19_out, not_20_out, not_21_out, not_22_out, not_23_out,
       not_24_out, not_25_out, not_26_out, not_27_out, not_28_out, not_29_out, not_30_out, not_31_out,
       not_32_out, not_33_out, not_34_out, not_35_out, not_36_out, not_37_out, not_38_out, not_39_out,
       not_40_out, not_41_out, not_42_out, not_43_out, not_44_out, not_45_out, not_46_out, not_47_out,
       not_48_out, not_49_out, not_50_out, not_51_out, not_52_out, not_53_out, not_54_out, not_55_out,
       not_56_out, not_57_out, not_58_out, not_59_out, not_60_out, not_61_out, not_62_out, not_63_out,
       not_64_out, not_65_out, not_66_out, not_67_out, not_68_out, not_69_out, not_70_out, not_71_out,
       not_72_out, not_73_out, not_74_out, not_75_out, not_76_out, not_77_out, not_78_out, not_79_out,
       not_80_out, not_81_out, not_82_out, not_83_out, not_84_out, not_85_out, not_86_out, not_87_out,
       not_88_out, not_89_out, not_90_out, not_91_out, not_92_out, not_93_out, not_94_out, not_95_out,
       not_96_out, not_97_out, not_98_out, not_99_out, not_100_out, not_101_out, not_102_out, not_103_out,
       not_104_out, not_105_out, not_106_out, not_107_out, not_108_out, not_109_out, not_110_out,
       not_111_out, not_112_out, not_113_out;

  not not_1 (not_1_out, EN);
  not not_2 (not_2_out, q2);
  not not_3 (not_3_out, q4);
  not not_4 (not_4_out, q3);
  not not_5 (not_5_out, q2);
  not not_6 (not_6_out, q1);
  not not_7 (not_7_out, q2);
  not not_8 (not_8_out, q0);
  not not_9 (not_9_out, q5);
  not not_10 (not_10_out, EN);
  not not_11 (not_11_out, q5);
  not not_12 (not_12_out, EN);
  not not_13 (not_13_out, q2);
  not not_14 (not_14_out, q5);
  not not_15 (not_15_out, q2);
  not not_16 (not_16_out, q5);
  not not_17 (not_17_out, q1);
  not not_18 (not_18_out, q5);
  not not_19 (not_19_out, q0);
  not not_20 (not_20_out, q3);
  not not_21 (not_21_out, q2);
  not not_22 (not_22_out, q1);
  not not_23 (not_23_out, q2);
  not not_24 (not_24_out, q0);
  not not_25 (not_25_out, q4);
  not not_26 (not_26_out, EN);
  not not_27 (not_27_out, q5);
  not not_28 (not_28_out, EN);
  not not_29 (not_29_out, q4);
  not not_30 (not_30_out, EN);
  not not_31 (not_31_out, q2);
  not not_32 (not_32_out, q5);
  not not_33 (not_33_out, q2);
  not not_34 (not_34_out, q5);
  not not_35 (not_35_out, q1);
  not not_36 (not_36_out, q5);
  not not_37 (not_37_out, q0);
  not not_38 (not_38_out, q4);
  not not_39 (not_39_out, q2);
  not not_40 (not_40_out, q4);
  not not_41 (not_41_out, q1);
  not not_42 (not_42_out, q4);
  not not_43 (not_43_out, q0);
  not not_44 (not_44_out, q2);
  not not_45 (not_45_out, q1);
  not not_46 (not_46_out, q2);
  not not_47 (not_47_out, q0);
  not not_48 (not_48_out, q3);
  not not_49 (not_49_out, EN);
  not not_50 (not_50_out, q5);
  not not_51 (not_51_out, EN);
  not not_52 (not_52_out, q4);
  not not_53 (not_53_out, EN);
  not not_54 (not_54_out, q3);
  not not_55 (not_55_out, q5);
  not not_56 (not_56_out, q1);
  not not_57 (not_57_out, q5);
  not not_58 (not_58_out, q0);
  not not_59 (not_59_out, q4);
  not not_60 (not_60_out, q1);
  not not_61 (not_61_out, q4);
  not not_62 (not_62_out, q0);
  not not_63 (not_63_out, q3);
  not not_64 (not_64_out, q1);
  not not_65 (not_65_out, q3);
  not not_66 (not_66_out, q0);
  not not_67 (not_67_out, q5);
  not not_68 (not_68_out, q2);
  not not_69 (not_69_out, q4);
  not not_70 (not_70_out, q2);
  not not_71 (not_71_out, q3);
  not not_72 (not_72_out, q2);
  not not_73 (not_73_out, EN);
  not not_74 (not_74_out, q5);
  not not_75 (not_75_out, EN);
  not not_76 (not_76_out, q4);
  not not_77 (not_77_out, EN);
  not not_78 (not_78_out, q3);
  not not_79 (not_79_out, EN);
  not not_80 (not_80_out, q2);
  not not_81 (not_81_out, q5);
  not not_82 (not_82_out, q0);
  not not_83 (not_83_out, q4);
  not not_84 (not_84_out, q0);
  not not_85 (not_85_out, q3);
  not not_86 (not_86_out, q0);
  not not_87 (not_87_out, q2);
  not not_88 (not_88_out, q0);
  not not_89 (not_89_out, q5);
  not not_90 (not_90_out, q1);
  not not_91 (not_91_out, q4);
  not not_92 (not_92_out, q1);
  not not_93 (not_93_out, q3);
  not not_94 (not_94_out, q1);
  not not_95 (not_95_out, q2);
  not not_96 (not_96_out, q1);
  not not_97 (not_97_out, EN);
  not not_98 (not_98_out, q5);
  not not_99 (not_99_out, EN);
  not not_100 (not_100_out, q4);
  not not_101 (not_101_out, EN);
  not not_102 (not_102_out, q3);
  not not_103 (not_103_out, EN);
  not not_104 (not_104_out, q2);
  not not_105 (not_105_out, q5);
  not not_106 (not_106_out, q0);
  not not_107 (not_107_out, q4);
  not not_108 (not_108_out, q0);
  not not_109 (not_109_out, q3);
  not not_110 (not_110_out, q0);
  not not_111 (not_111_out, q2);
  not not_112 (not_112_out, q0);
  not not_113 (not_113_out, q2);
  and and_1 (and_1_out, not_1_out, q5, not_2_out);
  and and_2 (and_2_out, q5, not_3_out);
  and and_3 (and_3_out, q5, not_4_out);
  and and_4 (and_4_out, q5, not_5_out, not_6_out);
  and and_5 (and_5_out, q5, not_7_out, not_8_out);
  and and_6 (and_6_out, EN, not_9_out, q4, q3, q2, q1, q0);
  and and_7 (and_7_out, not_10_out, not_11_out, q4);
  and and_8 (and_8_out, not_12_out, q4, not_13_out);
  and and_9 (and_9_out, not_14_out, q4, not_15_out);
  and and_10 (and_10_out, not_16_out, q4, not_17_out);
  and and_11 (and_11_out, not_18_out, q4, not_19_out);
  and and_12 (and_12_out, q4, not_20_out);
  and and_13 (and_13_out, q4, not_21_out, not_22_out);
  and and_14 (and_14_out, q4, not_23_out, not_24_out);
  and and_15 (and_15_out, EN, not_25_out, q3, q2, q1, q0);
  and and_16 (and_16_out, not_26_out, not_27_out, q3);
  and and_17 (and_17_out, not_28_out, not_29_out, q3);
  and and_18 (and_18_out, not_30_out, q3, not_31_out);
  and and_19 (and_19_out, not_32_out, q3, not_33_out);
  and and_20 (and_20_out, not_34_out, q3, not_35_out);
  and and_21 (and_21_out, not_36_out, q3, not_37_out);
  and and_22 (and_22_out, not_38_out, q3, not_39_out);
  and and_23 (and_23_out, not_40_out, q3, not_41_out);
  and and_24 (and_24_out, not_42_out, q3, not_43_out);
  and and_25 (and_25_out, q3, not_44_out, not_45_out);
  and and_26 (and_26_out, q3, not_46_out, not_47_out);
  and and_27 (and_27_out, EN, not_48_out, q2, q1, q0);
  and and_28 (and_28_out, not_49_out, not_50_out, q2);
  and and_29 (and_29_out, not_51_out, not_52_out, q2);
  and and_30 (and_30_out, not_53_out, not_54_out, q2);
  and and_31 (and_31_out, not_55_out, q2, not_56_out);
  and and_32 (and_32_out, not_57_out, q2, not_58_out);
  and and_33 (and_33_out, not_59_out, q2, not_60_out);
  and and_34 (and_34_out, not_61_out, q2, not_62_out);
  and and_35 (and_35_out, not_63_out, q2, not_64_out);
  and and_36 (and_36_out, not_65_out, q2, not_66_out);
  and and_37 (and_37_out, EN, not_67_out, not_68_out, q1, q0);
  and and_38 (and_38_out, EN, not_69_out, not_70_out, q1, q0);
  and and_39 (and_39_out, EN, not_71_out, not_72_out, q1, q0);
  and and_40 (and_40_out, not_73_out, not_74_out, q1);
  and and_41 (and_41_out, not_75_out, not_76_out, q1);
  and and_42 (and_42_out, not_77_out, not_78_out, q1);
  and and_43 (and_43_out, not_79_out, not_80_out, q1);
  and and_44 (and_44_out, not_81_out, q1, not_82_out);
  and and_45 (and_45_out, not_83_out, q1, not_84_out);
  and and_46 (and_46_out, not_85_out, q1, not_86_out);
  and and_47 (and_47_out, not_87_out, q1, not_88_out);
  and and_48 (and_48_out, EN, not_89_out, not_90_out, q0);
  and and_49 (and_49_out, EN, not_91_out, not_92_out, q0);
  and and_50 (and_50_out, EN, not_93_out, not_94_out, q0);
  and and_51 (and_51_out, EN, not_95_out, not_96_out, q0);
  and and_52 (and_52_out, not_97_out, not_98_out, q0);
  and and_53 (and_53_out, not_99_out, not_100_out, q0);
  and and_54 (and_54_out, not_101_out, not_102_out, q0);
  and and_55 (and_55_out, not_103_out, not_104_out, q0);
  and and_56 (and_56_out, EN, not_105_out, not_106_out);
  and and_57 (and_57_out, EN, not_107_out, not_108_out);
  and and_58 (and_58_out, EN, not_109_out, not_110_out);
  and and_59 (and_59_out, EN, not_111_out, not_112_out);
  and and_60 (ovr, EN, q5, q4, q3, not_113_out, q1, q0);
  or or_1 (d5, and_1_out, and_2_out, and_3_out, and_4_out, and_5_out, and_6_out);
  or or_2 (d4, and_7_out, and_8_out, and_9_out, and_10_out, and_11_out, and_12_out, and_13_out, and_14_out, and_15_out);
  or or_3 (d3, and_16_out, and_17_out, and_18_out, and_19_out, and_20_out, and_21_out, and_22_out, and_23_out, and_24_out, and_25_out, and_26_out, and_27_out);
  or or_4 (d2, and_28_out, and_29_out, and_30_out, and_31_out, and_32_out, and_33_out, and_34_out, and_35_out, and_36_out, and_37_out, and_38_out, and_39_out);
  or or_5 (d1, and_40_out, and_41_out, and_42_out, and_43_out, and_44_out, and_45_out, and_46_out, and_47_out, and_48_out, and_49_out, and_50_out, and_51_out);
  or or_6 (d0, and_52_out, and_53_out, and_54_out, and_55_out, and_56_out, and_57_out, and_58_out, and_59_out);
endmodule

module cndt (
  input  rst,
  input  clk,
  input  change,
  input  choice,
  input  inc,
  input  go,
  output [5:0] out_7,
  output [5:0] out_8,
  output [4:0] out_9
);

  wire and_1_out, and_2_out, and_3_out, and_7_out, and_8_out, and_9_out, and_10_out, mod24_1_undf,
       mod60_1_ovrf, mod60_2_ovrf, mod60_2_undf, or_1_out, or_2_out, shift3_1_out_4, shift3_1_out_5,
       shift3_1_out_6, t_ff_1_q, t_ff_1_qn, undriven;

  T_Flip_Flop t_ff_1 (.T(change), .clk(clk), .Q(t_ff_1_q), .Qn(t_ff_1_qn), .reset(rst));  // open: preset
  and and_1 (and_1_out, t_ff_1_q, choice);
  and and_2 (and_2_out, t_ff_1_q, inc);
  and and_3 (and_3_out, ~t_ff_1_q, go);  // AND_Gate
  shift3 shift3_1 (
    .EN(and_1_out), .rst(rst), .clk(clk), .out_4(shift3_1_out_4), .out_5(shift3_1_out_5),
    .out_6(shift3_1_out_6));
  // AND_Gate and_4 has open pins: in0=and_2_out, in1=shift3_1_out_4, out=open
  // AND_Gate and_5 has open pins: in0=and_2_out, in1=shift3_1_out_5, out=open
  // AND_Gate and_6 has open pins: in0=and_2_out, in1=shift3_1_out_6, out=open
  and and_7 (and_7_out, mod24_1_undf, t_ff_1_qn);
  buf and_8 (and_8_out, ~t_ff_1_qn);  // AND_Gate AND_Gate
  buf or_1 (or_1_out, and_9_out);  // OR_Gate
  and and_9 (and_9_out, t_ff_1_qn, mod60_2_undf);
  and and_10 (and_10_out, undriven, ~t_ff_1_qn);  // AND_Gate
  or or_2 (or_2_out, and_10_out, and_7_out);
  mod60 mod60_1 (
    .EN(or_1_out), .dir(t_ff_1_qn), .CLK(clk), .mrst(rst), .count(out_7), .ovrf(mod60_1_ovrf));  // open: undf
  mod60 mod60_2 (
    .EN(or_2_out), .dir(t_ff_1_qn), .CLK(clk), .mrst(rst), .count(out_8), .ovrf(mod60_2_ovrf),
    .undf(mod60_2_undf));
  mod24 mod24_1 (
    .en(and_8_out), .dir(t_ff_1_qn), .clk(clk), .rst(rst), .hour(out_9), .undf(mod24_1_undf));  // open: ovrf
endmodule

module updown60 (
  input  EN,
  input  DIR,
  input  Q5,
  input  Q4,
  input  Q3,
  input  Q2,
  input  Q1,
  input  Q0,
  output D5,
  output D4,
  output D3,
  output D2,
  output D1,
  output D0,
  output OVRF,
  output UNDF
);

  wire and_1_out, and_2_out, and_3_out, and_4_out, and_5_out, and_6_out, and_7_out, and_8_out, and_9_out,
       and_10_out, and_11_out, and_12_out, and_13_out, and_14_out, and_15_out, and_16_out, and_17_out,
       and_18_out, and_19_out, and_20_out, and_21_out, and_22_out, and_23_out, and_24_out, and_25_out,
       and_26_out, and_27_out, and_28_out, and_29_out, and_30_out, and_31_out, and_32_out, and_33_out,
       and_34_out, and_35_out, and_36_out, and_37_out, and_38_out, and_39_out, and_40_out, and_41_out,
       and_42_out, and_43_out, and_44_out, and_45_out, and_46_out, and_47_out, and_48_out, and_49_out,
       and_50_out, and_51_out, and_52_out, not_1_out, not_2_out, not_3_out, not_4_out, not_5_out, not_6_out,
       not_7_out, not_8_out, not_9_out, not_10_out, not_11_out, not_12_out, not_13_out, not_14_out,
       not_15_out, not_16_out, not_17_out, not_18_out, not_19_out, not_20_out, not_21_out, not_22_out,
       not_23_out, not_24_out, not_25_out, not_26_out, not_27_out, not_28_out, not_29_out, not_30_out,
       not_31_out, not_32_out, not_33_out, not_34_out, not_35_out, not_36_out, not_37_out, not_38_out,
       not_39_out, not_40_out, not_41_out, not_42_out, not_43_out, not_44_out, not_45_out, not_46_out,
       not_47_out, not_48_out, not_49_out, not_50_out, not_51_out, not_52_out, not_53_out, not_54_out,
       not_55_out, not_56_out, not_57_out, not_58_out, not_59_out, not_60_out, not_61_out, not_62_out,
       not_63_out, not_64_out, not_65_out, not_66_out, not_67_out, not_68_out, not_69_out, not_70_out,
       not_71_out, not_72_out, not_73_out, not_74_out, not_75_out, not_76_out, not_77_out, not_78_out,
       not_79_out, not_80_out, not_81_out, not_82_out, not_83_out, not_84_out, not_85_out, not_86_out,
       not_87_out, not_88_out, not_89_out, not_90_out, not_91_out, not_92_out, not_93_out, not_94_out,
       not_95_out, not_96_out;

  not not_1 (not_1_out, DIR);
  not not_2 (not_2_out, Q5);
  not not_3 (not_3_out, Q4);
  not not_4 (not_4_out, Q3);
  not not_5 (not_5_out, Q2);
  not not_6 (not_6_out, Q1);
  not not_7 (not_7_out, Q0);
  not not_8 (not_8_out, EN);
  not not_9 (not_9_out, DIR);
  not not_10 (not_10_out, Q3);
  not not_11 (not_11_out, Q3);
  not not_12 (not_12_out, Q3);
  not not_13 (not_13_out, Q3);
  not not_14 (not_14_out, Q5);
  not not_15 (not_15_out, Q2);
  not not_16 (not_16_out, Q1);
  not not_17 (not_17_out, Q0);
  not not_18 (not_18_out, DIR);
  not not_19 (not_19_out, Q4);
  not not_20 (not_20_out, Q4);
  not not_21 (not_21_out, Q3);
  not not_22 (not_22_out, Q2);
  not not_23 (not_23_out, Q1);
  not not_24 (not_24_out, Q0);
  not not_25 (not_25_out, EN);
  not not_26 (not_26_out, DIR);
  not not_27 (not_27_out, Q5);
  not not_28 (not_28_out, Q2);
  not not_29 (not_29_out, DIR);
  not not_30 (not_30_out, Q4);
  not not_31 (not_31_out, Q2);
  not not_32 (not_32_out, DIR);
  not not_33 (not_33_out, Q1);
  not not_34 (not_34_out, Q5);
  not not_35 (not_35_out, Q2);
  not not_36 (not_36_out, Q4);
  not not_37 (not_37_out, Q2);
  not not_38 (not_38_out, Q5);
  not not_39 (not_39_out, Q2);
  not not_40 (not_40_out, Q4);
  not not_41 (not_41_out, Q2);
  not not_42 (not_42_out, Q0);
  not not_43 (not_43_out, Q1);
  not not_44 (not_44_out, DIR);
  not not_45 (not_45_out, Q3);
  not not_46 (not_46_out, Q3);
  not not_47 (not_47_out, Q2);
  not not_48 (not_48_out, Q1);
  not not_49 (not_49_out, Q0);
  not not_50 (not_50_out, EN);
  not not_51 (not_51_out, DIR);
  not not_52 (not_52_out, Q1);
  not not_53 (not_53_out, Q0);
  not not_54 (not_54_out, DIR);
  not not_55 (not_55_out, Q5);
  not not_56 (not_56_out, Q2);
  not not_57 (not_57_out, DIR);
  not not_58 (not_58_out, Q4);
  not not_59 (not_59_out, Q2);
  not not_60 (not_60_out, DIR);
  not not_61 (not_61_out, Q3);
  not not_62 (not_62_out, Q2);
  not not_63 (not_63_out, Q2);
  not not_64 (not_64_out, Q1);
  not not_65 (not_65_out, Q0);
  not not_66 (not_66_out, Q2);
  not not_67 (not_67_out, Q1);
  not not_68 (not_68_out, Q0);
  not not_69 (not_69_out, Q2);
  not not_70 (not_70_out, Q1);
  not not_71 (not_71_out, Q0);
  not not_72 (not_72_out, EN);
  not not_73 (not_73_out, DIR);
  not not_74 (not_74_out, Q0);
  not not_75 (not_75_out, DIR);
  not not_76 (not_76_out, Q1);
  not not_77 (not_77_out, Q1);
  not not_78 (not_78_out, Q0);
  not not_79 (not_79_out, EN);
  not not_80 (not_80_out, Q0);
  not not_81 (not_81_out, DIR);
  not not_82 (not_82_out, Q5);
  not not_83 (not_83_out, Q4);
  not not_84 (not_84_out, Q3);
  not not_85 (not_85_out, Q2);
  not not_86 (not_86_out, Q1);
  not not_87 (not_87_out, Q0);
  not not_88 (not_88_out, EN);
  and and_1 (and_1_out, not_88_out, Q5);
  not not_89 (not_89_out, DIR);
  and and_2 (and_2_out, not_89_out, Q5, not_90_out);
  not not_90 (not_90_out, Q4);
  not not_91 (not_91_out, DIR);
  and and_3 (and_3_out, not_91_out, Q5, not_92_out);
  not not_92 (not_92_out, Q0);
  and and_4 (and_4_out, Q5, not_93_out, Q0);
  not not_93 (not_93_out, Q4);
  and and_5 (and_5_out, Q5, Q2);
  not not_94 (not_94_out, Q4);
  and and_6 (and_6_out, Q5, not_94_out, Q3);
  and and_7 (and_7_out, Q5, Q3, not_95_out);
  not not_95 (not_95_out, Q1);
  and and_8 (and_8_out, Q5, Q4, not_96_out);
  not not_96 (not_96_out, Q3);
  and and_9 (and_9_out, DIR, Q5, Q1);
  and and_10 (and_10_out, EN, not_1_out, Q4, Q3, Q2, Q1, Q0);
  and and_11 (and_11_out, EN, DIR, not_2_out, not_3_out, not_4_out, not_5_out, not_6_out, not_7_out);
  and and_12 (and_12_out, not_8_out, Q4);
  and and_13 (and_13_out, not_9_out, Q4, not_10_out);
  and and_14 (and_14_out, Q4, not_11_out, Q0);
  and and_15 (and_15_out, Q4, not_12_out, Q1);
  and and_16 (and_16_out, Q4, not_13_out, Q2);
  and and_17 (and_17_out, not_14_out, Q4, Q3, not_15_out);
  and and_18 (and_18_out, Q4, Q3, not_16_out);
  and and_19 (and_19_out, Q4, Q3, not_17_out);
  and and_20 (and_20_out, DIR, Q4, Q3);
  and and_21 (and_21_out, EN, not_18_out, not_19_out, Q3, Q2, Q1, Q0);
  and and_22 (and_22_out, EN, DIR, not_20_out, not_21_out, not_22_out, not_23_out, not_24_out);
  and and_23 (and_23_out, not_25_out, Q3);
  and and_24 (and_24_out, not_26_out, not_27_out, Q3, not_28_out);
  and and_25 (and_25_out, not_29_out, not_30_out, Q3, not_31_out);
  and and_26 (and_26_out, not_32_out, Q3, not_33_out);
  and and_27 (and_27_out, not_34_out, Q3, not_35_out, Q0);
  and and_28 (and_28_out, not_36_out, Q3, not_37_out, Q0);
  and and_29 (and_29_out, not_38_out, Q3, not_39_out, Q1);
  and and_30 (and_30_out, not_40_out, Q3, not_41_out, Q1);
  and and_31 (and_31_out, Q3, Q1, not_42_out);
  and and_32 (and_32_out, Q3, Q2, not_43_out);
  and and_33 (and_33_out, DIR, Q3, Q0);
  and and_34 (and_34_out, EN, not_44_out, not_45_out, Q2, Q1, Q0);
  and and_35 (and_35_out, EN, DIR, not_46_out, not_47_out, not_48_out, not_49_out);
  and and_36 (and_36_out, not_50_out, Q2);
  and and_37 (and_37_out, not_51_out, Q2, not_52_out);
  and and_38 (and_38_out, Q2, Q1, not_53_out);
  and and_39 (and_39_out, DIR, Q2, Q0);
  and and_40 (and_40_out, EN, not_54_out, not_55_out, not_56_out, Q1, Q0);
  and and_41 (and_41_out, EN, not_57_out, not_58_out, not_59_out, Q1, Q0);
  and and_42 (and_42_out, EN, not_60_out, not_61_out, not_62_out, Q1, Q0);
  and and_43 (and_43_out, EN, DIR, Q3, not_63_out, not_64_out, not_65_out);
  and and_44 (and_44_out, EN, DIR, Q4, not_66_out, not_67_out, not_68_out);
  and and_45 (and_45_out, EN, DIR, Q5, not_69_out, not_70_out, not_71_out);
  and and_46 (and_46_out, not_72_out, Q1);
  and and_47 (and_47_out, not_73_out, Q1, not_74_out);
  and and_48 (and_48_out, DIR, Q1, Q0);
  and and_49 (and_49_out, EN, not_75_out, not_76_out, Q0);
  and and_50 (and_50_out, EN, DIR, not_77_out, not_78_out);
  and and_51 (and_51_out, not_79_out, Q0);
  and and_52 (and_52_out, EN, not_80_out);
  and and_53 (OVRF, EN, not_81_out, Q5, Q4, Q3, Q1, Q0);
  and and_54 (UNDF, EN, DIR, not_82_out, not_83_out, not_84_out, not_85_out, not_86_out, not_87_out);
  or or_1 (D1, and_46_out, and_47_out, and_48_out, and_49_out, and_50_out);
  or or_2 (D0, and_51_out, and_52_out);
  or or_3 (D5, and_1_out, and_2_out, and_3_out, and_4_out, and_5_out, and_6_out, and_7_out, and_8_out, and_9_out, and_10_out, and_11_out);
  or or_4 (D4, and_12_out, and_13_out, and_14_out, and_15_out, and_16_out, and_17_out, and_18_out, and_19_out, and_20_out, and_21_out, and_22_out);
  or or_5 (D3, and_23_out, and_24_out, and_25_out, and_26_out, and_27_out, and_28_out, and_29_out, and_30_out, and_31_out, and_32_out, and_33_out, and_34_out, and_35_out);
  or or_6 (D2, and_36_out, and_37_out, and_38_out, and_39_out, and_40_out, and_41_out, and_42_out, and_43_out, and_44_out, and_45_out);
endmodule

module shift3 (
  input  EN,
  input  rst,
  input  clk,
  output out_4,
  output out_5,
  output out_6
);

  wire and_1_out, and_2_out, and_3_out, and_4_out, d_ff_1_q, d_ff_2_q, not_1_out, not_2_out, not_3_out,
       not_4_out, or_1_out, or_2_out;

  not not_1 (not_1_out, EN);
  not not_2 (not_2_out, EN);
  not not_3 (not_3_out, d_ff_2_q);
  not not_4 (not_4_out, d_ff_1_q);
  and and_1 (and_1_out, not_1_out, d_ff_2_q);
  and and_2 (and_2_out, EN, d_ff_1_q);
  and and_3 (and_3_out, not_2_out, d_ff_1_q);
  and and_4 (and_4_out, EN, not_3_out, not_4_out);
  or or_1 (or_1_out, and_1_out, and_2_out);
  or or_2 (or_2_out, and_3_out, and_4_out);
  D_Flip_Flop d_ff_1 (.D(or_2_out), .clk(clk), .Q(d_ff_1_q), .reset(rst));  // open: Qn, preset
  D_Flip_Flop d_ff_2 (.D(or_1_out), .clk(clk), .Q(d_ff_2_q));  // open: Qn, preset, reset
  and and_5 (out_4, ~d_ff_1_q, ~d_ff_2_q);  // AND_Gate
  and and_6 (out_5, d_ff_1_q, ~d_ff_2_q);  // AND_Gate
  and and_7 (out_6, ~d_ff_1_q, d_ff_2_q);  // AND_Gate
endmodule

module mod24 (
  input  en,
  input  dir,
  input  clk,
  input  rst,
  output [4:0] hour,
  output ovrf,
  output undf
);

  wire base24_1_d0, base24_1_d1, base24_1_d2, base24_1_d3, base24_1_d4, base24_1_ovrf, base24_1_undf,
       d_ff_6_q, d_ff_7_q, d_ff_8_q, d_ff_9_q;

  base24 base24_1 (
    .EN(en), .DIR(dir), .Q4(hour[4]), .Q3(hour[3]), .Q2(hour[2]), .Q1(hour[1]), .Q0(hour[0]),
    .D4(base24_1_d4), .D3(base24_1_d3), .D2(base24_1_d2), .D1(base24_1_d1), .D0(base24_1_d0),
    .OVRF(base24_1_ovrf), .UNDF(base24_1_undf));
  D_Flip_Flop d_ff_1 (.D(base24_1_d0), .clk(clk), .Q(hour[0]), .reset(rst));  // open: Qn, preset
  D_Flip_Flop d_ff_2 (.D(base24_1_d1), .clk(clk), .Q(hour[1]), .reset(rst));  // open: Qn, preset
  D_Flip_Flop d_ff_3 (.D(base24_1_d2), .clk(clk), .Q(hour[2]), .reset(rst));  // open: Qn, preset
  D_Flip_Flop d_ff_4 (.D(base24_1_d3), .clk(clk), .Q(hour[3]), .reset(rst));  // open: Qn, preset
  D_Flip_Flop d_ff_5 (.D(base24_1_d4), .clk(clk), .Q(hour[4]), .reset(rst));  // open: Qn, preset
  D_Flip_Flop d_ff_6 (.D(base24_1_ovrf), .clk(clk), .Q(d_ff_6_q), .reset(rst));  // open: Qn, preset
  D_Flip_Flop d_ff_7 (.D(base24_1_undf), .clk(clk), .Q(d_ff_7_q), .reset(rst));  // open: Qn, preset
  D_Flip_Flop d_ff_8 (.D(d_ff_6_q), .clk(clk), .Q(d_ff_8_q), .reset(rst));  // open: Qn, preset
  D_Flip_Flop d_ff_9 (.D(d_ff_7_q), .clk(clk), .Q(d_ff_9_q), .reset(rst));  // open: Qn, preset
  and and_1 (ovrf, d_ff_6_q, ~d_ff_8_q);  // AND_Gate
  and and_2 (undf, d_ff_7_q, ~d_ff_9_q);  // AND_Gate
endmodule

module base24 (
  input  EN,
  input  DIR,
  input  Q4,
  input  Q3,
  input  Q2,
  input  Q1,
  input  Q0,
  output D4,
  output D3,
  output D2,
  output D1,
  output D0,
  output OVRF,
  output UNDF
);

  wire and_1_out, and_2_out, and_3_out, and_4_out, and_5_out, and_6_out, and_7_out, and_8_out, and_9_out,
       and_10_out, and_11_out, and_12_out, and_13_out, and_14_out, and_15_out, and_16_out, and_17_out,
       and_18_out, and_19_out, and_20_out, and_21_out, and_22_out, and_23_out, and_24_out, and_25_out,
       and_26_out, and_27_out, and_28_out, and_29_out, not_1_out, not_2_out, not_3_out, not_4_out, not_5_out,
       not_6_out, not_7_out, not_8_out, not_9_out, not_10_out, not_11_out, not_12_out, not_13_out,
       not_14_out, not_15_out, not_16_out, not_17_out, not_18_out, not_19_out, not_20_out, not_21_out,
       not_22_out, not_23_out, not_24_out, not_25_out, not_26_out, not_27_out, not_28_out, not_29_out,
       not_30_out, not_31_out, not_32_out, not_33_out, not_34_out, not_35_out, not_36_out, not_37_out,
       not_38_out, not_39_out, not_40_out, not_41_out, not_42_out, not_43_out, not_44_out, not_45_out,
       not_46_out, not_47_out, not_48_out, not_49_out, not_50_out;

  not not_1 (not_1_out, EN);
  not not_2 (not_2_out, DIR);
  not not_3 (not_3_out, Q2);
  not not_4 (not_4_out, DIR);
  not not_5 (not_5_out, Q0);
  not not_6 (not_6_out, Q2);
  not not_7 (not_7_out, Q1);
  not not_8 (not_8_out, DIR);
  not not_9 (not_9_out, Q4);
  not not_10 (not_10_out, Q3);
  not not_11 (not_11_out, Q2);
  not not_12 (not_12_out, Q1);
  not not_13 (not_13_out, Q0);
  not not_14 (not_14_out, EN);
  not not_15 (not_15_out, DIR);
  not not_16 (not_16_out, Q2);
  not not_17 (not_17_out, DIR);
  not not_18 (not_18_out, Q0);
  not not_19 (not_19_out, Q2);
  not not_20 (not_20_out, Q1);
  not not_21 (not_21_out, DIR);
  not not_22 (not_22_out, Q4);
  not not_23 (not_23_out, Q3);
  not not_24 (not_24_out, Q2);
  not not_25 (not_25_out, Q1);
  not not_26 (not_26_out, Q0);
  not not_27 (not_27_out, EN);
  not not_28 (not_28_out, DIR);
  not not_29 (not_29_out, Q1);
  not not_30 (not_30_out, Q0);
  not not_31 (not_31_out, DIR);
  not not_32 (not_32_out, Q2);
  not not_33 (not_33_out, Q2);
  not not_34 (not_34_out, Q1);
  not not_35 (not_35_out, Q0);
  not not_36 (not_36_out, EN);
  not not_37 (not_37_out, DIR);
  not not_38 (not_38_out, Q0);
  not not_39 (not_39_out, DIR);
  not not_40 (not_40_out, Q1);
  not not_41 (not_41_out, Q1);
  not not_42 (not_42_out, Q0);
  not not_43 (not_43_out, EN);
  not not_44 (not_44_out, Q0);
  not not_45 (not_45_out, DIR);
  not not_46 (not_46_out, Q4);
  not not_47 (not_47_out, Q3);
  not not_48 (not_48_out, Q2);
  not not_49 (not_49_out, Q1);
  not not_50 (not_50_out, Q0);
  and and_1 (and_1_out, not_1_out, Q4);
  and and_2 (and_2_out, not_2_out, Q4, not_3_out);
  and and_3 (and_3_out, not_4_out, Q4, not_5_out);
  and and_4 (and_4_out, Q4, not_6_out, Q0);
  and and_5 (and_5_out, Q4, Q2, not_7_out);
  and and_6 (and_6_out, DIR, Q4, Q1);
  and and_7 (and_7_out, EN, not_8_out, Q3, Q2, Q1, Q0);
  and and_8 (and_8_out, EN, DIR, not_9_out, not_10_out, not_11_out, not_12_out, not_13_out);
  and and_9 (and_9_out, not_14_out, Q3);
  and and_10 (and_10_out, not_15_out, Q3, not_16_out);
  and and_11 (and_11_out, not_17_out, Q3, not_18_out);
  and and_12 (and_12_out, Q3, not_19_out, Q0);
  and and_13 (and_13_out, Q3, Q2, not_20_out);
  and and_14 (and_14_out, DIR, Q3, Q1);
  and and_15 (and_15_out, EN, not_21_out, not_22_out, not_23_out, Q2, Q1, Q0);
  and and_16 (and_16_out, EN, DIR, Q4, not_24_out, not_25_out, not_26_out);
  and and_17 (and_17_out, not_27_out, Q2);
  and and_18 (and_18_out, not_28_out, Q2, not_29_out);
  and and_19 (and_19_out, Q2, Q1, not_30_out);
  and and_20 (and_20_out, DIR, Q2, Q0);
  and and_21 (and_21_out, EN, not_31_out, not_32_out, Q1, Q0);
  and and_22 (and_22_out, EN, DIR, not_33_out, not_34_out, not_35_out);
  and and_23 (and_23_out, not_36_out, Q1);
  and and_24 (and_24_out, not_37_out, Q1, not_38_out);
  and and_25 (and_25_out, DIR, Q1, Q0);
  and and_26 (and_26_out, EN, not_39_out, not_40_out, Q0);
  and and_27 (and_27_out, EN, DIR, not_41_out, not_42_out);
  and and_28 (and_28_out, not_43_out, Q0);
  and and_29 (and_29_out, EN, not_44_out);
  and and_30 (OVRF, EN, not_45_out, Q4, Q2, Q1, Q0);
  and and_31 (UNDF, EN, DIR, not_46_out, not_47_out, not_48_out, not_49_out, not_50_out);
  or or_1 (D4, and_1_out, and_2_out, and_3_out, and_4_out, and_5_out, and_6_out, and_7_out, and_8_out);
  or or_2 (D3, and_9_out, and_10_out, and_11_out, and_12_out, and_13_out, and_14_out, and_15_out, and_16_out);
  or or_3 (D2, and_17_out, and_18_out, and_19_out, and_20_out, and_21_out, and_22_out);
  or or_4 (D1, and_23_out, and_24_out, and_25_out, and_26_out, and_27_out);
  or or_5 (D0, and_28_out, and_29_out);
endmodule
