// Logisim project ymca.circ as structural Verilog: 4 circuits, main circuit generator
module generator (
  input  EN,
  input  clk,
  input  rst,
  input  E4,
  input  F4,
  input  G4,
  input  A4,
  input  B4,
  input  C5,
  input  D5,
  input  E5,
  output sig
);

  wire and_1_out, and_2_out, and_3_out, and_4_out, and_5_out, and_6_out, and_7_out, and_8_out, and_9_out,
       and_10_out, and_11_out, and_12_out, and_13_out, and_14_out, and_15_out, and_16_out, and_17_out,
       and_18_out, and_19_out, and_20_out, and_21_out, or_1_out, or_2_out, t_ff_1_q, t_ff_2_q, t_ff_3_q,
       t_ff_4_q, t_ff_5_q, t_ff_6_q, t_ff_7_q, t_ff_9_q, t_ff_10_q, t_ff_11_q, t_ff_12_q, t_ff_13_q,
       t_ff_14_q;

  or or_1 (or_1_out, rst, or_2_out);
  and and_1 (and_1_out, EN, t_ff_1_q);
  T_Flip_Flop t_ff_1 (.T(EN), .clk(clk), .Q(t_ff_1_q), .reset(or_1_out), .preset(1'b0));  // open: Qn
  and and_2 (and_2_out, ~t_ff_12_q, ~t_ff_11_q, ~t_ff_10_q, ~t_ff_9_q, ~t_ff_7_q, ~t_ff_6_q, ~t_ff_5_q, ~t_ff_4_q, ~t_ff_3_q, ~t_ff_2_q, ~t_ff_1_q);  // AND_Gate
  and and_3 (and_3_out, and_1_out, t_ff_2_q);
  T_Flip_Flop t_ff_2 (.T(and_1_out), .clk(clk), .Q(t_ff_2_q), .reset(or_1_out), .preset(1'b0));  // open: Qn
  and and_4 (and_4_out, and_3_out, t_ff_3_q);
  T_Flip_Flop t_ff_3 (.T(and_3_out), .clk(clk), .Q(t_ff_3_q), .reset(or_1_out), .preset(1'b0));  // open: Qn
  and and_5 (and_5_out, and_4_out, t_ff_4_q);
  T_Flip_Flop t_ff_4 (.T(and_4_out), .clk(clk), .Q(t_ff_4_q), .reset(or_1_out), .preset(1'b0));  // open: Qn
  and and_6 (and_6_out, t_ff_6_q, t_ff_5_q, ~t_ff_4_q, ~t_ff_3_q, ~t_ff_2_q, ~t_ff_1_q, E4);  // AND_Gate
  and and_7 (and_7_out, t_ff_6_q, ~t_ff_5_q, t_ff_4_q, t_ff_3_q, t_ff_2_q, ~t_ff_1_q, F4);  // AND_Gate
  and and_8 (and_8_out, t_ff_6_q, ~t_ff_5_q, t_ff_4_q, ~t_ff_3_q, ~t_ff_2_q, t_ff_1_q, G4);  // AND_Gate
  and and_9 (and_9_out, t_ff_6_q, ~t_ff_5_q, ~t_ff_4_q, t_ff_3_q, ~t_ff_2_q, ~t_ff_1_q, A4);  // AND_Gate
  and and_10 (and_10_out, t_ff_6_q, ~t_ff_5_q, ~t_ff_4_q, ~t_ff_3_q, ~t_ff_2_q, ~t_ff_1_q, B4);  // AND_Gate
  and and_11 (and_11_out, ~t_ff_6_q, t_ff_5_q, t_ff_4_q, t_ff_3_q, t_ff_2_q, t_ff_1_q, C5);  // AND_Gate
  and and_12 (and_12_out, ~t_ff_6_q, t_ff_5_q, t_ff_4_q, t_ff_3_q, ~t_ff_2_q, ~t_ff_1_q, D5);  // AND_Gate
  and and_13 (and_13_out, ~t_ff_6_q, t_ff_5_q, t_ff_4_q, ~t_ff_3_q, ~t_ff_2_q, ~t_ff_1_q, E5);  // AND_Gate
  and and_14 (and_14_out, and_5_out, t_ff_5_q);
  T_Flip_Flop t_ff_5 (.T(and_5_out), .clk(clk), .Q(t_ff_5_q), .reset(or_1_out), .preset(1'b0));  // open: Qn
  or or_2 (or_2_out, and_6_out, and_7_out, and_8_out, and_9_out, and_10_out, and_11_out, and_12_out, and_13_out);
  and and_15 (and_15_out, and_14_out, t_ff_6_q);
  T_Flip_Flop t_ff_6 (.T(and_14_out), .clk(clk), .Q(t_ff_6_q), .reset(or_1_out), .preset(1'b0));  // open: Qn
  and and_16 (and_16_out, and_15_out, t_ff_7_q);
  T_Flip_Flop t_ff_7 (.T(and_15_out), .clk(clk), .Q(t_ff_7_q), .reset(or_1_out), .preset(1'b0));  // open: Qn
  T_Flip_Flop t_ff_8 (.T(and_2_out), .clk(clk), .Q(sig));  // open: Qn, reset, preset
  and and_17 (and_17_out, and_16_out, t_ff_9_q);
  T_Flip_Flop t_ff_9 (.T(and_16_out), .clk(clk), .Q(t_ff_9_q), .reset(or_1_out), .preset(1'b0));  // open: Qn
  and and_18 (and_18_out, and_17_out, t_ff_10_q);
  T_Flip_Flop t_ff_10 (.T(and_17_out), .clk(clk), .Q(t_ff_10_q), .reset(or_1_out), .preset(1'b0));  // open: Qn
  and and_19 (and_19_out, and_18_out, t_ff_11_q);
  T_Flip_Flop t_ff_11 (.T(and_18_out), .clk(clk), .Q(t_ff_11_q), .reset(or_1_out), .preset(1'b0));  // open: Qn
  and and_20 (and_20_out, and_19_out, t_ff_12_q);
  T_Flip_Flop t_ff_12 (.T(and_19_out), .clk(clk), .Q(t_ff_12_q), .reset(or_1_out), .preset(1'b0));  // open: Qn
  and and_21 (and_21_out, and_20_out, t_ff_13_q);
  T_Flip_Flop t_ff_13 (.T(and_20_out), .clk(clk), .Q(t_ff_13_q), .reset(or_1_out), .preset(1'b0));  // open: Qn
  T_Flip_Flop t_ff_14 (.T(and_21_out), .clk(clk), .Q(t_ff_14_q), .reset(or_1_out), .preset(1'b0));  // open: Qn
endmodule

module partition (
  output gnd,
  output sgn
);

  wire and_1_out, and_2_out, and_3_out, and_4_out, and_5_out, and_6_out, and_7_out, and_8_out, and_9_out,
       and_10_out, and_11_out, and_12_out, and_13_out, and_14_out, and_15_out, Button_1_out, Button_2_out,
       clock_1_out, d_ff_1_q, d_ff_2_q, d_ff_3_q, d_ff_4_q, d_ff_5_q, d_ff_6_q, or_1_out, or_2_out,
       score_1_a4, score_1_b4, score_1_c5, score_1_d5, score_1_e4, score_1_e5, score_1_f4, score_1_g4,
       t_ff_1_q, t_ff_2_q, t_ff_3_q, t_ff_4_q, t_ff_5_q, t_ff_6_q, t_ff_7_q, t_ff_8_q, t_ff_9_q, t_ff_10_q,
       t_ff_11_q, t_ff_12_q, t_ff_13_q, timing_1_d0, timing_1_d1, timing_1_d2, timing_1_d3, timing_1_d4;

  Button Button_1 (.out(Button_1_out));
  Clock clock_1 (.out(clock_1_out));
  Button Button_2 (.out(Button_2_out));
  D_Flip_Flop d_ff_1 (.D(Button_1_out), .clk(clock_1_out), .Q(d_ff_1_q), .reset(Button_2_out));  // open: Qn, preset
  or or_1 (or_1_out, Button_2_out, and_1_out);
  and and_1 (and_1_out, ~t_ff_11_q, t_ff_10_q, t_ff_9_q, t_ff_8_q, t_ff_7_q, t_ff_6_q, ~t_ff_5_q, t_ff_4_q, ~t_ff_3_q, ~t_ff_2_q, ~t_ff_1_q);  // AND_Gate
  and and_2 (and_2_out, ~d_ff_1_q, Button_1_out);  // AND_Gate
  T_Flip_Flop t_ff_1 (.T(Button_1_out), .clk(clock_1_out), .Q(t_ff_1_q), .reset(or_1_out), .preset(1'b0));  // open: Qn
  or or_2 (or_2_out, Button_2_out, and_2_out);
  and and_3 (and_3_out, Button_1_out, t_ff_1_q);
  T_Flip_Flop t_ff_2 (.T(and_3_out), .clk(clock_1_out), .Q(t_ff_2_q), .reset(or_1_out), .preset(1'b0));  // open: Qn
  and and_4 (and_4_out, and_3_out, t_ff_2_q);
  T_Flip_Flop t_ff_3 (.T(and_4_out), .clk(clock_1_out), .Q(t_ff_3_q), .reset(or_1_out), .preset(1'b0));  // open: Qn
  and and_5 (and_5_out, ~t_ff_1_q, ~t_ff_3_q, ~t_ff_8_q, ~t_ff_4_q, ~t_ff_5_q, ~t_ff_6_q, ~t_ff_7_q, ~t_ff_13_q, ~t_ff_2_q, ~t_ff_9_q, ~t_ff_10_q, ~t_ff_11_q, ~t_ff_12_q);  // AND_Gate
  and and_6 (and_6_out, and_4_out, t_ff_3_q);
  T_Flip_Flop t_ff_4 (.T(and_6_out), .clk(clock_1_out), .Q(t_ff_4_q), .reset(or_1_out), .preset(1'b0));  // open: Qn
  timing timing_1 (
    .en(and_5_out), .q4(d_ff_6_q), .q3(d_ff_5_q), .q2(d_ff_4_q), .q1(d_ff_3_q), .q0(d_ff_2_q),
    .d4(timing_1_d4), .d3(timing_1_d3), .d2(timing_1_d2), .d1(timing_1_d1), .d0(timing_1_d0));
  and and_7 (and_7_out, and_6_out, t_ff_4_q);
  T_Flip_Flop t_ff_5 (.T(and_7_out), .clk(clock_1_out), .Q(t_ff_5_q), .reset(or_1_out), .preset(1'b0));  // open: Qn
  D_Flip_Flop d_ff_2 (.D(timing_1_d0), .clk(clock_1_out), .Q(d_ff_2_q), .reset(or_2_out));  // open: Qn, preset
  and and_8 (and_8_out, and_7_out, t_ff_5_q);
  T_Flip_Flop t_ff_6 (.T(and_8_out), .clk(clock_1_out), .Q(t_ff_6_q), .reset(or_1_out), .preset(1'b0));  // open: Qn
  D_Flip_Flop d_ff_3 (.D(timing_1_d1), .clk(clock_1_out), .Q(d_ff_3_q), .reset(or_2_out));  // open: Qn, preset
  and and_9 (and_9_out, and_8_out, t_ff_6_q);
  T_Flip_Flop t_ff_7 (.T(and_9_out), .clk(clock_1_out), .Q(t_ff_7_q), .reset(or_1_out), .preset(1'b0));  // open: Qn
  D_Flip_Flop d_ff_4 (.D(timing_1_d2), .clk(clock_1_out), .Q(d_ff_4_q), .reset(or_2_out));  // open: Qn, preset
  and and_10 (and_10_out, and_9_out, t_ff_7_q);
  T_Flip_Flop t_ff_8 (.T(and_10_out), .clk(clock_1_out), .Q(t_ff_8_q), .reset(or_1_out), .preset(1'b0));  // open: Qn
  D_Flip_Flop d_ff_5 (.D(timing_1_d3), .clk(clock_1_out), .Q(d_ff_5_q), .reset(or_2_out));  // open: Qn, preset
  and and_11 (and_11_out, and_10_out, t_ff_8_q);
  T_Flip_Flop t_ff_9 (.T(and_11_out), .clk(clock_1_out), .Q(t_ff_9_q), .reset(or_1_out), .preset(1'b0));  // open: Qn
  D_Flip_Flop d_ff_6 (.D(timing_1_d4), .clk(clock_1_out), .Q(d_ff_6_q), .reset(or_2_out));  // open: Qn, preset
  and and_12 (and_12_out, and_11_out, t_ff_9_q);
  T_Flip_Flop t_ff_10 (.T(and_12_out), .clk(clock_1_out), .Q(t_ff_10_q), .reset(or_1_out), .preset(1'b0));  // open: Qn
  and and_13 (and_13_out, and_12_out, t_ff_10_q);
  T_Flip_Flop t_ff_11 (.T(and_13_out), .clk(clock_1_out), .Q(t_ff_11_q), .reset(or_1_out), .preset(1'b0));  // open: Qn
  and and_14 (and_14_out, and_13_out, t_ff_11_q);
  T_Flip_Flop t_ff_12 (.T(and_14_out), .clk(clock_1_out), .Q(t_ff_12_q), .reset(or_1_out), .preset(1'b0));  // open: Qn
  and and_15 (and_15_out, and_14_out, t_ff_12_q);
  T_Flip_Flop t_ff_13 (.T(and_15_out), .clk(clock_1_out), .Q(t_ff_13_q), .reset(or_1_out), .preset(1'b0));  // open: Qn
  score score_1 (
    .en(Button_1_out), .i4(d_ff_6_q), .i3(d_ff_5_q), .i2(d_ff_4_q), .i1(d_ff_3_q), .i0(d_ff_2_q),
    .e4(score_1_e4), .f4(score_1_f4), .g4(score_1_g4), .a4(score_1_a4), .b4(score_1_b4), .c5(score_1_c5),
    .d5(score_1_d5), .e5(score_1_e5));
  generator generator_1 (
    .EN(Button_1_out), .clk(clock_1_out), .rst(or_2_out), .E4(score_1_e4), .F4(score_1_f4), .G4(score_1_g4),
    .A4(score_1_a4), .B4(score_1_b4), .C5(score_1_c5), .D5(score_1_d5), .E5(score_1_e5), .sig(sgn));

  assign gnd = 1'b0;
endmodule

module timing (
  input  en,
  input  q4,
  input  q3,
  input  q2,
  input  q1,
  input  q0,
  output d4,
  output d3,
  output d2,
  output d1,
  output d0
);

  wire and_1_out, and_2_out, and_3_out, and_4_out, and_5_out, and_6_out, and_7_out, and_8_out, and_9_out,
       and_10_out, and_11_out, and_12_out, and_13_out, and_14_out, and_15_out, and_16_out, and_17_out,
       and_18_out, and_19_out, and_20_out, and_21_out, and_22_out, and_23_out, and_24_out, and_25_out,
       not_1_out, not_2_out, not_3_out, not_4_out, not_5_out, not_6_out, not_7_out, not_8_out, not_9_out,
       not_10_out, not_11_out, not_12_out, not_13_out, not_14_out, not_15_out, not_16_out, not_17_out,
       not_18_out, not_19_out, not_20_out, not_21_out, not_22_out, not_23_out, not_24_out, not_25_out,
       not_26_out, not_27_out, not_28_out, not_29_out, not_30_out, not_31_out, not_32_out, not_33_out,
       not_34_out, not_35_out;

  not not_1 (not_1_out, en);
  not not_2 (not_2_out, q3);
  not not_3 (not_3_out, q2);
  not not_4 (not_4_out, q1);
  not not_5 (not_5_out, q4);
  not not_6 (not_6_out, en);
  not not_7 (not_7_out, q4);
  not not_8 (not_8_out, q0);
  not not_9 (not_9_out, q2);
  not not_10 (not_10_out, q1);
  not not_11 (not_11_out, q3);
  not not_12 (not_12_out, en);
  not not_13 (not_13_out, q4);
  not not_14 (not_14_out, q0);
  not not_15 (not_15_out, q3);
  not not_16 (not_16_out, q0);
  not not_17 (not_17_out, q1);
  not not_18 (not_18_out, q2);
  not not_19 (not_19_out, en);
  and and_1 (and_1_out, not_19_out, q1);
  not not_20 (not_20_out, q4);
  and and_2 (and_2_out, not_20_out, q1, not_21_out);
  not not_21 (not_21_out, q0);
  not not_22 (not_22_out, q3);
  and and_3 (and_3_out, not_22_out, q1, not_23_out);
  not not_23 (not_23_out, q0);
  not not_24 (not_24_out, q2);
  and and_4 (and_4_out, not_24_out, q1, not_25_out);
  not not_25 (not_25_out, q0);
  and and_5 (and_5_out, en, not_26_out, q0);
  not not_26 (not_26_out, q1);
  not not_27 (not_27_out, en);
  and and_6 (and_6_out, not_27_out, q0);
  and and_7 (and_7_out, en, not_28_out, not_29_out);
  not not_28 (not_28_out, q4);
  not not_29 (not_29_out, q0);
  not not_30 (not_30_out, q3);
  and and_8 (and_8_out, en, not_30_out, not_31_out);
  not not_31 (not_31_out, q0);
  not not_32 (not_32_out, q2);
  and and_9 (and_9_out, en, not_32_out, not_33_out);
  not not_33 (not_33_out, q0);
  and and_10 (and_10_out, en, not_34_out, not_35_out);
  not not_34 (not_34_out, q1);
  not not_35 (not_35_out, q0);
  and and_11 (and_11_out, not_1_out, q4);
  and and_12 (and_12_out, q4, not_2_out);
  and and_13 (and_13_out, q4, not_3_out);
  and and_14 (and_14_out, q4, not_4_out);
  and and_15 (and_15_out, en, not_5_out, q3, q2, q1, q0);
  and and_16 (and_16_out, not_6_out, q3);
  and and_17 (and_17_out, not_7_out, q3, not_8_out);
  and and_18 (and_18_out, q3, not_9_out);
  and and_19 (and_19_out, q3, not_10_out);
  and and_20 (and_20_out, en, not_11_out, q2, q1, q0);
  and and_21 (and_21_out, not_12_out, q2);
  and and_22 (and_22_out, not_13_out, q2, not_14_out);
  and and_23 (and_23_out, not_15_out, q2, not_16_out);
  and and_24 (and_24_out, q2, not_17_out);
  and and_25 (and_25_out, en, not_18_out, q1, q0);
  or or_1 (d1, and_1_out, and_2_out, and_3_out, and_4_out, and_5_out);
  or or_2 (d0, and_6_out, and_7_out, and_8_out, and_9_out, and_10_out);
  or or_3 (d4, and_11_out, and_12_out, and_13_out, and_14_out, and_15_out);
  or or_4 (d3, and_16_out, and_17_out, and_18_out, and_19_out, and_20_out);
  or or_5 (d2, and_21_out, and_22_out, and_23_out, and_24_out, and_25_out);
endmodule

module score (
  input  en,
  input  i4,
  input  i3,
  input  i2,
  input  i1,
  input  i0,
  output e4,
  output f4,
  output g4,
  output a4,
  output b4,
  output c5,
  output d5,
  output e5
);

  wire and_1_out, and_2_out, and_3_out, and_4_out, and_5_out, and_6_out, and_7_out, and_8_out, and_9_out,
       and_10_out, and_11_out, and_12_out, and_13_out, not_1_out, not_2_out, not_3_out, not_4_out, not_5_out,
       not_6_out, not_7_out, not_8_out, not_9_out, not_10_out, not_11_out, not_12_out, not_13_out,
       not_14_out, not_15_out, not_16_out, not_17_out, not_18_out, not_19_out, not_20_out, not_21_out,
       not_22_out, not_23_out, not_24_out, not_25_out, not_26_out, not_27_out, not_28_out, not_29_out;

  not not_1 (not_1_out, i4);
  not not_2 (not_2_out, i3);
  not not_3 (not_3_out, i4);
  not not_4 (not_4_out, i2);
  not not_5 (not_5_out, i2);
  not not_6 (not_6_out, i1);
  not not_7 (not_7_out, i0);
  not not_8 (not_8_out, i4);
  not not_9 (not_9_out, i3);
  not not_10 (not_10_out, i1);
  not not_11 (not_11_out, i3);
  not not_12 (not_12_out, i2);
  not not_13 (not_13_out, i2);
  not not_14 (not_14_out, i0);
  not not_15 (not_15_out, i2);
  not not_16 (not_16_out, i1);
  not not_17 (not_17_out, i4);
  not not_18 (not_18_out, i3);
  not not_19 (not_19_out, i2);
  not not_20 (not_20_out, i3);
  not not_21 (not_21_out, i2);
  not not_22 (not_22_out, i1);
  not not_23 (not_23_out, i2);
  not not_24 (not_24_out, i1);
  not not_25 (not_25_out, i0);
  not not_26 (not_26_out, i3);
  not not_27 (not_27_out, i0);
  not not_28 (not_28_out, i3);
  not not_29 (not_29_out, i1);
  and and_1 (and_1_out, en, not_1_out, not_2_out, i2, i1);
  and and_2 (and_2_out, en, not_3_out, i3, not_4_out);
  and and_3 (and_3_out, en, i3, not_5_out, i1, i0);
  and and_4 (and_4_out, en, i3, i2, not_6_out);
  and and_5 (and_5_out, en, i4, i3, i2, not_7_out);
  and and_6 (and_6_out, en, not_8_out, not_9_out, i2, not_10_out);
  and and_7 (and_7_out, en, i4, not_11_out, not_12_out, i1);
  and and_8 (and_8_out, en, i4, not_13_out, i1, not_14_out);
  and and_9 (and_9_out, en, i4, i3, not_15_out, not_16_out, i0);
  and and_10 (and_10_out, en, not_17_out, not_18_out, not_19_out);
  and and_11 (and_11_out, en, not_20_out, not_21_out, not_22_out);
  and and_12 (and_12_out, en, i4, not_23_out, not_24_out, not_25_out);
  and and_13 (and_13_out, en, i4, not_26_out, i2, i1, not_27_out);
  and and_14 (d5, en, i4, not_28_out, i2, not_29_out);
  or or_1 (e4, and_1_out, and_2_out, and_3_out, and_4_out, and_5_out);
  or or_2 (a4, and_6_out, and_7_out, and_8_out, and_9_out);
  or or_3 (b4, and_10_out, and_11_out, and_12_out, and_13_out);

  assign c5 = 1'b0;
  assign e5 = 1'b0;
  assign f4 = 1'b0;
  assign g4 = 1'b0;
endmodule
